// Logisim project 11111.circ as structural Verilog: 20 circuits, main circuit ◇单周期MIPS
module \单周期MIPS  (
  input  IR1,
  input  IR2,
  input  IR3,
  output RegWrite,
  output MemWrite,
  output [31:0] PC,
  output [31:0] IR,
  output [31:0] RDin,
  output [31:0] MDin,
  output [31:0] LedData
);

  wire AluSrcB, and_1_out, and_2_out, and_3_out, and_6_out, and_7_out, Beq, BLTZ, Bne, CLK, clock_2_out,
       comparator_1_lt, comparator_2_eq, comparator_3_eq, comparator_3_lt, d_ff_1_q, equal, Go, halt, IR1_t,
       IR2_t, IR3_t, IRA, IRB, IRC, JAL, JMP, JR, LBU, LUI, MemToReg, nand_1_out, not_equal, or_1_out,
       or_2_out, RegDst, SignedExt, Syscall, W1, W2, W3;
  wire [3:0] AluOP;
  wire [4:0] multiplexer_3_out, multiplexer_4_out, multiplexer_5_out, multiplexer_7_out;
  wire [7:0] multiplexer_13_out;
  wire [12:0] CNT_num;
  wire [15:0] \总周期数 ;
  wire [27:0] adder_1_out;
  wire [31:0] adder_2_out, bit_extender_1_out, bit_extender_2_out, mips_alu_1_result, multiplexer_1_out,
       multiplexer_2_out, multiplexer_6_out, multiplexer_9_out, multiplexer_10_out, multiplexer_11_out,
       multiplexer_12_out, PC_q, R1, ram_1_data, shifter_1_out, shifter_2_out;
  wire [31:8] multiplexer_13_out_2;

  Clock #(.highDuration(1), .lowDuration(1)) clock_1 ();  // open: out
  Button _1 (.out(IRA));
  Button _2 (.out(IRB));
  Button _3 (.out(IRC));
  and and_1 (and_1_out, Bne, not_equal);
  or or_1 (or_1_out, and_1_out, and_2_out, and_3_out);
  Button \u_继续运行  (.out(Go));
  LED #(.active("true")) led_1 (.in(W1));
  LED #(.active("true")) led_2 (.in(W2));
  LED #(.active("true")) led_3 (.in(W3));
  not not_1 (not_equal, equal);
  and and_2 (and_2_out, equal, Beq);
  Multiplexer #(.select(1), .width(32), .disabled("Z"), .enable("false")) multiplexer_1 (
    .in0({shifter_1_out[31:28], adder_1_out}), .in1(adder_2_out), .out(multiplexer_1_out), .sel(or_1_out));
  Hex_Digit_Display hex_digit_display_1 (.value(LedData[31:28]));  // open: dp
  and and_3 (and_3_out, comparator_1_lt, BLTZ);
  Multiplexer #(.select(2), .width(32), .disabled("Z"), .enable("false")) multiplexer_2 (
    .in0(multiplexer_1_out), .in1(R1), .in2(shifter_1_out), .in3(R1), .out(multiplexer_2_out), .sel({JMP, JR}));
  Hex_Digit_Display hex_digit_display_2 (.value(LedData[23:20]));  // open: dp
  Hex_Digit_Display hex_digit_display_3 (.value(LedData[27:24]));  // open: dp
  Comparator #(.width(32), .mode("twosComplement")) comparator_1 (
    .a(R1), .b({32{1'b0}}), .lt(comparator_1_lt));  // open: gt, eq
  or or_2 (or_2_out, ~halt, Go);  // OR_Gate
  Hex_Digit_Display hex_digit_display_4 (.value(LedData[15:12]));  // open: dp
  Hex_Digit_Display hex_digit_display_5 (.value(LedData[19:16]));  // open: dp
  Register #(.width(32), .trigger("rising"), .Select("low")) u_PC (
    .D(multiplexer_2_out), .en(or_2_out), .Q(PC_q), .clk(CLK), .clr(1'b0));
  Counter #(.width(16), .max('hffff), .ongoal("wrap"), .trigger("rising"), .behavior("old")) counter_1 (
    .load(1'b0), .count(or_2_out), .Q(\总周期数 ), .clk(CLK), .clr(1'b0));  // open: D, carry, preset
  Hex_Digit_Display hex_digit_display_6 (.value(LedData[7:4]));  // open: dp
  Hex_Digit_Display hex_digit_display_7 (.value(LedData[11:8]));  // open: dp
  // Probe on \总周期数 
  Hex_Digit_Display hex_digit_display_8 (.value(LedData[3:0]));  // open: dp
  ROM #(.addrWidth(10), .dataWidth(32), .Select("high")) rom_1 (.addr(PC_q[11:2]), .data(IR));
  assign PC = PC_q & 32'hffff;  // AND_Gate and_4, 32 bits wide
  Adder #(.width(32)) adder_1 (.a(PC_q), .b(32'h4), .out({shifter_1_out[31:28], adder_1_out}));  // open: cin, cout
  // Mips_Probe mips_probe_1: pin names not known; wires that end beside it: IR
  or or_3 (IR1_t, IR1, IRA);
  Multiplexer #(.select(1), .width(5), .disabled("Z"), .enable("false")) multiplexer_3 (
    .in0(IR[25:21]), .in1(5'b00010), .out(multiplexer_3_out), .sel(Syscall));
  Multiplexer #(.select(1), .width(5), .disabled("Z"), .enable("false")) multiplexer_4 (
    .in0(IR[20:16]), .in1(IR[15:11]), .out(multiplexer_4_out), .sel(RegDst));
  assign bit_extender_1_out = {{16{1'b0}}, IR[15:0]};  // Bit_Extender bit_extender_1
  assign bit_extender_2_out = {{16{IR[15]}}, IR[15:0]};  // Bit_Extender bit_extender_2
  Shifter #(.width(28), .shift("ll")) shifter_1 (.in(IR[27:0]), .\dist (5'b00010), .out(shifter_1_out[27:0]));
  or or_4 (IR2_t, IR2, IRB);
  Multiplexer #(.select(1), .width(5), .disabled("Z"), .enable("false")) multiplexer_5 (
    .in0(multiplexer_4_out), .in1({5{1'b1}}), .out(multiplexer_5_out), .sel(JAL));
  Multiplexer #(.select(1), .width(32), .disabled("Z"), .enable("false")) multiplexer_6 (
    .in0(bit_extender_1_out), .in1(bit_extender_2_out), .out(multiplexer_6_out), .sel(SignedExt));
  Multiplexer #(.select(1), .width(5), .disabled("Z"), .enable("false")) multiplexer_7 (
    .in0(IR[20:16]), .in1(5'b00100), .out(multiplexer_7_out), .sel(Syscall));
  Multiplexer #(.select(1), .width(32), .disabled("Z"), .enable("false")) multiplexer_8 (
    .in0(multiplexer_12_out), .in1({shifter_1_out[31:28], adder_1_out}), .out(RDin), .sel(JAL));
  or or_5 (IR3_t, IR3, IRC);
  MIPS_Regifile mips_regifile_1 (
    .Din(RDin), .Clk(CLK), .R1(R1), .R2(MDin), .WE(RegWrite), .W_num(multiplexer_5_out),
    .R1_num(multiplexer_3_out), .R2_num(multiplexer_7_out));
  Multiplexer #(.select(1), .width(32), .disabled("Z"), .enable("false")) multiplexer_9 (
    .in0(MDin), .in1(multiplexer_6_out), .out(multiplexer_9_out), .sel(AluSrcB));
  Shifter #(.width(32), .shift("ll")) shifter_2 (.in(multiplexer_6_out), .\dist (5'b00010), .out(shifter_2_out));
  Multiplexer #(.select(1), .width(32), .disabled("Z"), .enable("false")) multiplexer_10 (
    .in0(multiplexer_9_out), .in1(32'h22), .out(multiplexer_10_out), .sel(Syscall));
  Adder #(.width(32)) adder_2 (
    .a(shifter_2_out), .b({shifter_1_out[31:28], adder_1_out}), .out(adder_2_out));  // open: cin, cout
  MIPS_ALU mips_alu_1 (
    .X(R1), .Y(multiplexer_10_out), .AluOP(AluOP), .Equal(equal), .Result(mips_alu_1_result), .shamt(IR[10:6]));  // open: Result_2
  Comparator #(.width(32), .mode("twosComplement")) comparator_2 (
    .a(R1), .b(32'h32), .eq(comparator_2_eq));  // open: gt, lt
  Multiplexer #(.select(1), .width(32), .disabled("Z"), .enable("false")) multiplexer_11 (
    .in0(mips_alu_1_result), .in1({IR[15:0], {16{1'b0}}}), .out(multiplexer_11_out), .sel(LUI));
  and and_5 (halt, comparator_2_eq, Syscall);
  and and_6 (and_6_out, ~comparator_2_eq, Syscall);  // AND_Gate
  and and_7 (and_7_out, and_6_out, Syscall);
  RAM #(.addrWidth(10), .dataWidth(32), .bus("separate"), .Select("high")) ram_1 (
    .addr(multiplexer_11_out[11:2]), .din(MDin), .data(ram_1_data), .str(MemWrite), .clk(CLK), .clr(1'b0));  // open: sel, ld
  Multiplexer #(.select(1), .width(32), .disabled("Z"), .enable("false")) multiplexer_12 (
    .in0({multiplexer_13_out_2, multiplexer_13_out}), .in1({{24{1'b0}}, multiplexer_13_out}),
    .out(multiplexer_12_out), .sel(LBU));
  Register #(.width(32), .trigger("rising"), .Select("low")) register_1 (
    .D(MDin), .en(and_7_out), .Q(LedData), .clk(CLK), .clr(1'b0));
  Multiplexer #(.select(1), .width(32), .disabled("Z"), .enable("false")) multiplexer_13 (
    .in0(multiplexer_11_out), .in1(ram_1_data), .out({multiplexer_13_out_2, multiplexer_13_out}),
    .sel(MemToReg));
  \单周期硬布线控制器  \u_单周期硬布线控制器_1  (
    .Func(IR[5:0]), .OP(IR[31:26]), .ALU_OP(AluOP), .MemToReg(MemToReg), .MemWrite(MemWrite),
    .ALU_SRC(AluSrcB), .RegWrite(RegWrite), .SysCALL(Syscall), .SignedExt(SignedExt), .RegDst(RegDst),
    .JR(JR), .JMP(JMP), .Beq(Beq), .JAL(JAL), .Bne(Bne), .BLTZ(BLTZ), .LBU(LBU), .LUI(LUI));  // open: ERET
  D_Flip_Flop #(.trigger("high"), .Pre_Clr_Positions("LEGACY"), .NegatePresetClear("false"), .enable("true"), .NewFFLayout("false")) d_ff_1 (.Q(d_ff_1_q));  // open: clk, D, Qn, preset, en, reset
  // Probe on 13'hc
  Comparator #(.width(13), .mode("twosComplement")) comparator_3 (
    .a(CNT_num), .b(13'hc), .eq(comparator_3_eq), .lt(comparator_3_lt));  // open: gt
  Clock #(.highDuration(1), .lowDuration(1)) clock_2 (.out(clock_2_out));
  nand nand_1 (nand_1_out, d_ff_1_q, comparator_3_eq);
  Counter #(.width(13), .max('h1fff), .ongoal("stay"), .trigger("rising"), .behavior("old")) counter_2 (
    .count(comparator_3_lt), .Q(CNT_num), .clk(clock_2_out));  // open: load, D, carry, clr, preset
  assign CLK = nand_1_out ? clock_2_out : 1'bz;  // Controlled_Buffer controlled_buffer_1
  Pull_Resistor #(.pull(1)) pull_resistor_1 (.node(CLK));

  // Other names for the same wires on the sheet: Func[5:0] = IR[5:0]; Imm[15:0] = IR[15:0]; SHMAT[4:0] = IR[10:6];
  //   OP[5:0] = IR[31:26]; R2[31:0] = MDin

  // Notes on the sheet:
  //   中断源
  //   中断等待指示
  //   总复位信号应将除ROM以外所有存储组件全部清零
  //   数码管输出
  //   数码管输出应该用寄存器锁存，否则显示数据只能一闪而过
  //   指令存储器
  //   contents of rom_1 (hex, n*v repeats v):
  //   20090000 200b0010 34118483 20120404 118c00 129400 36318281 22520404 ad310000 2328820 21290004
  //   216bffff 1560fffb 200b0020 20090000 91310000 112020 20020022 c 21290001 216bffff 1560fff9 2002000a c
  //   OP
  //   Func
  //   rs
  //   指令字
  //   rt
  //   rd
  //   为方便自动评测，需要输出PC，IR，寄存器堆写如数据RDin
  //   LUI指令实现
  //   RAM写使能MemWrite、RAM写入数据MDin等信号
  //   LBU指令实现（LW再处理）
  //   JMP
  //   JR
  //   OP
  //   Func
  //   控制位
  //   Beq
  //   Bne
  //   MemToReg
  //   MemWrite
  //   AluOP
  //   AluSrcB
  //   RegWrite
  //   JAL
  //   RegDst
  //   Syscall
  //   暂停节拍，不能为0
  //   用这个时钟源需要去掉电路中的其他时钟源
  //   戳工具置1进入计数暂停模式，ctrl+k时钟自动运行到对应节拍暂停
  //   ctrl+k关闭时钟连续运行，将控制位置零，进入单步调试模式调试
  //   可计数暂停的时钟源
endmodule

// 单周期硬布线控制器
module \单周期硬布线控制器  (
  input  [5:0] OP,
  input  [5:0] Func,
  output [3:0] ALU_OP,
  output MemToReg,
  output MemWrite,
  output ALU_SRC,
  output RegWrite,
  output SysCALL,
  output SignedExt,
  output RegDst,
  output Beq,
  output Bne,
  output JR,
  output JMP,
  output JAL,
  output ERET,
  output BLTZ,
  output LBU,
  output LUI
);

  \运算控制器自动生成  \u_运算控制器自动生成_1  (
    .OP0(OP[0]), .OP1(OP[1]), .OP2(OP[2]), .OP3(OP[3]), .OP4(OP[4]), .OP5(OP[5]), .F0(Func[0]), .F1(Func[1]),
    .F2(Func[2]), .F3(Func[3]), .F4(Func[4]), .F5(Func[5]), .S0(ALU_OP[0]), .S1(ALU_OP[1]), .S2(ALU_OP[2]),
    .S3(ALU_OP[3]));
  \控制信号自动生成  \u_控制信号自动生成_1  (
    .OP0(OP[0]), .OP1(OP[1]), .OP2(OP[2]), .OP3(OP[3]), .OP4(OP[4]), .OP5(OP[5]), .F0(Func[0]), .F1(Func[1]),
    .F2(Func[2]), .F3(Func[3]), .F4(Func[4]), .F5(Func[5]), .MemToReg(MemToReg), .MemWrite(MemWrite),
    .ALU_SRC(ALU_SRC), .RegWrite(RegWrite), .SysCALL(SysCALL), .SignedExt(SignedExt), .RegDst(RegDst),
    .BEQ(Beq), .BNE(Bne), .JR(JR), .JUMP(JMP), .JAL(JAL), .ERET(ERET), .BLTZ(BLTZ), .LBU(LBU), .LUI(LUI));

  // Other names for the same wires on the sheet: OP_CODE[5:0] = OP

  // Notes on the sheet:
  //   运算器控制器，根据指令生成运算器功能选择信号
  //   控制信号生成，产生数据通路需要的其他控制信号
endmodule

// 运算器控制器
module \运算控制器自动生成  (
  input  OP0,
  input  OP1,
  input  OP2,
  input  OP3,
  input  OP4,
  input  OP5,
  input  F0,
  input  F1,
  input  F2,
  input  F3,
  input  F4,
  input  F5,
  output S0,
  output S1,
  output S2,
  output S3
);

  wire and_1_out, and_2_out, and_3_out, and_4_out, and_5_out, and_6_out, and_7_out, and_8_out, and_9_out,
       and_10_out, and_11_out, and_12_out, and_13_out, and_14_out, and_15_out, and_16_out, and_17_out,
       and_18_out, and_19_out, and_20_out, and_21_out, and_22_out, and_23_out, and_24_out, and_25_out,
       and_26_out, and_27_out, and_28_out, and_29_out, and_30_out, and_31_out, and_32_out, and_33_out,
       and_34_out, and_35_out, and_36_out, and_37_out, and_38_out, not_1_out, not_2_out, not_3_out,
       not_4_out, not_5_out, not_6_out, not_7_out, not_8_out, not_9_out, not_10_out, not_11_out, not_12_out,
       not_13_out, not_14_out, not_15_out, not_16_out, not_17_out, not_18_out, not_19_out, not_20_out,
       not_21_out, not_22_out, not_23_out, not_24_out, not_25_out, not_26_out, not_27_out, not_28_out,
       not_29_out, not_30_out, not_31_out, not_32_out, not_33_out, not_34_out, not_35_out, not_36_out,
       not_37_out, not_38_out, not_39_out, not_40_out, not_41_out, not_42_out, not_43_out, not_44_out,
       not_45_out, not_46_out, not_47_out, not_48_out, not_49_out, not_50_out, not_51_out, not_52_out,
       not_53_out, not_54_out, not_55_out, not_56_out, not_57_out, not_58_out, not_59_out, not_60_out,
       not_61_out, not_62_out, not_63_out, not_64_out, not_65_out, not_66_out, not_67_out, not_68_out,
       not_69_out, not_70_out, not_71_out, not_72_out, not_73_out, not_74_out, not_75_out, not_76_out,
       not_77_out, not_78_out, not_79_out, not_80_out, not_81_out, not_82_out, not_83_out, not_84_out,
       not_85_out, not_86_out, not_87_out, not_88_out, not_89_out, not_90_out, not_91_out, not_92_out,
       not_93_out, not_94_out, not_95_out, not_96_out, not_97_out, not_98_out, not_99_out, not_100_out,
       not_101_out, not_102_out, not_103_out, not_104_out, not_105_out, not_106_out, not_107_out,
       not_108_out, not_109_out, not_110_out, not_111_out, not_112_out, not_113_out, not_114_out,
       not_115_out, not_116_out, not_117_out, not_118_out, not_119_out, not_120_out, not_121_out,
       not_122_out, not_123_out, not_124_out, not_125_out, not_126_out, not_127_out, not_128_out,
       not_129_out, not_130_out, not_131_out, not_132_out, not_133_out, not_134_out, not_135_out,
       not_136_out, not_137_out, not_138_out, not_139_out, not_140_out, not_141_out, not_142_out,
       not_143_out, not_144_out, not_145_out, not_146_out, not_147_out, not_148_out, not_149_out,
       not_150_out, not_151_out, not_152_out, not_153_out, not_154_out, not_155_out, not_156_out,
       not_157_out, not_158_out, not_159_out, not_160_out, not_161_out, not_162_out, not_163_out,
       not_164_out, not_165_out, not_166_out, not_167_out, not_168_out, not_169_out, not_170_out,
       not_171_out, not_172_out, not_173_out, not_174_out, not_175_out, not_176_out, not_177_out,
       not_178_out, not_179_out, not_180_out, not_181_out, not_182_out, not_183_out, not_184_out,
       not_185_out, not_186_out, not_187_out, not_188_out, not_189_out, not_190_out, not_191_out,
       not_192_out, not_193_out, not_194_out, not_195_out, not_196_out, not_197_out, not_198_out,
       not_199_out, not_200_out, not_201_out, not_202_out, not_203_out, not_204_out, not_205_out,
       not_206_out, not_207_out, not_208_out, not_209_out, not_210_out, not_211_out, not_212_out,
       not_213_out, not_214_out, not_215_out, not_216_out, not_217_out, not_218_out, not_219_out,
       not_220_out, not_221_out, not_222_out, not_223_out, not_224_out, not_225_out, not_226_out,
       not_227_out, not_228_out, not_229_out, not_230_out, not_231_out, not_232_out, not_233_out,
       not_234_out, not_235_out, not_236_out, not_237_out, not_238_out, not_239_out, not_240_out,
       not_241_out, not_242_out, not_243_out, not_244_out, not_245_out, not_246_out, not_247_out,
       not_248_out, not_249_out, not_250_out, not_251_out, not_252_out, not_253_out, not_254_out,
       not_255_out, not_256_out, not_257_out, not_258_out, not_259_out, not_260_out, not_261_out, not_262_out;

  not not_1 (not_1_out, OP5);
  not not_2 (not_2_out, OP4);
  not not_3 (not_3_out, OP3);
  not not_4 (not_4_out, OP2);
  not not_5 (not_5_out, OP1);
  not not_6 (not_6_out, OP0);
  not not_7 (not_7_out, F5);
  not not_8 (not_8_out, F4);
  not not_9 (not_9_out, F3);
  not not_10 (not_10_out, F2);
  not not_11 (not_11_out, OP5);
  not not_12 (not_12_out, OP4);
  not not_13 (not_13_out, OP3);
  not not_14 (not_14_out, OP2);
  not not_15 (not_15_out, OP1);
  not not_16 (not_16_out, OP0);
  not not_17 (not_17_out, F4);
  not not_18 (not_18_out, F3);
  not not_19 (not_19_out, F2);
  not not_20 (not_20_out, F1);
  not not_21 (not_21_out, F0);
  not not_22 (not_22_out, OP5);
  not not_23 (not_23_out, OP4);
  not not_24 (not_24_out, OP3);
  not not_25 (not_25_out, OP2);
  not not_26 (not_26_out, OP1);
  not not_27 (not_27_out, OP0);
  not not_28 (not_28_out, F4);
  not not_29 (not_29_out, F3);
  not not_30 (not_30_out, F2);
  not not_31 (not_31_out, F1);
  not not_32 (not_32_out, OP5);
  not not_33 (not_33_out, OP4);
  not not_34 (not_34_out, OP3);
  not not_35 (not_35_out, OP2);
  not not_36 (not_36_out, OP1);
  not not_37 (not_37_out, OP0);
  not not_38 (not_38_out, F4);
  not not_39 (not_39_out, F3);
  not not_40 (not_40_out, F1);
  not not_41 (not_41_out, F0);
  not not_42 (not_42_out, OP5);
  not not_43 (not_43_out, OP4);
  not not_44 (not_44_out, OP3);
  not not_45 (not_45_out, OP2);
  not not_46 (not_46_out, OP1);
  not not_47 (not_47_out, OP0);
  not not_48 (not_48_out, F4);
  not not_49 (not_49_out, F2);
  not not_50 (not_50_out, F0);
  not not_51 (not_51_out, OP5);
  not not_52 (not_52_out, OP4);
  not not_53 (not_53_out, OP2);
  not not_54 (not_54_out, OP1);
  not not_55 (not_55_out, OP0);
  not not_56 (not_56_out, OP5);
  not not_57 (not_57_out, OP4);
  not not_58 (not_58_out, OP1);
  not not_59 (not_59_out, OP0);
  not not_60 (not_60_out, OP5);
  not not_61 (not_61_out, OP4);
  not not_62 (not_62_out, OP2);
  not not_63 (not_63_out, OP1);
  not not_64 (not_64_out, OP5);
  not not_65 (not_65_out, OP4);
  not not_66 (not_66_out, OP2);
  not not_67 (not_67_out, OP0);
  not not_68 (not_68_out, OP4);
  not not_69 (not_69_out, OP3);
  not not_70 (not_70_out, OP2);
  not not_71 (not_71_out, OP4);
  not not_72 (not_72_out, OP2);
  not not_73 (not_73_out, OP5);
  not not_74 (not_74_out, OP4);
  not not_75 (not_75_out, OP3);
  not not_76 (not_76_out, OP2);
  not not_77 (not_77_out, OP1);
  not not_78 (not_78_out, OP0);
  not not_79 (not_79_out, F4);
  not not_80 (not_80_out, F3);
  not not_81 (not_81_out, F0);
  not not_82 (not_82_out, OP4);
  not not_83 (not_83_out, OP3);
  not not_84 (not_84_out, OP1);
  not not_85 (not_85_out, OP0);
  not not_86 (not_86_out, OP5);
  not not_87 (not_87_out, OP4);
  not not_88 (not_88_out, OP3);
  not not_89 (not_89_out, OP2);
  not not_90 (not_90_out, OP1);
  not not_91 (not_91_out, OP0);
  not not_92 (not_92_out, F5);
  not not_93 (not_93_out, F4);
  not not_94 (not_94_out, F3);
  not not_95 (not_95_out, F2);
  not not_96 (not_96_out, F0);
  not not_97 (not_97_out, OP5);
  not not_98 (not_98_out, OP4);
  not not_99 (not_99_out, OP3);
  not not_100 (not_100_out, OP2);
  not not_101 (not_101_out, OP1);
  not not_102 (not_102_out, OP0);
  not not_103 (not_103_out, F4);
  not not_104 (not_104_out, F3);
  not not_105 (not_105_out, F2);
  not not_106 (not_106_out, F0);
  not not_107 (not_107_out, OP5);
  not not_108 (not_108_out, OP4);
  not not_109 (not_109_out, OP3);
  not not_110 (not_110_out, OP2);
  not not_111 (not_111_out, OP1);
  not not_112 (not_112_out, OP0);
  not not_113 (not_113_out, F4);
  not not_114 (not_114_out, F3);
  not not_115 (not_115_out, F1);
  not not_116 (not_116_out, F0);
  not not_117 (not_117_out, OP5);
  not not_118 (not_118_out, OP4);
  not not_119 (not_119_out, OP3);
  not not_120 (not_120_out, OP2);
  not not_121 (not_121_out, OP1);
  not not_122 (not_122_out, OP0);
  not not_123 (not_123_out, F4);
  not not_124 (not_124_out, F3);
  not not_125 (not_125_out, OP5);
  not not_126 (not_126_out, OP4);
  not not_127 (not_127_out, OP3);
  not not_128 (not_128_out, OP2);
  not not_129 (not_129_out, OP1);
  not not_130 (not_130_out, OP0);
  not not_131 (not_131_out, F4);
  not not_132 (not_132_out, F2);
  not not_133 (not_133_out, F0);
  not not_134 (not_134_out, OP5);
  not not_135 (not_135_out, OP4);
  not not_136 (not_136_out, OP1);
  not not_137 (not_137_out, OP0);
  not not_138 (not_138_out, OP5);
  not not_139 (not_139_out, OP4);
  not not_140 (not_140_out, OP2);
  not not_141 (not_141_out, OP0);
  not not_142 (not_142_out, OP5);
  not not_143 (not_143_out, OP4);
  not not_144 (not_144_out, OP3);
  not not_145 (not_145_out, OP2);
  not not_146 (not_146_out, OP1);
  not not_147 (not_147_out, OP0);
  not not_148 (not_148_out, F4);
  not not_149 (not_149_out, F3);
  not not_150 (not_150_out, F2);
  not not_151 (not_151_out, F1);
  not not_152 (not_152_out, F0);
  not not_153 (not_153_out, OP5);
  not not_154 (not_154_out, OP4);
  not not_155 (not_155_out, OP3);
  not not_156 (not_156_out, OP2);
  not not_157 (not_157_out, OP1);
  not not_158 (not_158_out, OP0);
  not not_159 (not_159_out, F4);
  not not_160 (not_160_out, F3);
  not not_161 (not_161_out, F2);
  not not_162 (not_162_out, F1);
  not not_163 (not_163_out, OP5);
  not not_164 (not_164_out, OP4);
  not not_165 (not_165_out, OP3);
  not not_166 (not_166_out, OP2);
  not not_167 (not_167_out, OP1);
  not not_168 (not_168_out, OP0);
  not not_169 (not_169_out, F4);
  not not_170 (not_170_out, F3);
  not not_171 (not_171_out, F2);
  not not_172 (not_172_out, F0);
  not not_173 (not_173_out, OP5);
  not not_174 (not_174_out, OP4);
  not not_175 (not_175_out, OP3);
  not not_176 (not_176_out, OP2);
  not not_177 (not_177_out, OP1);
  not not_178 (not_178_out, OP0);
  not not_179 (not_179_out, F4);
  not not_180 (not_180_out, F3);
  not not_181 (not_181_out, F1);
  not not_182 (not_182_out, F0);
  not not_183 (not_183_out, OP5);
  not not_184 (not_184_out, OP4);
  not not_185 (not_185_out, OP3);
  not not_186 (not_186_out, OP2);
  not not_187 (not_187_out, OP1);
  not not_188 (not_188_out, OP0);
  not not_189 (not_189_out, F4);
  not not_190 (not_190_out, F2);
  not not_191 (not_191_out, OP5);
  not not_192 (not_192_out, OP4);
  not not_193 (not_193_out, OP2);
  not not_194 (not_194_out, OP1);
  not not_195 (not_195_out, OP0);
  not not_196 (not_196_out, OP5);
  not not_197 (not_197_out, OP4);
  not not_198 (not_198_out, OP1);
  not not_199 (not_199_out, OP0);
  not not_200 (not_200_out, OP5);
  not not_201 (not_201_out, OP4);
  not not_202 (not_202_out, OP2);
  not not_203 (not_203_out, OP1);
  not not_204 (not_204_out, OP4);
  not not_205 (not_205_out, OP3);
  not not_206 (not_206_out, OP2);
  not not_207 (not_207_out, OP4);
  not not_208 (not_208_out, OP2);
  not not_209 (not_209_out, OP4);
  not not_210 (not_210_out, OP3);
  not not_211 (not_211_out, OP1);
  not not_212 (not_212_out, OP0);
  not not_213 (not_213_out, OP5);
  not not_214 (not_214_out, OP4);
  not not_215 (not_215_out, OP3);
  not not_216 (not_216_out, OP2);
  not not_217 (not_217_out, OP1);
  not not_218 (not_218_out, OP0);
  not not_219 (not_219_out, F4);
  not not_220 (not_220_out, F3);
  not not_221 (not_221_out, F1);
  not not_222 (not_222_out, OP5);
  not not_223 (not_223_out, OP4);
  not not_224 (not_224_out, OP3);
  not not_225 (not_225_out, OP2);
  not not_226 (not_226_out, OP1);
  not not_227 (not_227_out, OP0);
  not not_228 (not_228_out, F4);
  not not_229 (not_229_out, F3);
  not not_230 (not_230_out, OP5);
  not not_231 (not_231_out, OP4);
  not not_232 (not_232_out, OP3);
  not not_233 (not_233_out, OP2);
  not not_234 (not_234_out, OP1);
  not not_235 (not_235_out, OP0);
  not not_236 (not_236_out, F4);
  not not_237 (not_237_out, F2);
  not not_238 (not_238_out, F0);
  not not_239 (not_239_out, OP5);
  not not_240 (not_240_out, OP4);
  not not_241 (not_241_out, OP3);
  not not_242 (not_242_out, OP2);
  not not_243 (not_243_out, OP1);
  not not_244 (not_244_out, OP0);
  not not_245 (not_245_out, F4);
  not not_246 (not_246_out, F2);
  not not_247 (not_247_out, OP5);
  not not_248 (not_248_out, OP4);
  not not_249 (not_249_out, OP2);
  not not_250 (not_250_out, OP0);
  not not_251 (not_251_out, OP5);
  not not_252 (not_252_out, OP4);
  not not_253 (not_253_out, OP1);
  not not_254 (not_254_out, OP5);
  not not_255 (not_255_out, OP4);
  not not_256 (not_256_out, OP3);
  not not_257 (not_257_out, OP2);
  not not_258 (not_258_out, OP1);
  not not_259 (not_259_out, OP0);
  not not_260 (not_260_out, F4);
  not not_261 (not_261_out, F3);
  not not_262 (not_262_out, F0);
  and and_1 (and_1_out, not_1_out, not_2_out, not_3_out, not_4_out, not_5_out, not_6_out, not_7_out, not_8_out, not_9_out, not_10_out, F1, F0);
  and and_2 (and_2_out, not_11_out, not_12_out, not_13_out, not_14_out, not_15_out, not_16_out, F5, not_17_out, not_18_out, not_19_out, not_20_out, not_21_out);
  and and_3 (and_3_out, not_22_out, not_23_out, not_24_out, not_25_out, not_26_out, not_27_out, F5, not_28_out, not_29_out, not_30_out, not_31_out, F0);
  and and_4 (and_4_out, not_32_out, not_33_out, not_34_out, not_35_out, not_36_out, not_37_out, F5, not_38_out, not_39_out, F2, not_40_out, not_41_out);
  and and_5 (and_5_out, not_42_out, not_43_out, not_44_out, not_45_out, not_46_out, not_47_out, F5, not_48_out, F3, not_49_out, F1, not_50_out);
  and and_6 (and_6_out, not_51_out, not_52_out, OP3, not_53_out, not_54_out, not_55_out);
  and and_7 (and_7_out, not_56_out, not_57_out, OP3, OP2, not_58_out, not_59_out);
  and and_8 (and_8_out, not_60_out, not_61_out, OP3, not_62_out, not_63_out, OP0);
  and and_9 (and_9_out, not_64_out, not_65_out, OP3, not_66_out, OP1, not_67_out);
  and and_10 (and_10_out, OP5, not_68_out, not_69_out, not_70_out, OP1, OP0);
  and and_11 (and_11_out, OP5, not_71_out, OP3, not_72_out, OP1, OP0);
  and and_12 (and_12_out, not_73_out, not_74_out, not_75_out, not_76_out, not_77_out, not_78_out, F5, not_79_out, not_80_out, F2, F1, not_81_out);
  and and_13 (and_13_out, OP5, not_82_out, not_83_out, OP2, not_84_out, not_85_out);
  and and_14 (and_14_out, not_86_out, not_87_out, not_88_out, not_89_out, not_90_out, not_91_out, not_92_out, not_93_out, not_94_out, not_95_out, F1, not_96_out);
  and and_15 (and_15_out, not_97_out, not_98_out, not_99_out, not_100_out, not_101_out, not_102_out, F5, not_103_out, not_104_out, not_105_out, F1, not_106_out);
  and and_16 (and_16_out, not_107_out, not_108_out, not_109_out, not_110_out, not_111_out, not_112_out, F5, not_113_out, not_114_out, F2, not_115_out, not_116_out);
  and and_17 (and_17_out, not_117_out, not_118_out, not_119_out, not_120_out, not_121_out, not_122_out, F5, not_123_out, not_124_out, F2, F1, F0);
  and and_18 (and_18_out, not_125_out, not_126_out, not_127_out, not_128_out, not_129_out, not_130_out, F5, not_131_out, F3, not_132_out, F1, not_133_out);
  and and_19 (and_19_out, not_134_out, not_135_out, OP3, OP2, not_136_out, not_137_out);
  and and_20 (and_20_out, not_138_out, not_139_out, OP3, not_140_out, OP1, not_141_out);
  and and_21 (and_21_out, not_142_out, not_143_out, not_144_out, not_145_out, not_146_out, not_147_out, F5, not_148_out, not_149_out, not_150_out, not_151_out, not_152_out);
  and and_22 (and_22_out, not_153_out, not_154_out, not_155_out, not_156_out, not_157_out, not_158_out, F5, not_159_out, not_160_out, not_161_out, not_162_out, F0);
  and and_23 (and_23_out, not_163_out, not_164_out, not_165_out, not_166_out, not_167_out, not_168_out, F5, not_169_out, not_170_out, not_171_out, F1, not_172_out);
  and and_24 (and_24_out, not_173_out, not_174_out, not_175_out, not_176_out, not_177_out, not_178_out, F5, not_179_out, not_180_out, F2, not_181_out, not_182_out);
  and and_25 (and_25_out, not_183_out, not_184_out, not_185_out, not_186_out, not_187_out, not_188_out, F5, not_189_out, F3, not_190_out, F1, F0);
  and and_26 (and_26_out, not_191_out, not_192_out, OP3, not_193_out, not_194_out, not_195_out);
  and and_27 (and_27_out, not_196_out, not_197_out, OP3, OP2, not_198_out, not_199_out);
  and and_28 (and_28_out, not_200_out, not_201_out, OP3, not_202_out, not_203_out, OP0);
  and and_29 (and_29_out, OP5, not_204_out, not_205_out, not_206_out, OP1, OP0);
  and and_30 (and_30_out, OP5, not_207_out, OP3, not_208_out, OP1, OP0);
  and and_31 (and_31_out, OP5, not_209_out, not_210_out, OP2, not_211_out, not_212_out);
  and and_32 (and_32_out, not_213_out, not_214_out, not_215_out, not_216_out, not_217_out, not_218_out, F5, not_219_out, not_220_out, F2, not_221_out, F0);
  and and_33 (and_33_out, not_222_out, not_223_out, not_224_out, not_225_out, not_226_out, not_227_out, F5, not_228_out, not_229_out, F2, F1, F0);
  and and_34 (and_34_out, not_230_out, not_231_out, not_232_out, not_233_out, not_234_out, not_235_out, F5, not_236_out, F3, not_237_out, F1, not_238_out);
  and and_35 (and_35_out, not_239_out, not_240_out, not_241_out, not_242_out, not_243_out, not_244_out, F5, not_245_out, F3, not_246_out, F1, F0);
  and and_36 (and_36_out, not_247_out, not_248_out, OP3, not_249_out, OP1, not_250_out);
  and and_37 (and_37_out, not_251_out, not_252_out, OP3, OP2, not_253_out, OP0);
  and and_38 (and_38_out, not_254_out, not_255_out, not_256_out, not_257_out, not_258_out, not_259_out, F5, not_260_out, not_261_out, F2, F1, not_262_out);
  or or_1 (S1, and_14_out, and_15_out, and_16_out, and_17_out, and_18_out, and_19_out, and_20_out);
  or or_2 (S2, and_21_out, and_22_out, and_23_out, and_24_out, and_25_out, and_26_out, and_27_out, and_28_out, and_29_out, and_30_out, and_31_out);
  or or_3 (S3, and_32_out, and_33_out, and_34_out, and_35_out, and_36_out, and_37_out, and_38_out);
  or or_4 (S0, and_1_out, and_2_out, and_3_out, and_4_out, and_5_out, and_6_out, and_7_out, and_8_out, and_9_out, and_10_out, and_11_out, and_12_out, and_13_out);
endmodule

// 控制信号生成
module \控制信号自动生成  (
  input  OP0,
  input  OP1,
  input  OP2,
  input  OP3,
  input  OP4,
  input  OP5,
  input  F0,
  input  F1,
  input  F2,
  input  F3,
  input  F4,
  input  F5,
  output MemToReg,
  output MemWrite,
  output ALU_SRC,
  output RegWrite,
  output SysCALL,
  output SignedExt,
  output RegDst,
  output BEQ,
  output BNE,
  output JR,
  output JUMP,
  output JAL,
  output ERET,
  output BLTZ,
  output LBU,
  output LUI
);

  wire and_1_out, and_2_out, and_4_out, and_5_out, and_6_out, and_7_out, and_8_out, and_9_out, and_10_out,
       and_11_out, and_12_out, and_13_out, and_14_out, and_15_out, and_16_out, and_17_out, and_18_out,
       and_20_out, and_21_out, and_22_out, and_23_out, and_24_out, and_25_out, and_26_out, and_27_out,
       and_28_out, and_29_out, and_33_out, and_34_out, not_1_out, not_2_out, not_3_out, not_4_out, not_5_out,
       not_6_out, not_7_out, not_8_out, not_9_out, not_10_out, not_11_out, not_12_out, not_13_out,
       not_14_out, not_15_out, not_16_out, not_17_out, not_18_out, not_19_out, not_20_out, not_21_out,
       not_22_out, not_23_out, not_24_out, not_25_out, not_26_out, not_27_out, not_28_out, not_29_out,
       not_30_out, not_31_out, not_32_out, not_33_out, not_34_out, not_35_out, not_36_out, not_37_out,
       not_38_out, not_39_out, not_40_out, not_41_out, not_42_out, not_43_out, not_44_out, not_45_out,
       not_46_out, not_47_out, not_48_out, not_49_out, not_50_out, not_51_out, not_52_out, not_53_out,
       not_54_out, not_55_out, not_56_out, not_57_out, not_58_out, not_59_out, not_60_out, not_61_out,
       not_62_out, not_63_out, not_64_out, not_65_out, not_66_out, not_67_out, not_68_out, not_69_out,
       not_70_out, not_71_out, not_72_out, not_73_out, not_74_out, not_75_out, not_76_out, not_77_out,
       not_78_out, not_79_out, not_80_out, not_81_out, not_82_out, not_83_out, not_84_out, not_85_out,
       not_86_out, not_87_out, not_88_out, not_89_out, not_90_out, not_91_out, not_92_out, not_93_out,
       not_94_out, not_95_out, not_96_out, not_97_out, not_98_out, not_99_out, not_100_out, not_101_out,
       not_102_out, not_103_out, not_104_out, not_105_out, not_106_out, not_107_out, not_108_out,
       not_109_out, not_110_out, not_111_out, not_112_out, not_113_out, not_114_out, not_115_out,
       not_116_out, not_117_out, not_118_out, not_119_out, not_120_out, not_121_out, not_122_out,
       not_123_out, not_124_out, not_125_out, not_126_out, not_127_out, not_128_out, not_129_out,
       not_130_out, not_131_out, not_132_out, not_133_out, not_134_out, not_135_out, not_136_out,
       not_137_out, not_138_out, not_139_out, not_140_out, not_141_out, not_142_out, not_143_out,
       not_144_out, not_145_out, not_146_out, not_147_out, not_148_out, not_149_out, not_150_out,
       not_151_out, not_152_out, not_153_out, not_154_out, not_155_out, not_156_out, not_157_out,
       not_158_out, not_159_out, not_160_out, not_161_out, not_162_out, not_163_out, not_164_out,
       not_165_out, not_166_out, not_167_out, not_168_out, not_169_out, not_170_out, not_171_out,
       not_172_out, not_173_out, not_174_out, not_175_out, not_176_out, not_177_out, not_178_out,
       not_179_out, not_180_out, not_181_out, not_182_out, not_183_out, not_184_out, not_185_out,
       not_186_out, not_187_out, not_188_out, not_189_out, not_190_out, not_191_out, not_192_out,
       not_193_out, not_194_out, not_195_out, not_196_out, not_197_out, not_198_out, not_199_out,
       not_200_out, not_201_out, not_202_out, not_203_out, not_204_out, not_205_out, not_206_out,
       not_207_out, not_208_out, not_209_out, not_210_out, not_211_out;

  not not_1 (not_1_out, OP0);
  not not_2 (not_2_out, OP1);
  not not_3 (not_3_out, OP3);
  not not_4 (not_4_out, OP4);
  not not_5 (not_5_out, OP2);
  not not_6 (not_6_out, OP3);
  not not_7 (not_7_out, OP4);
  not not_8 (not_8_out, OP2);
  not not_9 (not_9_out, OP4);
  not not_10 (not_10_out, OP0);
  not not_11 (not_11_out, OP2);
  not not_12 (not_12_out, OP4);
  not not_13 (not_13_out, OP5);
  not not_14 (not_14_out, OP1);
  not not_15 (not_15_out, OP4);
  not not_16 (not_16_out, OP5);
  not not_17 (not_17_out, OP0);
  not not_18 (not_18_out, OP1);
  not not_19 (not_19_out, OP3);
  not not_20 (not_20_out, OP4);
  not not_21 (not_21_out, OP4);
  not not_22 (not_22_out, OP5);
  not not_23 (not_23_out, OP2);
  not not_24 (not_24_out, OP4);
  not not_25 (not_25_out, OP0);
  not not_26 (not_26_out, OP1);
  not not_27 (not_27_out, OP2);
  not not_28 (not_28_out, OP4);
  not not_29 (not_29_out, OP5);
  not not_30 (not_30_out, F0);
  not not_31 (not_31_out, F2);
  not not_32 (not_32_out, F3);
  not not_33 (not_33_out, F4);
  not not_34 (not_34_out, OP0);
  not not_35 (not_35_out, OP1);
  not not_36 (not_36_out, OP2);
  not not_37 (not_37_out, OP4);
  not not_38 (not_38_out, OP5);
  not not_39 (not_39_out, F1);
  not not_40 (not_40_out, F3);
  not not_41 (not_41_out, F4);
  not not_42 (not_42_out, OP0);
  not not_43 (not_43_out, OP1);
  not not_44 (not_44_out, OP2);
  not not_45 (not_45_out, OP4);
  not not_46 (not_46_out, OP5);
  not not_47 (not_47_out, F3);
  not not_48 (not_48_out, F4);
  not not_49 (not_49_out, OP0);
  not not_50 (not_50_out, OP1);
  not not_51 (not_51_out, OP2);
  not not_52 (not_52_out, OP4);
  not not_53 (not_53_out, OP5);
  not not_54 (not_54_out, F2);
  not not_55 (not_55_out, F3);
  not not_56 (not_56_out, F4);
  not not_57 (not_57_out, F5);
  not not_58 (not_58_out, OP0);
  not not_59 (not_59_out, OP1);
  not not_60 (not_60_out, OP2);
  not not_61 (not_61_out, OP4);
  not not_62 (not_62_out, OP5);
  not not_63 (not_63_out, F2);
  not not_64 (not_64_out, F4);
  not not_65 (not_65_out, OP0);
  not not_66 (not_66_out, OP2);
  not not_67 (not_67_out, OP4);
  not not_68 (not_68_out, OP5);
  not not_69 (not_69_out, OP1);
  not not_70 (not_70_out, OP4);
  not not_71 (not_71_out, OP5);
  not not_72 (not_72_out, OP0);
  not not_73 (not_73_out, OP1);
  not not_74 (not_74_out, OP3);
  not not_75 (not_75_out, OP4);
  not not_76 (not_76_out, OP4);
  not not_77 (not_77_out, OP5);
  not not_78 (not_78_out, OP2);
  not not_79 (not_79_out, OP3);
  not not_80 (not_80_out, OP4);
  not not_81 (not_81_out, OP0);
  not not_82 (not_82_out, OP1);
  not not_83 (not_83_out, OP2);
  not not_84 (not_84_out, OP3);
  not not_85 (not_85_out, OP4);
  not not_86 (not_86_out, OP5);
  not not_87 (not_87_out, F0);
  not not_88 (not_88_out, F1);
  not not_89 (not_89_out, F4);
  not not_90 (not_90_out, F5);
  not not_91 (not_91_out, OP0);
  not not_92 (not_92_out, OP2);
  not not_93 (not_93_out, OP4);
  not not_94 (not_94_out, OP5);
  not not_95 (not_95_out, OP0);
  not not_96 (not_96_out, OP1);
  not not_97 (not_97_out, OP3);
  not not_98 (not_98_out, OP4);
  not not_99 (not_99_out, OP1);
  not not_100 (not_100_out, OP3);
  not not_101 (not_101_out, OP4);
  not not_102 (not_102_out, OP5);
  not not_103 (not_103_out, OP1);
  not not_104 (not_104_out, OP2);
  not not_105 (not_105_out, OP4);
  not not_106 (not_106_out, OP5);
  not not_107 (not_107_out, OP2);
  not not_108 (not_108_out, OP4);
  not not_109 (not_109_out, OP0);
  not not_110 (not_110_out, OP1);
  not not_111 (not_111_out, OP2);
  not not_112 (not_112_out, OP3);
  not not_113 (not_113_out, OP4);
  not not_114 (not_114_out, OP5);
  not not_115 (not_115_out, F0);
  not not_116 (not_116_out, F2);
  not not_117 (not_117_out, F3);
  not not_118 (not_118_out, F4);
  not not_119 (not_119_out, OP0);
  not not_120 (not_120_out, OP1);
  not not_121 (not_121_out, OP2);
  not not_122 (not_122_out, OP3);
  not not_123 (not_123_out, OP4);
  not not_124 (not_124_out, OP5);
  not not_125 (not_125_out, F1);
  not not_126 (not_126_out, F3);
  not not_127 (not_127_out, F4);
  not not_128 (not_128_out, OP0);
  not not_129 (not_129_out, OP1);
  not not_130 (not_130_out, OP2);
  not not_131 (not_131_out, OP3);
  not not_132 (not_132_out, OP4);
  not not_133 (not_133_out, OP5);
  not not_134 (not_134_out, F3);
  not not_135 (not_135_out, F4);
  not not_136 (not_136_out, OP0);
  not not_137 (not_137_out, OP1);
  not not_138 (not_138_out, OP2);
  not not_139 (not_139_out, OP3);
  not not_140 (not_140_out, OP4);
  not not_141 (not_141_out, OP5);
  not not_142 (not_142_out, F2);
  not not_143 (not_143_out, F3);
  not not_144 (not_144_out, F4);
  not not_145 (not_145_out, F5);
  not not_146 (not_146_out, OP0);
  not not_147 (not_147_out, OP1);
  not not_148 (not_148_out, OP2);
  not not_149 (not_149_out, OP3);
  not not_150 (not_150_out, OP4);
  not not_151 (not_151_out, OP5);
  not not_152 (not_152_out, F2);
  not not_153 (not_153_out, F4);
  not not_154 (not_154_out, OP0);
  not not_155 (not_155_out, OP1);
  not not_156 (not_156_out, OP3);
  not not_157 (not_157_out, OP4);
  not not_158 (not_158_out, OP5);
  not not_159 (not_159_out, OP1);
  not not_160 (not_160_out, OP3);
  not not_161 (not_161_out, OP4);
  not not_162 (not_162_out, OP5);
  not not_163 (not_163_out, OP0);
  not not_164 (not_164_out, OP1);
  not not_165 (not_165_out, OP2);
  not not_166 (not_166_out, OP3);
  not not_167 (not_167_out, OP4);
  not not_168 (not_168_out, OP5);
  not not_169 (not_169_out, F0);
  not not_170 (not_170_out, F1);
  not not_171 (not_171_out, F2);
  not not_172 (not_172_out, F4);
  not not_173 (not_173_out, F5);
  not not_174 (not_174_out, OP0);
  not not_175 (not_175_out, OP2);
  not not_176 (not_176_out, OP3);
  not not_177 (not_177_out, OP4);
  not not_178 (not_178_out, OP5);
  not not_179 (not_179_out, F0);
  not not_180 (not_180_out, F1);
  not not_181 (not_181_out, F2);
  not not_182 (not_182_out, F4);
  not not_183 (not_183_out, F5);
  not not_184 (not_184_out, OP2);
  not not_185 (not_185_out, OP3);
  not not_186 (not_186_out, OP4);
  not not_187 (not_187_out, OP5);
  not not_188 (not_188_out, OP2);
  not not_189 (not_189_out, OP3);
  not not_190 (not_190_out, OP4);
  not not_191 (not_191_out, OP5);
  not not_192 (not_192_out, OP5);
  not not_193 (not_193_out, OP3);
  not not_194 (not_194_out, OP2);
  not not_195 (not_195_out, OP1);
  not not_196 (not_196_out, OP0);
  not not_197 (not_197_out, F5);
  not not_198 (not_198_out, F2);
  not not_199 (not_199_out, F1);
  not not_200 (not_200_out, F0);
  not not_201 (not_201_out, OP1);
  not not_202 (not_202_out, OP2);
  not not_203 (not_203_out, OP3);
  not not_204 (not_204_out, OP4);
  not not_205 (not_205_out, OP5);
  not not_206 (not_206_out, OP0);
  not not_207 (not_207_out, OP1);
  not not_208 (not_208_out, OP3);
  not not_209 (not_209_out, OP4);
  not not_210 (not_210_out, OP4);
  not not_211 (not_211_out, OP5);
  and and_1 (and_1_out, not_1_out, not_2_out, OP2, not_3_out, not_4_out, OP5);
  and and_2 (and_2_out, OP0, OP1, not_5_out, not_6_out, not_7_out, OP5);
  and and_3 (MemWrite, OP0, OP1, not_8_out, OP3, not_9_out, OP5);
  and and_4 (and_4_out, not_10_out, not_11_out, OP3, not_12_out, not_13_out);
  and and_5 (and_5_out, not_14_out, OP3, not_15_out, not_16_out);
  and and_6 (and_6_out, not_17_out, not_18_out, OP2, not_19_out, not_20_out, OP5);
  and and_7 (and_7_out, OP0, OP2, OP3, not_21_out, not_22_out);
  and and_8 (and_8_out, OP0, OP1, not_23_out, not_24_out, OP5);
  and and_9 (and_9_out, not_25_out, not_26_out, not_27_out, not_28_out, not_29_out, not_30_out, not_31_out, not_32_out, not_33_out);
  and and_10 (and_10_out, not_34_out, not_35_out, not_36_out, not_37_out, not_38_out, not_39_out, not_40_out, not_41_out, F5);
  and and_11 (and_11_out, not_42_out, not_43_out, not_44_out, not_45_out, not_46_out, F2, not_47_out, not_48_out, F5);
  and and_12 (and_12_out, not_49_out, not_50_out, not_51_out, not_52_out, not_53_out, F1, not_54_out, not_55_out, not_56_out, not_57_out);
  and and_13 (and_13_out, not_58_out, not_59_out, not_60_out, not_61_out, not_62_out, F1, not_63_out, F3, not_64_out, F5);
  and and_14 (and_14_out, not_65_out, not_66_out, OP3, not_67_out, not_68_out);
  and and_15 (and_15_out, not_69_out, OP3, not_70_out, not_71_out);
  and and_16 (and_16_out, not_72_out, not_73_out, OP2, not_74_out, not_75_out, OP5);
  and and_17 (and_17_out, OP0, OP2, OP3, not_76_out, not_77_out);
  and and_18 (and_18_out, OP0, OP1, not_78_out, not_79_out, not_80_out);
  and and_19 (SysCALL, not_81_out, not_82_out, not_83_out, not_84_out, not_85_out, not_86_out, not_87_out, not_88_out, F2, F3, not_89_out, not_90_out);
  and and_20 (and_20_out, not_91_out, not_92_out, OP3, not_93_out, not_94_out);
  and and_21 (and_21_out, not_95_out, not_96_out, OP2, not_97_out, not_98_out);
  and and_22 (and_22_out, not_99_out, OP2, not_100_out, not_101_out, not_102_out);
  and and_23 (and_23_out, OP0, not_103_out, not_104_out, not_105_out, not_106_out);
  and and_24 (and_24_out, OP0, OP1, not_107_out, not_108_out, OP5);
  and and_25 (and_25_out, not_109_out, not_110_out, not_111_out, not_112_out, not_113_out, not_114_out, not_115_out, not_116_out, not_117_out, not_118_out);
  and and_26 (and_26_out, not_119_out, not_120_out, not_121_out, not_122_out, not_123_out, not_124_out, not_125_out, not_126_out, not_127_out, F5);
  and and_27 (and_27_out, not_128_out, not_129_out, not_130_out, not_131_out, not_132_out, not_133_out, F2, not_134_out, not_135_out, F5);
  and and_28 (and_28_out, not_136_out, not_137_out, not_138_out, not_139_out, not_140_out, not_141_out, F1, not_142_out, not_143_out, not_144_out, not_145_out);
  and and_29 (and_29_out, not_146_out, not_147_out, not_148_out, not_149_out, not_150_out, not_151_out, F1, not_152_out, F3, not_153_out, F5);
  and and_30 (BEQ, not_154_out, not_155_out, OP2, not_156_out, not_157_out, not_158_out);
  and and_31 (BNE, OP0, not_159_out, OP2, not_160_out, not_161_out, not_162_out);
  and and_32 (JR, not_163_out, not_164_out, not_165_out, not_166_out, not_167_out, not_168_out, not_169_out, not_170_out, not_171_out, F3, not_172_out, not_173_out);
  and and_33 (and_33_out, not_174_out, not_175_out, not_176_out, not_177_out, not_178_out, not_179_out, not_180_out, not_181_out, F3, not_182_out, not_183_out);
  and and_34 (and_34_out, OP1, not_184_out, not_185_out, not_186_out, not_187_out);
  and and_35 (JAL, OP0, OP1, not_188_out, not_189_out, not_190_out, not_191_out);
  and and_36 (ERET, not_192_out, OP4, not_193_out, not_194_out, not_195_out, not_196_out, not_197_out, F4, F3, not_198_out, not_199_out, not_200_out);
  and and_37 (BLTZ, OP0, not_201_out, not_202_out, not_203_out, not_204_out, not_205_out);
  and and_38 (LBU, not_206_out, not_207_out, OP2, not_208_out, not_209_out, OP5);
  and and_39 (LUI, OP0, OP1, OP2, OP3, not_210_out, not_211_out);
  or or_1 (MemToReg, and_1_out, and_2_out);
  or or_2 (ALU_SRC, and_4_out, and_5_out, and_6_out, and_7_out, and_8_out);
  or or_3 (RegWrite, and_9_out, and_10_out, and_11_out, and_12_out, and_13_out, and_14_out, and_15_out, and_16_out, and_17_out, and_18_out);
  or or_4 (SignedExt, and_20_out, and_21_out, and_22_out, and_23_out, and_24_out);
  or or_5 (RegDst, and_25_out, and_26_out, and_27_out, and_28_out, and_29_out);
  or or_6 (JUMP, and_33_out, and_34_out);
endmodule

// ALU
module MIPS_ALU (
  input  [4:0] shamt,
  input  [31:0] X,
  input  [31:0] Y,
  input  [3:0] AluOP,
  output Equal,
  output [31:0] Result,
  output [31:0] Result_2
);

  wire [0:0] comparator_1_lt, comparator_2_lt;
  wire [31:0] adder_1_out, AND_out, divider_1_out, divider_1_rem, multiplier_1_cout, multiplier_1_out,
       NOR_out, OR_out, shifter_1_out, shifter_2_out, shifter_3_out, subtractor_1_out, XOR_out;

  assign AND_out = X & Y;  // AND_Gate AND, 32 bits wide
  assign OR_out = X | Y;  // OR_Gate OR, 32 bits wide
  Shifter #(.width(32), .shift("ll")) shifter_1 (.in(Y), .\dist (shamt), .out(shifter_1_out));
  Shifter #(.width(32), .shift("ar")) shifter_2 (.in(Y), .\dist (shamt), .out(shifter_2_out));
  Shifter #(.width(32), .shift("lr")) shifter_3 (.in(Y), .\dist (shamt), .out(shifter_3_out));
  Multiplier #(.width(32)) multiplier_1 (.a(X), .b(Y), .out(multiplier_1_out), .cout(multiplier_1_cout));  // open: cin
  Divider #(.width(32)) divider_1 (.a(X), .b(Y), .out(divider_1_out), .rem(divider_1_rem));  // open: upper
  Adder #(.width(32)) adder_1 (.a(X), .b(Y), .out(adder_1_out));  // open: cin, cout
  Subtractor #(.width(32)) subtractor_1 (.a(X), .b(Y), .out(subtractor_1_out));  // open: bin, bout
  assign XOR_out = X ^ Y;  // XOR_Gate XOR, 32 bits wide
  assign NOR_out = ~(X | Y);  // NOR_Gate NOR, 32 bits wide
  Comparator #(.width(32), .mode("twosComplement")) comparator_1 (
    .a(X), .b(Y), .eq(Equal), .lt(comparator_1_lt[0]));  // open: gt
  Comparator #(.width(32), .mode("unsigned")) comparator_2 (.a(X), .b(Y), .lt(comparator_2_lt[0]));  // open: gt, eq
  Multiplexer #(.select(4), .width(32), .disabled("Z"), .enable("false")) multiplexer_1 (
    .in0(shifter_1_out), .in1(shifter_2_out), .in2(shifter_3_out), .in3(multiplier_1_out),
    .in4(divider_1_out), .in5(adder_1_out), .in6(subtractor_1_out), .in7(AND_out), .in8(OR_out),
    .in9(XOR_out), .in10(NOR_out), .in11({{31{1'b0}}, comparator_1_lt[0]}),
    .in12({{31{1'b0}}, comparator_2_lt[0]}), .in13({32{1'b0}}), .in14({32{1'b0}}), .in15({32{1'b0}}),
    .out(Result), .sel(AluOP));
  Multiplexer #(.select(4), .width(32), .disabled("Z"), .enable("false")) multiplexer_2 (
    .in0({32{1'b0}}), .in1({32{1'b0}}), .in2({32{1'b0}}), .in3(multiplier_1_cout), .in4(divider_1_rem),
    .in5({32{1'b0}}), .in6({32{1'b0}}), .in7({32{1'b0}}), .in8({32{1'b0}}), .in9({32{1'b0}}),
    .in10({32{1'b0}}), .in11({32{1'b0}}), .in12({32{1'b0}}), .in13({32{1'b0}}), .in14({32{1'b0}}),
    .in15({32{1'b0}}), .out(Result_2), .sel(AluOP));

  // Other names for the same wires on the sheet: Result2[31:0] = Result_2; S[3:0] = AluOP

  // Notes on the sheet:
  //   不要改变此引脚区域内容，也不要改变ALU封装形式
  //   输入引脚
  //   输出引脚
endmodule

module MIPS_Regifile (
  input  [31:0] Din,
  input  Clk,
  input  WE,
  input  [4:0] R1_num,
  input  [4:0] W_num,
  input  [4:0] R2_num,
  output [31:0] R1,
  output [31:0] R2
);

  // RegisterFile registerfile_1: pin names not known; wires that end beside it: Din, Clk, WE, W_num, R1_num, R2_num, R1, R2
endmodule

module \理想流水线  (
  output RegWrite,
  output MemWrite,
  output [31:0] IF_PC,
  output [31:0] ID_PC,
  output [31:0] EX_PC,
  output [31:0] M_PC,
  output [31:0] WB_PC,
  output [31:0] RDin,
  output [31:0] MDin,
  output [31:0] LedData
);

  wire and_1_out, and_2_out, CLK, clock_1_out, clock_2_out, comparator_1_eq, comparator_1_lt,
       comparator_2_eq, Con_flag, d_ff_1_q, ex_men_1_equal_out, ex_men_1_jal_out, ex_men_1_memtoreg_out,
       ex_men_1_regdst_out, ex_men_1_regwrite_out, ex_men_1_syscall_out, Go, halt, id_ex_1_alusrc_out,
       id_ex_1_beq_out, id_ex_1_bne_out, id_ex_1_jal_out, id_ex_1_memtoreg_out, id_ex_1_memwrite_out,
       id_ex_1_regdst_out, id_ex_1_regwrite_out, id_ex_1_syscall_out, IR1, IR2, IR3, JMP, JR, Jump, Ledout,
       men_wb_1_jal_out, men_wb_1_memtoreg_out, men_wb_1_regdst_out, men_wb_1_syscall_out, mips_alu_1_equal,
       nand_2_out, not_1_out, not_2_out, or_1_out, RST, W1, W2, W3, Write, \单周期硬布线控制器_1_alu_src ,
       \单周期硬布线控制器_1_beq , \单周期硬布线控制器_1_bne , \单周期硬布线控制器_1_jal , \单周期硬布线控制器_1_jmp , \单周期硬布线控制器_1_jr ,
       \单周期硬布线控制器_1_memtoreg , \单周期硬布线控制器_1_memwrite , \单周期硬布线控制器_1_regdst , \单周期硬布线控制器_1_regwrite ,
       \单周期硬布线控制器_1_signedext , \单周期硬布线控制器_1_syscall ;
  wire [3:0] id_ex_1_aluop_out, \单周期硬布线控制器_1_alu_op ;
  wire [4:0] multiplexer_3_out, multiplexer_5_out, multiplexer_9_out, W_num;
  wire [12:0] CNT_num;
  wire [15:0] \LoadUse次数 , \总周期数 , \插入气泡数 , \无条件分支数 , \条件分支成功数 ;
  wire [27:0] shifter_2_out;
  wire [31:0] adder_1_out, adder_2_out, adder_3_out, adder_4_out, bit_extender_1_out, bit_extender_2_out,
       EX_IR, ex_men_1_aluresult_out, id_ex_1_r2_out, ID_IR, IF_IR, Immediate, MEM_IR,
       men_wb_1_aluresult_out, men_wb_1_memorydata_out, mips_alu_1_result, mips_regifile_1_r1,
       mips_regifile_1_r2, multiplexer_1_out, multiplexer_2_out, multiplexer_4_out, multiplexer_6_out,
       multiplexer_7_out, multiplexer_8_out, R1, R2, ram_1_data, register_2_q, register_3_q, shifter_1_out,
       WB_IR;

  Button \u_总复位  (.out(RST));
  Button _1 (.out(IR1));
  Button _2 (.out(IR2));
  Button _3 (.out(IR3));
  // Probe on \总周期数 
  // Probe on \总周期数 
  Button \u_继续运行  (.out(Go));
  LED #(.active("true")) led_1 (.in(W1));
  LED #(.active("true")) led_2 (.in(W2));
  LED #(.active("true")) led_3 (.in(W3));
  nand nand_1 (Write, not_1_out, halt);
  Hex_Digit_Display hex_digit_display_1 (.value(LedData[31:28]));  // open: dp
  // Probe on IF_PC[19:0]
  // Mips_Probe mips_probe_1: pin names not known; wires that end beside it: IF_IR
  not not_1 (not_1_out, Go);
  Shifter #(.width(32), .shift("ll")) shifter_1 (.in(Immediate), .\dist (5'b00010), .out(shifter_1_out));
  Adder #(.width(32)) adder_1 (.a(EX_PC), .b(32'h4), .out(adder_1_out));  // open: cin, cout
  Shifter #(.width(28), .shift("ll")) shifter_2 (.in(EX_IR[27:0]), .\dist (5'b00010), .out(shifter_2_out));
  Hex_Digit_Display hex_digit_display_2 (.value(LedData[27:24]));  // open: dp
  Hex_Digit_Display hex_digit_display_3 (.value(LedData[23:20]));  // open: dp
  // Probe on ID_PC[19:0]
  // Mips_Probe mips_probe_2: pin names not known; wires that end beside it: ID_IR
  Multiplexer #(.select(1), .width(32), .disabled("Z"), .enable("false")) multiplexer_1 (
    .in0(adder_3_out), .in1(adder_2_out), .out(multiplexer_1_out), .sel(Con_flag));
  Adder #(.width(32)) adder_2 (.a(shifter_1_out), .b(adder_1_out), .out(adder_2_out));  // open: cin, cout
  Hex_Digit_Display hex_digit_display_4 (.value(LedData[19:16]));  // open: dp
  Hex_Digit_Display hex_digit_display_5 (.value(LedData[15:12]));  // open: dp
  Hex_Digit_Display hex_digit_display_6 (.value(LedData[7:4]));  // open: dp
  Hex_Digit_Display hex_digit_display_7 (.value(LedData[11:8]));  // open: dp
  Clock #(.highDuration(1), .lowDuration(1)) clock_1 (.out(clock_1_out));
  // Probe on EX_PC[19:0]
  // Mips_Probe mips_probe_3: pin names not known; wires that end beside it: clock_1_out, EX_IR, CLK
  Multiplexer #(.select(2), .width(32), .disabled("Z"), .enable("false")) multiplexer_2 (
    .in0(multiplexer_1_out), .in1(R1), .in2({adder_1_out[31:28], shifter_2_out}), .in3(R1),
    .out(multiplexer_2_out), .sel({JMP, JR}));
  or or_1 (or_1_out, ~halt, Go);  // OR_Gate
  Hex_Digit_Display hex_digit_display_8 (.value(LedData[3:0]));  // open: dp
  Register #(.width(32), .trigger("rising"), .Select("low")) PC (
    .D(multiplexer_2_out), .en(or_1_out), .Q(IF_PC), .clk(CLK), .clr(RST));
  Counter #(.width(16), .max('hffff), .ongoal("wrap"), .trigger("rising"), .behavior("old")) counter_1 (
    .load(1'b0), .count(or_1_out), .Q(\总周期数 ), .clk(CLK), .clr(RST));  // open: D, carry, preset
  // Probe on \总周期数 
  // Probe on M_PC[19:0]
  // Mips_Probe mips_probe_4: pin names not known; wires that end beside it: MEM_IR
  // Probe on \总周期数 
  // Probe on \无条件分支数 
  // Probe on \条件分支成功数 
  // Probe on \插入气泡数 
  // Probe on \LoadUse次数 
  ROM #(.addrWidth(10), .dataWidth(32), .Select("high")) rom_1 (.addr(IF_PC[11:2]), .data(IF_IR));
  Adder #(.width(32)) adder_3 (.a(IF_PC), .b(32'h4), .out(adder_3_out));  // open: cin, cout
  // Probe on IF_PC[11:0]
  // Probe on WB_PC[19:0]
  // Mips_Probe mips_probe_5: pin names not known; wires that end beside it: WB_IR
  // Probe on ID_PC[11:0]
  // Probe on EX_PC[11:0]
  IF_ID if_id_1 (
    .IR_in(IF_IR), .PC_in(IF_PC), .IR_out(ID_IR), .PC_out(ID_PC), .clk(CLK), .clear(RST), .enable(Write),
    .\气泡_高电平时有效 (Jump));
  // Probe on M_PC[11:0]
  D_Flip_Flop #(.trigger("high"), .Pre_Clr_Positions("LEGACY"), .NegatePresetClear("false"), .enable("true"), .NewFFLayout("false")) d_ff_1 (.Q(d_ff_1_q));  // open: clk, D, Qn, preset, en, reset
  // Probe on 13'hc
  // Probe on WB_PC[11:0]
  Comparator #(.width(13), .mode("twosComplement")) comparator_1 (
    .a(CNT_num), .b(13'hc), .eq(comparator_1_eq), .lt(comparator_1_lt));  // open: gt
  Clock #(.highDuration(1), .lowDuration(1)) clock_2 (.out(clock_2_out));
  \单周期硬布线控制器  \u_单周期硬布线控制器_1  (
    .Func(ID_IR[5:0]), .OP(ID_IR[31:26]), .ALU_OP(\单周期硬布线控制器_1_alu_op ), .MemToReg(\单周期硬布线控制器_1_memtoreg ),
    .MemWrite(\单周期硬布线控制器_1_memwrite ), .ALU_SRC(\单周期硬布线控制器_1_alu_src ), .RegWrite(\单周期硬布线控制器_1_regwrite ),
    .SysCALL(\单周期硬布线控制器_1_syscall ), .SignedExt(\单周期硬布线控制器_1_signedext ), .RegDst(\单周期硬布线控制器_1_regdst ),
    .JR(\单周期硬布线控制器_1_jr ), .JMP(\单周期硬布线控制器_1_jmp ), .Beq(\单周期硬布线控制器_1_beq ), .JAL(\单周期硬布线控制器_1_jal ),
    .Bne(\单周期硬布线控制器_1_bne ), .ERET(\单周期硬布线控制器_1_jr ));  // open: BLTZ, LBU, LUI
  Multiplexer #(.select(1), .width(5), .disabled("Z"), .enable("false")) multiplexer_3 (
    .in0(ID_IR[25:21]), .in1(5'b00010), .out(multiplexer_3_out), .sel(\单周期硬布线控制器_1_syscall ));
  assign bit_extender_1_out = {{16{1'b0}}, ID_IR[15:0]};  // Bit_Extender bit_extender_1
  assign bit_extender_2_out = {{16{ID_IR[15]}}, ID_IR[15:0]};  // Bit_Extender bit_extender_2
  nand nand_2 (nand_2_out, d_ff_1_q, comparator_1_eq);
  Counter #(.width(13), .max('h1fff), .ongoal("stay"), .trigger("rising"), .behavior("old")) counter_2 (
    .count(comparator_1_lt), .Q(CNT_num), .clk(clock_2_out));  // open: load, D, carry, clr, preset
  Multiplexer #(.select(1), .width(32), .disabled("Z"), .enable("false")) multiplexer_4 (
    .in0(bit_extender_1_out), .in1(bit_extender_2_out), .out(multiplexer_4_out), .sel(\单周期硬布线控制器_1_signedext ));
  assign CLK = nand_2_out ? clock_2_out : 1'bz;  // Controlled_Buffer controlled_buffer_1
  Multiplexer #(.select(1), .width(5), .disabled("Z"), .enable("false")) multiplexer_5 (
    .in0(ID_IR[20:16]), .in1(5'b00100), .out(multiplexer_5_out), .sel(\单周期硬布线控制器_1_syscall ));
  Pull_Resistor #(.pull(1)) pull_resistor_1 (.node(CLK));
  MIPS_Regifile mips_regifile_1 (
    .Din(RDin), .Clk(CLK), .R1(mips_regifile_1_r1), .R2(mips_regifile_1_r2), .WE(RegWrite), .W_num(W_num),
    .R1_num(multiplexer_3_out), .R2_num(multiplexer_5_out));
  Register #(.width(32), .trigger("rising"), .Select("low")) register_1 (
    .D(mips_regifile_1_r2), .Q(LedData), .clk(CLK), .clr(RST));  // open: en
  ID_EX id_ex_1 (
    .Beq_in(\单周期硬布线控制器_1_beq ), .Bne_in(\单周期硬布线控制器_1_bne ), .MemToReg_in(\单周期硬布线控制器_1_memtoreg ),
    .MemWrite_in(\单周期硬布线控制器_1_memwrite ), .AluOP_in(\单周期硬布线控制器_1_alu_op ), .AluSrc_in(\单周期硬布线控制器_1_alu_src ),
    .RegWrite_in(\单周期硬布线控制器_1_regwrite ), .JAL_in(\单周期硬布线控制器_1_jal ), .RegDst_in(\单周期硬布线控制器_1_regdst ),
    .JMP_in(\单周期硬布线控制器_1_jmp ), .JR_in(\单周期硬布线控制器_1_jr ), .IR_in(ID_IR), .PC_in(ID_PC),
    .R1_in(mips_regifile_1_r1), .R2_in(mips_regifile_1_r2), .Imm_in(multiplexer_4_out),
    .Beq_out(id_ex_1_beq_out), .Bne_out(id_ex_1_bne_out), .MemToReg_out(id_ex_1_memtoreg_out),
    .MemWrite_out(id_ex_1_memwrite_out), .AluOP_out(id_ex_1_aluop_out), .AluSrc_out(id_ex_1_alusrc_out),
    .RegWrite_out(id_ex_1_regwrite_out), .JAL_out(id_ex_1_jal_out), .RegDst_out(id_ex_1_regdst_out),
    .JMP_out(JMP), .JR_out(JR), .IR_out(EX_IR), .PC_out(EX_PC), .R1_out(R1), .R2_out(id_ex_1_r2_out),
    .Imm_out(Immediate), .clk(CLK), .clear(RST), .enable(Write), .Syscall_out(id_ex_1_syscall_out),
    .Syscall_in(\单周期硬布线控制器_1_syscall ), .\气泡_高电平时有效 (Jump));  // open: LUI_in, LUI_out, LBU_in, LBU_out, BLTZ_in, BLTZ_out
  and and_1 (and_1_out, mips_alu_1_equal, id_ex_1_beq_out);
  not not_2 (not_2_out, mips_alu_1_equal);
  and and_2 (and_2_out, not_2_out, id_ex_1_bne_out);
  Multiplexer #(.select(1), .width(32), .disabled("Z"), .enable("false")) multiplexer_6 (
    .in0(id_ex_1_r2_out), .in1(Immediate), .out(multiplexer_6_out), .sel(id_ex_1_alusrc_out));
  or or_2 (Con_flag, and_1_out, and_2_out);
  Multiplexer #(.select(1), .width(32), .disabled("Z"), .enable("false")) multiplexer_7 (
    .in0(multiplexer_6_out), .in1(32'h32), .out(multiplexer_7_out), .sel(id_ex_1_syscall_out));
  MIPS_ALU mips_alu_1 (
    .X(R1), .Y(multiplexer_7_out), .AluOP(id_ex_1_aluop_out), .Equal(mips_alu_1_equal),
    .Result(mips_alu_1_result), .shamt(EX_IR[10:6]));  // open: Result_2
  EX_MEN ex_men_1 (
    .MemToReg_in(id_ex_1_memtoreg_out), .MemWrite_in(id_ex_1_memwrite_out),
    .RegWrite_in(id_ex_1_regwrite_out), .JAL_in(id_ex_1_jal_out), .RegDst_in(id_ex_1_regdst_out),
    .Syscall_in(id_ex_1_syscall_out), .equal_in(mips_alu_1_equal), .IR_in(EX_IR), .PC_in(EX_PC),
    .ALUResult_in(mips_alu_1_result), .R2_in(id_ex_1_r2_out), .MemToReg_out(ex_men_1_memtoreg_out),
    .MemWrite_out(MemWrite), .RegWrite_out(ex_men_1_regwrite_out), .JAL_out(ex_men_1_jal_out),
    .RegDst_out(ex_men_1_regdst_out), .Syscall_out(ex_men_1_syscall_out), .equal_out(ex_men_1_equal_out),
    .IR_out(MEM_IR), .PC_out(M_PC), .ALUResult_out(ex_men_1_aluresult_out), .R2_out(MDin), .clk(CLK),
    .clear(RST), .enable(Write), .\气泡_高电平时有效 (1'b0));  // open: LUI_in, LUI_out, LBU_in, LBU_out, BLTZ_in, BLTZ_out, R1_in, R1_out, Imm_in, Imm_out
  or or_3 (Jump, JMP, JR, Con_flag);
  RAM #(.addrWidth(10), .dataWidth(32), .bus("separate"), .Select("high")) ram_1 (
    .addr(ex_men_1_aluresult_out[11:2]), .din(MDin), .data(ram_1_data), .str(MemWrite), .clk(CLK), .clr(RST));  // open: sel, ld
  MEN_WB men_wb_1 (
    .MemToReg_in(ex_men_1_memtoreg_out), .MemWrite_in(MemWrite), .RegWrite_in(ex_men_1_regwrite_out),
    .JAL_in(ex_men_1_jal_out), .RegDst_in(ex_men_1_regdst_out), .Syscall_in(ex_men_1_syscall_out),
    .equal_in(ex_men_1_equal_out), .IR_in(MEM_IR), .PC_in(M_PC), .ALUResult_in(ex_men_1_aluresult_out),
    .Memorydata_in(ram_1_data), .MemToReg_out(men_wb_1_memtoreg_out), .RegWrite_out(RegWrite),
    .JAL_out(men_wb_1_jal_out), .RegDst_out(men_wb_1_regdst_out), .Syscall_out(men_wb_1_syscall_out),
    .IR_out(WB_IR), .PC_out(WB_PC), .ALUResult_out(men_wb_1_aluresult_out),
    .Memorydata_out(men_wb_1_memorydata_out), .clk(CLK), .clear(RST), .enable(Write), .\气泡_高电平时有效 (1'b0));  // open: MemWrite_out, equal_out, LBU_in, LBU_out, Memorydata_in_2, Memorydata_out_2
  Register #(.width(32), .trigger("rising"), .Select("low")) register_2 (
    .D(R1), .Q(register_2_q), .clk(CLK));  // open: en, clr
  Multiplexer #(.select(1), .width(32), .disabled("Z"), .enable("false")) multiplexer_8 (
    .in0(men_wb_1_aluresult_out), .in1(men_wb_1_memorydata_out), .out(multiplexer_8_out),
    .sel(men_wb_1_memtoreg_out));
  Register #(.width(32), .trigger("rising"), .Select("low")) register_3 (
    .D(register_2_q), .Q(register_3_q), .clk(CLK));  // open: en, clr
  Multiplexer #(.select(1), .width(5), .disabled("Z"), .enable("false")) multiplexer_9 (
    .in0(WB_IR[20:16]), .in1(WB_IR[15:11]), .out(multiplexer_9_out), .sel(men_wb_1_regdst_out));
  Adder #(.width(32)) adder_4 (.a(WB_PC), .b(32'h4), .out(adder_4_out));  // open: cin, cout
  Multiplexer #(.select(1), .width(32), .disabled("Z"), .enable("false")) multiplexer_10 (
    .in0(multiplexer_8_out), .in1(adder_4_out), .out(RDin), .sel(men_wb_1_jal_out));
  Multiplexer #(.select(1), .width(5), .disabled("Z"), .enable("false")) multiplexer_11 (
    .in0(multiplexer_9_out), .in1({5{1'b1}}), .out(W_num), .sel(men_wb_1_jal_out));
  Comparator #(.width(32), .mode("twosComplement")) comparator_2 (
    .a(register_3_q), .b(32'h32), .eq(comparator_2_eq));  // open: gt, lt
  and and_3 (halt, comparator_2_eq, men_wb_1_syscall_out);
  and and_4 (Ledout, ~comparator_2_eq, men_wb_1_syscall_out);  // AND_Gate
  Register #(.width(32), .trigger("rising"), .Select("low")) register_4 (
    .D(R2), .en(Ledout), .Q(LedData), .clk(CLK), .clr(RST));

  // Other names for the same wires on the sheet: MEM_PC[31:0] = M_PC

  // Notes on the sheet:
  //   中断源
  //   时空图监测，可删除
  //   中断等待指示
  //   数码管输出
  //   指令存储器
  //   contents of rom_1 (hex, n*v repeats v):
  //   20100000 20110000 20120000 20130000 36100000 36310001 36520002 36730003 ae100000 ae110004 ae120008
  //   ae13000c 2002000a 20110000 20120000 20130000 c
  //   控制位
  //   流水调试日志用
  //   暂停节拍，不能为0
  //   SignedExt
  //   OP
  //   Func
  //   rs
  //   rt
  //   戳工具置1进入计数暂停模式，ctrl+k时钟自动运行到对应节拍暂停
  //   ctrl+k关闭时钟连续运行，将控制位置零，进入单步调试模式调试
  //   用这个时钟源需要去掉电路中的其他时钟源
  //   JMP
  //   JR
  //   OP
  //   Func
  //   Syscall
  //   Beq
  //   Bne
  //   MemToReg
  //   MemWrite
  //   AluOP
  //   AluSrcB
  //   RegWrite
  //   JAL
  //   RegDst
  //   可计数暂停的时钟源
  //   为方便自动评测，需要输出流水线各段保存的PC值，注意是PC不是PC+4，另外ID段寄存器写入信息，Mem段内存写入信息也要输出
endmodule

module \气泡流水线  (
  output RegWrite,
  output MemWrite,
  output [31:0] IF_PC,
  output [31:0] ID_PC,
  output [31:0] EX_PC,
  output [31:0] M_PC,
  output [31:0] WB_PC,
  output [31:0] RDin,
  output [31:0] MDin,
  output [31:0] LedData
);

  wire and_1_out, and_2_out, and_3_out, and_4_out, and_5_out, CLK, clock_1_out, clock_2_out, comparator_1_eq,
       comparator_1_lt, comparator_2_eq, Con_flag, d_ff_1_q, ex_men_1_equal_out, ex_men_1_jal_out,
       ex_men_1_memtoreg_out, ex_men_1_regdst_out, ex_men_1_syscall_out, EX_WriteReg, Go, halt,
       id_ex_1_alusrc_out, id_ex_1_beq_out, id_ex_1_bne_out, id_ex_1_jal_out, id_ex_1_memtoreg_out,
       id_ex_1_memwrite_out, id_ex_1_regdst_out, id_ex_1_syscall_out, IR1, IR2, IR3, JMP, JR, Jump, Ledout,
       MemRegWrite, men_wb_1_jal_out, men_wb_1_memtoreg_out, men_wb_1_regdst_out, men_wb_1_syscall_out,
       mips_alu_1_equal, mips_probe_5_p2, nand_2_out, not_1_out, not_2_out, not_3_out, not_4_out, not_5_out,
       or_1_out, or_2_out, RST, W1, W2, W3, Write, \单周期硬布线控制器_1_alu_src , \单周期硬布线控制器_1_beq ,
       \单周期硬布线控制器_1_bne , \单周期硬布线控制器_1_jal , \单周期硬布线控制器_1_jmp , \单周期硬布线控制器_1_jr , \单周期硬布线控制器_1_memtoreg ,
       \单周期硬布线控制器_1_memwrite , \单周期硬布线控制器_1_regdst , \单周期硬布线控制器_1_regwrite , \单周期硬布线控制器_1_signedext ,
       \单周期硬布线控制器_1_syscall , \数据相关 ;
  wire [3:0] id_ex_1_aluop_out, \单周期硬布线控制器_1_alu_op ;
  wire [4:0] EX_WriteReg_num, MemRegWrite_num, multiplexer_8_out, multiplexer_10_out, multiplexer_13_out,
       R1_num, R2_num, W_num;
  wire [12:0] CNT_num;
  wire [15:0] \LoadUse次数 , \总周期数 , \插入气泡数 , \无条件分支数 , \条件分支成功数 ;
  wire [27:0] shifter_2_out;
  wire [31:0] adder_1_out, adder_2_out, adder_3_out, adder_4_out, bit_extender_1_out, bit_extender_2_out,
       EX_IR, ex_men_1_aluresult_out, id_ex_1_imm_out, id_ex_1_r2_out, ID_IR, IF_IR, Immediate, MEM_IR,
       men_wb_1_aluresult_out, men_wb_1_memorydata_out, mips_alu_1_result, mips_regifile_1_r1,
       mips_regifile_1_r2, multiplexer_1_out, multiplexer_2_out, multiplexer_4_out, multiplexer_6_out,
       multiplexer_7_out, multiplexer_12_out, R1, R2, ram_1_data, register_1_q, register_2_q, shifter_1_out,
       WB_IR;

  Button \u_总复位  (.out(RST));
  Button _1 (.out(IR1));
  Button _2 (.out(IR2));
  Button _3 (.out(IR3));
  // Probe on \总周期数 
  // Probe on \总周期数 
  Button \u_继续运行  (.out(Go));
  LED #(.active("true")) led_1 (.in(W1));
  LED #(.active("true")) led_2 (.in(W2));
  LED #(.active("true")) led_3 (.in(W3));
  nand nand_1 (Write, not_1_out, halt);
  Hex_Digit_Display hex_digit_display_1 (.value(LedData[31:28]));  // open: dp
  // Probe on IF_PC[19:0]
  // Mips_Probe mips_probe_1: pin names not known; wires that end beside it: IF_IR
  not not_1 (not_1_out, Go);
  Shifter #(.width(32), .shift("ll")) shifter_1 (.in(Immediate), .\dist (5'b00010), .out(shifter_1_out));
  Adder #(.width(32)) adder_1 (.a(EX_PC), .b(32'h4), .out(adder_1_out));  // open: cin, cout
  Shifter #(.width(28), .shift("ll")) shifter_2 (.in(EX_IR[27:0]), .\dist (5'b00010), .out(shifter_2_out));
  Hex_Digit_Display hex_digit_display_2 (.value(LedData[23:20]));  // open: dp
  Hex_Digit_Display hex_digit_display_3 (.value(LedData[27:24]));  // open: dp
  // Probe on ID_PC[19:0]
  // Mips_Probe mips_probe_2: pin names not known; wires that end beside it: ID_IR
  Adder #(.width(32)) adder_2 (.a(shifter_1_out), .b(adder_1_out), .out(adder_2_out));  // open: cin, cout
  Hex_Digit_Display hex_digit_display_4 (.value(LedData[15:12]));  // open: dp
  Hex_Digit_Display hex_digit_display_5 (.value(LedData[19:16]));  // open: dp
  Multiplexer #(.select(1), .width(32), .disabled("Z"), .enable("false")) multiplexer_1 (
    .in0(adder_3_out), .in1(adder_2_out), .out(multiplexer_1_out), .sel(Con_flag));
  Hex_Digit_Display hex_digit_display_6 (.value(LedData[7:4]));  // open: dp
  Hex_Digit_Display hex_digit_display_7 (.value(LedData[11:8]));  // open: dp
  Clock #(.highDuration(1), .lowDuration(1)) clock_1 (.out(clock_1_out));
  // Probe on EX_PC[19:0]
  // Mips_Probe mips_probe_3: pin names not known; wires that end beside it: clock_1_out, EX_IR, CLK
  Multiplexer #(.select(2), .width(32), .disabled("Z"), .enable("false")) multiplexer_2 (
    .in0(multiplexer_1_out), .in1(R1), .in2({adder_1_out[31:28], shifter_2_out}), .in3(R1),
    .out(multiplexer_2_out), .sel({JMP, JR}));
  and and_1 (and_1_out, not_2_out, or_1_out);
  not not_2 (not_2_out, \数据相关 );
  Hex_Digit_Display hex_digit_display_8 (.value(LedData[3:0]));  // open: dp
  Register #(.width(32), .trigger("rising"), .Select("low")) PC (
    .D(multiplexer_2_out), .en(and_1_out), .Q(IF_PC), .clk(CLK), .clr(RST));
  or or_1 (or_1_out, ~halt, Go);  // OR_Gate
  // Probe on M_PC[19:0]
  // Mips_Probe mips_probe_4: pin names not known; wires that end beside it: MEM_IR
  \数据相关性检测  \u_数据相关性检测_1  (
    .OP(ID_IR[31:26]), .FUNCT(ID_IR[5:0]), .rs(R1_num), .EX_WriteReg_num(EX_WriteReg_num),
    .EX_RegWrite(EX_WriteReg), .rt(R2_num), .DataHazzard(\数据相关 ), .MEM_RegWrite(MemRegWrite),
    .MEM_WriteReg_num(MemRegWrite_num));
  Counter #(.width(16), .max('hffff), .ongoal("wrap"), .trigger("rising"), .behavior("old")) counter_1 (
    .load(1'b0), .count(or_1_out), .Q(\总周期数 ), .clk(CLK), .clr(RST));  // open: D, carry, preset
  // Probe on \总周期数 
  // Probe on \无条件分支数 
  // Probe on \条件分支成功数 
  // Probe on \插入气泡数 
  // Probe on \LoadUse次数 
  ROM #(.addrWidth(10), .dataWidth(32), .Select("high")) rom_1 (.addr(IF_PC[11:2]), .data(IF_IR));
  Adder #(.width(32)) adder_3 (.a(IF_PC), .b(32'h4), .out(adder_3_out));  // open: cin, cout
  // Probe on \总周期数 
  // Probe on IF_PC[11:0]
  // Probe on WB_PC[19:0]
  // Mips_Probe mips_probe_5: pin names not known; wires that end beside it: WB_IR, mips_probe_5_p2
  // Probe on ID_PC[11:0]
  // Probe on EX_PC[11:0]
  not not_3 (not_3_out, \数据相关 );
  and and_2 (and_2_out, not_3_out, Write);
  IF_ID if_id_1 (
    .IR_in(IF_IR), .PC_in(IF_PC), .IR_out(ID_IR), .PC_out(ID_PC), .clk(CLK), .clear(RST), .enable(and_2_out),
    .\气泡_高电平时有效 (Jump));
  // Probe on M_PC[11:0]
  D_Flip_Flop #(.trigger("high"), .Pre_Clr_Positions("LEGACY"), .NegatePresetClear("false"), .enable("true"), .NewFFLayout("false")) d_ff_1 (.Q(d_ff_1_q));  // open: clk, D, Qn, preset, en, reset
  // Probe on 13'hc
  // Probe on WB_PC[11:0]
  Comparator #(.width(13), .mode("twosComplement")) comparator_1 (
    .a(CNT_num), .b(13'hc), .eq(comparator_1_eq), .lt(comparator_1_lt));  // open: gt
  Clock #(.highDuration(1), .lowDuration(1)) clock_2 (.out(clock_2_out));
  nand nand_2 (nand_2_out, d_ff_1_q, comparator_1_eq);
  Counter #(.width(13), .max('h1fff), .ongoal("stay"), .trigger("rising"), .behavior("old")) counter_2 (
    .count(comparator_1_lt), .Q(CNT_num), .clk(clock_2_out));  // open: load, D, carry, clr, preset
  \单周期硬布线控制器  \u_单周期硬布线控制器_1  (
    .Func(ID_IR[5:0]), .OP(ID_IR[31:26]), .ALU_OP(\单周期硬布线控制器_1_alu_op ), .MemToReg(\单周期硬布线控制器_1_memtoreg ),
    .MemWrite(\单周期硬布线控制器_1_memwrite ), .ALU_SRC(\单周期硬布线控制器_1_alu_src ), .RegWrite(\单周期硬布线控制器_1_regwrite ),
    .SysCALL(\单周期硬布线控制器_1_syscall ), .SignedExt(\单周期硬布线控制器_1_signedext ), .RegDst(\单周期硬布线控制器_1_regdst ),
    .JR(\单周期硬布线控制器_1_jr ), .JMP(\单周期硬布线控制器_1_jmp ), .Beq(\单周期硬布线控制器_1_beq ), .JAL(\单周期硬布线控制器_1_jal ),
    .Bne(\单周期硬布线控制器_1_bne ));  // open: ERET, BLTZ, LBU, LUI
  Multiplexer #(.select(1), .width(5), .disabled("Z"), .enable("false")) multiplexer_3 (
    .in0(ID_IR[25:21]), .in1(5'b00010), .out(R1_num), .sel(\单周期硬布线控制器_1_syscall ));
  assign bit_extender_1_out = {{16{1'b0}}, ID_IR[15:0]};  // Bit_Extender bit_extender_1
  Multiplexer #(.select(1), .width(32), .disabled("Z"), .enable("false")) multiplexer_4 (
    .in0(bit_extender_1_out), .in1(bit_extender_2_out), .out(multiplexer_4_out), .sel(\单周期硬布线控制器_1_signedext ));
  assign bit_extender_2_out = {{16{ID_IR[15]}}, ID_IR[15:0]};  // Bit_Extender bit_extender_2
  assign CLK = nand_2_out ? clock_2_out : 1'bz;  // Controlled_Buffer controlled_buffer_1
  Multiplexer #(.select(1), .width(5), .disabled("Z"), .enable("false")) multiplexer_5 (
    .in0(ID_IR[20:16]), .in1(5'b00100), .out(R2_num), .sel(\单周期硬布线控制器_1_syscall ));
  Pull_Resistor #(.pull(1)) pull_resistor_1 (.node(CLK));
  not not_4 (not_4_out, CLK);
  MIPS_Regifile mips_regifile_1 (
    .Din(RDin), .Clk(not_4_out), .R1(mips_regifile_1_r1), .R2(mips_regifile_1_r2), .WE(RegWrite),
    .W_num(W_num), .R1_num(R1_num), .R2_num(R2_num));
  or or_2 (or_2_out, \数据相关 , Jump);
  ID_EX id_ex_1 (
    .Beq_in(\单周期硬布线控制器_1_beq ), .Bne_in(\单周期硬布线控制器_1_bne ), .MemToReg_in(\单周期硬布线控制器_1_memtoreg ),
    .MemWrite_in(\单周期硬布线控制器_1_memwrite ), .AluOP_in(\单周期硬布线控制器_1_alu_op ), .AluSrc_in(\单周期硬布线控制器_1_alu_src ),
    .RegWrite_in(\单周期硬布线控制器_1_regwrite ), .JAL_in(\单周期硬布线控制器_1_jal ), .RegDst_in(\单周期硬布线控制器_1_regdst ),
    .JMP_in(\单周期硬布线控制器_1_jmp ), .JR_in(\单周期硬布线控制器_1_jr ), .IR_in(ID_IR), .PC_in(ID_PC),
    .R1_in(mips_regifile_1_r1), .R2_in(mips_regifile_1_r2), .Imm_in(multiplexer_4_out),
    .Beq_out(id_ex_1_beq_out), .Bne_out(id_ex_1_bne_out), .MemToReg_out(id_ex_1_memtoreg_out),
    .MemWrite_out(id_ex_1_memwrite_out), .AluOP_out(id_ex_1_aluop_out), .AluSrc_out(id_ex_1_alusrc_out),
    .RegWrite_out(EX_WriteReg), .JAL_out(id_ex_1_jal_out), .RegDst_out(id_ex_1_regdst_out), .JMP_out(JMP),
    .JR_out(JR), .IR_out(EX_IR), .PC_out(EX_PC), .R1_out(R1), .R2_out(id_ex_1_r2_out),
    .Imm_out(id_ex_1_imm_out), .clk(CLK), .clear(RST), .enable(Write), .Syscall_out(id_ex_1_syscall_out),
    .Syscall_in(\单周期硬布线控制器_1_syscall ), .\气泡_高电平时有效 (or_2_out));  // open: LUI_in, LUI_out, LBU_in, LBU_out, BLTZ_in, BLTZ_out
  and and_3 (and_3_out, mips_alu_1_equal, id_ex_1_beq_out);
  not not_5 (not_5_out, mips_alu_1_equal);
  and and_4 (and_4_out, Write, \数据相关 );
  Multiplexer #(.select(1), .width(32), .disabled("Z"), .enable("false")) multiplexer_6 (
    .in0(id_ex_1_r2_out), .in1(id_ex_1_imm_out), .out(multiplexer_6_out), .sel(id_ex_1_alusrc_out));
  assign Immediate = {{16{id_ex_1_imm_out[15]}}, id_ex_1_imm_out[15:0]};  // Bit_Extender bit_extender_3
  Counter #(.width(16), .max('hffff), .ongoal("wrap"), .trigger("rising"), .behavior("old")) counter_3 (
    .D({16{1'b0}}), .count(and_4_out), .Q(\插入气泡数 ), .clk(CLK), .clr(RST));  // open: load, carry, preset
  or or_3 (Con_flag, and_3_out, and_5_out);
  and and_5 (and_5_out, not_5_out, id_ex_1_bne_out);
  Multiplexer #(.select(1), .width(32), .disabled("Z"), .enable("false")) multiplexer_7 (
    .in0(multiplexer_6_out), .in1(32'h32), .out(multiplexer_7_out), .sel(id_ex_1_syscall_out));
  Multiplexer #(.select(1), .width(5), .disabled("Z"), .enable("false")) multiplexer_8 (
    .in0(EX_IR[20:16]), .in1(EX_IR[15:11]), .out(multiplexer_8_out), .sel(id_ex_1_regdst_out));
  Multiplexer #(.select(1), .width(5), .disabled("Z"), .enable("false")) multiplexer_9 (
    .in0(multiplexer_8_out), .in1({5{1'b1}}), .out(EX_WriteReg_num), .sel(id_ex_1_jal_out));
  MIPS_ALU mips_alu_1 (
    .X(R1), .Y(multiplexer_7_out), .AluOP(id_ex_1_aluop_out), .Equal(mips_alu_1_equal),
    .Result(mips_alu_1_result), .shamt(EX_IR[10:6]));  // open: Result_2
  EX_MEN ex_men_1 (
    .MemToReg_in(id_ex_1_memtoreg_out), .MemWrite_in(id_ex_1_memwrite_out), .RegWrite_in(EX_WriteReg),
    .JAL_in(id_ex_1_jal_out), .RegDst_in(id_ex_1_regdst_out), .Syscall_in(id_ex_1_syscall_out),
    .equal_in(mips_alu_1_equal), .IR_in(EX_IR), .PC_in(EX_PC), .ALUResult_in(mips_alu_1_result),
    .R2_in(id_ex_1_r2_out), .MemToReg_out(ex_men_1_memtoreg_out), .MemWrite_out(MemWrite),
    .RegWrite_out(MemRegWrite), .JAL_out(ex_men_1_jal_out), .RegDst_out(ex_men_1_regdst_out),
    .Syscall_out(ex_men_1_syscall_out), .equal_out(ex_men_1_equal_out), .IR_out(MEM_IR), .PC_out(M_PC),
    .ALUResult_out(ex_men_1_aluresult_out), .R2_out(MDin), .clk(CLK), .clear(RST), .enable(Write),
    .\气泡_高电平时有效 (1'b0));  // open: LUI_in, LUI_out, LBU_in, LBU_out, BLTZ_in, BLTZ_out, R1_in, R1_out, Imm_in, Imm_out
  or or_4 (Jump, JMP, JR, Con_flag);
  Multiplexer #(.select(1), .width(5), .disabled("Z"), .enable("false")) multiplexer_10 (
    .in0(MEM_IR[20:16]), .in1(MEM_IR[15:11]), .out(multiplexer_10_out), .sel(ex_men_1_regdst_out));
  RAM #(.addrWidth(10), .dataWidth(32), .bus("separate"), .Select("high")) ram_1 (
    .addr(ex_men_1_aluresult_out[11:2]), .din(MDin), .data(ram_1_data), .str(MemWrite), .clk(CLK), .clr(RST));  // open: sel, ld
  Multiplexer #(.select(1), .width(5), .disabled("Z"), .enable("false")) multiplexer_11 (
    .in0(multiplexer_10_out), .in1({5{1'b1}}), .out(MemRegWrite_num), .sel(ex_men_1_jal_out));
  MEN_WB men_wb_1 (
    .MemToReg_in(ex_men_1_memtoreg_out), .MemWrite_in(MemWrite), .RegWrite_in(MemRegWrite),
    .JAL_in(ex_men_1_jal_out), .RegDst_in(ex_men_1_regdst_out), .Syscall_in(ex_men_1_syscall_out),
    .equal_in(ex_men_1_equal_out), .IR_in(MEM_IR), .PC_in(M_PC), .ALUResult_in(ex_men_1_aluresult_out),
    .Memorydata_in(ram_1_data), .MemToReg_out(men_wb_1_memtoreg_out), .RegWrite_out(RegWrite),
    .JAL_out(men_wb_1_jal_out), .RegDst_out(men_wb_1_regdst_out), .Syscall_out(men_wb_1_syscall_out),
    .IR_out(WB_IR), .PC_out(WB_PC), .ALUResult_out(men_wb_1_aluresult_out),
    .Memorydata_out(men_wb_1_memorydata_out), .clk(CLK), .clear(RST), .enable(Write), .\气泡_高电平时有效 (1'b0));  // open: MemWrite_out, equal_out, LBU_in, LBU_out, Memorydata_in_2, Memorydata_out_2
  Multiplexer #(.select(1), .width(32), .disabled("Z"), .enable("false")) multiplexer_12 (
    .in0(men_wb_1_aluresult_out), .in1(men_wb_1_memorydata_out), .out(multiplexer_12_out),
    .sel(men_wb_1_memtoreg_out));
  Register #(.width(32), .trigger("rising"), .Select("low")) register_1 (
    .D(R1), .Q(register_1_q), .clk(CLK));  // open: en, clr
  Multiplexer #(.select(1), .width(5), .disabled("Z"), .enable("false")) multiplexer_13 (
    .in0(WB_IR[20:16]), .in1(WB_IR[15:11]), .out(multiplexer_13_out), .sel(men_wb_1_regdst_out));
  Adder #(.width(32)) adder_4 (.a(WB_PC), .b(32'h4), .out(adder_4_out));  // open: cin, cout
  Register #(.width(32), .trigger("rising"), .Select("low")) register_2 (
    .D(register_1_q), .Q(register_2_q), .clk(CLK));  // open: en, clr
  Multiplexer #(.select(1), .width(32), .disabled("Z"), .enable("false")) multiplexer_14 (
    .in0(multiplexer_12_out), .in1(adder_4_out), .out(RDin), .sel(men_wb_1_jal_out));
  Multiplexer #(.select(1), .width(5), .disabled("Z"), .enable("false")) multiplexer_15 (
    .in0(multiplexer_13_out), .in1({5{1'b1}}), .out(W_num), .sel(men_wb_1_jal_out));
  Comparator #(.width(32), .mode("twosComplement")) comparator_2 (
    .a(register_2_q), .b(32'h32), .eq(comparator_2_eq));  // open: gt, lt
  and and_6 (halt, comparator_2_eq, men_wb_1_syscall_out);
  and and_7 (Ledout, ~comparator_2_eq, men_wb_1_syscall_out);  // AND_Gate
  Register #(.width(32), .trigger("rising"), .Select("low")) register_3 (
    .D(R2), .en(Ledout), .Q(LedData), .clk(CLK), .clr(RST));

  // Other names for the same wires on the sheet: MEM_PC[31:0] = M_PC

  // Notes on the sheet:
  //   中断源
  //   时空图监测，可删除
  //   时空图监测，可删除
  //   中断等待指示
  //   数码管输出
  //   指令存储器
  //   contents of rom_1 (hex, n*v repeats v):
  //   20110001 8000c05 20110001 20120002 20130003 8000c09 20110001 20120002 20130003 8000c0d 20110001
  //   20120002 20130003 8000c11 20110001 20120002 20130003 c000cb8 20100001 20110001 118fc0 112020
  //   20020022 c 118882 12200001 8000c15 112020 20020022 c 20110001 118880 112020 20020022 c 12200001
  //   8000c1f 20110001 118fc0 112020 20020022 c 1188c3 112020 20020022 c 118903 112020 20020022 c 118903
  //   112020 20020022 c 118903 112020 20020022 c 118903 112020 20020022 c 118903 112020 20020022 c 118903
  //   112020 20020022 c 118903 112020 20020022 c 20100001 109fc0 139fc3 8021 2012000c 24160003 26100001
  //   3210000f 20080008 20090001 139900 2709825 132020 20020022 c 1094022 1500fff9 22100001 2018000f
  //   2188024 108700 20080008 20090001 139902 2709825 132021 20020022 c 1094022 1500fff9 108702 2c9b022
  //   12c00001 8000c50 4020 1084027 84400 3508ffff 82021 20020022 c 2010ffff 20110000 ae300000 22100001
  //   22310004 ae300000 22100001 22310004 ae300000 22100001 22310004 ae300000 22100001 22310004 ae300000
  //   22100001 22310004 ae300000 22100001 22310004 ae300000 22100001 22310004 ae300000 22100001 22310004
  //   ae300000 22100001 22310004 ae300000 22100001 22310004 ae300000 22100001 22310004 ae300000 22100001
  //   22310004 ae300000 22100001 22310004 ae300000 22100001 22310004 ae300000 22100001 22310004 ae300000
  //   22100001 22310004 22100001 8020 2011003c 8e130000 8e340000 274402a 11000002 ae330000 ae140000
  //   2231fffc 1611fff8 102020 20020022 c 22100004 2011003c 1611fff2 20020032 c 20100000 22100001 102020
  //   20020022 c 22100002 102020 20020022 c 22100003 102020 20020022 c 22100004 102020 20020022 c 22100005
  //   102020 20020022 c 22100006 102020 20020022 c 22100007 102020 20020022 c 22100008 102020 20020022
  //   20020022 c 3e00008
  //   控制位
  //   流水调试日志用
  //   暂停节拍，不能为0
  //   OP
  //   Func
  //   rs
  //   rt
  //   戳工具置1进入计数暂停模式，ctrl+k时钟自动运行到对应节拍暂停
  //   戳工具置1进入计数暂停模式，ctrl+k时钟自动运行到对应节拍暂停
  //   ctrl+k关闭时钟连续运行，将控制位置零，进入单步调试模式调试
  //   ctrl+k关闭时钟连续运行，将控制位置零，进入单步调试模式调试
  //   用这个时钟源需要去掉电路中的其他时钟源
  //   JR
  //   SignedExt
  //   OP
  //   Func
  //   Beq
  //   Bne
  //   MemToReg
  //   MemWrite
  //   AluOP
  //   AluSrcB
  //   RegWrite
  //   JAL
  //   RegDst
  //   Syscall
  //   可计数暂停的时钟源
  //   为方便自动评测，需要输出流水线各段保存的PC值，注意是PC不是PC+4，另外ID段寄存器写入信息，Mem段内存写入信息也要输出
endmodule

module \重定向流水线  (
  output RegWrite,
  output MemWrite,
  output [31:0] IF_PC,
  output [31:0] ID_PC,
  output [31:0] EX_PC,
  output [31:0] M_PC,
  output [31:0] WB_PC,
  output [31:0] RDin,
  output [31:0] MDin,
  output [31:0] LedData
);

  wire and_1_out, and_2_out, and_3_out, and_4_out, and_5_out, BLTZ, CLK, clock_1_out, clock_2_out,
       comparator_1_eq, comparator_1_lt, comparator_2_lt, comparator_3_eq, Con_flag, d_ff_1_q, EX_MemToReg,
       ex_men_1_equal_out, ex_men_1_jal_out, ex_men_1_lbu_out, ex_men_1_memtoreg_out, ex_men_1_regdst_out,
       ex_men_1_syscall_out, EX_WriteReg, Go, halt, id_ex_1_alusrc_out, id_ex_1_beq_out, id_ex_1_bne_out,
       id_ex_1_jal_out, id_ex_1_memwrite_out, id_ex_1_regdst_out, IR1, IR2, IR3, JMP, JR, Jump, Ledout,
       MemRegWrite, men_wb_1_jal_out, men_wb_1_memtoreg_out, men_wb_1_regdst_out, mips_alu_1_equal,
       nand_2_out, nand_3_out, not_1_out, not_2_out, not_3_out, not_4_out, or_1_out, or_2_out, RST, Syscall,
       W1, W2, W3, Write, \单周期硬布线控制器_1_alu_src , \单周期硬布线控制器_1_beq , \单周期硬布线控制器_1_bne , \单周期硬布线控制器_1_jal ,
       \单周期硬布线控制器_1_jmp , \单周期硬布线控制器_1_jr , \单周期硬布线控制器_1_memtoreg , \单周期硬布线控制器_1_memwrite ,
       \单周期硬布线控制器_1_regdst , \单周期硬布线控制器_1_regwrite , \单周期硬布线控制器_1_signedext , \单周期硬布线控制器_1_syscall , \数据相关 ;
  wire [1:0] choice, \loaduse检测_1_rsfoward , \loaduse检测_1_rtfoward , persona_ex, RsForward, RtForward;
  wire [2:0] persona_id;
  wire [3:0] id_ex_1_aluop_out, \单周期硬布线控制器_1_alu_op ;
  wire [4:0] EX_WriteReg_num, MemRegWrite_num, multiplexer_8_out, multiplexer_12_out, multiplexer_17_out,
       R1_num, R2_num, W_num;
  wire [7:0] multiplexer_14_out;
  wire [12:0] CNT_num;
  wire [15:0] id_ex_1_imm_out, \LoadUse次数 , \总周期数 , \插入气泡数 , \无条件分支数 , \条件分支成功数 ;
  wire [27:0] shifter_2_out;
  wire [31:0] adder_1_out, adder_2_out, adder_3_out, adder_4_out, bit_extender_1_out, bit_extender_2_out,
       bit_extender_4_out, EX_IR, ex_men_1_r1_out, id_ex_1_r1_out, id_ex_1_r2_out, ID_IR, IF_IR, Immediate,
       MEM_IR, men_wb_1_aluresult_out, men_wb_1_memorydata_out, men_wb_1_memorydata_out_2, mips_alu_1_result,
       mips_regifile_1_r1, mips_regifile_1_r2, multiplexer_1_out, multiplexer_2_out, multiplexer_4_out,
       multiplexer_10_out, multiplexer_11_out, multiplexer_15_out, multiplexer_16_out, R1, R2, ram_1_data,
       shifter_1_out, WB_IR;
  wire [31:2] ex_men_1_aluresult_out;
  wire [31:16] id_ex_1_imm_out_2;

  Button \u_总复位  (.out(RST));
  Button _1 (.out(IR1));
  Button _2 (.out(IR2));
  Button _3 (.out(IR3));
  // Probe on \总周期数 
  // Probe on \总周期数 
  Button \u_继续运行  (.out(Go));
  LED #(.active("true")) led_1 (.in(W1));
  LED #(.active("true")) led_2 (.in(W2));
  LED #(.active("true")) led_3 (.in(W3));
  nand nand_1 (Write, not_1_out, halt);
  Hex_Digit_Display hex_digit_display_1 (.value(LedData[31:28]));  // open: dp
  // Probe on IF_PC[19:0]
  // Mips_Probe mips_probe_1: pin names not known; wires that end beside it: IF_IR
  not not_1 (not_1_out, Go);
  Shifter #(.width(32), .shift("ll")) shifter_1 (.in(Immediate), .\dist (5'b00010), .out(shifter_1_out));
  Adder #(.width(32)) adder_1 (.a(EX_PC), .b(32'h4), .out(adder_1_out));  // open: cin, cout
  Shifter #(.width(28), .shift("ll")) shifter_2 (.in(EX_IR[27:0]), .\dist (5'b00010), .out(shifter_2_out));
  Hex_Digit_Display hex_digit_display_2 (.value(LedData[27:24]));  // open: dp
  Hex_Digit_Display hex_digit_display_3 (.value(LedData[23:20]));  // open: dp
  // Probe on ID_PC[19:0]
  // Mips_Probe mips_probe_2: pin names not known; wires that end beside it: ID_IR
  Adder #(.width(32)) adder_2 (.a(shifter_1_out), .b(adder_1_out), .out(adder_2_out));  // open: cin, cout
  Hex_Digit_Display hex_digit_display_4 (.value(LedData[15:12]));  // open: dp
  Hex_Digit_Display hex_digit_display_5 (.value(LedData[19:16]));  // open: dp
  Multiplexer #(.select(1), .width(32), .disabled("Z"), .enable("false")) multiplexer_1 (
    .in0(adder_3_out), .in1(adder_2_out), .out(multiplexer_1_out), .sel(Con_flag));
  Hex_Digit_Display hex_digit_display_6 (.value(LedData[11:8]));  // open: dp
  Hex_Digit_Display hex_digit_display_7 (.value(LedData[7:4]));  // open: dp
  Clock #(.highDuration(1), .lowDuration(1)) clock_1 (.out(clock_1_out));
  // Probe on EX_PC[19:0]
  // Mips_Probe mips_probe_3: pin names not known; wires that end beside it: clock_1_out, EX_IR, CLK
  Multiplexer #(.select(2), .width(32), .disabled("Z"), .enable("false")) multiplexer_2 (
    .in0(multiplexer_1_out), .in1(R1), .in2({adder_1_out[31:28], shifter_2_out}), .in3(R1),
    .out(multiplexer_2_out), .sel({JMP, JR}));
  and and_1 (and_1_out, not_2_out, or_1_out);
  not not_2 (not_2_out, \数据相关 );
  Hex_Digit_Display hex_digit_display_8 (.value(LedData[3:0]));  // open: dp
  Register #(.width(32), .trigger("rising"), .Select("low")) PC (
    .D(multiplexer_2_out), .en(and_1_out), .Q(IF_PC), .clk(CLK), .clr(RST));
  or or_1 (or_1_out, ~halt, Go);  // OR_Gate
  // Probe on \总周期数 
  // Probe on M_PC[19:0]
  // Mips_Probe mips_probe_4: pin names not known; wires that end beside it: MEM_IR
  \LoadUse检测  \loaduse检测_1  (
    .OP(ID_IR[31:26]), .FUNCT(ID_IR[5:0]), .MEM_WriteReg_num(MemRegWrite_num), .MEM_RegWrite(MemRegWrite),
    .EX_RegWrite(EX_WriteReg), .rs(R1_num), .EX_WriteReg_num(EX_WriteReg_num), .EX_MemToReg(EX_MemToReg),
    .rt(R2_num), .RsFoward(\loaduse检测_1_rsfoward ), .LoadUse(\数据相关 ), .RtFoward(\loaduse检测_1_rtfoward ));
  Counter #(.width(16), .max('hffff), .ongoal("wrap"), .trigger("rising"), .behavior("old")) counter_1 (
    .load(1'b0), .count(or_1_out), .Q(\总周期数 ), .clk(CLK), .clr(RST));  // open: D, carry, preset
  // Probe on \总周期数 
  // Probe on \无条件分支数 
  // Probe on \条件分支成功数 
  // Probe on \插入气泡数 
  // Probe on \LoadUse次数 
  Register #(.width(2), .trigger("rising"), .Select("low")) register_1 (
    .D(\loaduse检测_1_rsfoward ), .Q(RsForward), .clk(CLK));  // open: en, clr
  Register #(.width(2), .trigger("rising"), .Select("low")) register_2 (
    .D(\loaduse检测_1_rtfoward ), .Q(RtForward), .clk(CLK));  // open: en, clr
  ROM #(.addrWidth(10), .dataWidth(32), .Select("high")) rom_1 (.addr(IF_PC[11:2]), .data(IF_IR));
  Adder #(.width(32)) adder_3 (.a(IF_PC), .b(32'h4), .out(adder_3_out));  // open: cin, cout
  // Probe on IF_PC[11:0]
  // Probe on WB_PC[19:0]
  // Mips_Probe mips_probe_5: pin names not known; wires that end beside it: WB_IR
  // Probe on EX_PC[11:0]
  // Probe on ID_PC[11:0]
  nand nand_2 (nand_2_out, ~Jump, \数据相关 );  // NAND_Gate
  IF_ID if_id_1 (
    .IR_in(IF_IR), .PC_in(IF_PC), .IR_out(ID_IR), .PC_out(ID_PC), .clk(CLK), .clear(RST),
    .enable(nand_2_out), .\气泡_高电平时有效 (Jump));
  // Probe on M_PC[11:0]
  D_Flip_Flop #(.trigger("high"), .Pre_Clr_Positions("LEGACY"), .NegatePresetClear("false"), .enable("true"), .NewFFLayout("false")) d_ff_1 (.Q(d_ff_1_q));  // open: clk, D, Qn, preset, en, reset
  // Probe on 13'hc
  // Probe on WB_PC[11:0]
  Comparator #(.width(13), .mode("twosComplement")) comparator_1 (
    .a(CNT_num), .b(13'hc), .eq(comparator_1_eq), .lt(comparator_1_lt));  // open: gt
  Clock #(.highDuration(1), .lowDuration(1)) clock_2 (.out(clock_2_out));
  nand nand_3 (nand_3_out, d_ff_1_q, comparator_1_eq);
  Counter #(.width(13), .max('h1fff), .ongoal("stay"), .trigger("rising"), .behavior("old")) counter_2 (
    .count(comparator_1_lt), .Q(CNT_num), .clk(clock_2_out));  // open: load, D, carry, clr, preset
  \单周期硬布线控制器  \u_单周期硬布线控制器_1  (
    .Func(ID_IR[5:0]), .OP(ID_IR[31:26]), .ALU_OP(\单周期硬布线控制器_1_alu_op ), .MemToReg(\单周期硬布线控制器_1_memtoreg ),
    .MemWrite(\单周期硬布线控制器_1_memwrite ), .ALU_SRC(\单周期硬布线控制器_1_alu_src ), .RegWrite(\单周期硬布线控制器_1_regwrite ),
    .SysCALL(\单周期硬布线控制器_1_syscall ), .SignedExt(\单周期硬布线控制器_1_signedext ), .RegDst(\单周期硬布线控制器_1_regdst ),
    .JR(\单周期硬布线控制器_1_jr ), .JMP(\单周期硬布线控制器_1_jmp ), .Beq(\单周期硬布线控制器_1_beq ), .JAL(\单周期硬布线控制器_1_jal ),
    .Bne(\单周期硬布线控制器_1_bne ), .BLTZ(persona_id[2]), .LBU(persona_id[1]), .LUI(persona_id[0]));  // open: ERET
  Multiplexer #(.select(1), .width(5), .disabled("Z"), .enable("false")) multiplexer_3 (
    .in0(ID_IR[25:21]), .in1(5'b00010), .out(R1_num), .sel(\单周期硬布线控制器_1_syscall ));
  assign bit_extender_1_out = {{16{1'b0}}, ID_IR[15:0]};  // Bit_Extender bit_extender_1
  Multiplexer #(.select(1), .width(32), .disabled("Z"), .enable("false")) multiplexer_4 (
    .in0(bit_extender_1_out), .in1(bit_extender_2_out), .out(multiplexer_4_out), .sel(\单周期硬布线控制器_1_signedext ));
  assign bit_extender_2_out = {{16{ID_IR[15]}}, ID_IR[15:0]};  // Bit_Extender bit_extender_2
  assign CLK = nand_3_out ? clock_2_out : 1'bz;  // Controlled_Buffer controlled_buffer_1
  Multiplexer #(.select(1), .width(5), .disabled("Z"), .enable("false")) multiplexer_5 (
    .in0(ID_IR[20:16]), .in1(5'b00100), .out(R2_num), .sel(\单周期硬布线控制器_1_syscall ));
  Pull_Resistor #(.pull(1)) pull_resistor_1 (.node(CLK));
  not not_3 (not_3_out, CLK);
  MIPS_Regifile mips_regifile_1 (
    .Din(RDin), .Clk(not_3_out), .R1(mips_regifile_1_r1), .R2(mips_regifile_1_r2), .WE(RegWrite),
    .W_num(W_num), .R1_num(R1_num), .R2_num(R2_num));
  or or_2 (or_2_out, Jump, \数据相关 );
  ID_EX id_ex_1 (
    .Beq_in(\单周期硬布线控制器_1_beq ), .Bne_in(\单周期硬布线控制器_1_bne ), .MemToReg_in(\单周期硬布线控制器_1_memtoreg ),
    .MemWrite_in(\单周期硬布线控制器_1_memwrite ), .AluOP_in(\单周期硬布线控制器_1_alu_op ), .AluSrc_in(\单周期硬布线控制器_1_alu_src ),
    .RegWrite_in(\单周期硬布线控制器_1_regwrite ), .JAL_in(\单周期硬布线控制器_1_jal ), .RegDst_in(\单周期硬布线控制器_1_regdst ),
    .JMP_in(\单周期硬布线控制器_1_jmp ), .JR_in(\单周期硬布线控制器_1_jr ), .IR_in(ID_IR), .PC_in(ID_PC),
    .R1_in(mips_regifile_1_r1), .R2_in(mips_regifile_1_r2), .Imm_in(multiplexer_4_out),
    .Beq_out(id_ex_1_beq_out), .Bne_out(id_ex_1_bne_out), .MemToReg_out(EX_MemToReg),
    .MemWrite_out(id_ex_1_memwrite_out), .AluOP_out(id_ex_1_aluop_out), .AluSrc_out(id_ex_1_alusrc_out),
    .RegWrite_out(EX_WriteReg), .JAL_out(id_ex_1_jal_out), .RegDst_out(id_ex_1_regdst_out), .JMP_out(JMP),
    .JR_out(JR), .IR_out(EX_IR), .PC_out(EX_PC), .R1_out(id_ex_1_r1_out), .R2_out(id_ex_1_r2_out),
    .Imm_out({id_ex_1_imm_out_2, id_ex_1_imm_out}), .clk(CLK), .clear(RST), .enable(Write),
    .Syscall_out(Syscall), .Syscall_in(\单周期硬布线控制器_1_syscall ), .\气泡_高电平时有效 (or_2_out),
    .LUI_in(persona_id[0]), .LUI_out(persona_ex[0]), .LBU_in(persona_id[1]), .LBU_out(persona_ex[1]),
    .BLTZ_in(persona_id[2]), .BLTZ_out(BLTZ));
  and and_2 (and_2_out, mips_alu_1_equal, id_ex_1_beq_out);
  not not_4 (not_4_out, mips_alu_1_equal);
  and and_3 (and_3_out, Write, \数据相关 );
  assign Immediate = {{16{id_ex_1_imm_out[15]}}, id_ex_1_imm_out};  // Bit_Extender bit_extender_3
  Counter #(.width(16), .max('hffff), .ongoal("wrap"), .trigger("rising"), .behavior("old")) counter_3 (
    .D({16{1'b0}}), .count(and_3_out), .Q(\插入气泡数 ), .clk(CLK), .clr(RST));  // open: load, carry, preset
  or or_3 (Con_flag, and_2_out, and_4_out);
  and and_4 (and_4_out, not_4_out, id_ex_1_bne_out);
  Multiplexer #(.select(2), .width(32), .disabled("Z"), .enable("false")) multiplexer_6 (
    .in0(id_ex_1_r1_out), .in1(RDin), .in2({ex_men_1_aluresult_out, choice}), .out(R1), .sel(RsForward));  // open: in3
  Multiplexer #(.select(2), .width(32), .disabled("Z"), .enable("false")) multiplexer_7 (
    .in0(id_ex_1_r2_out), .in1(RDin), .in2({ex_men_1_aluresult_out, choice}), .out(R2), .sel(RtForward));  // open: in3
  Multiplexer #(.select(1), .width(5), .disabled("Z"), .enable("false")) multiplexer_8 (
    .in0(EX_IR[20:16]), .in1(EX_IR[15:11]), .out(multiplexer_8_out), .sel(id_ex_1_regdst_out));
  Multiplexer #(.select(1), .width(5), .disabled("Z"), .enable("false")) multiplexer_9 (
    .in0(multiplexer_8_out), .in1({5{1'b1}}), .out(EX_WriteReg_num), .sel(id_ex_1_jal_out));
  Multiplexer #(.select(1), .width(32), .disabled("Z"), .enable("false")) multiplexer_10 (
    .in0(R2), .in1({id_ex_1_imm_out_2, id_ex_1_imm_out}), .out(multiplexer_10_out), .sel(id_ex_1_alusrc_out));
  MIPS_ALU mips_alu_1 (
    .X(R1), .Y(multiplexer_10_out), .AluOP(id_ex_1_aluop_out), .Equal(mips_alu_1_equal),
    .Result(mips_alu_1_result), .shamt(EX_IR[10:6]));  // open: Result_2
  Comparator #(.width(32), .mode("twosComplement")) comparator_2 (
    .a(id_ex_1_r1_out), .b({32{1'b0}}), .lt(comparator_2_lt));  // open: gt, eq
  Multiplexer #(.select(1), .width(32), .disabled("Z"), .enable("false")) multiplexer_11 (
    .in0(mips_alu_1_result), .in1({id_ex_1_imm_out, {16{1'b0}}}), .out(multiplexer_11_out),
    .sel(persona_ex[0]));
  and and_5 (and_5_out, comparator_2_lt, BLTZ);
  EX_MEN ex_men_1 (
    .MemToReg_in(EX_MemToReg), .MemWrite_in(id_ex_1_memwrite_out), .RegWrite_in(EX_WriteReg),
    .JAL_in(id_ex_1_jal_out), .RegDst_in(id_ex_1_regdst_out), .Syscall_in(Syscall),
    .equal_in(mips_alu_1_equal), .IR_in(EX_IR), .PC_in(EX_PC), .ALUResult_in(multiplexer_11_out), .R2_in(R2),
    .MemToReg_out(ex_men_1_memtoreg_out), .MemWrite_out(MemWrite), .RegWrite_out(MemRegWrite),
    .JAL_out(ex_men_1_jal_out), .RegDst_out(ex_men_1_regdst_out), .Syscall_out(ex_men_1_syscall_out),
    .equal_out(ex_men_1_equal_out), .IR_out(MEM_IR), .PC_out(M_PC),
    .ALUResult_out({ex_men_1_aluresult_out, choice}), .R2_out(MDin), .clk(CLK), .clear(RST), .enable(Write),
    .\气泡_高电平时有效 (1'b0), .LUI_in(persona_ex[0]), .LBU_in(persona_ex[1]), .LBU_out(ex_men_1_lbu_out),
    .R1_in(R1), .R1_out(ex_men_1_r1_out));  // open: LUI_out, BLTZ_in, BLTZ_out, Imm_in, Imm_out
  or or_4 (Jump, JMP, id_ex_1_jal_out, and_5_out, JR, Con_flag);
  Multiplexer #(.select(1), .width(5), .disabled("Z"), .enable("false")) multiplexer_12 (
    .in0(MEM_IR[20:16]), .in1(MEM_IR[15:11]), .out(multiplexer_12_out), .sel(ex_men_1_regdst_out));
  Multiplexer #(.select(1), .width(5), .disabled("Z"), .enable("false")) multiplexer_13 (
    .in0(multiplexer_12_out), .in1({5{1'b1}}), .out(MemRegWrite_num), .sel(ex_men_1_jal_out));
  RAM #(.addrWidth(10), .dataWidth(32), .bus("separate"), .Select("high")) ram_1 (
    .addr(ex_men_1_aluresult_out[11:2]), .din(MDin), .data(ram_1_data), .str(MemWrite), .clk(CLK), .clr(RST));  // open: sel, ld
  Multiplexer #(.select(2), .width(8), .disabled("Z"), .enable("false")) multiplexer_14 (
    .in0(ram_1_data[7:0]), .in1(ram_1_data[15:8]), .in2(ram_1_data[23:16]), .in3(ram_1_data[31:24]),
    .out(multiplexer_14_out), .sel(choice));
  assign bit_extender_4_out = {{24{1'b0}}, multiplexer_14_out};  // Bit_Extender bit_extender_4
  Multiplexer #(.select(1), .width(32), .disabled("Z"), .enable("false")) multiplexer_15 (
    .in0(ram_1_data), .in1(bit_extender_4_out), .out(multiplexer_15_out), .sel(ex_men_1_lbu_out));
  MEN_WB men_wb_1 (
    .MemToReg_in(ex_men_1_memtoreg_out), .MemWrite_in(MemWrite), .RegWrite_in(MemRegWrite),
    .JAL_in(ex_men_1_jal_out), .RegDst_in(ex_men_1_regdst_out), .Syscall_in(ex_men_1_syscall_out),
    .equal_in(ex_men_1_equal_out), .IR_in(MEM_IR), .PC_in(M_PC),
    .ALUResult_in({ex_men_1_aluresult_out, choice}), .Memorydata_in(multiplexer_15_out),
    .MemToReg_out(men_wb_1_memtoreg_out), .RegWrite_out(RegWrite), .JAL_out(men_wb_1_jal_out),
    .RegDst_out(men_wb_1_regdst_out), .IR_out(WB_IR), .PC_out(WB_PC), .ALUResult_out(men_wb_1_aluresult_out),
    .Memorydata_out(men_wb_1_memorydata_out), .clk(CLK), .clear(RST), .enable(Write), .\气泡_高电平时有效 (1'b0),
    .Memorydata_in_2(ex_men_1_r1_out), .Memorydata_out_2(men_wb_1_memorydata_out_2));  // open: MemWrite_out, Syscall_out, equal_out, LBU_in, LBU_out
  Multiplexer #(.select(1), .width(32), .disabled("Z"), .enable("false")) multiplexer_16 (
    .in0(men_wb_1_aluresult_out), .in1(men_wb_1_memorydata_out), .out(multiplexer_16_out),
    .sel(men_wb_1_memtoreg_out));
  Multiplexer #(.select(1), .width(5), .disabled("Z"), .enable("false")) multiplexer_17 (
    .in0(WB_IR[20:16]), .in1(WB_IR[15:11]), .out(multiplexer_17_out), .sel(men_wb_1_regdst_out));
  Comparator #(.width(32), .mode("twosComplement")) comparator_3 (
    .a(men_wb_1_memorydata_out_2), .b(32'h32), .eq(comparator_3_eq));  // open: gt, lt
  Multiplexer #(.select(1), .width(32), .disabled("Z"), .enable("false")) multiplexer_18 (
    .in0(multiplexer_16_out), .in1(adder_4_out), .out(RDin), .sel(men_wb_1_jal_out));
  Adder #(.width(32)) adder_4 (.a(WB_PC), .b(32'h4), .out(adder_4_out));  // open: cin, cout
  Multiplexer #(.select(1), .width(5), .disabled("Z"), .enable("false")) multiplexer_19 (
    .in0(multiplexer_17_out), .in1({5{1'b1}}), .out(W_num), .sel(men_wb_1_jal_out));
  and and_6 (halt, comparator_3_eq, Syscall);
  and and_7 (Ledout, ~comparator_3_eq, Syscall);  // AND_Gate
  Register #(.width(32), .trigger("rising"), .Select("low")) register_3 (
    .D(R2), .en(Ledout), .Q(LedData), .clk(CLK), .clr(RST));

  // Other names for the same wires on the sheet: MEM_PC[31:0] = M_PC

  // Notes on the sheet:
  //   中断源
  //   时空图监测，可删除
  //   中断等待指示
  //   数码管输出
  //   指令存储器
  //   contents of rom_1 (hex, n*v repeats v):
  //   2011fff1 112020 20020022 c 22310001 620fffb 2002000a c
  //   控制位
  //   流水调试日志用
  //   暂停节拍，不能为0
  //   OP
  //   Func
  //   rs
  //   rt
  //   戳工具置1进入计数暂停模式，ctrl+k时钟自动运行到对应节拍暂停
  //   ctrl+k关闭时钟连续运行，将控制位置零，进入单步调试模式调试
  //   ctrl+k关闭时钟连续运行，将控制位置零，进入单步调试模式调试
  //   用这个时钟源需要去掉电路中的其他时钟源
  //   JMP
  //   JR
  //   SignedExt
  //   OP
  //   Func
  //   Beq
  //   Bne
  //   MemToReg
  //   MemWrite
  //   AluOP
  //   AluSrcB
  //   RegWrite
  //   JAL
  //   RegDst
  //   Syscall
  //   可计数暂停的时钟源
  //   为方便自动评测，需要输出流水线各段保存的PC值，注意是PC不是PC+4，另外ID段寄存器写入信息，Mem段内存写入信息也要输出
endmodule

module \中断按键参考电路  (
  input  \同步清零信号 ,
  output \与中断屏蔽位与 
);

  wire \_1号中断_out , and_1_out, clock_1_out, d_ff_1_q, or_1_out, or_2_out;

  Clock #(.highDuration(1), .lowDuration(1)) clock_1 (.out(clock_1_out));
  Button \_1号中断  (.out(\_1号中断_out ));
  or or_1 (or_1_out, \与中断屏蔽位与 , d_ff_1_q);
  LED #(.active("true")) \_1号中断等待指示灯  (.in(or_1_out));
  D_Flip_Flop #(.trigger("rising"), .Pre_Clr_Positions("LEGACY"), .NegatePresetClear("false"), .enable("true"), .NewFFLayout("false")) d_ff_1 (
    .clk(\_1号中断_out ), .D(1'b1), .Q(d_ff_1_q), .reset(\与中断屏蔽位与 ));  // open: Qn, preset, en
  or or_2 (or_2_out, d_ff_1_q, \与中断屏蔽位与 );
  and and_1 (and_1_out, or_2_out, ~\同步清零信号 );  // AND_Gate
  D_Flip_Flop #(.trigger("rising"), .Pre_Clr_Positions("LEGACY"), .NegatePresetClear("false"), .enable("true"), .NewFFLayout("false")) IR1 (
    .clk(clock_1_out), .D(and_1_out), .Q(\与中断屏蔽位与 ));  // open: Qn, preset, en, reset

  // Notes on the sheet:
  //   中断信号采样参考电路
  //   Reset 
endmodule
module \单周期MIPS_多级中断  (
  input  IR1,
  input  IR2,
  input  IR3,
  output RegWrite,
  output MemWrite,
  output [31:0] PC,
  output [31:0] IR,
  output [31:0] RDin,
  output [31:0] MDin,
  output [31:0] LedData
);

  wire AluSrcB, and_1_out, and_2_out, and_4_out, and_5_out, and_6_out, and_7_out, and_8_out, Beq, Bne, CLK,
       clock_2_out, CLR1, CLR2, CLR3, comparator_1_eq, comparator_2_eq, comparator_2_lt, comparator_3_eq,
       comparator_4_eq, comparator_5_eq, comparator_6_eq, comparator_6_lt, comparator_7_lt, d_ff_1_q,
       d_ff_2_q, d_ff_3_q, d_ff_4_q, decoder_1_out1, decoder_1_out2, decoder_1_out3, equal, ERET, Go, halt,
       IE, INT, INT1, INT2, INT3, IR1_t, IR2_t, IR3_t, IRA, IRB, IRC, JAL, JMP, JR, MemToReg, MFC0, MTC0,
       nand_1_out, not_equal, or_1_out, or_2_out, or_9_out, or_10_out, or_11_out, or_12_out, or_13_out,
       or_15_out, RegDst, register_2_q, SignedExt, Syscall, W1, W2, W3;
  wire [1:0] lr, lr1, lr2, multiplexer_17_out, multiplexer_19_out, multiplexer_20_out, priority_encoder_1_out;
  wire [3:0] AluOP;
  wire [4:0] multiplexer_5_out, multiplexer_6_out, multiplexer_7_out, multiplexer_9_out;
  wire [12:0] CNT_num;
  wire [15:0] \总周期数 ;
  wire [27:0] shifter_1_out;
  wire [31:0] adder_1_out, adder_2_out, bit_extender_1_out, bit_extender_2_out, EPC_ADDR, EPC_ADDR1,
       EPC_ADDR2, INT_ADDR, mips_alu_1_result, multiplexer_1_out, multiplexer_3_out, multiplexer_4_out,
       multiplexer_8_out, multiplexer_11_out, multiplexer_12_out, multiplexer_13_out, multiplexer_14_out,
       multiplexer_15_out, multiplexer_18_out, R1, ram_1_data, RET_ADDR, shifter_2_out;

  Clock #(.highDuration(1), .lowDuration(1)) clock_1 ();  // open: out
  Button _1 ();  // open: out
  Button _2 ();  // open: out
  Button _3 ();  // open: out
  and and_1 (and_1_out, Bne, not_equal);
  Button \u_继续运行  (.out(Go));
  LED #(.active("true")) led_1 (.in(W1));
  LED #(.active("true")) led_2 (.in(W2));
  LED #(.active("true")) led_3 (.in(W3));
  not not_1 (not_equal, equal);
  and and_2 (and_2_out, equal, Beq);
  or or_1 (or_1_out, and_1_out, and_2_out);
  Multiplexer #(.select(1), .width(32), .disabled("Z"), .enable("false")) multiplexer_1 (
    .in0(adder_1_out), .in1(adder_2_out), .out(multiplexer_1_out), .sel(or_1_out));
  Hex_Digit_Display hex_digit_display_1 (.value(LedData[31:28]));  // open: dp
  Multiplexer #(.select(2), .width(32), .disabled("Z"), .enable("false")) multiplexer_2 (
    .in0(multiplexer_1_out), .in1(R1), .in2({adder_1_out[31:28], shifter_1_out}), .in3(R1), .out(RET_ADDR),
    .sel({JMP, JR}));
  Hex_Digit_Display hex_digit_display_2 (.value(LedData[23:20]));  // open: dp
  Hex_Digit_Display hex_digit_display_3 (.value(LedData[27:24]));  // open: dp
  Multiplexer #(.select(1), .width(32), .disabled("Z"), .enable("false")) multiplexer_3 (
    .in0(RET_ADDR), .in1(INT_ADDR), .out(multiplexer_3_out), .sel(IE));
  Multiplexer #(.select(1), .width(32), .disabled("Z"), .enable("false")) multiplexer_4 (
    .in0(multiplexer_3_out), .in1(EPC_ADDR), .out(multiplexer_4_out), .sel(ERET));
  or or_2 (or_2_out, ~halt, Go);  // OR_Gate
  Hex_Digit_Display hex_digit_display_4 (.value(LedData[15:12]));  // open: dp
  Hex_Digit_Display hex_digit_display_5 (.value(LedData[19:16]));  // open: dp
  Register #(.width(32), .trigger("rising"), .Select("low")) u_PC (
    .D(multiplexer_4_out), .en(or_2_out), .Q(PC), .clk(CLK), .clr(1'b0));
  Counter #(.width(16), .max('hffff), .ongoal("wrap"), .trigger("rising"), .behavior("old")) counter_1 (
    .load(1'b0), .count(or_2_out), .Q(\总周期数 ), .clk(CLK), .clr(1'b0));  // open: D, carry, preset
  Hex_Digit_Display hex_digit_display_6 (.value(LedData[11:8]));  // open: dp
  Hex_Digit_Display hex_digit_display_7 (.value(LedData[7:4]));  // open: dp
  // Probe on \总周期数 
  Hex_Digit_Display hex_digit_display_8 (.value(LedData[3:0]));  // open: dp
  // Probe on \总周期数 
  ROM #(.addrWidth(10), .dataWidth(32), .Select("high")) rom_1 (.addr(PC[11:2]), .data(IR));
  Adder #(.width(32)) adder_1 (.a(PC), .b(32'h4), .out(adder_1_out));  // open: cin, cout
  // Mips_Probe mips_probe_1: pin names not known; wires that end beside it: IR
  or or_3 (IR1_t, IR1, IRA);
  Multiplexer #(.select(1), .width(5), .disabled("Z"), .enable("false")) multiplexer_5 (
    .in0(IR[25:21]), .in1(5'b00010), .out(multiplexer_5_out), .sel(Syscall));
  Multiplexer #(.select(1), .width(5), .disabled("Z"), .enable("false")) multiplexer_6 (
    .in0(IR[20:16]), .in1(IR[15:11]), .out(multiplexer_6_out), .sel(RegDst));
  assign bit_extender_1_out = {{16{1'b0}}, IR[15:0]};  // Bit_Extender bit_extender_1
  assign bit_extender_2_out = {{16{IR[15]}}, IR[15:0]};  // Bit_Extender bit_extender_2
  or or_4 (IR2_t, IR2, IRB);
  Multiplexer #(.select(1), .width(5), .disabled("Z"), .enable("false")) multiplexer_7 (
    .in0(multiplexer_6_out), .in1({5{1'b1}}), .out(multiplexer_7_out), .sel(JAL));
  Multiplexer #(.select(1), .width(32), .disabled("Z"), .enable("false")) multiplexer_8 (
    .in0(bit_extender_1_out), .in1(bit_extender_2_out), .out(multiplexer_8_out), .sel(SignedExt));
  Shifter #(.width(28), .shift("ll")) shifter_1 (.in(IR[27:0]), .\dist (5'b00010), .out(shifter_1_out));
  Multiplexer #(.select(1), .width(5), .disabled("Z"), .enable("false")) multiplexer_9 (
    .in0(IR[20:16]), .in1(5'b00100), .out(multiplexer_9_out), .sel(Syscall));
  Multiplexer #(.select(1), .width(32), .disabled("Z"), .enable("false")) multiplexer_10 (
    .in0(multiplexer_13_out), .in1(adder_1_out), .out(RDin), .sel(JAL));
  or or_5 (IR3_t, IR3, IRC);
  MIPS_Regifile mips_regifile_1 (
    .Din(RDin), .Clk(CLK), .R1(R1), .R2(MDin), .WE(RegWrite), .W_num(multiplexer_7_out),
    .R1_num(multiplexer_5_out), .R2_num(multiplexer_9_out));
  Multiplexer #(.select(1), .width(32), .disabled("Z"), .enable("false")) multiplexer_11 (
    .in0(MDin), .in1(multiplexer_8_out), .out(multiplexer_11_out), .sel(AluSrcB));
  Shifter #(.width(32), .shift("ll")) shifter_2 (.in(bit_extender_2_out), .\dist (5'b00010), .out(shifter_2_out));
  Multiplexer #(.select(1), .width(32), .disabled("Z"), .enable("false")) multiplexer_12 (
    .in0(multiplexer_11_out), .in1(32'h22), .out(multiplexer_12_out), .sel(Syscall));
  Adder #(.width(32)) adder_2 (.a(shifter_2_out), .b(adder_1_out), .out(adder_2_out));  // open: cin, cout
  MIPS_ALU mips_alu_1 (
    .X(R1), .Y(multiplexer_12_out), .AluOP(AluOP), .Equal(equal), .Result(mips_alu_1_result), .shamt(IR[10:6]));  // open: Result_2
  Comparator #(.width(32), .mode("twosComplement")) comparator_1 (
    .a(R1), .b(32'h32), .eq(comparator_1_eq));  // open: gt, lt
  and and_3 (halt, comparator_1_eq, Syscall);
  and and_4 (and_4_out, ~comparator_1_eq, Syscall);  // AND_Gate
  and and_5 (and_5_out, and_4_out, Syscall);
  RAM #(.addrWidth(10), .dataWidth(32), .bus("separate"), .Select("high")) ram_1 (
    .addr(mips_alu_1_result[11:2]), .din(MDin), .data(ram_1_data), .str(MemWrite), .clk(CLK), .clr(1'b0));  // open: sel, ld
  Register #(.width(32), .trigger("rising"), .Select("low")) register_1 (
    .D(MDin), .en(and_5_out), .Q(LedData), .clk(CLK), .clr(1'b0));
  Multiplexer #(.select(1), .width(32), .disabled("Z"), .enable("false")) multiplexer_13 (
    .in0(mips_alu_1_result), .in1(ram_1_data), .out(multiplexer_13_out), .sel(MemToReg));
  \单周期硬布线控制器  \u_单周期硬布线控制器_1  (
    .Func(IR[5:0]), .OP(IR[31:26]), .ALU_OP(AluOP), .MemToReg(MemToReg), .MemWrite(MemWrite),
    .ALU_SRC(AluSrcB), .RegWrite(RegWrite), .SysCALL(Syscall), .SignedExt(SignedExt), .RegDst(RegDst),
    .JR(JR), .JMP(JMP), .Beq(Beq), .JAL(JAL), .Bne(Bne), .ERET(ERET));  // open: BLTZ, LBU, LUI
  D_Flip_Flop #(.trigger("high"), .Pre_Clr_Positions("LEGACY"), .NegatePresetClear("false"), .enable("true"), .NewFFLayout("false")) d_ff_1 (.Q(d_ff_1_q));  // open: clk, D, Qn, preset, en, reset
  // Probe on 13'hc
  or or_6 (W1, INT1, d_ff_2_q);
  or or_7 (W2, INT2, d_ff_3_q);
  or or_8 (W3, INT3, d_ff_4_q);
  Comparator #(.width(13), .mode("twosComplement")) comparator_2 (
    .a(CNT_num), .b(13'hc), .eq(comparator_2_eq), .lt(comparator_2_lt));  // open: gt
  Clock #(.highDuration(1), .lowDuration(1)) clock_2 (.out(clock_2_out));
  D_Flip_Flop #(.trigger("rising"), .Pre_Clr_Positions("LEGACY"), .NegatePresetClear("false"), .enable("true"), .NewFFLayout("false")) d_ff_2 (
    .clk(IR1_t), .D(1'b1), .Q(d_ff_2_q), .reset(INT1));  // open: Qn, preset, en
  D_Flip_Flop #(.trigger("rising"), .Pre_Clr_Positions("LEGACY"), .NegatePresetClear("false"), .enable("true"), .NewFFLayout("false")) d_ff_3 (
    .clk(IR2_t), .D(1'b1), .Q(d_ff_3_q), .reset(INT2));  // open: Qn, preset, en
  D_Flip_Flop #(.trigger("rising"), .Pre_Clr_Positions("LEGACY"), .NegatePresetClear("false"), .enable("true"), .NewFFLayout("false")) d_ff_4 (
    .clk(IR3_t), .D(1'b1), .Q(d_ff_4_q), .reset(INT3));  // open: Qn, preset, en
  nand nand_1 (nand_1_out, d_ff_1_q, comparator_2_eq);
  Counter #(.width(13), .max('h1fff), .ongoal("stay"), .trigger("rising"), .behavior("old")) counter_2 (
    .count(comparator_2_lt), .Q(CNT_num), .clk(clock_2_out));  // open: load, D, carry, clr, preset
  or or_9 (or_9_out, d_ff_2_q, INT1);
  and and_6 (and_6_out, or_9_out, ~CLR1);  // AND_Gate
  or or_10 (or_10_out, d_ff_3_q, INT2);
  and and_7 (and_7_out, or_10_out, ~CLR2);  // AND_Gate
  or or_11 (or_11_out, d_ff_4_q, INT3);
  and and_8 (and_8_out, or_11_out, ~CLR3);  // AND_Gate
  assign CLK = nand_1_out ? clock_2_out : 1'bz;  // Controlled_Buffer controlled_buffer_1
  D_Flip_Flop #(.trigger("rising"), .Pre_Clr_Positions("LEGACY"), .NegatePresetClear("false"), .enable("true"), .NewFFLayout("false")) u_IR1 (
    .clk(CLK), .D(and_6_out), .Q(INT1));  // open: Qn, preset, en, reset
  D_Flip_Flop #(.trigger("rising"), .Pre_Clr_Positions("LEGACY"), .NegatePresetClear("false"), .enable("true"), .NewFFLayout("false")) u_IR2 (
    .clk(CLK), .D(and_7_out), .Q(INT2));  // open: Qn, preset, en, reset
  D_Flip_Flop #(.trigger("rising"), .Pre_Clr_Positions("LEGACY"), .NegatePresetClear("false"), .enable("true"), .NewFFLayout("false")) u_IR3 (
    .clk(CLK), .D(and_8_out), .Q(INT3));  // open: Qn, preset, en, reset
  Pull_Resistor #(.pull(1)) pull_resistor_1 (.node(CLK));
  Comparator #(.width(16), .mode("twosComplement")) comparator_3 (
    .a(16'h258), .b(\总周期数 ), .eq(comparator_3_eq));  // open: gt, lt
  Comparator #(.width(16), .mode("twosComplement")) comparator_4 (
    .a(\总周期数 ), .b(16'h1), .eq(comparator_4_eq));  // open: gt, lt
  Comparator #(.width(16), .mode("twosComplement")) comparator_5 (
    .a(\总周期数 ), .b(16'h4), .eq(comparator_5_eq));  // open: gt, lt
  Comparator #(.width(16), .mode("twosComplement")) comparator_6 (
    .a(\总周期数 ), .b(16'h241), .eq(comparator_6_eq), .lt(comparator_6_lt));  // open: gt
  or or_12 (or_12_out, comparator_3_eq, comparator_4_eq);
  Pull_Resistor #(.pull(0)) pull_resistor_2 (.node(IRA));
  assign IRA = or_12_out ? ~CLK : 1'bz;  // Controlled_Inverter controlled_inverter_1
  Pull_Resistor #(.pull(0)) pull_resistor_3 (.node(IRB));
  assign IRB = comparator_5_eq ? ~CLK : 1'bz;  // Controlled_Inverter controlled_inverter_2
  Pull_Resistor #(.pull(0)) pull_resistor_4 (.node(IRC));
  assign IRC = comparator_6_eq ? ~CLK : 1'bz;  // Controlled_Inverter controlled_inverter_3
  Multiplexer #(.select(1), .width(32), .disabled("Z"), .enable("false")) multiplexer_14 (
    .in0(RET_ADDR), .in1(EPC_ADDR1), .out(multiplexer_14_out), .sel(ERET));
  or or_13 (or_13_out, IE, MTC0);
  Register #(.width(32), .trigger("rising"), .Select("low")) \EPC寄存器  (
    .D(multiplexer_14_out), .en(INT), .Q(EPC_ADDR), .clk(CLK));  // open: clr
  or or_14 (INT, IE, ERET);
  Register #(.width(1), .trigger("rising"), .Select("low")) register_2 (
    .D(or_13_out), .en(or_15_out), .Q(register_2_q), .clk(CLK));  // open: clr
  or or_15 (or_15_out, MTC0, IE, MFC0, ERET);
  and and_9 (IE, ~register_2_q, comparator_7_lt);  // AND_Gate
  Priority_Encoder #(.select(2), .disabled("Z")) priority_encoder_1 (
    .in0(1'b1), .in1(INT1), .in2(INT2), .in3(INT3), .out(priority_encoder_1_out));  // open: gs, en_out, en_in
  Multiplexer #(.select(1), .width(32), .disabled("Z"), .enable("false")) multiplexer_15 (
    .in0(EPC_ADDR), .in1(EPC_ADDR2), .out(multiplexer_15_out), .sel(ERET));
  Comparator #(.width(2), .mode("unsigned")) comparator_7 (
    .a(lr), .b(priority_encoder_1_out), .lt(comparator_7_lt));  // open: gt, eq
  Multiplexer #(.select(2), .width(32), .disabled("Z"), .enable("false")) multiplexer_16 (
    .in1(32'h30ac), .in2(32'h3158), .in3(32'h3204), .out(INT_ADDR), .sel(priority_encoder_1_out));  // open: in0
  Register #(.width(32), .trigger("rising"), .Select("low")) \EPC寄存器_2  (
    .D(multiplexer_15_out), .en(INT), .Q(EPC_ADDR1), .clk(CLK));  // open: clr
  Multiplexer #(.select(1), .width(2), .disabled("Z"), .enable("false")) multiplexer_17 (
    .in0(priority_encoder_1_out), .in1(lr1), .out(multiplexer_17_out), .sel(ERET));
  Decoder #(.select(2), .tristate("false"), .disabled("Z"), .enable("false")) decoder_1 (
    .out1(decoder_1_out1), .out2(decoder_1_out2), .out3(decoder_1_out3), .sel(priority_encoder_1_out));  // open: out0
  Register #(.width(2), .trigger("rising"), .Select("low")) register_3 (
    .D(multiplexer_17_out), .en(INT), .Q(lr), .clk(CLK));  // open: clr
  Multiplexer #(.select(1), .width(32), .disabled("Z"), .enable("false")) multiplexer_18 (
    .in0(EPC_ADDR1), .in1({32{1'b0}}), .out(multiplexer_18_out), .sel(ERET));
  Register #(.width(32), .trigger("rising"), .Select("low")) \EPC寄存器_3  (
    .D(multiplexer_18_out), .en(INT), .Q(EPC_ADDR2), .clk(CLK));  // open: clr
  Multiplexer #(.select(1), .width(2), .disabled("Z"), .enable("false")) multiplexer_19 (
    .in0(lr), .in1(lr2), .out(multiplexer_19_out), .sel(ERET));
  and and_10 (CLR1, ERET, decoder_1_out1);
  and and_11 (CLR2, decoder_1_out2, ERET);
  and and_12 (CLR3, decoder_1_out3, ERET);
  and and_13 (MTC0, ~IR[26], ~IR[27], ~IR[28], ~IR[29], IR[30], ~IR[31], ~IR[21], ~IR[22], IR[23], ~IR[24], ~IR[25]);  // AND_Gate
  and and_14 (MFC0, ~IR[26], ~IR[27], ~IR[28], ~IR[29], IR[30], ~IR[31], ~IR[21], ~IR[22], ~IR[23], ~IR[24], ~IR[25]);  // AND_Gate
  Register #(.width(2), .trigger("rising"), .Select("low")) register_4 (
    .D(multiplexer_19_out), .en(INT), .Q(lr1), .clk(CLK));  // open: clr
  Multiplexer #(.select(1), .width(2), .disabled("Z"), .enable("false")) multiplexer_20 (
    .in0(lr1), .in1(2'b00), .out(multiplexer_20_out), .sel(ERET));
  Register #(.width(2), .trigger("rising"), .Select("low")) register_5 (
    .D(multiplexer_20_out), .en(INT), .Q(lr2), .clk(CLK));  // open: clr

  // Other names for the same wires on the sheet: Func[5:0] = IR[5:0]; SHMAT[4:0] = IR[10:6]; Rs[4:0] = IR[25:21];
  //   OP[5:0] = IR[31:26]; R2[31:0] = MDin

  // Notes on the sheet:
  //   中断源
  //   中断等待指示
  //   总复位信号应将除ROM以外所有存储组件全部清零
  //   数码管输出
  //   数码管输出应该用寄存器锁存，否则显示数据只能一闪而过
  //   指令存储器
  //   contents of rom_1 (hex, n*v repeats v):
  //   201d07d0 20100001 109fc0 139fc3 8021 2012000c 24160008 26100001 3210000f 20080008 20090001 139900
  //   2709825 132020 20020022 c 1094022 1500fff9 22100001 2018000f 2188024 108700 20080008 20090001 139902
  //   2709825 132021 20020022 c 1094022 1500fff9 108702 2c9b022 12c00001 8000c07 4020 1084027 84400
  //   3508ffff 82021 20020022 c 8000c01 afa20000 23bd0004 afa40000 23bd0004 afb00000 23bd0004 afb30000
  //   23bd0004 afb40000 23bd0004 afb50000 23bd0004 afb60000 23bd0004 40000000 20160001 20140003 20150001
  //   168020 108100 2149825 132020 20020022 c 1600fffa 295a022 1680fff7 40800000 23bdfffc 8fb60000
  //   23bdfffc 8fb50000 23bdfffc 8fb40000 23bdfffc 8fb30000 23bdfffc 8fb00000 23bdfffc 8fa40000 23bdfffc
  //   8fa20000 42000018 afa20000 23bd0004 afa40000 23bd0004 afb00000 23bd0004 afb30000 23bd0004 afb40000
  //   23bd0004 afb50000 23bd0004 afb60000 23bd0004 40000000 20160002 20140003 20150001 168020 108100
  //   2149825 132020 20020022 c 1600fffa 295a022 1680fff7 40800000 23bdfffc 8fb60000 23bdfffc 8fb50000
  //   23bdfffc 8fb40000 23bdfffc 8fb30000 23bdfffc 8fb00000 23bdfffc 8fa40000 23bdfffc 8fa20000 42000018
  //   afa20000 23bd0004 afa40000 23bd0004 afb00000 23bd0004 afb30000 23bd0004 afb40000 23bd0004 afb50000
  //   23bd0004 afb60000 23bd0004 40000000 20160003 20140003 20150001 168020 108100 2149825 132020 20020022
  //   c 1600fffa 295a022 1680fff7 40800000 23bdfffc 8fb60000 23bdfffc 8fb50000 23bdfffc 8fb40000 23bdfffc
  //   8fb30000 23bdfffc 8fb00000 23bdfffc 8fa40000 23bdfffc 8fa20000 42000018
  //   OP
  //   Func
  //   rs
  //   指令字
  //   rt
  //   rd
  //   为方便自动评测，需要输出PC，IR，寄存器堆写如数据RDin
  //   RAM写使能MemWrite、RAM写入数据MDin等信号
  //   JMP
  //   JR
  //   OP
  //   Func
  //   控制位
  //   Beq
  //   Bne
  //   AluOP
  //   AluSrcB
  //   RegWrite
  //   JAL
  //   RegDst
  //   Syscall
  //   暂停节拍，不能为0
  //   MemToReg
  //   MemWrite
  //   戳工具置1进入计数暂停模式，ctrl+k时钟自动运行到对应节拍暂停
  //   ctrl+k关闭时钟连续运行，将控制位置零，进入单步调试模式调试
  //   用这个时钟源需要去掉电路中的其他时钟源
  //   可计数暂停的时钟源
  //   Reset 
  //   Reset 
  //   Reset 
  //   单级中断测试信号模拟器
endmodule

module \单周期MIPS_单级中断  (
  input  IR1,
  input  IR2,
  input  IR3,
  output RegWrite,
  output MemWrite,
  output [31:0] PC,
  output [31:0] IR,
  output [31:0] RDin,
  output [31:0] MDin,
  output [31:0] LedData
);

  wire AluSrcB, and_1_out, and_2_out, and_5_out, and_6_out, and_7_out, and_8_out, and_9_out, and_10_out, Beq,
       Bne, CLK, clock_2_out, CLR1, CLR2, CLR3, comparator_1_eq, comparator_2_eq, comparator_2_lt,
       comparator_3_eq, comparator_4_eq, comparator_5_eq, comparator_6_eq, d_ff_1_q, d_ff_2_q, d_ff_3_q,
       d_ff_4_q, equal, ERET, Go, halt, IE, INT, INT0, INT1, INT2, INT3, IR1_t, IR2_t, IR3_t, IRA, IRB, IRC,
       JAL, JMP, JR, MemToReg, nand_1_out, not_equal, or_1_out, or_2_out, or_9_out, or_10_out, or_11_out,
       or_12_out, RegDst, SignedExt, Syscall, W1, W2, W3;
  wire [1:0] priority_encoder_1_out, register_2_q;
  wire [3:0] AluOP;
  wire [4:0] multiplexer_5_out, multiplexer_6_out, multiplexer_7_out, multiplexer_9_out;
  wire [12:0] CNT_num;
  wire [15:0] \总周期数 ;
  wire [27:0] adder_1_out;
  wire [31:0] adder_2_out, bit_extender_1_out, bit_extender_2_out, EPC_ADDR, INT_ADDR, mips_alu_1_result,
       multiplexer_1_out, multiplexer_3_out, multiplexer_4_out, multiplexer_8_out, multiplexer_11_out,
       multiplexer_12_out, multiplexer_13_out, PC_q, R1, ram_1_data, RET_ADDR, shifter_1_out, shifter_2_out;

  Clock #(.highDuration(1), .lowDuration(1)) clock_1 ();  // open: out
  Button _1 ();  // open: out
  Button _2 ();  // open: out
  Button _3 ();  // open: out
  and and_1 (and_1_out, Bne, not_equal);
  or or_1 (or_1_out, and_1_out, and_2_out);
  Button \u_继续运行  (.out(Go));
  LED #(.active("true")) led_1 (.in(W1));
  LED #(.active("true")) led_2 (.in(W2));
  LED #(.active("true")) led_3 (.in(W3));
  not not_1 (not_equal, equal);
  and and_2 (and_2_out, equal, Beq);
  Multiplexer #(.select(1), .width(32), .disabled("Z"), .enable("false")) multiplexer_1 (
    .in0({shifter_1_out[31:28], adder_1_out}), .in1(adder_2_out), .out(multiplexer_1_out), .sel(or_1_out));
  Hex_Digit_Display hex_digit_display_1 (.value(LedData[31:28]));  // open: dp
  Multiplexer #(.select(2), .width(32), .disabled("Z"), .enable("false")) multiplexer_2 (
    .in0(multiplexer_1_out), .in1(R1), .in2(shifter_1_out), .in3(R1), .out(RET_ADDR), .sel({JMP, JR}));
  Hex_Digit_Display hex_digit_display_2 (.value(LedData[23:20]));  // open: dp
  Hex_Digit_Display hex_digit_display_3 (.value(LedData[27:24]));  // open: dp
  Multiplexer #(.select(1), .width(32), .disabled("Z"), .enable("false")) multiplexer_3 (
    .in0(RET_ADDR), .in1(INT_ADDR), .out(multiplexer_3_out), .sel(INT));
  Multiplexer #(.select(1), .width(32), .disabled("Z"), .enable("false")) multiplexer_4 (
    .in0(multiplexer_3_out), .in1(EPC_ADDR), .out(multiplexer_4_out), .sel(ERET));
  or or_2 (or_2_out, ~halt, Go);  // OR_Gate
  Hex_Digit_Display hex_digit_display_4 (.value(LedData[15:12]));  // open: dp
  Hex_Digit_Display hex_digit_display_5 (.value(LedData[19:16]));  // open: dp
  Register #(.width(32), .trigger("rising"), .Select("low")) u_PC (
    .D(multiplexer_4_out), .en(or_2_out), .Q(PC_q), .clk(CLK), .clr(1'b0));
  Counter #(.width(16), .max('hffff), .ongoal("wrap"), .trigger("rising"), .behavior("old")) counter_1 (
    .load(1'b0), .count(or_2_out), .Q(\总周期数 ), .clk(CLK), .clr(1'b0));  // open: D, carry, preset
  Hex_Digit_Display hex_digit_display_6 (.value(LedData[11:8]));  // open: dp
  Hex_Digit_Display hex_digit_display_7 (.value(LedData[7:4]));  // open: dp
  // Probe on \总周期数 
  Hex_Digit_Display hex_digit_display_8 (.value(LedData[3:0]));  // open: dp
  // Probe on \总周期数 
  ROM #(.addrWidth(10), .dataWidth(32), .Select("high")) rom_1 (.addr(PC_q[11:2]), .data(IR));
  assign PC = PC_q & 32'hffff;  // AND_Gate and_3, 32 bits wide
  Adder #(.width(32)) adder_1 (.a(PC_q), .b(32'h4), .out({shifter_1_out[31:28], adder_1_out}));  // open: cin, cout
  // Mips_Probe mips_probe_1: pin names not known; wires that end beside it: IR
  or or_3 (IR1_t, IR1, IRA);
  Multiplexer #(.select(1), .width(5), .disabled("Z"), .enable("false")) multiplexer_5 (
    .in0(IR[25:21]), .in1(5'b00010), .out(multiplexer_5_out), .sel(Syscall));
  Multiplexer #(.select(1), .width(5), .disabled("Z"), .enable("false")) multiplexer_6 (
    .in0(IR[20:16]), .in1(IR[15:11]), .out(multiplexer_6_out), .sel(RegDst));
  assign bit_extender_1_out = {{16{1'b0}}, IR[15:0]};  // Bit_Extender bit_extender_1
  assign bit_extender_2_out = {{16{IR[15]}}, IR[15:0]};  // Bit_Extender bit_extender_2
  Shifter #(.width(28), .shift("ll")) shifter_1 (.in(IR[27:0]), .\dist (5'b00010), .out(shifter_1_out[27:0]));
  or or_4 (IR2_t, IR2, IRB);
  Multiplexer #(.select(1), .width(5), .disabled("Z"), .enable("false")) multiplexer_7 (
    .in0(multiplexer_6_out), .in1({5{1'b1}}), .out(multiplexer_7_out), .sel(JAL));
  Multiplexer #(.select(1), .width(32), .disabled("Z"), .enable("false")) multiplexer_8 (
    .in0(bit_extender_1_out), .in1(bit_extender_2_out), .out(multiplexer_8_out), .sel(SignedExt));
  Multiplexer #(.select(1), .width(5), .disabled("Z"), .enable("false")) multiplexer_9 (
    .in0(IR[20:16]), .in1(5'b00100), .out(multiplexer_9_out), .sel(Syscall));
  Multiplexer #(.select(1), .width(32), .disabled("Z"), .enable("false")) multiplexer_10 (
    .in0(multiplexer_13_out), .in1({shifter_1_out[31:28], adder_1_out}), .out(RDin), .sel(JAL));
  or or_5 (IR3_t, IR3, IRC);
  MIPS_Regifile mips_regifile_1 (
    .Din(RDin), .Clk(CLK), .R1(R1), .R2(MDin), .WE(RegWrite), .W_num(multiplexer_7_out),
    .R1_num(multiplexer_5_out), .R2_num(multiplexer_9_out));
  Multiplexer #(.select(1), .width(32), .disabled("Z"), .enable("false")) multiplexer_11 (
    .in0(MDin), .in1(multiplexer_8_out), .out(multiplexer_11_out), .sel(AluSrcB));
  Shifter #(.width(32), .shift("ll")) shifter_2 (.in(multiplexer_8_out), .\dist (5'b00010), .out(shifter_2_out));
  Multiplexer #(.select(1), .width(32), .disabled("Z"), .enable("false")) multiplexer_12 (
    .in0(multiplexer_11_out), .in1(32'h22), .out(multiplexer_12_out), .sel(Syscall));
  Adder #(.width(32)) adder_2 (
    .a(shifter_2_out), .b({shifter_1_out[31:28], adder_1_out}), .out(adder_2_out));  // open: cin, cout
  MIPS_ALU mips_alu_1 (
    .X(R1), .Y(multiplexer_12_out), .AluOP(AluOP), .Equal(equal), .Result(mips_alu_1_result), .shamt(IR[10:6]));  // open: Result_2
  Comparator #(.width(32), .mode("twosComplement")) comparator_1 (
    .a(R1), .b(32'h32), .eq(comparator_1_eq));  // open: gt, lt
  and and_4 (halt, comparator_1_eq, Syscall);
  and and_5 (and_5_out, ~comparator_1_eq, Syscall);  // AND_Gate
  and and_6 (and_6_out, and_5_out, Syscall);
  RAM #(.addrWidth(10), .dataWidth(32), .bus("separate"), .Select("high")) ram_1 (
    .addr(mips_alu_1_result[11:2]), .din(MDin), .data(ram_1_data), .str(MemWrite), .clk(CLK), .clr(1'b0));  // open: sel, ld
  Register #(.width(32), .trigger("rising"), .Select("low")) register_1 (
    .D(MDin), .en(and_6_out), .Q(LedData), .clk(CLK), .clr(1'b0));
  Multiplexer #(.select(1), .width(32), .disabled("Z"), .enable("false")) multiplexer_13 (
    .in0(mips_alu_1_result), .in1(ram_1_data), .out(multiplexer_13_out), .sel(MemToReg));
  \单周期硬布线控制器  \u_单周期硬布线控制器_1  (
    .Func(IR[5:0]), .OP(IR[31:26]), .ALU_OP(AluOP), .MemToReg(MemToReg), .MemWrite(MemWrite),
    .ALU_SRC(AluSrcB), .RegWrite(RegWrite), .SysCALL(Syscall), .SignedExt(SignedExt), .RegDst(RegDst),
    .JR(JR), .JMP(JMP), .Beq(Beq), .JAL(JAL), .Bne(Bne), .ERET(ERET));  // open: BLTZ, LBU, LUI
  D_Flip_Flop #(.trigger("high"), .Pre_Clr_Positions("LEGACY"), .NegatePresetClear("false"), .enable("true"), .NewFFLayout("false")) d_ff_1 (.Q(d_ff_1_q));  // open: clk, D, Qn, preset, en, reset
  // Probe on 13'hc
  D_Flip_Flop #(.trigger("rising"), .Pre_Clr_Positions("LEGACY"), .NegatePresetClear("false"), .enable("true"), .NewFFLayout("false")) d_ff_2 (
    .clk(IR1_t), .D(1'b1), .Q(d_ff_2_q), .reset(INT1));  // open: Qn, preset, en
  or or_6 (W1, INT1, d_ff_2_q);
  D_Flip_Flop #(.trigger("rising"), .Pre_Clr_Positions("LEGACY"), .NegatePresetClear("false"), .enable("true"), .NewFFLayout("false")) d_ff_3 (
    .clk(IR2_t), .D(1'b1), .Q(d_ff_3_q), .reset(INT2));  // open: Qn, preset, en
  or or_7 (W2, INT2, d_ff_3_q);
  D_Flip_Flop #(.trigger("rising"), .Pre_Clr_Positions("LEGACY"), .NegatePresetClear("false"), .enable("true"), .NewFFLayout("false")) d_ff_4 (
    .clk(IR3_t), .D(1'b1), .Q(d_ff_4_q), .reset(INT3));  // open: Qn, preset, en
  or or_8 (W3, INT3, d_ff_4_q);
  Comparator #(.width(13), .mode("twosComplement")) comparator_2 (
    .a(CNT_num), .b(13'hc), .eq(comparator_2_eq), .lt(comparator_2_lt));  // open: gt
  Clock #(.highDuration(1), .lowDuration(1)) clock_2 (.out(clock_2_out));
  nand nand_1 (nand_1_out, d_ff_1_q, comparator_2_eq);
  Counter #(.width(13), .max('h1fff), .ongoal("stay"), .trigger("rising"), .behavior("old")) counter_2 (
    .count(comparator_2_lt), .Q(CNT_num), .clk(clock_2_out));  // open: load, D, carry, clr, preset
  or or_9 (or_9_out, d_ff_2_q, INT1);
  and and_7 (and_7_out, or_9_out, ~CLR1);  // AND_Gate
  or or_10 (or_10_out, d_ff_3_q, INT2);
  and and_8 (and_8_out, or_10_out, ~CLR2);  // AND_Gate
  or or_11 (or_11_out, d_ff_4_q, INT3);
  and and_9 (and_9_out, or_11_out, ~CLR3);  // AND_Gate
  assign CLK = nand_1_out ? clock_2_out : 1'bz;  // Controlled_Buffer controlled_buffer_1
  D_Flip_Flop #(.trigger("rising"), .Pre_Clr_Positions("LEGACY"), .NegatePresetClear("false"), .enable("true"), .NewFFLayout("false")) u_IR1 (
    .clk(CLK), .D(and_7_out), .Q(INT1));  // open: Qn, preset, en, reset
  D_Flip_Flop #(.trigger("rising"), .Pre_Clr_Positions("LEGACY"), .NegatePresetClear("false"), .enable("true"), .NewFFLayout("false")) u_IR2 (
    .clk(CLK), .D(and_8_out), .Q(INT2));  // open: Qn, preset, en, reset
  D_Flip_Flop #(.trigger("rising"), .Pre_Clr_Positions("LEGACY"), .NegatePresetClear("false"), .enable("true"), .NewFFLayout("false")) u_IR3 (
    .clk(CLK), .D(and_9_out), .Q(INT3));  // open: Qn, preset, en, reset
  Pull_Resistor #(.pull(1)) pull_resistor_1 (.node(CLK));
  Comparator #(.width(16), .mode("twosComplement")) comparator_3 (
    .a(16'h23b), .b(\总周期数 ), .eq(comparator_3_eq));  // open: gt, lt
  or or_12 (or_12_out, comparator_3_eq, comparator_4_eq);
  Comparator #(.width(16), .mode("twosComplement")) comparator_4 (
    .a(\总周期数 ), .b(16'h1), .eq(comparator_4_eq));  // open: gt, lt
  Comparator #(.width(16), .mode("twosComplement")) comparator_5 (
    .a(\总周期数 ), .b(16'h4), .eq(comparator_5_eq));  // open: gt, lt
  Comparator #(.width(16), .mode("twosComplement")) comparator_6 (
    .a(\总周期数 ), .b(16'h7), .eq(comparator_6_eq));  // open: gt, lt
  Pull_Resistor #(.pull(0)) pull_resistor_2 (.node(IRA));
  assign IRA = or_12_out ? ~CLK : 1'bz;  // Controlled_Inverter controlled_inverter_1
  Pull_Resistor #(.pull(0)) pull_resistor_3 (.node(IRB));
  assign IRB = comparator_5_eq ? ~CLK : 1'bz;  // Controlled_Inverter controlled_inverter_2
  Pull_Resistor #(.pull(0)) pull_resistor_4 (.node(IRC));
  assign IRC = comparator_6_eq ? ~CLK : 1'bz;  // Controlled_Inverter controlled_inverter_3
  and and_10 (and_10_out, INT0, ~ERET);  // AND_Gate
  or or_13 (INT0, INT3, INT2, INT1);
  D_Flip_Flop #(.trigger("rising"), .Pre_Clr_Positions("ABOVE_BELOW"), .NegatePresetClear("false"), .enable("false"), .NewFFLayout("true")) d_ff_5 (
    .clk(CLK), .D(and_10_out), .Q(IE));  // open: Qn, preset, reset
  Priority_Encoder #(.select(2), .disabled("Z")) priority_encoder_1 (
    .in0(INT1), .in1(INT2), .in2(INT3), .out(priority_encoder_1_out));  // open: in3, gs, en_out, en_in
  Register #(.width(32), .trigger("rising"), .Select("low")) \EPC寄存器  (
    .D(RET_ADDR), .en(INT), .Q(EPC_ADDR), .clk(CLK));  // open: clr
  Multiplexer #(.select(2), .width(32), .disabled("Z"), .enable("false")) multiplexer_14 (
    .in0(32'h30ac), .in1(32'h3150), .in2(32'h31f4), .out(INT_ADDR), .sel(priority_encoder_1_out));  // open: in3
  Register #(.width(2), .trigger("rising"), .Select("low")) register_2 (
    .D(priority_encoder_1_out), .en(INT), .Q(register_2_q), .clk(CLK));  // open: clr
  Demultiplexer #(.select(2), .width(1), .tristate("false"), .disabled("Z"), .enable("false")) demultiplexer_1 (
    .out0(CLR1), .out1(CLR2), .out2(CLR3), .in(ERET), .sel(register_2_q));  // open: out3
  and and_11 (INT, INT0, ~IE);  // AND_Gate

  // Other names for the same wires on the sheet: Func[5:0] = IR[5:0]; SHMAT[4:0] = IR[10:6]; OP[5:0] = IR[31:26];
  //   R2[31:0] = MDin

  // Notes on the sheet:
  //   中断源
  //   中断等待指示
  //   总复位信号应将除ROM以外所有存储组件全部清零
  //   数码管输出
  //   数码管输出应该用寄存器锁存，否则显示数据只能一闪而过
  //   指令存储器
  //   contents of rom_1 (hex, n*v repeats v):
  //   201d07d0 20100001 109fc0 139fc3 8021 2012000c 24160008 26100001 3210000f 20080008 20090001 139900
  //   2709825 132020 20020022 c 1094022 1500fff9 22100001 2018000f 2188024 108700 20080008 20090001 139902
  //   2709825 132021 20020022 c 1094022 1500fff9 108702 2c9b022 12c00001 8000c07 4020 1084027 84400
  //   3508ffff 82021 20020022 c 8000c01 afa20000 23bd0004 afa40000 23bd0004 afb00000 23bd0004 afb30000
  //   23bd0004 afb40000 23bd0004 afb50000 23bd0004 afb60000 23bd0004 20160001 20140003 20150001 168020
  //   108100 2149825 132020 20020022 c 1600fffa 295a022 1680fff7 23bdfffc 8fb60000 23bdfffc 8fb50000
  //   23bdfffc 8fb40000 23bdfffc 8fb30000 23bdfffc 8fb00000 23bdfffc 8fa40000 23bdfffc 8fa20000 42000018
  //   afa20000 23bd0004 afa40000 23bd0004 afb00000 23bd0004 afb30000 23bd0004 afb40000 23bd0004 afb50000
  //   23bd0004 afb60000 23bd0004 20160002 20140003 20150001 168020 108100 2149825 132020 20020022 c
  //   1600fffa 295a022 1680fff7 23bdfffc 8fb60000 23bdfffc 8fb50000 23bdfffc 8fb40000 23bdfffc 8fb30000
  //   23bdfffc 8fb00000 23bdfffc 8fa40000 23bdfffc 8fa20000 42000018 afa20000 23bd0004 afa40000 23bd0004
  //   afb00000 23bd0004 afb30000 23bd0004 afb40000 23bd0004 afb50000 23bd0004 afb60000 23bd0004 20160003
  //   20140003 20150001 168020 108100 2149825 132020 20020022 c 1600fffa 295a022 1680fff7 23bdfffc
  //   8fb60000 23bdfffc 8fb50000 23bdfffc 8fb40000 23bdfffc 8fb30000 23bdfffc 8fb00000 23bdfffc 8fa40000
  //   23bdfffc 8fa20000 42000018
  //   OP
  //   Func
  //   rs
  //   指令字
  //   rt
  //   rd
  //   为方便自动评测，需要输出PC，IR，寄存器堆写如数据RDin
  //   RAM写使能MemWrite、RAM写入数据MDin等信号
  //   JMP
  //   JR
  //   OP
  //   Func
  //   控制位
  //   Beq
  //   Bne
  //   MemToReg
  //   MemWrite
  //   AluOP
  //   AluSrcB
  //   RegWrite
  //   JAL
  //   RegDst
  //   Syscall
  //   暂停节拍，不能为0
  //   用这个时钟源需要去掉电路中的其他时钟源
  //   戳工具置1进入计数暂停模式，ctrl+k时钟自动运行到对应节拍暂停
  //   ctrl+k关闭时钟连续运行，将控制位置零，进入单步调试模式调试
  //   可计数暂停的时钟源
  //   Reset 
  //   Reset 
  //   Reset 
  //   单级中断测试信号模拟器
endmodule

module \封装正确性测试  (
);

  wire IR1, IR2, IR3, MemW, RegW;
  wire [31:0] EX_PC, ID_PC, IF_PC, IR, LED, MDin, MDinr, MEM_PC, PC, RDin, RDinr, WB_PC;

  \单周期MIPS  \u_单周期mips_1  (
    .RegWrite(RegW), .MemWrite(MemW), .PC(PC), .IR(IR), .RDin(RDin), .MDin(MDin), .LedData(LED));  // open: IR1, IR2, IR3
  \气泡流水线  \u_气泡流水线_1  (
    .RegWrite(RegW), .MemWrite(MemW), .IF_PC(IF_PC), .ID_PC(ID_PC), .EX_PC(EX_PC), .M_PC(MEM_PC),
    .WB_PC(WB_PC), .RDin(RDinr), .MDin(MDinr), .LedData(LED));
  \单周期MIPS_单级中断  \u_单周期mips_单级中断_1  (
    .IR1(IR1), .IR2(IR2), .IR3(IR3), .RegWrite(RegW), .MemWrite(MemW), .PC(PC), .IR(IR), .RDin(RDin),
    .MDin(MDin), .LedData(LED));
  \理想流水线  \u_理想流水线_1  (
    .RegWrite(RegW), .MemWrite(MemW), .IF_PC(IF_PC), .ID_PC(ID_PC), .EX_PC(EX_PC), .M_PC(MEM_PC),
    .WB_PC(WB_PC), .RDin(RDinr), .MDin(MDinr), .LedData(LED));
  \重定向流水线  \u_重定向流水线_1  (
    .RegWrite(RegW), .MemWrite(MemW), .IF_PC(IF_PC), .ID_PC(ID_PC), .EX_PC(EX_PC), .M_PC(MEM_PC),
    .WB_PC(WB_PC), .RDin(RDinr), .MDin(MDinr), .LedData(LED));
  \单周期MIPS_多级中断  \u_单周期mips_多级中断_1  (
    .IR1(IR1), .IR2(IR2), .IR3(IR3), .RegWrite(RegW), .MemWrite(MemW), .PC(PC), .IR(IR), .RDin(RDin),
    .MDin(MDin), .LedData(LED));

  // Notes on the sheet:
  //   单周期封装测试
  //   气泡流水封装测试
  //   单周期+单级中断封装测试
  //   请检查上面封装有无位宽不匹配，引脚标签是否和连接的标签相对应，否则无法在educoder平台上正确测试
  //   理想流水封装测试
  //   重定向流水封装测试
  //   单周期+多级中断封装测试
endmodule

module IF_ID (
  input  \气泡_高电平时有效 ,
  input  clk,
  input  clear,
  input  enable,
  input  [31:0] IR_in,
  input  [31:0] PC_in,
  output [31:0] IR_out,
  output [31:0] PC_out
);

  wire [31:0] multiplexer_1_out, multiplexer_2_out;

  Multiplexer #(.select(1), .width(32), .disabled("Z"), .enable("false")) multiplexer_1 (
    .in0(IR_in), .in1({32{1'b0}}), .out(multiplexer_1_out), .sel(\气泡_高电平时有效 ));
  Multiplexer #(.select(1), .width(32), .disabled("Z"), .enable("false")) multiplexer_2 (
    .in0(PC_in), .in1({32{1'b0}}), .out(multiplexer_2_out), .sel(\气泡_高电平时有效 ));
  Register #(.width(32), .trigger("rising"), .Select("low")) IR (
    .D(multiplexer_1_out), .en(enable), .Q(IR_out), .clk(clk), .clr(clear));
  Register #(.width(32), .trigger("rising"), .Select("low")) PC (
    .D(multiplexer_2_out), .en(enable), .Q(PC_out), .clk(clk), .clr(clear));
endmodule

module ID_EX (
  input  \气泡_高电平时有效 ,
  input  clk,
  input  clear,
  input  enable,
  input  Beq_in,
  input  Bne_in,
  input  MemToReg_in,
  input  MemWrite_in,
  input  [3:0] AluOP_in,
  input  AluSrc_in,
  input  RegWrite_in,
  input  JAL_in,
  input  RegDst_in,
  input  Syscall_in,
  input  JMP_in,
  input  JR_in,
  input  LUI_in,
  input  LBU_in,
  input  BLTZ_in,
  input  [31:0] IR_in,
  input  [31:0] PC_in,
  input  [31:0] R1_in,
  input  [31:0] R2_in,
  input  [31:0] Imm_in,
  output Beq_out,
  output Bne_out,
  output MemToReg_out,
  output MemWrite_out,
  output [3:0] AluOP_out,
  output AluSrc_out,
  output RegWrite_out,
  output JAL_out,
  output RegDst_out,
  output Syscall_out,
  output JMP_out,
  output JR_out,
  output LUI_out,
  output LBU_out,
  output BLTZ_out,
  output [31:0] IR_out,
  output [31:0] PC_out,
  output [31:0] R1_out,
  output [31:0] R2_out,
  output [31:0] Imm_out
);

  wire multiplexer_1_out, multiplexer_2_out, multiplexer_3_out, multiplexer_4_out, multiplexer_5_out,
       multiplexer_6_out, multiplexer_7_out, multiplexer_8_out, multiplexer_9_out, multiplexer_10_out,
       multiplexer_11_out, multiplexer_12_out, multiplexer_13_out, multiplexer_14_out;
  wire [3:0] multiplexer_15_out;
  wire [31:0] multiplexer_16_out, multiplexer_17_out, multiplexer_18_out, multiplexer_19_out,
       multiplexer_20_out;

  Multiplexer #(.select(1), .width(1), .disabled("Z"), .enable("false")) multiplexer_1 (
    .in0(Beq_in), .in1(1'b0), .out(multiplexer_1_out), .sel(\气泡_高电平时有效 ));
  Multiplexer #(.select(1), .width(1), .disabled("Z"), .enable("false")) multiplexer_2 (
    .in0(Bne_in), .in1(1'b0), .out(multiplexer_2_out), .sel(\气泡_高电平时有效 ));
  Multiplexer #(.select(1), .width(1), .disabled("Z"), .enable("false")) multiplexer_3 (
    .in0(MemToReg_in), .in1(1'b0), .out(multiplexer_3_out), .sel(\气泡_高电平时有效 ));
  Multiplexer #(.select(1), .width(1), .disabled("Z"), .enable("false")) multiplexer_4 (
    .in0(MemWrite_in), .in1(1'b0), .out(multiplexer_4_out), .sel(\气泡_高电平时有效 ));
  Multiplexer #(.select(1), .width(1), .disabled("Z"), .enable("false")) multiplexer_5 (
    .in0(AluSrc_in), .in1(1'b0), .out(multiplexer_5_out), .sel(\气泡_高电平时有效 ));
  Multiplexer #(.select(1), .width(1), .disabled("Z"), .enable("false")) multiplexer_6 (
    .in0(RegWrite_in), .in1(1'b0), .out(multiplexer_6_out), .sel(\气泡_高电平时有效 ));
  Multiplexer #(.select(1), .width(1), .disabled("Z"), .enable("false")) multiplexer_7 (
    .in0(JAL_in), .in1(1'b0), .out(multiplexer_7_out), .sel(\气泡_高电平时有效 ));
  Multiplexer #(.select(1), .width(1), .disabled("Z"), .enable("false")) multiplexer_8 (
    .in0(RegDst_in), .in1(1'b0), .out(multiplexer_8_out), .sel(\气泡_高电平时有效 ));
  Multiplexer #(.select(1), .width(1), .disabled("Z"), .enable("false")) multiplexer_9 (
    .in0(Syscall_in), .in1(1'b0), .out(multiplexer_9_out), .sel(\气泡_高电平时有效 ));
  Multiplexer #(.select(1), .width(1), .disabled("Z"), .enable("false")) multiplexer_10 (
    .in0(JMP_in), .in1(1'b0), .out(multiplexer_10_out), .sel(\气泡_高电平时有效 ));
  Multiplexer #(.select(1), .width(1), .disabled("Z"), .enable("false")) multiplexer_11 (
    .in0(JR_in), .in1(1'b0), .out(multiplexer_11_out), .sel(\气泡_高电平时有效 ));
  Multiplexer #(.select(1), .width(1), .disabled("Z"), .enable("false")) multiplexer_12 (
    .in0(LUI_in), .in1(1'b0), .out(multiplexer_12_out), .sel(\气泡_高电平时有效 ));
  Multiplexer #(.select(1), .width(1), .disabled("Z"), .enable("false")) multiplexer_13 (
    .in0(LBU_in), .in1(1'b0), .out(multiplexer_13_out), .sel(\气泡_高电平时有效 ));
  Multiplexer #(.select(1), .width(1), .disabled("Z"), .enable("false")) multiplexer_14 (
    .in0(BLTZ_in), .in1(1'b0), .out(multiplexer_14_out), .sel(\气泡_高电平时有效 ));
  Multiplexer #(.select(1), .width(4), .disabled("Z"), .enable("false")) multiplexer_15 (
    .in0(AluOP_in), .in1(4'b0000), .out(multiplexer_15_out), .sel(\气泡_高电平时有效 ));
  Multiplexer #(.select(1), .width(32), .disabled("Z"), .enable("false")) multiplexer_16 (
    .in0(IR_in), .in1({32{1'b0}}), .out(multiplexer_16_out), .sel(\气泡_高电平时有效 ));
  Multiplexer #(.select(1), .width(32), .disabled("Z"), .enable("false")) multiplexer_17 (
    .in0(PC_in), .in1({32{1'b0}}), .out(multiplexer_17_out), .sel(\气泡_高电平时有效 ));
  Multiplexer #(.select(1), .width(32), .disabled("Z"), .enable("false")) multiplexer_18 (
    .in0(R1_in), .in1({32{1'b0}}), .out(multiplexer_18_out), .sel(\气泡_高电平时有效 ));
  Multiplexer #(.select(1), .width(32), .disabled("Z"), .enable("false")) multiplexer_19 (
    .in0(R2_in), .in1({32{1'b0}}), .out(multiplexer_19_out), .sel(\气泡_高电平时有效 ));
  Multiplexer #(.select(1), .width(32), .disabled("Z"), .enable("false")) multiplexer_20 (
    .in0(Imm_in), .in1({32{1'b0}}), .out(multiplexer_20_out), .sel(\气泡_高电平时有效 ));
  Register #(.width(1), .trigger("rising"), .Select("low")) Beq (
    .D(multiplexer_1_out), .en(enable), .Q(Beq_out), .clk(clk), .clr(clear));
  Register #(.width(1), .trigger("rising"), .Select("low")) Bne (
    .D(multiplexer_2_out), .en(enable), .Q(Bne_out), .clk(clk), .clr(clear));
  Register #(.width(1), .trigger("rising"), .Select("low")) MemToReg (
    .D(multiplexer_3_out), .en(enable), .Q(MemToReg_out), .clk(clk), .clr(clear));
  Register #(.width(1), .trigger("rising"), .Select("low")) MemWrite (
    .D(multiplexer_4_out), .en(enable), .Q(MemWrite_out), .clk(clk), .clr(clear));
  Register #(.width(4), .trigger("rising"), .Select("low")) AluOP (
    .D(multiplexer_15_out), .en(enable), .Q(AluOP_out), .clk(clk), .clr(clear));
  Register #(.width(1), .trigger("rising"), .Select("low")) AluSrc (
    .D(multiplexer_5_out), .en(enable), .Q(AluSrc_out), .clk(clk), .clr(clear));
  Register #(.width(1), .trigger("rising"), .Select("low")) RegWrite (
    .D(multiplexer_6_out), .en(enable), .Q(RegWrite_out), .clk(clk), .clr(clear));
  Register #(.width(1), .trigger("rising"), .Select("low")) JAL (
    .D(multiplexer_7_out), .en(enable), .Q(JAL_out), .clk(clk), .clr(clear));
  Register #(.width(1), .trigger("rising"), .Select("low")) RegDst (
    .D(multiplexer_8_out), .en(enable), .Q(RegDst_out), .clk(clk), .clr(clear));
  Register #(.width(1), .trigger("rising"), .Select("low")) Syscall (
    .D(multiplexer_9_out), .en(enable), .Q(Syscall_out), .clk(clk), .clr(clear));
  Register #(.width(1), .trigger("rising"), .Select("low")) JMP (
    .D(multiplexer_10_out), .en(enable), .Q(JMP_out), .clk(clk), .clr(clear));
  Register #(.width(1), .trigger("rising"), .Select("low")) JR (
    .D(multiplexer_11_out), .en(enable), .Q(JR_out), .clk(clk), .clr(clear));
  Register #(.width(1), .trigger("rising"), .Select("low")) JMP_2 (
    .D(multiplexer_12_out), .en(enable), .Q(LUI_out), .clk(clk), .clr(clear));
  Register #(.width(1), .trigger("rising"), .Select("low")) JR_2 (
    .D(multiplexer_13_out), .en(enable), .Q(LBU_out), .clk(clk), .clr(clear));
  Register #(.width(1), .trigger("rising"), .Select("low")) JR_3 (
    .D(multiplexer_14_out), .en(enable), .Q(BLTZ_out), .clk(clk), .clr(clear));
  Register #(.width(32), .trigger("rising"), .Select("low")) IR (
    .D(multiplexer_16_out), .en(enable), .Q(IR_out), .clk(clk), .clr(clear));
  Register #(.width(32), .trigger("rising"), .Select("low")) PC (
    .D(multiplexer_17_out), .en(enable), .Q(PC_out), .clk(clk), .clr(clear));
  Register #(.width(32), .trigger("rising"), .Select("low")) R1 (
    .D(multiplexer_18_out), .en(enable), .Q(R1_out), .clk(clk), .clr(clear));
  Register #(.width(32), .trigger("rising"), .Select("low")) R2 (
    .D(multiplexer_19_out), .en(enable), .Q(R2_out), .clk(clk), .clr(clear));
  Register #(.width(32), .trigger("rising"), .Select("low")) Imm (
    .D(multiplexer_20_out), .en(enable), .Q(Imm_out), .clk(clk), .clr(clear));
endmodule

module EX_MEN (
  input  \气泡_高电平时有效 ,
  input  clk,
  input  clear,
  input  enable,
  input  MemToReg_in,
  input  MemWrite_in,
  input  RegWrite_in,
  input  JAL_in,
  input  RegDst_in,
  input  Syscall_in,
  input  equal_in,
  input  LUI_in,
  input  LBU_in,
  input  BLTZ_in,
  input  [31:0] IR_in,
  input  [31:0] PC_in,
  input  [31:0] ALUResult_in,
  input  [31:0] R2_in,
  input  [31:0] R1_in,
  input  [15:0] Imm_in,
  output MemToReg_out,
  output MemWrite_out,
  output RegWrite_out,
  output JAL_out,
  output RegDst_out,
  output Syscall_out,
  output equal_out,
  output LUI_out,
  output LBU_out,
  output BLTZ_out,
  output [31:0] IR_out,
  output [31:0] PC_out,
  output [31:0] ALUResult_out,
  output [31:0] R2_out,
  output [31:0] R1_out,
  output [15:0] Imm_out
);

  wire multiplexer_1_out, multiplexer_2_out, multiplexer_3_out, multiplexer_4_out, multiplexer_5_out,
       multiplexer_6_out, multiplexer_7_out, multiplexer_8_out, multiplexer_9_out, multiplexer_10_out;
  wire [15:0] multiplexer_16_out;
  wire [31:0] multiplexer_11_out, multiplexer_12_out, multiplexer_13_out, multiplexer_14_out,
       multiplexer_15_out;

  Multiplexer #(.select(1), .width(1), .disabled("Z"), .enable("false")) multiplexer_1 (
    .in0(MemToReg_in), .in1(1'b0), .out(multiplexer_1_out), .sel(\气泡_高电平时有效 ));
  Multiplexer #(.select(1), .width(1), .disabled("Z"), .enable("false")) multiplexer_2 (
    .in0(MemWrite_in), .in1(1'b0), .out(multiplexer_2_out), .sel(\气泡_高电平时有效 ));
  Multiplexer #(.select(1), .width(1), .disabled("Z"), .enable("false")) multiplexer_3 (
    .in0(RegWrite_in), .in1(1'b0), .out(multiplexer_3_out), .sel(\气泡_高电平时有效 ));
  Multiplexer #(.select(1), .width(1), .disabled("Z"), .enable("false")) multiplexer_4 (
    .in0(JAL_in), .in1(1'b0), .out(multiplexer_4_out), .sel(\气泡_高电平时有效 ));
  Multiplexer #(.select(1), .width(1), .disabled("Z"), .enable("false")) multiplexer_5 (
    .in0(RegDst_in), .in1(1'b0), .out(multiplexer_5_out), .sel(\气泡_高电平时有效 ));
  Multiplexer #(.select(1), .width(1), .disabled("Z"), .enable("false")) multiplexer_6 (
    .in0(Syscall_in), .in1(1'b0), .out(multiplexer_6_out), .sel(\气泡_高电平时有效 ));
  Multiplexer #(.select(1), .width(1), .disabled("Z"), .enable("false")) multiplexer_7 (
    .in0(equal_in), .in1(1'b0), .out(multiplexer_7_out), .sel(\气泡_高电平时有效 ));
  Multiplexer #(.select(1), .width(1), .disabled("Z"), .enable("false")) multiplexer_8 (
    .in0(LUI_in), .in1(1'b0), .out(multiplexer_8_out), .sel(\气泡_高电平时有效 ));
  Multiplexer #(.select(1), .width(1), .disabled("Z"), .enable("false")) multiplexer_9 (
    .in0(LBU_in), .in1(1'b0), .out(multiplexer_9_out), .sel(\气泡_高电平时有效 ));
  Multiplexer #(.select(1), .width(1), .disabled("Z"), .enable("false")) multiplexer_10 (
    .in0(BLTZ_in), .in1(1'b0), .out(multiplexer_10_out), .sel(\气泡_高电平时有效 ));
  Multiplexer #(.select(1), .width(32), .disabled("Z"), .enable("false")) multiplexer_11 (
    .in0(IR_in), .in1({32{1'b0}}), .out(multiplexer_11_out), .sel(\气泡_高电平时有效 ));
  Multiplexer #(.select(1), .width(32), .disabled("Z"), .enable("false")) multiplexer_12 (
    .in0(PC_in), .in1({32{1'b0}}), .out(multiplexer_12_out), .sel(\气泡_高电平时有效 ));
  Multiplexer #(.select(1), .width(32), .disabled("Z"), .enable("false")) multiplexer_13 (
    .in0(ALUResult_in), .in1({32{1'b0}}), .out(multiplexer_13_out), .sel(\气泡_高电平时有效 ));
  Multiplexer #(.select(1), .width(32), .disabled("Z"), .enable("false")) multiplexer_14 (
    .in0(R2_in), .in1({32{1'b0}}), .out(multiplexer_14_out), .sel(\气泡_高电平时有效 ));
  Multiplexer #(.select(1), .width(32), .disabled("Z"), .enable("false")) multiplexer_15 (
    .in0(R1_in), .in1({32{1'b0}}), .out(multiplexer_15_out), .sel(\气泡_高电平时有效 ));
  Multiplexer #(.select(1), .width(16), .disabled("Z"), .enable("false")) multiplexer_16 (
    .in0(Imm_in), .in1({16{1'b0}}), .out(multiplexer_16_out), .sel(\气泡_高电平时有效 ));
  Register #(.width(1), .trigger("rising"), .Select("low")) MemToReg (
    .D(multiplexer_1_out), .en(enable), .Q(MemToReg_out), .clk(clk), .clr(clear));
  Register #(.width(1), .trigger("rising"), .Select("low")) MemWrite (
    .D(multiplexer_2_out), .en(enable), .Q(MemWrite_out), .clk(clk), .clr(clear));
  Register #(.width(1), .trigger("rising"), .Select("low")) RegWrite (
    .D(multiplexer_3_out), .en(enable), .Q(RegWrite_out), .clk(clk), .clr(clear));
  Register #(.width(1), .trigger("rising"), .Select("low")) JAL (
    .D(multiplexer_4_out), .en(enable), .Q(JAL_out), .clk(clk), .clr(clear));
  Register #(.width(1), .trigger("rising"), .Select("low")) RegDst (
    .D(multiplexer_5_out), .en(enable), .Q(RegDst_out), .clk(clk), .clr(clear));
  Register #(.width(1), .trigger("rising"), .Select("low")) Syscall (
    .D(multiplexer_6_out), .en(enable), .Q(Syscall_out), .clk(clk), .clr(clear));
  Register #(.width(1), .trigger("rising"), .Select("low")) equal (
    .D(multiplexer_7_out), .en(enable), .Q(equal_out), .clk(clk), .clr(clear));
  Register #(.width(1), .trigger("rising"), .Select("low")) JMP (
    .D(multiplexer_8_out), .en(enable), .Q(LUI_out), .clk(clk), .clr(clear));
  Register #(.width(1), .trigger("rising"), .Select("low")) JR (
    .D(multiplexer_9_out), .en(enable), .Q(LBU_out), .clk(clk), .clr(clear));
  Register #(.width(1), .trigger("rising"), .Select("low")) JR_2 (
    .D(multiplexer_10_out), .en(enable), .Q(BLTZ_out), .clk(clk), .clr(clear));
  Register #(.width(32), .trigger("rising"), .Select("low")) IR (
    .D(multiplexer_11_out), .en(enable), .Q(IR_out), .clk(clk), .clr(clear));
  Register #(.width(32), .trigger("rising"), .Select("low")) PC (
    .D(multiplexer_12_out), .en(enable), .Q(PC_out), .clk(clk), .clr(clear));
  Register #(.width(32), .trigger("rising"), .Select("low")) ALUResult (
    .D(multiplexer_13_out), .en(enable), .Q(ALUResult_out), .clk(clk), .clr(clear));
  Register #(.width(32), .trigger("rising"), .Select("low")) R2 (
    .D(multiplexer_14_out), .en(enable), .Q(R2_out), .clk(clk), .clr(clear));
  Register #(.width(32), .trigger("rising"), .Select("low")) R2_2 (
    .D(multiplexer_15_out), .en(enable), .Q(R1_out), .clk(clk), .clr(clear));
  Register #(.width(16), .trigger("rising"), .Select("low")) R2_3 (
    .D(multiplexer_16_out), .en(enable), .Q(Imm_out), .clk(clk), .clr(clear));
endmodule

module MEN_WB (
  input  \气泡_高电平时有效 ,
  input  clk,
  input  clear,
  input  enable,
  input  MemToReg_in,
  input  MemWrite_in,
  input  RegWrite_in,
  input  JAL_in,
  input  RegDst_in,
  input  Syscall_in,
  input  equal_in,
  input  LBU_in,
  input  [31:0] IR_in,
  input  [31:0] PC_in,
  input  [31:0] ALUResult_in,
  input  [31:0] Memorydata_in,
  input  [31:0] Memorydata_in_2,
  output MemToReg_out,
  output MemWrite_out,
  output RegWrite_out,
  output JAL_out,
  output RegDst_out,
  output Syscall_out,
  output equal_out,
  output LBU_out,
  output [31:0] IR_out,
  output [31:0] PC_out,
  output [31:0] ALUResult_out,
  output [31:0] Memorydata_out,
  output [31:0] Memorydata_out_2
);

  wire multiplexer_1_out, multiplexer_2_out, multiplexer_3_out, multiplexer_4_out, multiplexer_5_out,
       multiplexer_6_out, multiplexer_7_out, multiplexer_8_out, undriven, undriven_2;
  wire [31:0] multiplexer_9_out, multiplexer_10_out, multiplexer_11_out, multiplexer_12_out,
       multiplexer_13_out;

  Multiplexer #(.select(1), .width(1), .disabled("Z"), .enable("false")) multiplexer_1 (
    .in0(MemToReg_in), .in1(1'b0), .out(multiplexer_1_out), .sel(\气泡_高电平时有效 ));
  Multiplexer #(.select(1), .width(1), .disabled("Z"), .enable("false")) multiplexer_2 (
    .in0(MemWrite_in), .in1(1'b0), .out(multiplexer_2_out), .sel(\气泡_高电平时有效 ));
  Multiplexer #(.select(1), .width(1), .disabled("Z"), .enable("false")) multiplexer_3 (
    .in0(RegWrite_in), .in1(1'b0), .out(multiplexer_3_out), .sel(\气泡_高电平时有效 ));
  Multiplexer #(.select(1), .width(1), .disabled("Z"), .enable("false")) multiplexer_4 (
    .in0(JAL_in), .in1(1'b0), .out(multiplexer_4_out), .sel(\气泡_高电平时有效 ));
  Multiplexer #(.select(1), .width(1), .disabled("Z"), .enable("false")) multiplexer_5 (
    .in0(RegDst_in), .in1(1'b0), .out(multiplexer_5_out), .sel(\气泡_高电平时有效 ));
  Multiplexer #(.select(1), .width(1), .disabled("Z"), .enable("false")) multiplexer_6 (
    .in0(Syscall_in), .in1(1'b0), .out(multiplexer_6_out), .sel(\气泡_高电平时有效 ));
  Multiplexer #(.select(1), .width(1), .disabled("Z"), .enable("false")) multiplexer_7 (
    .in0(equal_in), .in1(1'b0), .out(multiplexer_7_out), .sel(\气泡_高电平时有效 ));
  Multiplexer #(.select(1), .width(1), .disabled("Z"), .enable("false")) multiplexer_8 (
    .in0(LBU_in), .in1(1'b0), .out(multiplexer_8_out), .sel(\气泡_高电平时有效 ));
  Multiplexer #(.select(1), .width(32), .disabled("Z"), .enable("false")) multiplexer_9 (
    .in0(IR_in), .in1({32{1'b0}}), .out(multiplexer_9_out), .sel(\气泡_高电平时有效 ));
  Multiplexer #(.select(1), .width(32), .disabled("Z"), .enable("false")) multiplexer_10 (
    .in0(PC_in), .in1({32{1'b0}}), .out(multiplexer_10_out), .sel(\气泡_高电平时有效 ));
  Multiplexer #(.select(1), .width(32), .disabled("Z"), .enable("false")) multiplexer_11 (
    .in0(ALUResult_in), .in1({32{1'b0}}), .out(multiplexer_11_out), .sel(\气泡_高电平时有效 ));
  Multiplexer #(.select(1), .width(32), .disabled("Z"), .enable("false")) multiplexer_12 (
    .in0(Memorydata_in), .in1({32{1'b0}}), .out(multiplexer_12_out), .sel(\气泡_高电平时有效 ));
  Multiplexer #(.select(1), .width(32), .disabled("Z"), .enable("false")) multiplexer_13 (
    .in0(Memorydata_in_2), .in1({32{1'b0}}), .out(multiplexer_13_out), .sel(\气泡_高电平时有效 ));
  Register #(.width(1), .trigger("rising"), .Select("low")) MemToReg (
    .D(multiplexer_1_out), .en(enable), .Q(MemToReg_out), .clk(clk), .clr(clear));
  Register #(.width(1), .trigger("rising"), .Select("low")) MemWrite (
    .D(multiplexer_2_out), .en(enable), .Q(MemWrite_out), .clk(clk), .clr(clear));
  Register #(.width(1), .trigger("rising"), .Select("low")) RegWrite (
    .D(multiplexer_3_out), .en(enable), .Q(RegWrite_out), .clk(clk), .clr(clear));
  Register #(.width(1), .trigger("rising"), .Select("low")) JAL (
    .D(multiplexer_4_out), .en(enable), .Q(JAL_out), .clk(clk), .clr(clear));
  Register #(.width(1), .trigger("rising"), .Select("low")) RegDst (
    .D(multiplexer_5_out), .en(enable), .Q(RegDst_out), .clk(clk), .clr(clear));
  Register #(.width(1), .trigger("rising"), .Select("low")) Syscall (
    .D(multiplexer_6_out), .en(enable), .Q(Syscall_out), .clk(clk), .clr(clear));
  Register #(.width(1), .trigger("rising"), .Select("low")) equal (
    .D(multiplexer_7_out), .en(enable), .Q(equal_out), .clk(clk), .clr(clear));
  Register #(.width(1), .trigger("rising"), .Select("low")) equal_2 (
    .D(multiplexer_8_out), .en(enable), .Q(LBU_out), .clk(clk), .clr(clear));
  Register #(.width(32), .trigger("rising"), .Select("low")) IR (
    .D(multiplexer_9_out), .en(enable), .Q(IR_out), .clk(clk), .clr(clear));
  Register #(.width(32), .trigger("rising"), .Select("low")) PC (
    .D(multiplexer_10_out), .en(enable), .Q(PC_out), .clk(clk), .clr(clear));
  Register #(.width(32), .trigger("rising"), .Select("low")) ALUResult (
    .D(multiplexer_11_out), .en(enable), .Q(ALUResult_out), .clk(clk), .clr(clear));
  Register #(.width(32), .trigger("rising"), .Select("low")) Memorydata (
    .D(multiplexer_12_out), .en(enable), .Q(Memorydata_out), .clk(clk), .clr(clear));
  Register #(.width(32), .trigger("rising"), .Select("low")) Memorydata_2 (
    .D(multiplexer_13_out), .en(undriven), .Q(Memorydata_out_2), .clk(clk), .clr(undriven_2));
endmodule

module \源寄存器检测  (
  input  OP0,
  input  OP1,
  input  OP2,
  input  OP3,
  input  OP4,
  input  OP5,
  input  F0,
  input  F1,
  input  F2,
  input  F3,
  input  F4,
  input  F5,
  output R1_Used,
  output R2_Used
);

  wire and_1_out, and_2_out, and_3_out, and_4_out, and_5_out, and_6_out, and_7_out, and_8_out, and_9_out,
       and_10_out, and_11_out, and_12_out, and_13_out, and_14_out, and_15_out, and_16_out, and_17_out,
       and_18_out, and_19_out, and_20_out, and_21_out, and_22_out, and_23_out, and_24_out, and_25_out,
       and_26_out, and_27_out, and_28_out, and_29_out, and_30_out, and_31_out, and_32_out, and_33_out,
       and_34_out, and_35_out, and_36_out, and_37_out, and_38_out, and_39_out, and_40_out, not_1_out,
       not_2_out, not_3_out, not_4_out, not_5_out, not_6_out, not_7_out, not_8_out, not_9_out, not_10_out,
       not_11_out, not_12_out, not_13_out, not_14_out, not_15_out, not_16_out, not_17_out, not_18_out,
       not_19_out, not_20_out, not_21_out, not_22_out, not_23_out, not_24_out, not_25_out, not_26_out,
       not_27_out, not_28_out, not_29_out, not_30_out, not_31_out, not_32_out, not_33_out, not_34_out,
       not_35_out, not_36_out, not_37_out, not_38_out, not_39_out, not_40_out, not_41_out, not_42_out,
       not_43_out, not_44_out, not_45_out, not_46_out, not_47_out, not_48_out, not_49_out, not_50_out,
       not_51_out, not_52_out, not_53_out, not_54_out, not_55_out, not_56_out, not_57_out, not_58_out,
       not_59_out, not_60_out, not_61_out, not_62_out, not_63_out, not_64_out, not_65_out, not_66_out,
       not_67_out, not_68_out, not_69_out, not_70_out, not_71_out, not_72_out, not_73_out, not_74_out,
       not_75_out, not_76_out, not_77_out, not_78_out, not_79_out, not_80_out, not_81_out, not_82_out,
       not_83_out, not_84_out, not_85_out, not_86_out, not_87_out, not_88_out, not_89_out, not_90_out,
       not_91_out, not_92_out, not_93_out, not_94_out, not_95_out, not_96_out, not_97_out, not_98_out,
       not_99_out, not_100_out, not_101_out, not_102_out, not_103_out, not_104_out, not_105_out, not_106_out,
       not_107_out, not_108_out, not_109_out, not_110_out, not_111_out, not_112_out, not_113_out,
       not_114_out, not_115_out, not_116_out, not_117_out, not_118_out, not_119_out, not_120_out,
       not_121_out, not_122_out, not_123_out, not_124_out, not_125_out, not_126_out, not_127_out,
       not_128_out, not_129_out, not_130_out, not_131_out, not_132_out, not_133_out, not_134_out,
       not_135_out, not_136_out, not_137_out, not_138_out, not_139_out, not_140_out, not_141_out,
       not_142_out, not_143_out, not_144_out, not_145_out, not_146_out, not_147_out, not_148_out,
       not_149_out, not_150_out, not_151_out, not_152_out, not_153_out, not_154_out, not_155_out,
       not_156_out, not_157_out, not_158_out, not_159_out, not_160_out, not_161_out, not_162_out,
       not_163_out, not_164_out, not_165_out, not_166_out, not_167_out, not_168_out, not_169_out,
       not_170_out, not_171_out, not_172_out, not_173_out, not_174_out, not_175_out, not_176_out,
       not_177_out, not_178_out, not_179_out, not_180_out, not_181_out, not_182_out, not_183_out,
       not_184_out, not_185_out, not_186_out, not_187_out, not_188_out, not_189_out, not_190_out,
       not_191_out, not_192_out, not_193_out, not_194_out, not_195_out, not_196_out, not_197_out,
       not_198_out, not_199_out, not_200_out, not_201_out, not_202_out, not_203_out, not_204_out,
       not_205_out, not_206_out, not_207_out, not_208_out, not_209_out, not_210_out, not_211_out,
       not_212_out, not_213_out, not_214_out, not_215_out, not_216_out, not_217_out, not_218_out,
       not_219_out, not_220_out, not_221_out, not_222_out, not_223_out, not_224_out, not_225_out,
       not_226_out, not_227_out, not_228_out, not_229_out, not_230_out, not_231_out, not_232_out,
       not_233_out, not_234_out, not_235_out, not_236_out, not_237_out, not_238_out, not_239_out,
       not_240_out, not_241_out, not_242_out, not_243_out, not_244_out, not_245_out, not_246_out,
       not_247_out, not_248_out, not_249_out, not_250_out, not_251_out, not_252_out, not_253_out,
       not_254_out, not_255_out, not_256_out, not_257_out, not_258_out, not_259_out, not_260_out,
       not_261_out, not_262_out, not_263_out, not_264_out, not_265_out, not_266_out, not_267_out,
       not_268_out, not_269_out, not_270_out, not_271_out, not_272_out, not_273_out, not_274_out,
       not_275_out, not_276_out, not_277_out, not_278_out, not_279_out, not_280_out, not_281_out,
       not_282_out, not_283_out, not_284_out, not_285_out, not_286_out, not_287_out, not_288_out,
       not_289_out, not_290_out;

  not not_1 (not_1_out, OP5);
  not not_2 (not_2_out, OP4);
  not not_3 (not_3_out, OP3);
  not not_4 (not_4_out, OP2);
  not not_5 (not_5_out, OP1);
  not not_6 (not_6_out, OP0);
  not not_7 (not_7_out, F4);
  not not_8 (not_8_out, F3);
  not not_9 (not_9_out, F2);
  not not_10 (not_10_out, F1);
  not not_11 (not_11_out, F0);
  not not_12 (not_12_out, OP5);
  not not_13 (not_13_out, OP4);
  not not_14 (not_14_out, OP3);
  not not_15 (not_15_out, OP2);
  not not_16 (not_16_out, OP1);
  not not_17 (not_17_out, OP0);
  not not_18 (not_18_out, F4);
  not not_19 (not_19_out, F3);
  not not_20 (not_20_out, F2);
  not not_21 (not_21_out, F1);
  not not_22 (not_22_out, OP5);
  not not_23 (not_23_out, OP4);
  not not_24 (not_24_out, OP3);
  not not_25 (not_25_out, OP2);
  not not_26 (not_26_out, OP1);
  not not_27 (not_27_out, OP0);
  not not_28 (not_28_out, F4);
  not not_29 (not_29_out, F3);
  not not_30 (not_30_out, F2);
  not not_31 (not_31_out, F0);
  not not_32 (not_32_out, OP5);
  not not_33 (not_33_out, OP4);
  not not_34 (not_34_out, OP3);
  not not_35 (not_35_out, OP2);
  not not_36 (not_36_out, OP1);
  not not_37 (not_37_out, OP0);
  not not_38 (not_38_out, F4);
  not not_39 (not_39_out, F3);
  not not_40 (not_40_out, F1);
  not not_41 (not_41_out, F0);
  not not_42 (not_42_out, OP5);
  not not_43 (not_43_out, OP4);
  not not_44 (not_44_out, OP3);
  not not_45 (not_45_out, OP2);
  not not_46 (not_46_out, OP1);
  not not_47 (not_47_out, OP0);
  not not_48 (not_48_out, F4);
  not not_49 (not_49_out, F3);
  not not_50 (not_50_out, F1);
  not not_51 (not_51_out, OP5);
  not not_52 (not_52_out, OP4);
  not not_53 (not_53_out, OP3);
  not not_54 (not_54_out, OP2);
  not not_55 (not_55_out, OP1);
  not not_56 (not_56_out, OP0);
  not not_57 (not_57_out, F4);
  not not_58 (not_58_out, F3);
  not not_59 (not_59_out, OP5);
  not not_60 (not_60_out, OP4);
  not not_61 (not_61_out, OP3);
  not not_62 (not_62_out, OP2);
  not not_63 (not_63_out, OP1);
  not not_64 (not_64_out, OP0);
  not not_65 (not_65_out, F4);
  not not_66 (not_66_out, F2);
  not not_67 (not_67_out, F0);
  not not_68 (not_68_out, OP5);
  not not_69 (not_69_out, OP4);
  not not_70 (not_70_out, OP3);
  not not_71 (not_71_out, OP2);
  not not_72 (not_72_out, OP1);
  not not_73 (not_73_out, OP0);
  not not_74 (not_74_out, F4);
  not not_75 (not_75_out, F2);
  not not_76 (not_76_out, OP5);
  not not_77 (not_77_out, OP4);
  not not_78 (not_78_out, OP3);
  not not_79 (not_79_out, OP2);
  not not_80 (not_80_out, OP1);
  not not_81 (not_81_out, OP0);
  not not_82 (not_82_out, F5);
  not not_83 (not_83_out, F4);
  not not_84 (not_84_out, F2);
  not not_85 (not_85_out, F1);
  not not_86 (not_86_out, F0);
  not not_87 (not_87_out, OP5);
  not not_88 (not_88_out, OP4);
  not not_89 (not_89_out, OP3);
  not not_90 (not_90_out, OP2);
  not not_91 (not_91_out, OP1);
  not not_92 (not_92_out, OP0);
  not not_93 (not_93_out, F5);
  not not_94 (not_94_out, F4);
  not not_95 (not_95_out, F1);
  not not_96 (not_96_out, F0);
  not not_97 (not_97_out, OP5);
  not not_98 (not_98_out, OP4);
  not not_99 (not_99_out, OP3);
  not not_100 (not_100_out, OP1);
  not not_101 (not_101_out, OP0);
  not not_102 (not_102_out, OP5);
  not not_103 (not_103_out, OP4);
  not not_104 (not_104_out, OP3);
  not not_105 (not_105_out, OP1);
  not not_106 (not_106_out, OP5);
  not not_107 (not_107_out, OP4);
  not not_108 (not_108_out, OP2);
  not not_109 (not_109_out, OP1);
  not not_110 (not_110_out, OP0);
  not not_111 (not_111_out, OP5);
  not not_112 (not_112_out, OP4);
  not not_113 (not_113_out, OP1);
  not not_114 (not_114_out, OP0);
  not not_115 (not_115_out, OP5);
  not not_116 (not_116_out, OP4);
  not not_117 (not_117_out, OP2);
  not not_118 (not_118_out, OP1);
  not not_119 (not_119_out, OP5);
  not not_120 (not_120_out, OP4);
  not not_121 (not_121_out, OP2);
  not not_122 (not_122_out, OP0);
  not not_123 (not_123_out, OP5);
  not not_124 (not_124_out, OP4);
  not not_125 (not_125_out, OP1);
  not not_126 (not_126_out, OP4);
  not not_127 (not_127_out, OP3);
  not not_128 (not_128_out, OP2);
  not not_129 (not_129_out, OP4);
  not not_130 (not_130_out, OP2);
  not not_131 (not_131_out, OP5);
  not not_132 (not_132_out, OP4);
  not not_133 (not_133_out, OP3);
  not not_134 (not_134_out, OP2);
  not not_135 (not_135_out, OP1);
  not not_136 (not_136_out, OP0);
  not not_137 (not_137_out, F4);
  not not_138 (not_138_out, F3);
  not not_139 (not_139_out, F0);
  not not_140 (not_140_out, OP5);
  not not_141 (not_141_out, OP4);
  not not_142 (not_142_out, OP4);
  not not_143 (not_143_out, OP3);
  not not_144 (not_144_out, OP1);
  not not_145 (not_145_out, OP0);
  not not_146 (not_146_out, OP5);
  not not_147 (not_147_out, OP4);
  not not_148 (not_148_out, OP3);
  not not_149 (not_149_out, OP2);
  not not_150 (not_150_out, OP1);
  not not_151 (not_151_out, OP5);
  not not_152 (not_152_out, OP4);
  not not_153 (not_153_out, OP3);
  not not_154 (not_154_out, OP2);
  not not_155 (not_155_out, OP1);
  not not_156 (not_156_out, OP0);
  not not_157 (not_157_out, F5);
  not not_158 (not_158_out, F4);
  not not_159 (not_159_out, F3);
  not not_160 (not_160_out, F2);
  not not_161 (not_161_out, F1);
  not not_162 (not_162_out, F0);
  not not_163 (not_163_out, OP5);
  not not_164 (not_164_out, OP4);
  not not_165 (not_165_out, OP3);
  not not_166 (not_166_out, OP2);
  not not_167 (not_167_out, OP1);
  not not_168 (not_168_out, OP0);
  not not_169 (not_169_out, F5);
  not not_170 (not_170_out, F4);
  not not_171 (not_171_out, F3);
  not not_172 (not_172_out, F2);
  not not_173 (not_173_out, OP5);
  not not_174 (not_174_out, OP4);
  not not_175 (not_175_out, OP3);
  not not_176 (not_176_out, OP2);
  not not_177 (not_177_out, OP1);
  not not_178 (not_178_out, OP0);
  not not_179 (not_179_out, F5);
  not not_180 (not_180_out, F4);
  not not_181 (not_181_out, F3);
  not not_182 (not_182_out, F2);
  not not_183 (not_183_out, F0);
  not not_184 (not_184_out, OP5);
  not not_185 (not_185_out, OP4);
  not not_186 (not_186_out, OP3);
  not not_187 (not_187_out, OP2);
  not not_188 (not_188_out, OP1);
  not not_189 (not_189_out, OP0);
  not not_190 (not_190_out, F4);
  not not_191 (not_191_out, F3);
  not not_192 (not_192_out, F2);
  not not_193 (not_193_out, F1);
  not not_194 (not_194_out, F0);
  not not_195 (not_195_out, OP5);
  not not_196 (not_196_out, OP4);
  not not_197 (not_197_out, OP3);
  not not_198 (not_198_out, OP2);
  not not_199 (not_199_out, OP1);
  not not_200 (not_200_out, OP0);
  not not_201 (not_201_out, F4);
  not not_202 (not_202_out, F3);
  not not_203 (not_203_out, F2);
  not not_204 (not_204_out, F1);
  not not_205 (not_205_out, OP5);
  not not_206 (not_206_out, OP4);
  not not_207 (not_207_out, OP3);
  not not_208 (not_208_out, OP2);
  not not_209 (not_209_out, OP1);
  not not_210 (not_210_out, OP0);
  not not_211 (not_211_out, F4);
  not not_212 (not_212_out, F3);
  not not_213 (not_213_out, F2);
  not not_214 (not_214_out, F0);
  not not_215 (not_215_out, OP5);
  not not_216 (not_216_out, OP4);
  not not_217 (not_217_out, OP3);
  not not_218 (not_218_out, OP2);
  not not_219 (not_219_out, OP1);
  not not_220 (not_220_out, OP0);
  not not_221 (not_221_out, F4);
  not not_222 (not_222_out, F3);
  not not_223 (not_223_out, F1);
  not not_224 (not_224_out, F0);
  not not_225 (not_225_out, OP5);
  not not_226 (not_226_out, OP4);
  not not_227 (not_227_out, OP3);
  not not_228 (not_228_out, OP2);
  not not_229 (not_229_out, OP1);
  not not_230 (not_230_out, OP0);
  not not_231 (not_231_out, F4);
  not not_232 (not_232_out, F3);
  not not_233 (not_233_out, F1);
  not not_234 (not_234_out, OP5);
  not not_235 (not_235_out, OP4);
  not not_236 (not_236_out, OP3);
  not not_237 (not_237_out, OP2);
  not not_238 (not_238_out, OP1);
  not not_239 (not_239_out, OP0);
  not not_240 (not_240_out, F4);
  not not_241 (not_241_out, F3);
  not not_242 (not_242_out, OP5);
  not not_243 (not_243_out, OP4);
  not not_244 (not_244_out, OP3);
  not not_245 (not_245_out, OP2);
  not not_246 (not_246_out, OP1);
  not not_247 (not_247_out, OP0);
  not not_248 (not_248_out, F4);
  not not_249 (not_249_out, F2);
  not not_250 (not_250_out, F0);
  not not_251 (not_251_out, OP5);
  not not_252 (not_252_out, OP4);
  not not_253 (not_253_out, OP3);
  not not_254 (not_254_out, OP2);
  not not_255 (not_255_out, OP1);
  not not_256 (not_256_out, OP0);
  not not_257 (not_257_out, F4);
  not not_258 (not_258_out, F2);
  not not_259 (not_259_out, OP5);
  not not_260 (not_260_out, OP4);
  not not_261 (not_261_out, OP3);
  not not_262 (not_262_out, OP2);
  not not_263 (not_263_out, OP1);
  not not_264 (not_264_out, OP0);
  not not_265 (not_265_out, F5);
  not not_266 (not_266_out, F4);
  not not_267 (not_267_out, F1);
  not not_268 (not_268_out, F0);
  not not_269 (not_269_out, OP5);
  not not_270 (not_270_out, OP4);
  not not_271 (not_271_out, OP3);
  not not_272 (not_272_out, OP1);
  not not_273 (not_273_out, OP0);
  not not_274 (not_274_out, OP5);
  not not_275 (not_275_out, OP4);
  not not_276 (not_276_out, OP3);
  not not_277 (not_277_out, OP1);
  not not_278 (not_278_out, OP4);
  not not_279 (not_279_out, OP2);
  not not_280 (not_280_out, OP5);
  not not_281 (not_281_out, OP4);
  not not_282 (not_282_out, OP3);
  not not_283 (not_283_out, OP2);
  not not_284 (not_284_out, OP1);
  not not_285 (not_285_out, OP0);
  not not_286 (not_286_out, F4);
  not not_287 (not_287_out, F3);
  not not_288 (not_288_out, F0);
  not not_289 (not_289_out, OP5);
  not not_290 (not_290_out, OP4);
  and and_1 (and_1_out, not_1_out, not_2_out, not_3_out, not_4_out, not_5_out, not_6_out, F5, not_7_out, not_8_out, not_9_out, not_10_out, not_11_out);
  and and_2 (and_2_out, not_12_out, not_13_out, not_14_out, not_15_out, not_16_out, not_17_out, F5, not_18_out, not_19_out, not_20_out, not_21_out, F0);
  and and_3 (and_3_out, not_22_out, not_23_out, not_24_out, not_25_out, not_26_out, not_27_out, F5, not_28_out, not_29_out, not_30_out, F1, not_31_out);
  and and_4 (and_4_out, not_32_out, not_33_out, not_34_out, not_35_out, not_36_out, not_37_out, F5, not_38_out, not_39_out, F2, not_40_out, not_41_out);
  and and_5 (and_5_out, not_42_out, not_43_out, not_44_out, not_45_out, not_46_out, not_47_out, F5, not_48_out, not_49_out, F2, not_50_out, F0);
  and and_6 (and_6_out, not_51_out, not_52_out, not_53_out, not_54_out, not_55_out, not_56_out, F5, not_57_out, not_58_out, F2, F1, F0);
  and and_7 (and_7_out, not_59_out, not_60_out, not_61_out, not_62_out, not_63_out, not_64_out, F5, not_65_out, F3, not_66_out, F1, not_67_out);
  and and_8 (and_8_out, not_68_out, not_69_out, not_70_out, not_71_out, not_72_out, not_73_out, F5, not_74_out, F3, not_75_out, F1, F0);
  and and_9 (and_9_out, not_76_out, not_77_out, not_78_out, not_79_out, not_80_out, not_81_out, not_82_out, not_83_out, F3, not_84_out, not_85_out, not_86_out);
  and and_10 (and_10_out, not_87_out, not_88_out, not_89_out, not_90_out, not_91_out, not_92_out, not_93_out, not_94_out, F3, F2, not_95_out, not_96_out);
  and and_11 (and_11_out, not_97_out, not_98_out, not_99_out, OP2, not_100_out, not_101_out);
  and and_12 (and_12_out, not_102_out, not_103_out, not_104_out, OP2, not_105_out, OP0);
  and and_13 (and_13_out, not_106_out, not_107_out, OP3, not_108_out, not_109_out, not_110_out);
  and and_14 (and_14_out, not_111_out, not_112_out, OP3, OP2, not_113_out, not_114_out);
  and and_15 (and_15_out, not_115_out, not_116_out, OP3, not_117_out, not_118_out, OP0);
  and and_16 (and_16_out, not_119_out, not_120_out, OP3, not_121_out, OP1, not_122_out);
  and and_17 (and_17_out, not_123_out, not_124_out, OP3, OP2, not_125_out, OP0);
  and and_18 (and_18_out, OP5, not_126_out, not_127_out, not_128_out, OP1, OP0);
  and and_19 (and_19_out, OP5, not_129_out, OP3, not_130_out, OP1, OP0);
  and and_20 (and_20_out, not_131_out, not_132_out, not_133_out, not_134_out, not_135_out, not_136_out, F5, not_137_out, not_138_out, F2, F1, not_139_out);
  and and_21 (and_21_out, not_140_out, not_141_out, OP3, OP2, OP1, OP0);
  and and_22 (and_22_out, OP5, not_142_out, not_143_out, OP2, not_144_out, not_145_out);
  and and_23 (and_23_out, not_146_out, not_147_out, not_148_out, not_149_out, not_150_out, OP0);
  and and_24 (and_24_out, not_151_out, not_152_out, not_153_out, not_154_out, not_155_out, not_156_out, not_157_out, not_158_out, not_159_out, not_160_out, not_161_out, not_162_out);
  and and_25 (and_25_out, not_163_out, not_164_out, not_165_out, not_166_out, not_167_out, not_168_out, not_169_out, not_170_out, not_171_out, not_172_out, F1, F0);
  and and_26 (and_26_out, not_173_out, not_174_out, not_175_out, not_176_out, not_177_out, not_178_out, not_179_out, not_180_out, not_181_out, not_182_out, F1, not_183_out);
  and and_27 (and_27_out, not_184_out, not_185_out, not_186_out, not_187_out, not_188_out, not_189_out, F5, not_190_out, not_191_out, not_192_out, not_193_out, not_194_out);
  and and_28 (and_28_out, not_195_out, not_196_out, not_197_out, not_198_out, not_199_out, not_200_out, F5, not_201_out, not_202_out, not_203_out, not_204_out, F0);
  and and_29 (and_29_out, not_205_out, not_206_out, not_207_out, not_208_out, not_209_out, not_210_out, F5, not_211_out, not_212_out, not_213_out, F1, not_214_out);
  and and_30 (and_30_out, not_215_out, not_216_out, not_217_out, not_218_out, not_219_out, not_220_out, F5, not_221_out, not_222_out, F2, not_223_out, not_224_out);
  and and_31 (and_31_out, not_225_out, not_226_out, not_227_out, not_228_out, not_229_out, not_230_out, F5, not_231_out, not_232_out, F2, not_233_out, F0);
  and and_32 (and_32_out, not_234_out, not_235_out, not_236_out, not_237_out, not_238_out, not_239_out, F5, not_240_out, not_241_out, F2, F1, F0);
  and and_33 (and_33_out, not_242_out, not_243_out, not_244_out, not_245_out, not_246_out, not_247_out, F5, not_248_out, F3, not_249_out, F1, not_250_out);
  and and_34 (and_34_out, not_251_out, not_252_out, not_253_out, not_254_out, not_255_out, not_256_out, F5, not_257_out, F3, not_258_out, F1, F0);
  and and_35 (and_35_out, not_259_out, not_260_out, not_261_out, not_262_out, not_263_out, not_264_out, not_265_out, not_266_out, F3, F2, not_267_out, not_268_out);
  and and_36 (and_36_out, not_269_out, not_270_out, not_271_out, OP2, not_272_out, not_273_out);
  and and_37 (and_37_out, not_274_out, not_275_out, not_276_out, OP2, not_277_out, OP0);
  and and_38 (and_38_out, OP5, not_278_out, OP3, not_279_out, OP1, OP0);
  and and_39 (and_39_out, not_280_out, not_281_out, not_282_out, not_283_out, not_284_out, not_285_out, F5, not_286_out, not_287_out, F2, F1, not_288_out);
  and and_40 (and_40_out, not_289_out, not_290_out, OP3, OP2, OP1, OP0);
  or or_1 (R1_Used, and_1_out, and_2_out, and_3_out, and_4_out, and_5_out, and_6_out, and_7_out, and_8_out, and_9_out, and_10_out, and_11_out, and_12_out, and_13_out, and_14_out, and_15_out, and_16_out, and_17_out, and_18_out, and_19_out, and_20_out, and_21_out, and_22_out, and_23_out);
  or or_2 (R2_Used, and_24_out, and_25_out, and_26_out, and_27_out, and_28_out, and_29_out, and_30_out, and_31_out, and_32_out, and_33_out, and_34_out, and_35_out, and_36_out, and_37_out, and_38_out, and_39_out, and_40_out);
endmodule

module \数据相关性检测  (
  input  [5:0] OP,
  input  [5:0] FUNCT,
  input  [4:0] rs,
  input  [4:0] EX_WriteReg_num,
  input  EX_RegWrite,
  input  [4:0] rt,
  input  MEM_RegWrite,
  input  [4:0] MEM_WriteReg_num,
  output DataHazzard
);

  wire and_1_out, and_2_out, and_3_out, and_4_out, comparator_1_eq, comparator_2_eq, comparator_3_eq,
       comparator_4_eq, comparator_5_eq, comparator_6_eq, not_1_out, not_2_out, RsUsed, RtUsed;

  Comparator #(.width(5), .mode("twosComplement")) comparator_1 (
    .a(rs), .b({5{1'b0}}), .eq(comparator_1_eq));  // open: gt, lt
  Comparator #(.width(5), .mode("twosComplement")) comparator_2 (
    .a(rs), .b(EX_WriteReg_num), .eq(comparator_2_eq));  // open: gt, lt
  Comparator #(.width(5), .mode("twosComplement")) comparator_3 (
    .a(rt), .b({5{1'b0}}), .eq(comparator_3_eq));  // open: gt, lt
  Comparator #(.width(5), .mode("twosComplement")) comparator_4 (
    .a(rt), .b(EX_WriteReg_num), .eq(comparator_4_eq));  // open: gt, lt
  Comparator #(.width(5), .mode("twosComplement")) comparator_5 (
    .a(rs), .b(MEM_WriteReg_num), .eq(comparator_5_eq));  // open: gt, lt
  Comparator #(.width(5), .mode("twosComplement")) comparator_6 (
    .a(rt), .b(MEM_WriteReg_num), .eq(comparator_6_eq));  // open: gt, lt
  \源寄存器检测  \u_源寄存器检测_1  (
    .OP0(OP[0]), .OP1(OP[1]), .OP2(OP[2]), .OP3(OP[3]), .OP4(OP[4]), .OP5(OP[5]), .F0(FUNCT[0]),
    .F1(FUNCT[1]), .F2(FUNCT[2]), .F3(FUNCT[3]), .F4(FUNCT[4]), .F5(FUNCT[5]), .R1_Used(RsUsed),
    .R2_Used(RtUsed));
  not not_1 (not_1_out, comparator_1_eq);
  not not_2 (not_2_out, comparator_3_eq);
  and and_1 (and_1_out, RsUsed, not_1_out, comparator_2_eq, EX_RegWrite);
  and and_2 (and_2_out, EX_RegWrite, RtUsed, not_2_out, comparator_4_eq);
  and and_3 (and_3_out, RsUsed, not_1_out, MEM_RegWrite, comparator_5_eq);
  and and_4 (and_4_out, RtUsed, not_2_out, MEM_RegWrite, comparator_6_eq);
  or or_1 (DataHazzard, and_1_out, and_2_out, and_3_out, and_4_out);
endmodule

module \LoadUse检测  (
  input  [5:0] OP,
  input  [5:0] FUNCT,
  input  [4:0] MEM_WriteReg_num,
  input  MEM_RegWrite,
  input  EX_RegWrite,
  input  [4:0] rs,
  input  [4:0] EX_WriteReg_num,
  input  EX_MemToReg,
  input  [4:0] rt,
  output [1:0] RsFoward,
  output LoadUse,
  output [1:0] RtFoward
);

  wire and_3_out, and_4_out, comparator_1_eq, comparator_2_eq, comparator_3_eq, comparator_4_eq,
       comparator_5_eq, comparator_6_eq, not_1_out, not_2_out, RsUsed, RtUsed;
  wire [1:0] and_2_out, and_6_out;

  Comparator #(.width(5), .mode("twosComplement")) comparator_1 (
    .a(MEM_WriteReg_num), .b(rs), .eq(comparator_1_eq));  // open: gt, lt
  Comparator #(.width(5), .mode("twosComplement")) comparator_2 (
    .a(rs), .b({5{1'b0}}), .eq(comparator_2_eq));  // open: gt, lt
  Comparator #(.width(5), .mode("twosComplement")) comparator_3 (
    .a(rs), .b(EX_WriteReg_num), .eq(comparator_3_eq));  // open: gt, lt
  Comparator #(.width(5), .mode("twosComplement")) comparator_4 (
    .a(rt), .b({5{1'b0}}), .eq(comparator_4_eq));  // open: gt, lt
  Comparator #(.width(5), .mode("twosComplement")) comparator_5 (
    .a(rt), .b(EX_WriteReg_num), .eq(comparator_5_eq));  // open: gt, lt
  Comparator #(.width(5), .mode("twosComplement")) comparator_6 (
    .a(MEM_WriteReg_num), .b(rt), .eq(comparator_6_eq));  // open: gt, lt
  \源寄存器检测  \u_源寄存器检测_1  (
    .OP0(OP[0]), .OP1(OP[1]), .OP2(OP[2]), .OP3(OP[3]), .OP4(OP[4]), .OP5(OP[5]), .F0(FUNCT[0]),
    .F1(FUNCT[1]), .F2(FUNCT[2]), .F3(FUNCT[3]), .F4(FUNCT[4]), .F5(FUNCT[5]), .R1_Used(RsUsed),
    .R2_Used(RtUsed));
  not not_1 (not_1_out, comparator_2_eq);
  not not_2 (not_2_out, comparator_4_eq);
  and and_1 (and_2_out[1], EX_RegWrite, comparator_3_eq, not_1_out, RsUsed);
  and and_2 (and_2_out[0], MEM_RegWrite, comparator_1_eq, not_1_out, RsUsed);
  and and_3 (and_3_out, RsUsed, not_1_out, comparator_3_eq, EX_MemToReg);
  and and_4 (and_4_out, RtUsed, not_2_out, EX_MemToReg, comparator_5_eq);
  and and_5 (and_6_out[1], EX_RegWrite, comparator_5_eq, not_2_out, RtUsed);
  and and_6 (and_6_out[0], MEM_RegWrite, comparator_6_eq, not_2_out, RtUsed);
  or or_1 (LoadUse, and_3_out, and_4_out);
  Multiplexer #(.select(2), .width(2), .disabled("Z"), .enable("false")) multiplexer_1 (
    .in0(2'b00), .in1(2'b01), .in2(2'b10), .in3(2'b10), .out(RsFoward), .sel(and_2_out));
  Multiplexer #(.select(2), .width(2), .disabled("Z"), .enable("false")) multiplexer_2 (
    .in0(2'b00), .in1(2'b01), .in2(2'b10), .in3(2'b10), .out(RtFoward), .sel(and_6_out));
endmodule
