// Logisim project cpu24_五子棋组队.circ as structural Verilog: 32 circuits, main circuit ◇单周期MIPS
module \单周期MIPS  (
  input  IR1,
  input  IR2,
  input  IR3,
  output RegWrite,
  output MemWrite,
  output [31:0] PC,
  output [31:0] IR,
  output [31:0] RDin,
  output [31:0] MDin,
  output [31:0] LedData
);

  wire AluSrcB, and_1_out, and_2_out, Beq, Bne, CLK, clock_1_out, clock_2_out, comparator_1_eq,
       comparator_2_eq, comparator_2_lt, d_ff_1_q, Equal, Go, Halt, IR1_t, IR2_t, IR3_t, IRA, IRB, IRC, J2,
       JAL, JMP, JR, LED, MemToReg, nand_1_out, not_1_out, not_2_out, not_3_out, or_1_out, RegDst, SignedExt,
       Syscall, W1, W2, W3;
  wire [3:0] AluOP;
  wire [4:0] multiplexer_2_out, multiplexer_3_out, multiplexer_4_out, multiplexer_5_out;
  wire [12:0] CNT_num;
  wire [15:0] \总周期数 ;
  wire [31:0] bit_extender_1_out, bit_extender_2_out, mips_alu_1_result, multiplexer_1_out,
       multiplexer_6_out, multiplexer_8_out, PC4, PC_JR, PCimm, ram_1_data, shifter_1_out;

  Clock #(.highDuration(1), .lowDuration(1)) clock_1 (.out(clock_1_out));
  Button _1 (.out(IRA));
  Button _2 (.out(IRB));
  Button _3 (.out(IRC));
  Button \u_继续运行  (.out(Go));
  LED #(.active("true")) led_1 (.in(W1));
  LED #(.active("true")) led_2 (.in(W2));
  LED #(.active("true")) led_3 (.in(W3));
  Hex_Digit_Display hex_digit_display_1 (.value(LedData[31:28]));  // open: dp
  ROM #(.addrWidth(10), .dataWidth(32), .Select("high")) rom_1 (.addr(PC[11:2]), .data(IR));
  Hex_Digit_Display hex_digit_display_2 (.value(LedData[23:20]));  // open: dp
  Hex_Digit_Display hex_digit_display_3 (.value(LedData[27:24]));  // open: dp
  // Mips_Probe mips_probe_1: pin names not known; wires that end beside it: clock_1_out, CLK, IR
  not not_1 (not_1_out, Equal);
  Hex_Digit_Display hex_digit_display_4 (.value(LedData[19:16]));  // open: dp
  Hex_Digit_Display hex_digit_display_5 (.value(LedData[15:12]));  // open: dp
  Multiplexer #(.select(3), .width(32), .disabled("Z"), .enable("false")) multiplexer_1 (
    .in0(PC4), .in1(PCimm), .in2({PC4[31:28], IR[25:0], 2'b00}), .in6(PC_JR), .out(multiplexer_1_out),
    .sel({JR, JMP, J2}));  // open: in3, in4, in5, in7
  Adder #(.width(32)) adder_1 (.a(PC), .b(32'h4), .out(PC4));  // open: cin, cout
  and and_1 (and_1_out, Beq, Equal);
  and and_2 (and_2_out, Bne, not_1_out);
  Hex_Digit_Display hex_digit_display_6 (.value(LedData[11:8]));  // open: dp
  Hex_Digit_Display hex_digit_display_7 (.value(LedData[7:4]));  // open: dp
  // Probe on \总周期数 
  or or_1 (or_1_out, not_2_out, Go);
  not not_2 (not_2_out, Halt);
  or or_2 (J2, and_1_out, and_2_out);
  Hex_Digit_Display hex_digit_display_8 (.value(LedData[3:0]));  // open: dp
  Register #(.width(32), .trigger("rising"), .Select("low")) u_PC (
    .D(multiplexer_1_out), .en(or_1_out), .Q(PC), .clk(CLK), .clr(1'b0));
  or or_3 (IR1_t, IR1, IRA);
  or or_4 (IR2_t, IR2, IRB);
  or or_5 (IR3_t, IR3, IRC);
  Multiplexer #(.select(1), .width(5), .disabled("Z"), .enable("false")) multiplexer_2 (
    .in0(IR[20:16]), .in1(IR[15:11]), .out(multiplexer_2_out), .sel(RegDst));
  Multiplexer #(.select(1), .width(5), .disabled("Z"), .enable("false")) multiplexer_3 (
    .in0(IR[25:21]), .in1(5'b00010), .out(multiplexer_3_out), .sel(Syscall));
  Multiplexer #(.select(1), .width(5), .disabled("Z"), .enable("false")) multiplexer_4 (
    .in0(IR[20:16]), .in1(5'b00100), .out(multiplexer_4_out), .sel(Syscall));
  Multiplexer #(.select(1), .width(5), .disabled("Z"), .enable("false")) multiplexer_5 (
    .in0(multiplexer_2_out), .in1({5{1'b1}}), .out(multiplexer_5_out), .sel(JAL));
  assign bit_extender_1_out = {{16{1'b0}}, IR[15:0]};  // Bit_Extender bit_extender_1
  assign bit_extender_2_out = {{16{IR[15]}}, IR[15:0]};  // Bit_Extender bit_extender_2
  Shifter #(.width(32), .shift("ll")) shifter_1 (.in(bit_extender_2_out), .\dist (5'b00010), .out(shifter_1_out));
  Register #(.width(32), .trigger("rising"), .Select("low")) register_1 (
    .D(MDin), .en(LED), .Q(LedData), .clk(CLK), .clr(1'b0));
  MIPS_Regifile mips_regifile_1 (
    .Din(RDin), .Clk(CLK), .R1(PC_JR), .R2(MDin), .WE(RegWrite), .W_num(multiplexer_5_out),
    .R1_num(multiplexer_3_out), .R2_num(multiplexer_4_out));
  Comparator #(.width(32), .mode("twosComplement")) comparator_1 (
    .a(32'h22), .b(PC_JR), .eq(comparator_1_eq));  // open: gt, lt
  Adder #(.width(32)) adder_2 (.a(shifter_1_out), .b(PC4), .out(PCimm));  // open: cin, cout
  and and_3 (LED, Syscall, comparator_1_eq);
  not not_3 (not_3_out, comparator_1_eq);
  and and_4 (Halt, not_3_out, Syscall);
  Multiplexer #(.select(2), .width(32), .disabled("Z"), .enable("false")) multiplexer_6 (
    .in0(MDin), .in1(MDin), .in2(bit_extender_1_out), .in3(bit_extender_2_out), .out(multiplexer_6_out),
    .sel({AluSrcB, SignedExt}));
  Multiplexer #(.select(1), .width(32), .disabled("Z"), .enable("false")) multiplexer_7 (
    .in0(multiplexer_8_out), .in1(PC4), .out(RDin), .sel(JAL));
  \单周期硬布线控制器  \u_单周期硬布线控制器_1  (
    .Func(IR[5:0]), .OP(IR[31:26]), .ALU_OP(AluOP), .MemToReg(MemToReg), .MemWrite(MemWrite),
    .ALU_SRC(AluSrcB), .RegWrite(RegWrite), .SysCALL(Syscall), .SignedExt(SignedExt), .RegDst(RegDst),
    .JR(JR), .JMP(JMP), .Beq(Beq), .JAL(JAL), .Bne(Bne));  // open: ERET, BLTZ, LUI, SB
  MIPS_ALU mips_alu_1 (
    .X(PC_JR), .Y(multiplexer_6_out), .AluOP(AluOP), .Equal(Equal), .Result(mips_alu_1_result),
    .shamt(IR[10:6]));  // open: Result_2
  D_Flip_Flop #(.trigger("high"), .Pre_Clr_Positions("LEGACY"), .NegatePresetClear("false"), .enable("true"), .NewFFLayout("false")) d_ff_1 (.Q(d_ff_1_q));  // open: clk, D, Qn, preset, en, reset
  // Probe on 13'hf
  Comparator #(.width(13), .mode("twosComplement")) comparator_2 (
    .a(CNT_num), .b(13'hf), .eq(comparator_2_eq), .lt(comparator_2_lt));  // open: gt
  Clock #(.highDuration(1), .lowDuration(1)) clock_2 (.out(clock_2_out));
  Counter #(.width(13), .max('h1fff), .ongoal("stay"), .trigger("rising"), .behavior("old")) counter_1 (
    .count(comparator_2_lt), .Q(CNT_num), .clk(clock_2_out));  // open: load, D, carry, clr, preset
  nand nand_1 (nand_1_out, d_ff_1_q, comparator_2_eq);
  RAM #(.addrWidth(10), .dataWidth(32), .bus("separate"), .Select("high")) ram_1 (
    .addr(mips_alu_1_result[11:2]), .din(MDin), .data(ram_1_data), .str(MemWrite), .clk(CLK), .clr(1'b0));  // open: sel, ld
  assign CLK = nand_1_out ? clock_2_out : 1'bz;  // Controlled_Buffer controlled_buffer_1
  Pull_Resistor #(.pull(1)) pull_resistor_1 (.node(CLK));
  Multiplexer #(.select(1), .width(32), .disabled("Z"), .enable("false")) multiplexer_8 (
    .in0(mips_alu_1_result), .in1(ram_1_data), .out(multiplexer_8_out), .sel(MemToReg));

  // Other names for the same wires on the sheet: OP[5:0] = IR[31:26]; LEDD[31:0] = MDin;
  //   PC_JAL[31:2] = {PC4[31:28], IR[25:0]}; addr[25:0] = IR[25:0]; Func[5:0] = IR[5:0]; imm[15:0] = IR[15:0];
  //   shamt[4:0] = IR[10:6]; rd[4:0] = IR[15:11]; rt[4:0] = IR[20:16]; rs[4:0] = IR[25:21]

  // Notes on the sheet:
  //   中断源
  //   中断等待指示
  //   总复位信号应将除ROM以外所有存储组件全部清零
  //   指令存储器
  //   contents of rom_1 (hex, n*v repeats v):
  //   20110001 8000c05 20110001 20120002 20130003 8000c09 20110001 20120002 20130003 8000c0d 20110001
  //   20120002 20130003 8000c11 20110001 20120002 20130003 c000cb8 20100001 20110001 118fc0 112020
  //   20020022 c 118882 12200001 8000c15 112020 20020022 c 20110001 118880 112020 20020022 c 12200001
  //   8000c1f 20110001 118fc0 112020 20020022 c 1188c3 112020 20020022 c 118903 112020 20020022 c 118903
  //   112020 20020022 c 118903 112020 20020022 c 118903 112020 20020022 c 118903 112020 20020022 c 118903
  //   112020 20020022 c 118903 112020 20020022 c 20100001 109fc0 139fc3 8021 2012000c 24160003 26100001
  //   3210000f 20080008 20090001 139900 2709825 132020 20020022 c 1094022 1500fff9 22100001 2018000f
  //   2188024 108700 20080008 20090001 139902 2709825 132021 20020022 c 1094022 1500fff9 108702 2c9b022
  //   12c00001 8000c50 4020 1084027 84400 3508ffff 82021 20020022 c 2010ffff 20110000 ae300000 22100001
  //   22310004 ae300000 22100001 22310004 ae300000 22100001 22310004 ae300000 22100001 22310004 ae300000
  //   22100001 22310004 ae300000 22100001 22310004 ae300000 22100001 22310004 ae300000 22100001 22310004
  //   ae300000 22100001 22310004 ae300000 22100001 22310004 ae300000 22100001 22310004 ae300000 22100001
  //   22310004 ae300000 22100001 22310004 ae300000 22100001 22310004 ae300000 22100001 22310004 ae300000
  //   22100001 22310004 22100001 8020 2011003c 8e130000 8e340000 274402a 11000002 ae330000 ae140000
  //   2231fffc 1611fff8 102020 20020022 c 22100004 2011003c 1611fff2 20020032 c 20100000 22100001 102020
  //   20020022 c 22100002 102020 20020022 c 22100003 102020 20020022 c 22100004 102020 20020022 c 22100005
  //   102020 20020022 c 22100006 102020 20020022 c 22100007 102020 20020022 c 22100008 102020 20020022
  //   20020022 c 3e00008
  //   OP
  //   Func
  //   rs
  //   指令字
  //   rt
  //   rd
  //   数码管输出
  //   数码管输出应该用寄存器锁存，否则显示数据只能一闪而过
  //   为方便自动评测，需要输出PC，IR，寄存器堆写如数据RDin
  //   RAM写使能MemWrite、RAM写入数据MDin等信号
  //   Beq
  //   JMP
  //   JR
  //   Bne
  //   OP
  //   JAL
  //   Func
  //   Syscall
  //   控制位
  //   暂停节拍，不能为0
  //   MemToReg
  //   MemWrite
  //   AluOP
  //   AluSrcB
  //   RegWrite
  //   RegDst
  //   戳工具置1进入计数暂停模式，ctrl+k时钟自动运行到对应节拍暂停
  //   ctrl+k关闭时钟连续运行，将控制位置零，进入单步调试模式调试
  //   用这个时钟源需要去掉电路中的其他时钟源
  //   可计数暂停的时钟源
endmodule

// 单周期硬布线控制器
module \单周期硬布线控制器  (
  input  [5:0] OP,
  input  [5:0] Func,
  output [3:0] ALU_OP,
  output MemToReg,
  output MemWrite,
  output ALU_SRC,
  output RegWrite,
  output SysCALL,
  output SignedExt,
  output RegDst,
  output Beq,
  output Bne,
  output JR,
  output JMP,
  output JAL,
  output BLTZ,
  output SB,
  output LUI,
  output ERET
);

  \运算控制器自动生成  \u_运算控制器自动生成_1  (
    .OP0(OP[0]), .OP1(OP[1]), .OP2(OP[2]), .OP3(OP[3]), .OP4(OP[4]), .OP5(OP[5]), .F0(Func[0]), .F1(Func[1]),
    .F2(Func[2]), .F3(Func[3]), .F4(Func[4]), .F5(Func[5]), .S0(ALU_OP[0]), .S1(ALU_OP[1]), .S2(ALU_OP[2]),
    .S3(ALU_OP[3]));
  \控制信号自动生成  \u_控制信号自动生成_1  (
    .OP0(OP[0]), .OP1(OP[1]), .OP2(OP[2]), .OP3(OP[3]), .OP4(OP[4]), .OP5(OP[5]), .F0(Func[0]), .F1(Func[1]),
    .F2(Func[2]), .F3(Func[3]), .F4(Func[4]), .F5(Func[5]), .MemToReg(MemToReg), .MemWrite(MemWrite),
    .ALU_SRC(ALU_SRC), .RegWrite(RegWrite), .SysCALL(SysCALL), .SignedExt(SignedExt), .RegDst(RegDst),
    .BEQ(Beq), .BNE(Bne), .JR(JR), .JUMP(JMP), .JAL(JAL), .BLTZ(BLTZ), .SB(SB), .LUI(LUI), .ERET(ERET));

  // Other names for the same wires on the sheet: OP_CODE[5:0] = OP

  // Notes on the sheet:
  //   运算器控制器，根据指令生成运算器功能选择信号
  //   控制信号生成，产生数据通路需要的其他控制信号
endmodule

// 运算器控制器
module \运算控制器自动生成  (
  input  OP0,
  input  OP1,
  input  OP2,
  input  OP3,
  input  OP4,
  input  OP5,
  input  F0,
  input  F1,
  input  F2,
  input  F3,
  input  F4,
  input  F5,
  output S0,
  output S1,
  output S2,
  output S3
);

  wire and_1_out, and_2_out, and_3_out, and_4_out, and_5_out, and_6_out, and_7_out, and_8_out, and_9_out,
       and_10_out, and_11_out, and_12_out, and_13_out, and_14_out, and_15_out, and_16_out, and_17_out,
       and_18_out, and_19_out, and_20_out, and_21_out, and_22_out, and_23_out, and_24_out, and_25_out,
       and_26_out, and_27_out, and_28_out, and_29_out, and_30_out, and_31_out, and_32_out, and_33_out,
       and_34_out, and_35_out, and_36_out, and_37_out, and_38_out, not_1_out, not_2_out, not_3_out,
       not_4_out, not_5_out, not_6_out, not_7_out, not_8_out, not_9_out, not_10_out, not_11_out, not_12_out,
       not_13_out, not_14_out, not_15_out, not_16_out, not_17_out, not_18_out, not_19_out, not_20_out,
       not_21_out, not_22_out, not_23_out, not_24_out, not_25_out, not_26_out, not_27_out, not_28_out,
       not_29_out, not_30_out, not_31_out, not_32_out, not_33_out, not_34_out, not_35_out, not_36_out,
       not_37_out, not_38_out, not_39_out, not_40_out, not_41_out, not_42_out, not_43_out, not_44_out,
       not_45_out, not_46_out, not_47_out, not_48_out, not_49_out, not_50_out, not_51_out, not_52_out,
       not_53_out, not_54_out, not_55_out, not_56_out, not_57_out, not_58_out, not_59_out, not_60_out,
       not_61_out, not_62_out, not_63_out, not_64_out, not_65_out, not_66_out, not_67_out, not_68_out,
       not_69_out, not_70_out, not_71_out, not_72_out, not_73_out, not_74_out, not_75_out, not_76_out,
       not_77_out, not_78_out, not_79_out, not_80_out, not_81_out, not_82_out, not_83_out, not_84_out,
       not_85_out, not_86_out, not_87_out, not_88_out, not_89_out, not_90_out, not_91_out, not_92_out,
       not_93_out, not_94_out, not_95_out, not_96_out, not_97_out, not_98_out, not_99_out, not_100_out,
       not_101_out, not_102_out, not_103_out, not_104_out, not_105_out, not_106_out, not_107_out,
       not_108_out, not_109_out, not_110_out, not_111_out, not_112_out, not_113_out, not_114_out,
       not_115_out, not_116_out, not_117_out, not_118_out, not_119_out, not_120_out, not_121_out,
       not_122_out, not_123_out, not_124_out, not_125_out, not_126_out, not_127_out, not_128_out,
       not_129_out, not_130_out, not_131_out, not_132_out, not_133_out, not_134_out, not_135_out,
       not_136_out, not_137_out, not_138_out, not_139_out, not_140_out, not_141_out, not_142_out,
       not_143_out, not_144_out, not_145_out, not_146_out, not_147_out, not_148_out, not_149_out,
       not_150_out, not_151_out, not_152_out, not_153_out, not_154_out, not_155_out, not_156_out,
       not_157_out, not_158_out, not_159_out, not_160_out, not_161_out, not_162_out, not_163_out,
       not_164_out, not_165_out, not_166_out, not_167_out, not_168_out, not_169_out, not_170_out,
       not_171_out, not_172_out, not_173_out, not_174_out, not_175_out, not_176_out, not_177_out,
       not_178_out, not_179_out, not_180_out, not_181_out, not_182_out, not_183_out, not_184_out,
       not_185_out, not_186_out, not_187_out, not_188_out, not_189_out, not_190_out, not_191_out,
       not_192_out, not_193_out, not_194_out, not_195_out, not_196_out, not_197_out, not_198_out,
       not_199_out, not_200_out, not_201_out, not_202_out, not_203_out, not_204_out, not_205_out,
       not_206_out, not_207_out, not_208_out, not_209_out, not_210_out, not_211_out, not_212_out,
       not_213_out, not_214_out, not_215_out, not_216_out, not_217_out, not_218_out, not_219_out,
       not_220_out, not_221_out, not_222_out, not_223_out, not_224_out, not_225_out, not_226_out,
       not_227_out, not_228_out, not_229_out, not_230_out, not_231_out, not_232_out, not_233_out,
       not_234_out, not_235_out, not_236_out, not_237_out, not_238_out, not_239_out, not_240_out,
       not_241_out, not_242_out, not_243_out, not_244_out, not_245_out, not_246_out, not_247_out,
       not_248_out, not_249_out, not_250_out, not_251_out, not_252_out, not_253_out, not_254_out,
       not_255_out, not_256_out, not_257_out, not_258_out, not_259_out, not_260_out, not_261_out, not_262_out;

  not not_1 (not_1_out, OP5);
  not not_2 (not_2_out, OP4);
  not not_3 (not_3_out, OP3);
  not not_4 (not_4_out, OP2);
  not not_5 (not_5_out, OP1);
  not not_6 (not_6_out, OP0);
  not not_7 (not_7_out, F5);
  not not_8 (not_8_out, F4);
  not not_9 (not_9_out, F3);
  not not_10 (not_10_out, F2);
  not not_11 (not_11_out, OP5);
  not not_12 (not_12_out, OP4);
  not not_13 (not_13_out, OP3);
  not not_14 (not_14_out, OP2);
  not not_15 (not_15_out, OP1);
  not not_16 (not_16_out, OP0);
  not not_17 (not_17_out, F4);
  not not_18 (not_18_out, F3);
  not not_19 (not_19_out, F2);
  not not_20 (not_20_out, F1);
  not not_21 (not_21_out, F0);
  not not_22 (not_22_out, OP5);
  not not_23 (not_23_out, OP4);
  not not_24 (not_24_out, OP3);
  not not_25 (not_25_out, OP2);
  not not_26 (not_26_out, OP1);
  not not_27 (not_27_out, OP0);
  not not_28 (not_28_out, F4);
  not not_29 (not_29_out, F3);
  not not_30 (not_30_out, F2);
  not not_31 (not_31_out, F1);
  not not_32 (not_32_out, OP5);
  not not_33 (not_33_out, OP4);
  not not_34 (not_34_out, OP3);
  not not_35 (not_35_out, OP2);
  not not_36 (not_36_out, OP1);
  not not_37 (not_37_out, OP0);
  not not_38 (not_38_out, F4);
  not not_39 (not_39_out, F3);
  not not_40 (not_40_out, F1);
  not not_41 (not_41_out, F0);
  not not_42 (not_42_out, OP5);
  not not_43 (not_43_out, OP4);
  not not_44 (not_44_out, OP3);
  not not_45 (not_45_out, OP2);
  not not_46 (not_46_out, OP1);
  not not_47 (not_47_out, OP0);
  not not_48 (not_48_out, F4);
  not not_49 (not_49_out, F2);
  not not_50 (not_50_out, F0);
  not not_51 (not_51_out, OP5);
  not not_52 (not_52_out, OP4);
  not not_53 (not_53_out, OP2);
  not not_54 (not_54_out, OP1);
  not not_55 (not_55_out, OP0);
  not not_56 (not_56_out, OP5);
  not not_57 (not_57_out, OP4);
  not not_58 (not_58_out, OP1);
  not not_59 (not_59_out, OP0);
  not not_60 (not_60_out, OP5);
  not not_61 (not_61_out, OP4);
  not not_62 (not_62_out, OP2);
  not not_63 (not_63_out, OP1);
  not not_64 (not_64_out, OP5);
  not not_65 (not_65_out, OP4);
  not not_66 (not_66_out, OP2);
  not not_67 (not_67_out, OP0);
  not not_68 (not_68_out, OP4);
  not not_69 (not_69_out, OP3);
  not not_70 (not_70_out, OP2);
  not not_71 (not_71_out, OP4);
  not not_72 (not_72_out, OP2);
  not not_73 (not_73_out, OP4);
  not not_74 (not_74_out, OP2);
  not not_75 (not_75_out, OP1);
  not not_76 (not_76_out, OP0);
  not not_77 (not_77_out, OP5);
  not not_78 (not_78_out, OP4);
  not not_79 (not_79_out, OP3);
  not not_80 (not_80_out, OP2);
  not not_81 (not_81_out, OP1);
  not not_82 (not_82_out, OP0);
  not not_83 (not_83_out, F5);
  not not_84 (not_84_out, F4);
  not not_85 (not_85_out, F3);
  not not_86 (not_86_out, F2);
  not not_87 (not_87_out, F0);
  not not_88 (not_88_out, OP5);
  not not_89 (not_89_out, OP4);
  not not_90 (not_90_out, OP3);
  not not_91 (not_91_out, OP2);
  not not_92 (not_92_out, OP1);
  not not_93 (not_93_out, OP0);
  not not_94 (not_94_out, F4);
  not not_95 (not_95_out, F3);
  not not_96 (not_96_out, F2);
  not not_97 (not_97_out, F0);
  not not_98 (not_98_out, OP5);
  not not_99 (not_99_out, OP4);
  not not_100 (not_100_out, OP3);
  not not_101 (not_101_out, OP2);
  not not_102 (not_102_out, OP1);
  not not_103 (not_103_out, OP0);
  not not_104 (not_104_out, F4);
  not not_105 (not_105_out, F3);
  not not_106 (not_106_out, F1);
  not not_107 (not_107_out, F0);
  not not_108 (not_108_out, OP5);
  not not_109 (not_109_out, OP4);
  not not_110 (not_110_out, OP3);
  not not_111 (not_111_out, OP2);
  not not_112 (not_112_out, OP1);
  not not_113 (not_113_out, OP0);
  not not_114 (not_114_out, F4);
  not not_115 (not_115_out, F3);
  not not_116 (not_116_out, OP5);
  not not_117 (not_117_out, OP4);
  not not_118 (not_118_out, OP3);
  not not_119 (not_119_out, OP2);
  not not_120 (not_120_out, OP1);
  not not_121 (not_121_out, OP0);
  not not_122 (not_122_out, F4);
  not not_123 (not_123_out, F2);
  not not_124 (not_124_out, F0);
  not not_125 (not_125_out, OP5);
  not not_126 (not_126_out, OP4);
  not not_127 (not_127_out, OP1);
  not not_128 (not_128_out, OP0);
  not not_129 (not_129_out, OP5);
  not not_130 (not_130_out, OP4);
  not not_131 (not_131_out, OP2);
  not not_132 (not_132_out, OP0);
  not not_133 (not_133_out, OP5);
  not not_134 (not_134_out, OP4);
  not not_135 (not_135_out, OP3);
  not not_136 (not_136_out, OP2);
  not not_137 (not_137_out, OP1);
  not not_138 (not_138_out, OP0);
  not not_139 (not_139_out, F4);
  not not_140 (not_140_out, F3);
  not not_141 (not_141_out, F2);
  not not_142 (not_142_out, OP5);
  not not_143 (not_143_out, OP4);
  not not_144 (not_144_out, OP3);
  not not_145 (not_145_out, OP2);
  not not_146 (not_146_out, OP1);
  not not_147 (not_147_out, OP0);
  not not_148 (not_148_out, F4);
  not not_149 (not_149_out, F3);
  not not_150 (not_150_out, F2);
  not not_151 (not_151_out, F1);
  not not_152 (not_152_out, F0);
  not not_153 (not_153_out, OP5);
  not not_154 (not_154_out, OP4);
  not not_155 (not_155_out, OP3);
  not not_156 (not_156_out, OP2);
  not not_157 (not_157_out, OP1);
  not not_158 (not_158_out, OP0);
  not not_159 (not_159_out, F4);
  not not_160 (not_160_out, F3);
  not not_161 (not_161_out, F2);
  not not_162 (not_162_out, F1);
  not not_163 (not_163_out, OP5);
  not not_164 (not_164_out, OP4);
  not not_165 (not_165_out, OP3);
  not not_166 (not_166_out, OP2);
  not not_167 (not_167_out, OP1);
  not not_168 (not_168_out, OP0);
  not not_169 (not_169_out, F4);
  not not_170 (not_170_out, F3);
  not not_171 (not_171_out, F2);
  not not_172 (not_172_out, F0);
  not not_173 (not_173_out, OP5);
  not not_174 (not_174_out, OP4);
  not not_175 (not_175_out, OP3);
  not not_176 (not_176_out, OP2);
  not not_177 (not_177_out, OP1);
  not not_178 (not_178_out, OP0);
  not not_179 (not_179_out, F4);
  not not_180 (not_180_out, F3);
  not not_181 (not_181_out, F1);
  not not_182 (not_182_out, F0);
  not not_183 (not_183_out, OP5);
  not not_184 (not_184_out, OP4);
  not not_185 (not_185_out, OP3);
  not not_186 (not_186_out, OP2);
  not not_187 (not_187_out, OP1);
  not not_188 (not_188_out, OP0);
  not not_189 (not_189_out, F4);
  not not_190 (not_190_out, F2);
  not not_191 (not_191_out, OP5);
  not not_192 (not_192_out, OP4);
  not not_193 (not_193_out, OP2);
  not not_194 (not_194_out, OP1);
  not not_195 (not_195_out, OP0);
  not not_196 (not_196_out, OP5);
  not not_197 (not_197_out, OP4);
  not not_198 (not_198_out, OP1);
  not not_199 (not_199_out, OP0);
  not not_200 (not_200_out, OP5);
  not not_201 (not_201_out, OP4);
  not not_202 (not_202_out, OP2);
  not not_203 (not_203_out, OP1);
  not not_204 (not_204_out, OP4);
  not not_205 (not_205_out, OP3);
  not not_206 (not_206_out, OP2);
  not not_207 (not_207_out, OP4);
  not not_208 (not_208_out, OP2);
  not not_209 (not_209_out, OP5);
  not not_210 (not_210_out, OP4);
  not not_211 (not_211_out, OP3);
  not not_212 (not_212_out, OP2);
  not not_213 (not_213_out, OP1);
  not not_214 (not_214_out, OP0);
  not not_215 (not_215_out, F4);
  not not_216 (not_216_out, F3);
  not not_217 (not_217_out, F2);
  not not_218 (not_218_out, OP4);
  not not_219 (not_219_out, OP2);
  not not_220 (not_220_out, OP1);
  not not_221 (not_221_out, OP0);
  not not_222 (not_222_out, OP5);
  not not_223 (not_223_out, OP4);
  not not_224 (not_224_out, OP3);
  not not_225 (not_225_out, OP2);
  not not_226 (not_226_out, OP1);
  not not_227 (not_227_out, OP0);
  not not_228 (not_228_out, F4);
  not not_229 (not_229_out, F3);
  not not_230 (not_230_out, F1);
  not not_231 (not_231_out, OP5);
  not not_232 (not_232_out, OP4);
  not not_233 (not_233_out, OP3);
  not not_234 (not_234_out, OP2);
  not not_235 (not_235_out, OP1);
  not not_236 (not_236_out, OP0);
  not not_237 (not_237_out, F4);
  not not_238 (not_238_out, F3);
  not not_239 (not_239_out, OP5);
  not not_240 (not_240_out, OP4);
  not not_241 (not_241_out, OP3);
  not not_242 (not_242_out, OP2);
  not not_243 (not_243_out, OP1);
  not not_244 (not_244_out, OP0);
  not not_245 (not_245_out, F4);
  not not_246 (not_246_out, F2);
  not not_247 (not_247_out, F0);
  not not_248 (not_248_out, OP5);
  not not_249 (not_249_out, OP4);
  not not_250 (not_250_out, OP3);
  not not_251 (not_251_out, OP2);
  not not_252 (not_252_out, OP1);
  not not_253 (not_253_out, OP0);
  not not_254 (not_254_out, F4);
  not not_255 (not_255_out, F2);
  not not_256 (not_256_out, OP5);
  not not_257 (not_257_out, OP4);
  not not_258 (not_258_out, OP2);
  not not_259 (not_259_out, OP0);
  not not_260 (not_260_out, OP5);
  not not_261 (not_261_out, OP4);
  not not_262 (not_262_out, OP1);
  and and_1 (and_1_out, not_1_out, not_2_out, not_3_out, not_4_out, not_5_out, not_6_out, not_7_out, not_8_out, not_9_out, not_10_out, F1, F0);
  and and_2 (and_2_out, not_11_out, not_12_out, not_13_out, not_14_out, not_15_out, not_16_out, F5, not_17_out, not_18_out, not_19_out, not_20_out, not_21_out);
  and and_3 (and_3_out, not_22_out, not_23_out, not_24_out, not_25_out, not_26_out, not_27_out, F5, not_28_out, not_29_out, not_30_out, not_31_out, F0);
  and and_4 (and_4_out, not_32_out, not_33_out, not_34_out, not_35_out, not_36_out, not_37_out, F5, not_38_out, not_39_out, F2, not_40_out, not_41_out);
  and and_5 (and_5_out, not_42_out, not_43_out, not_44_out, not_45_out, not_46_out, not_47_out, F5, not_48_out, F3, not_49_out, F1, not_50_out);
  and and_6 (and_6_out, not_51_out, not_52_out, OP3, not_53_out, not_54_out, not_55_out);
  and and_7 (and_7_out, not_56_out, not_57_out, OP3, OP2, not_58_out, not_59_out);
  and and_8 (and_8_out, not_60_out, not_61_out, OP3, not_62_out, not_63_out, OP0);
  and and_9 (and_9_out, not_64_out, not_65_out, OP3, not_66_out, OP1, not_67_out);
  and and_10 (and_10_out, OP5, not_68_out, not_69_out, not_70_out, OP1, OP0);
  and and_11 (and_11_out, OP5, not_71_out, OP3, not_72_out, OP1, OP0);
  and and_12 (and_12_out, OP5, not_73_out, OP3, not_74_out, not_75_out, not_76_out);
  and and_13 (and_13_out, not_77_out, not_78_out, not_79_out, not_80_out, not_81_out, not_82_out, not_83_out, not_84_out, not_85_out, not_86_out, F1, not_87_out);
  and and_14 (and_14_out, not_88_out, not_89_out, not_90_out, not_91_out, not_92_out, not_93_out, F5, not_94_out, not_95_out, not_96_out, F1, not_97_out);
  and and_15 (and_15_out, not_98_out, not_99_out, not_100_out, not_101_out, not_102_out, not_103_out, F5, not_104_out, not_105_out, F2, not_106_out, not_107_out);
  and and_16 (and_16_out, not_108_out, not_109_out, not_110_out, not_111_out, not_112_out, not_113_out, F5, not_114_out, not_115_out, F2, F1, F0);
  and and_17 (and_17_out, not_116_out, not_117_out, not_118_out, not_119_out, not_120_out, not_121_out, F5, not_122_out, F3, not_123_out, F1, not_124_out);
  and and_18 (and_18_out, not_125_out, not_126_out, OP3, OP2, not_127_out, not_128_out);
  and and_19 (and_19_out, not_129_out, not_130_out, OP3, not_131_out, OP1, not_132_out);
  and and_20 (and_20_out, not_133_out, not_134_out, not_135_out, not_136_out, not_137_out, not_138_out, F5, not_139_out, not_140_out, not_141_out, F1, F0);
  and and_21 (and_21_out, not_142_out, not_143_out, not_144_out, not_145_out, not_146_out, not_147_out, F5, not_148_out, not_149_out, not_150_out, not_151_out, not_152_out);
  and and_22 (and_22_out, not_153_out, not_154_out, not_155_out, not_156_out, not_157_out, not_158_out, F5, not_159_out, not_160_out, not_161_out, not_162_out, F0);
  and and_23 (and_23_out, not_163_out, not_164_out, not_165_out, not_166_out, not_167_out, not_168_out, F5, not_169_out, not_170_out, not_171_out, F1, not_172_out);
  and and_24 (and_24_out, not_173_out, not_174_out, not_175_out, not_176_out, not_177_out, not_178_out, F5, not_179_out, not_180_out, F2, not_181_out, not_182_out);
  and and_25 (and_25_out, not_183_out, not_184_out, not_185_out, not_186_out, not_187_out, not_188_out, F5, not_189_out, F3, not_190_out, F1, F0);
  and and_26 (and_26_out, not_191_out, not_192_out, OP3, not_193_out, not_194_out, not_195_out);
  and and_27 (and_27_out, not_196_out, not_197_out, OP3, OP2, not_198_out, not_199_out);
  and and_28 (and_28_out, not_200_out, not_201_out, OP3, not_202_out, not_203_out, OP0);
  and and_29 (and_29_out, OP5, not_204_out, not_205_out, not_206_out, OP1, OP0);
  and and_30 (and_30_out, OP5, not_207_out, OP3, not_208_out, OP1, OP0);
  and and_31 (and_31_out, not_209_out, not_210_out, not_211_out, not_212_out, not_213_out, not_214_out, F5, not_215_out, not_216_out, not_217_out, F1, F0);
  and and_32 (and_32_out, OP5, not_218_out, OP3, not_219_out, not_220_out, not_221_out);
  and and_33 (and_33_out, not_222_out, not_223_out, not_224_out, not_225_out, not_226_out, not_227_out, F5, not_228_out, not_229_out, F2, not_230_out, F0);
  and and_34 (and_34_out, not_231_out, not_232_out, not_233_out, not_234_out, not_235_out, not_236_out, F5, not_237_out, not_238_out, F2, F1, F0);
  and and_35 (and_35_out, not_239_out, not_240_out, not_241_out, not_242_out, not_243_out, not_244_out, F5, not_245_out, F3, not_246_out, F1, not_247_out);
  and and_36 (and_36_out, not_248_out, not_249_out, not_250_out, not_251_out, not_252_out, not_253_out, F5, not_254_out, F3, not_255_out, F1, F0);
  and and_37 (and_37_out, not_256_out, not_257_out, OP3, not_258_out, OP1, not_259_out);
  and and_38 (and_38_out, not_260_out, not_261_out, OP3, OP2, not_262_out, OP0);
  or or_1 (S1, and_13_out, and_14_out, and_15_out, and_16_out, and_17_out, and_18_out, and_19_out, and_20_out);
  or or_2 (S3, and_33_out, and_34_out, and_35_out, and_36_out, and_37_out, and_38_out);
  or or_3 (S0, and_1_out, and_2_out, and_3_out, and_4_out, and_5_out, and_6_out, and_7_out, and_8_out, and_9_out, and_10_out, and_11_out, and_12_out);
  or or_4 (S2, and_21_out, and_22_out, and_23_out, and_24_out, and_25_out, and_26_out, and_27_out, and_28_out, and_29_out, and_30_out, and_31_out, and_32_out);
endmodule

// 控制信号生成
module \控制信号自动生成  (
  input  OP0,
  input  OP1,
  input  OP2,
  input  OP3,
  input  OP4,
  input  OP5,
  input  F0,
  input  F1,
  input  F2,
  input  F3,
  input  F4,
  input  F5,
  output MemToReg,
  output MemWrite,
  output ALU_SRC,
  output RegWrite,
  output SysCALL,
  output SignedExt,
  output RegDst,
  output BEQ,
  output BNE,
  output JR,
  output JUMP,
  output JAL,
  output BLTZ,
  output SB,
  output LUI,
  output ERET
);

  wire and_2_out, and_3_out, and_4_out, and_5_out, and_6_out, and_7_out, and_8_out, and_9_out, and_10_out,
       and_11_out, and_12_out, and_13_out, and_14_out, and_15_out, and_16_out, and_17_out, and_18_out,
       and_19_out, and_20_out, and_21_out, and_22_out, and_23_out, and_24_out, and_25_out, and_26_out,
       and_27_out, and_28_out, and_29_out, and_30_out, and_31_out, and_32_out, and_34_out, and_35_out,
       and_36_out, and_37_out, and_38_out, and_39_out, and_40_out, and_41_out, and_42_out, and_43_out,
       and_44_out, and_45_out, and_46_out, and_47_out, and_48_out, and_49_out, and_50_out, and_51_out,
       and_52_out, and_53_out, and_54_out, and_58_out, and_59_out, and_60_out, not_1_out, not_2_out,
       not_3_out, not_4_out, not_5_out, not_6_out, not_7_out, not_8_out, not_9_out, not_10_out, not_11_out,
       not_12_out, not_13_out, not_14_out, not_15_out, not_16_out, not_17_out, not_18_out, not_19_out,
       not_20_out, not_21_out, not_22_out, not_23_out, not_24_out, not_25_out, not_26_out, not_27_out,
       not_28_out, not_29_out, not_30_out, not_31_out, not_32_out, not_33_out, not_34_out, not_35_out,
       not_36_out, not_37_out, not_38_out, not_39_out, not_40_out, not_41_out, not_42_out, not_43_out,
       not_44_out, not_45_out, not_46_out, not_47_out, not_48_out, not_49_out, not_50_out, not_51_out,
       not_52_out, not_53_out, not_54_out, not_55_out, not_56_out, not_57_out, not_58_out, not_59_out,
       not_60_out, not_61_out, not_62_out, not_63_out, not_64_out, not_65_out, not_66_out, not_67_out,
       not_68_out, not_69_out, not_70_out, not_71_out, not_72_out, not_73_out, not_74_out, not_75_out,
       not_76_out, not_77_out, not_78_out, not_79_out, not_80_out, not_81_out, not_82_out, not_83_out,
       not_84_out, not_85_out, not_86_out, not_87_out, not_88_out, not_89_out, not_90_out, not_91_out,
       not_92_out, not_93_out, not_94_out, not_95_out, not_96_out, not_97_out, not_98_out, not_99_out,
       not_100_out, not_101_out, not_102_out, not_103_out, not_104_out, not_105_out, not_106_out,
       not_107_out, not_108_out, not_109_out, not_110_out, not_111_out, not_112_out, not_113_out,
       not_114_out, not_115_out, not_116_out, not_117_out, not_118_out, not_119_out, not_120_out,
       not_121_out, not_122_out, not_123_out, not_124_out, not_125_out, not_126_out, not_127_out,
       not_128_out, not_129_out, not_130_out, not_131_out, not_132_out, not_133_out, not_134_out,
       not_135_out, not_136_out, not_137_out, not_138_out, not_139_out, not_140_out, not_141_out,
       not_142_out, not_143_out, not_144_out, not_145_out, not_146_out, not_147_out, not_148_out,
       not_149_out, not_150_out, not_151_out, not_152_out, not_153_out, not_154_out, not_155_out,
       not_156_out, not_157_out, not_158_out, not_159_out, not_160_out, not_161_out, not_162_out,
       not_163_out, not_164_out, not_165_out, not_166_out, not_167_out, not_168_out, not_169_out,
       not_170_out, not_171_out, not_172_out, not_173_out, not_174_out, not_175_out, not_176_out,
       not_177_out, not_178_out, not_179_out, not_180_out, not_181_out, not_182_out, not_183_out,
       not_184_out, not_185_out, not_186_out, not_187_out, not_188_out, not_189_out, not_190_out,
       not_191_out, not_192_out, not_193_out, not_194_out, not_195_out, not_196_out, not_197_out,
       not_198_out, not_199_out, not_200_out, not_201_out, not_202_out, not_203_out, not_204_out,
       not_205_out, not_206_out, not_207_out, not_208_out, not_209_out, not_210_out, not_211_out,
       not_212_out, not_213_out, not_214_out, not_215_out, not_216_out, not_217_out, not_218_out,
       not_219_out, not_220_out, not_221_out, not_222_out, not_223_out, not_224_out, not_225_out,
       not_226_out, not_227_out, not_228_out, not_229_out, not_230_out, not_231_out, not_232_out,
       not_233_out, not_234_out, not_235_out, not_236_out, not_237_out, not_238_out, not_239_out,
       not_240_out, not_241_out, not_242_out, not_243_out, not_244_out, not_245_out, not_246_out,
       not_247_out, not_248_out, not_249_out, not_250_out, not_251_out, not_252_out, not_253_out,
       not_254_out, not_255_out, not_256_out, not_257_out, not_258_out, not_259_out, not_260_out,
       not_261_out, not_262_out, not_263_out, not_264_out, not_265_out, not_266_out, not_267_out,
       not_268_out, not_269_out, not_270_out, not_271_out, not_272_out, not_273_out, not_274_out,
       not_275_out, not_276_out, not_277_out, not_278_out, not_279_out, not_280_out, not_281_out,
       not_282_out, not_283_out, not_284_out, not_285_out, not_286_out, not_287_out, not_288_out,
       not_289_out, not_290_out, not_291_out, not_292_out, not_293_out, not_294_out, not_295_out,
       not_296_out, not_297_out, not_298_out, not_299_out, not_300_out, not_301_out, not_302_out,
       not_303_out, not_304_out, not_305_out, not_306_out, not_307_out, not_308_out, not_309_out,
       not_310_out, not_311_out, not_312_out, not_313_out, not_314_out, not_315_out, not_316_out,
       not_317_out, not_318_out, not_319_out, not_320_out, not_321_out, not_322_out, not_323_out,
       not_324_out, not_325_out, not_326_out, not_327_out, not_328_out, not_329_out, not_330_out,
       not_331_out, not_332_out, not_333_out, not_334_out, not_335_out, not_336_out, not_337_out,
       not_338_out, not_339_out, not_340_out, not_341_out, not_342_out, not_343_out, not_344_out,
       not_345_out, not_346_out, not_347_out, not_348_out, not_349_out, not_350_out, not_351_out,
       not_352_out, not_353_out, not_354_out, not_355_out, not_356_out, not_357_out, not_358_out,
       not_359_out, not_360_out, not_361_out, not_362_out, not_363_out, not_364_out, not_365_out,
       not_366_out, not_367_out, not_368_out, not_369_out, not_370_out, not_371_out, not_372_out,
       not_373_out, not_374_out, not_375_out, not_376_out, not_377_out, not_378_out, not_379_out,
       not_380_out, not_381_out, not_382_out, not_383_out, not_384_out, not_385_out, not_386_out,
       not_387_out, not_388_out, not_389_out, not_390_out, not_391_out, not_392_out, not_393_out,
       not_394_out, not_395_out, not_396_out, not_397_out, not_398_out, not_399_out, not_400_out,
       not_401_out, not_402_out, not_403_out, not_404_out, not_405_out, not_406_out, not_407_out,
       not_408_out, not_409_out, not_410_out, not_411_out, not_412_out, not_413_out;

  not not_1 (not_1_out, OP4);
  not not_2 (not_2_out, OP3);
  not not_3 (not_3_out, OP2);
  not not_4 (not_4_out, OP4);
  not not_5 (not_5_out, OP2);
  not not_6 (not_6_out, OP4);
  not not_7 (not_7_out, OP2);
  not not_8 (not_8_out, OP1);
  not not_9 (not_9_out, OP0);
  not not_10 (not_10_out, OP5);
  not not_11 (not_11_out, OP4);
  not not_12 (not_12_out, OP2);
  not not_13 (not_13_out, OP1);
  not not_14 (not_14_out, OP0);
  not not_15 (not_15_out, OP5);
  not not_16 (not_16_out, OP4);
  not not_17 (not_17_out, OP1);
  not not_18 (not_18_out, OP0);
  not not_19 (not_19_out, OP5);
  not not_20 (not_20_out, OP4);
  not not_21 (not_21_out, OP2);
  not not_22 (not_22_out, OP1);
  not not_23 (not_23_out, OP5);
  not not_24 (not_24_out, OP4);
  not not_25 (not_25_out, OP2);
  not not_26 (not_26_out, OP0);
  not not_27 (not_27_out, OP5);
  not not_28 (not_28_out, OP4);
  not not_29 (not_29_out, OP1);
  not not_30 (not_30_out, OP4);
  not not_31 (not_31_out, OP3);
  not not_32 (not_32_out, OP2);
  not not_33 (not_33_out, OP4);
  not not_34 (not_34_out, OP2);
  not not_35 (not_35_out, OP5);
  not not_36 (not_36_out, OP4);
  not not_37 (not_37_out, OP4);
  not not_38 (not_38_out, OP2);
  not not_39 (not_39_out, OP1);
  not not_40 (not_40_out, OP0);
  not not_41 (not_41_out, OP5);
  not not_42 (not_42_out, OP4);
  not not_43 (not_43_out, OP3);
  not not_44 (not_44_out, OP2);
  not not_45 (not_45_out, OP1);
  not not_46 (not_46_out, OP0);
  not not_47 (not_47_out, F5);
  not not_48 (not_48_out, F4);
  not not_49 (not_49_out, F3);
  not not_50 (not_50_out, F2);
  not not_51 (not_51_out, F1);
  not not_52 (not_52_out, F0);
  not not_53 (not_53_out, OP5);
  not not_54 (not_54_out, OP4);
  not not_55 (not_55_out, OP3);
  not not_56 (not_56_out, OP2);
  not not_57 (not_57_out, OP1);
  not not_58 (not_58_out, OP0);
  not not_59 (not_59_out, F5);
  not not_60 (not_60_out, F4);
  not not_61 (not_61_out, F3);
  not not_62 (not_62_out, F2);
  not not_63 (not_63_out, OP5);
  not not_64 (not_64_out, OP4);
  not not_65 (not_65_out, OP3);
  not not_66 (not_66_out, OP2);
  not not_67 (not_67_out, OP1);
  not not_68 (not_68_out, OP0);
  not not_69 (not_69_out, F5);
  not not_70 (not_70_out, F4);
  not not_71 (not_71_out, F3);
  not not_72 (not_72_out, F2);
  not not_73 (not_73_out, F0);
  not not_74 (not_74_out, OP5);
  not not_75 (not_75_out, OP4);
  not not_76 (not_76_out, OP3);
  not not_77 (not_77_out, OP2);
  not not_78 (not_78_out, OP1);
  not not_79 (not_79_out, OP0);
  not not_80 (not_80_out, F4);
  not not_81 (not_81_out, F3);
  not not_82 (not_82_out, F2);
  not not_83 (not_83_out, F1);
  not not_84 (not_84_out, F0);
  not not_85 (not_85_out, OP5);
  not not_86 (not_86_out, OP4);
  not not_87 (not_87_out, OP3);
  not not_88 (not_88_out, OP2);
  not not_89 (not_89_out, OP1);
  not not_90 (not_90_out, OP0);
  not not_91 (not_91_out, F4);
  not not_92 (not_92_out, F3);
  not not_93 (not_93_out, F2);
  not not_94 (not_94_out, F1);
  not not_95 (not_95_out, OP5);
  not not_96 (not_96_out, OP4);
  not not_97 (not_97_out, OP3);
  not not_98 (not_98_out, OP2);
  not not_99 (not_99_out, OP1);
  not not_100 (not_100_out, OP0);
  not not_101 (not_101_out, F4);
  not not_102 (not_102_out, F3);
  not not_103 (not_103_out, F2);
  not not_104 (not_104_out, F0);
  not not_105 (not_105_out, OP5);
  not not_106 (not_106_out, OP4);
  not not_107 (not_107_out, OP3);
  not not_108 (not_108_out, OP2);
  not not_109 (not_109_out, OP1);
  not not_110 (not_110_out, OP0);
  not not_111 (not_111_out, F4);
  not not_112 (not_112_out, F3);
  not not_113 (not_113_out, F1);
  not not_114 (not_114_out, F0);
  not not_115 (not_115_out, OP5);
  not not_116 (not_116_out, OP4);
  not not_117 (not_117_out, OP3);
  not not_118 (not_118_out, OP2);
  not not_119 (not_119_out, OP1);
  not not_120 (not_120_out, OP0);
  not not_121 (not_121_out, F4);
  not not_122 (not_122_out, F3);
  not not_123 (not_123_out, F1);
  not not_124 (not_124_out, OP5);
  not not_125 (not_125_out, OP4);
  not not_126 (not_126_out, OP3);
  not not_127 (not_127_out, OP2);
  not not_128 (not_128_out, OP1);
  not not_129 (not_129_out, OP0);
  not not_130 (not_130_out, F4);
  not not_131 (not_131_out, F3);
  not not_132 (not_132_out, OP5);
  not not_133 (not_133_out, OP4);
  not not_134 (not_134_out, OP3);
  not not_135 (not_135_out, OP2);
  not not_136 (not_136_out, OP1);
  not not_137 (not_137_out, OP0);
  not not_138 (not_138_out, F4);
  not not_139 (not_139_out, F2);
  not not_140 (not_140_out, F0);
  not not_141 (not_141_out, OP5);
  not not_142 (not_142_out, OP4);
  not not_143 (not_143_out, OP3);
  not not_144 (not_144_out, OP2);
  not not_145 (not_145_out, OP1);
  not not_146 (not_146_out, OP0);
  not not_147 (not_147_out, F4);
  not not_148 (not_148_out, F2);
  not not_149 (not_149_out, OP5);
  not not_150 (not_150_out, OP4);
  not not_151 (not_151_out, OP3);
  not not_152 (not_152_out, OP2);
  not not_153 (not_153_out, OP5);
  not not_154 (not_154_out, OP4);
  not not_155 (not_155_out, OP2);
  not not_156 (not_156_out, OP1);
  not not_157 (not_157_out, OP0);
  not not_158 (not_158_out, OP5);
  not not_159 (not_159_out, OP4);
  not not_160 (not_160_out, OP1);
  not not_161 (not_161_out, OP0);
  not not_162 (not_162_out, OP5);
  not not_163 (not_163_out, OP4);
  not not_164 (not_164_out, OP2);
  not not_165 (not_165_out, OP1);
  not not_166 (not_166_out, OP5);
  not not_167 (not_167_out, OP4);
  not not_168 (not_168_out, OP2);
  not not_169 (not_169_out, OP0);
  not not_170 (not_170_out, OP5);
  not not_171 (not_171_out, OP4);
  not not_172 (not_172_out, OP1);
  not not_173 (not_173_out, OP4);
  not not_174 (not_174_out, OP3);
  not not_175 (not_175_out, OP2);
  not not_176 (not_176_out, OP5);
  not not_177 (not_177_out, OP4);
  not not_178 (not_178_out, OP3);
  not not_179 (not_179_out, OP2);
  not not_180 (not_180_out, OP1);
  not not_181 (not_181_out, OP0);
  not not_182 (not_182_out, F4);
  not not_183 (not_183_out, F3);
  not not_184 (not_184_out, F2);
  not not_185 (not_185_out, OP5);
  not not_186 (not_186_out, OP4);
  not not_187 (not_187_out, OP5);
  not not_188 (not_188_out, OP4);
  not not_189 (not_189_out, OP3);
  not not_190 (not_190_out, OP2);
  not not_191 (not_191_out, OP1);
  not not_192 (not_192_out, OP0);
  not not_193 (not_193_out, F5);
  not not_194 (not_194_out, F4);
  not not_195 (not_195_out, F1);
  not not_196 (not_196_out, F0);
  not not_197 (not_197_out, OP5);
  not not_198 (not_198_out, OP4);
  not not_199 (not_199_out, OP3);
  not not_200 (not_200_out, OP1);
  not not_201 (not_201_out, OP0);
  not not_202 (not_202_out, OP5);
  not not_203 (not_203_out, OP4);
  not not_204 (not_204_out, OP3);
  not not_205 (not_205_out, OP1);
  not not_206 (not_206_out, OP5);
  not not_207 (not_207_out, OP4);
  not not_208 (not_208_out, OP2);
  not not_209 (not_209_out, OP1);
  not not_210 (not_210_out, OP0);
  not not_211 (not_211_out, OP5);
  not not_212 (not_212_out, OP4);
  not not_213 (not_213_out, OP2);
  not not_214 (not_214_out, OP1);
  not not_215 (not_215_out, OP5);
  not not_216 (not_216_out, OP4);
  not not_217 (not_217_out, OP2);
  not not_218 (not_218_out, OP0);
  not not_219 (not_219_out, OP4);
  not not_220 (not_220_out, OP3);
  not not_221 (not_221_out, OP2);
  not not_222 (not_222_out, OP4);
  not not_223 (not_223_out, OP2);
  not not_224 (not_224_out, OP4);
  not not_225 (not_225_out, OP2);
  not not_226 (not_226_out, OP1);
  not not_227 (not_227_out, OP0);
  not not_228 (not_228_out, OP5);
  not not_229 (not_229_out, OP4);
  not not_230 (not_230_out, OP3);
  not not_231 (not_231_out, OP2);
  not not_232 (not_232_out, OP1);
  not not_233 (not_233_out, OP5);
  not not_234 (not_234_out, OP4);
  not not_235 (not_235_out, OP3);
  not not_236 (not_236_out, OP2);
  not not_237 (not_237_out, OP1);
  not not_238 (not_238_out, OP0);
  not not_239 (not_239_out, F5);
  not not_240 (not_240_out, F4);
  not not_241 (not_241_out, F3);
  not not_242 (not_242_out, F2);
  not not_243 (not_243_out, F1);
  not not_244 (not_244_out, F0);
  not not_245 (not_245_out, OP5);
  not not_246 (not_246_out, OP4);
  not not_247 (not_247_out, OP3);
  not not_248 (not_248_out, OP2);
  not not_249 (not_249_out, OP1);
  not not_250 (not_250_out, OP0);
  not not_251 (not_251_out, F5);
  not not_252 (not_252_out, F4);
  not not_253 (not_253_out, F3);
  not not_254 (not_254_out, F2);
  not not_255 (not_255_out, OP5);
  not not_256 (not_256_out, OP4);
  not not_257 (not_257_out, OP3);
  not not_258 (not_258_out, OP2);
  not not_259 (not_259_out, OP1);
  not not_260 (not_260_out, OP0);
  not not_261 (not_261_out, F5);
  not not_262 (not_262_out, F4);
  not not_263 (not_263_out, F3);
  not not_264 (not_264_out, F2);
  not not_265 (not_265_out, F0);
  not not_266 (not_266_out, OP5);
  not not_267 (not_267_out, OP4);
  not not_268 (not_268_out, OP3);
  not not_269 (not_269_out, OP2);
  not not_270 (not_270_out, OP1);
  not not_271 (not_271_out, OP0);
  not not_272 (not_272_out, F4);
  not not_273 (not_273_out, F3);
  not not_274 (not_274_out, F2);
  not not_275 (not_275_out, F1);
  not not_276 (not_276_out, F0);
  not not_277 (not_277_out, OP5);
  not not_278 (not_278_out, OP4);
  not not_279 (not_279_out, OP3);
  not not_280 (not_280_out, OP2);
  not not_281 (not_281_out, OP1);
  not not_282 (not_282_out, OP0);
  not not_283 (not_283_out, F4);
  not not_284 (not_284_out, F3);
  not not_285 (not_285_out, F2);
  not not_286 (not_286_out, F1);
  not not_287 (not_287_out, OP5);
  not not_288 (not_288_out, OP4);
  not not_289 (not_289_out, OP3);
  not not_290 (not_290_out, OP2);
  not not_291 (not_291_out, OP1);
  not not_292 (not_292_out, OP0);
  not not_293 (not_293_out, F4);
  not not_294 (not_294_out, F3);
  not not_295 (not_295_out, F2);
  not not_296 (not_296_out, F0);
  not not_297 (not_297_out, OP5);
  not not_298 (not_298_out, OP4);
  not not_299 (not_299_out, OP3);
  not not_300 (not_300_out, OP2);
  not not_301 (not_301_out, OP1);
  not not_302 (not_302_out, OP0);
  not not_303 (not_303_out, F4);
  not not_304 (not_304_out, F3);
  not not_305 (not_305_out, F1);
  not not_306 (not_306_out, F0);
  not not_307 (not_307_out, OP5);
  not not_308 (not_308_out, OP4);
  not not_309 (not_309_out, OP3);
  not not_310 (not_310_out, OP2);
  not not_311 (not_311_out, OP1);
  not not_312 (not_312_out, OP0);
  not not_313 (not_313_out, F4);
  not not_314 (not_314_out, F3);
  not not_315 (not_315_out, F1);
  not not_316 (not_316_out, OP5);
  not not_317 (not_317_out, OP4);
  not not_318 (not_318_out, OP3);
  not not_319 (not_319_out, OP2);
  not not_320 (not_320_out, OP1);
  not not_321 (not_321_out, OP0);
  not not_322 (not_322_out, F4);
  not not_323 (not_323_out, F3);
  not not_324 (not_324_out, OP5);
  not not_325 (not_325_out, OP4);
  not not_326 (not_326_out, OP3);
  not not_327 (not_327_out, OP2);
  not not_328 (not_328_out, OP1);
  not not_329 (not_329_out, OP0);
  not not_330 (not_330_out, F4);
  not not_331 (not_331_out, F2);
  not not_332 (not_332_out, F0);
  not not_333 (not_333_out, OP5);
  not not_334 (not_334_out, OP4);
  not not_335 (not_335_out, OP3);
  not not_336 (not_336_out, OP2);
  not not_337 (not_337_out, OP1);
  not not_338 (not_338_out, OP0);
  not not_339 (not_339_out, F4);
  not not_340 (not_340_out, F2);
  not not_341 (not_341_out, OP5);
  not not_342 (not_342_out, OP4);
  not not_343 (not_343_out, OP3);
  not not_344 (not_344_out, OP2);
  not not_345 (not_345_out, OP1);
  not not_346 (not_346_out, OP0);
  not not_347 (not_347_out, F4);
  not not_348 (not_348_out, F3);
  not not_349 (not_349_out, F2);
  not not_350 (not_350_out, OP5);
  not not_351 (not_351_out, OP4);
  not not_352 (not_352_out, OP3);
  not not_353 (not_353_out, OP1);
  not not_354 (not_354_out, OP0);
  not not_355 (not_355_out, OP5);
  not not_356 (not_356_out, OP4);
  not not_357 (not_357_out, OP3);
  not not_358 (not_358_out, OP1);
  not not_359 (not_359_out, OP5);
  not not_360 (not_360_out, OP4);
  not not_361 (not_361_out, OP3);
  not not_362 (not_362_out, OP2);
  not not_363 (not_363_out, OP1);
  not not_364 (not_364_out, OP0);
  not not_365 (not_365_out, F5);
  not not_366 (not_366_out, F4);
  not not_367 (not_367_out, F2);
  not not_368 (not_368_out, F1);
  not not_369 (not_369_out, F0);
  not not_370 (not_370_out, OP5);
  not not_371 (not_371_out, OP4);
  not not_372 (not_372_out, OP3);
  not not_373 (not_373_out, OP2);
  not not_374 (not_374_out, OP1);
  not not_375 (not_375_out, OP0);
  not not_376 (not_376_out, F5);
  not not_377 (not_377_out, F4);
  not not_378 (not_378_out, F2);
  not not_379 (not_379_out, F1);
  not not_380 (not_380_out, F0);
  not not_381 (not_381_out, OP5);
  not not_382 (not_382_out, OP4);
  not not_383 (not_383_out, OP3);
  not not_384 (not_384_out, OP2);
  not not_385 (not_385_out, OP0);
  not not_386 (not_386_out, OP5);
  not not_387 (not_387_out, OP4);
  not not_388 (not_388_out, OP3);
  not not_389 (not_389_out, OP2);
  not not_390 (not_390_out, OP5);
  not not_391 (not_391_out, OP4);
  not not_392 (not_392_out, OP3);
  not not_393 (not_393_out, OP2);
  not not_394 (not_394_out, OP5);
  not not_395 (not_395_out, OP4);
  not not_396 (not_396_out, OP3);
  not not_397 (not_397_out, OP2);
  not not_398 (not_398_out, OP1);
  not not_399 (not_399_out, OP4);
  not not_400 (not_400_out, OP2);
  not not_401 (not_401_out, OP1);
  not not_402 (not_402_out, OP0);
  not not_403 (not_403_out, OP5);
  not not_404 (not_404_out, OP4);
  not not_405 (not_405_out, OP5);
  not not_406 (not_406_out, OP3);
  not not_407 (not_407_out, OP2);
  not not_408 (not_408_out, OP1);
  not not_409 (not_409_out, OP0);
  not not_410 (not_410_out, F5);
  not not_411 (not_411_out, F2);
  not not_412 (not_412_out, F1);
  not not_413 (not_413_out, F0);
  and and_1 (MemToReg, OP5, not_1_out, not_2_out, not_3_out, OP1, OP0);
  and and_2 (and_2_out, OP5, not_4_out, OP3, not_5_out, OP1, OP0);
  and and_3 (and_3_out, OP5, not_6_out, OP3, not_7_out, not_8_out, not_9_out);
  and and_4 (and_4_out, not_10_out, not_11_out, OP3, not_12_out, not_13_out, not_14_out);
  and and_5 (and_5_out, not_15_out, not_16_out, OP3, OP2, not_17_out, not_18_out);
  and and_6 (and_6_out, not_19_out, not_20_out, OP3, not_21_out, not_22_out, OP0);
  and and_7 (and_7_out, not_23_out, not_24_out, OP3, not_25_out, OP1, not_26_out);
  and and_8 (and_8_out, not_27_out, not_28_out, OP3, OP2, not_29_out, OP0);
  and and_9 (and_9_out, OP5, not_30_out, not_31_out, not_32_out, OP1, OP0);
  and and_10 (and_10_out, OP5, not_33_out, OP3, not_34_out, OP1, OP0);
  and and_11 (and_11_out, not_35_out, not_36_out, OP3, OP2, OP1, OP0);
  and and_12 (and_12_out, OP5, not_37_out, OP3, not_38_out, not_39_out, not_40_out);
  and and_13 (and_13_out, not_41_out, not_42_out, not_43_out, not_44_out, not_45_out, not_46_out, not_47_out, not_48_out, not_49_out, not_50_out, not_51_out, not_52_out);
  and and_14 (and_14_out, not_53_out, not_54_out, not_55_out, not_56_out, not_57_out, not_58_out, not_59_out, not_60_out, not_61_out, not_62_out, F1, F0);
  and and_15 (and_15_out, not_63_out, not_64_out, not_65_out, not_66_out, not_67_out, not_68_out, not_69_out, not_70_out, not_71_out, not_72_out, F1, not_73_out);
  and and_16 (and_16_out, not_74_out, not_75_out, not_76_out, not_77_out, not_78_out, not_79_out, F5, not_80_out, not_81_out, not_82_out, not_83_out, not_84_out);
  and and_17 (and_17_out, not_85_out, not_86_out, not_87_out, not_88_out, not_89_out, not_90_out, F5, not_91_out, not_92_out, not_93_out, not_94_out, F0);
  and and_18 (and_18_out, not_95_out, not_96_out, not_97_out, not_98_out, not_99_out, not_100_out, F5, not_101_out, not_102_out, not_103_out, F1, not_104_out);
  and and_19 (and_19_out, not_105_out, not_106_out, not_107_out, not_108_out, not_109_out, not_110_out, F5, not_111_out, not_112_out, F2, not_113_out, not_114_out);
  and and_20 (and_20_out, not_115_out, not_116_out, not_117_out, not_118_out, not_119_out, not_120_out, F5, not_121_out, not_122_out, F2, not_123_out, F0);
  and and_21 (and_21_out, not_124_out, not_125_out, not_126_out, not_127_out, not_128_out, not_129_out, F5, not_130_out, not_131_out, F2, F1, F0);
  and and_22 (and_22_out, not_132_out, not_133_out, not_134_out, not_135_out, not_136_out, not_137_out, F5, not_138_out, F3, not_139_out, F1, not_140_out);
  and and_23 (and_23_out, not_141_out, not_142_out, not_143_out, not_144_out, not_145_out, not_146_out, F5, not_147_out, F3, not_148_out, F1, F0);
  and and_24 (and_24_out, not_149_out, not_150_out, not_151_out, not_152_out, OP1, OP0);
  and and_25 (and_25_out, not_153_out, not_154_out, OP3, not_155_out, not_156_out, not_157_out);
  and and_26 (and_26_out, not_158_out, not_159_out, OP3, OP2, not_160_out, not_161_out);
  and and_27 (and_27_out, not_162_out, not_163_out, OP3, not_164_out, not_165_out, OP0);
  and and_28 (and_28_out, not_166_out, not_167_out, OP3, not_168_out, OP1, not_169_out);
  and and_29 (and_29_out, not_170_out, not_171_out, OP3, OP2, not_172_out, OP0);
  and and_30 (and_30_out, OP5, not_173_out, not_174_out, not_175_out, OP1, OP0);
  and and_31 (and_31_out, not_176_out, not_177_out, not_178_out, not_179_out, not_180_out, not_181_out, F5, not_182_out, not_183_out, not_184_out, F1, F0);
  and and_32 (and_32_out, not_185_out, not_186_out, OP3, OP2, OP1, OP0);
  and and_33 (SysCALL, not_187_out, not_188_out, not_189_out, not_190_out, not_191_out, not_192_out, not_193_out, not_194_out, F3, F2, not_195_out, not_196_out);
  and and_34 (and_34_out, not_197_out, not_198_out, not_199_out, OP2, not_200_out, not_201_out);
  and and_35 (and_35_out, not_202_out, not_203_out, not_204_out, OP2, not_205_out, OP0);
  and and_36 (and_36_out, not_206_out, not_207_out, OP3, not_208_out, not_209_out, not_210_out);
  and and_37 (and_37_out, not_211_out, not_212_out, OP3, not_213_out, not_214_out, OP0);
  and and_38 (and_38_out, not_215_out, not_216_out, OP3, not_217_out, OP1, not_218_out);
  and and_39 (and_39_out, OP5, not_219_out, not_220_out, not_221_out, OP1, OP0);
  and and_40 (and_40_out, OP5, not_222_out, OP3, not_223_out, OP1, OP0);
  and and_41 (and_41_out, OP5, not_224_out, OP3, not_225_out, not_226_out, not_227_out);
  and and_42 (and_42_out, not_228_out, not_229_out, not_230_out, not_231_out, not_232_out, OP0);
  and and_43 (and_43_out, not_233_out, not_234_out, not_235_out, not_236_out, not_237_out, not_238_out, not_239_out, not_240_out, not_241_out, not_242_out, not_243_out, not_244_out);
  and and_44 (and_44_out, not_245_out, not_246_out, not_247_out, not_248_out, not_249_out, not_250_out, not_251_out, not_252_out, not_253_out, not_254_out, F1, F0);
  and and_45 (and_45_out, not_255_out, not_256_out, not_257_out, not_258_out, not_259_out, not_260_out, not_261_out, not_262_out, not_263_out, not_264_out, F1, not_265_out);
  and and_46 (and_46_out, not_266_out, not_267_out, not_268_out, not_269_out, not_270_out, not_271_out, F5, not_272_out, not_273_out, not_274_out, not_275_out, not_276_out);
  and and_47 (and_47_out, not_277_out, not_278_out, not_279_out, not_280_out, not_281_out, not_282_out, F5, not_283_out, not_284_out, not_285_out, not_286_out, F0);
  and and_48 (and_48_out, not_287_out, not_288_out, not_289_out, not_290_out, not_291_out, not_292_out, F5, not_293_out, not_294_out, not_295_out, F1, not_296_out);
  and and_49 (and_49_out, not_297_out, not_298_out, not_299_out, not_300_out, not_301_out, not_302_out, F5, not_303_out, not_304_out, F2, not_305_out, not_306_out);
  and and_50 (and_50_out, not_307_out, not_308_out, not_309_out, not_310_out, not_311_out, not_312_out, F5, not_313_out, not_314_out, F2, not_315_out, F0);
  and and_51 (and_51_out, not_316_out, not_317_out, not_318_out, not_319_out, not_320_out, not_321_out, F5, not_322_out, not_323_out, F2, F1, F0);
  and and_52 (and_52_out, not_324_out, not_325_out, not_326_out, not_327_out, not_328_out, not_329_out, F5, not_330_out, F3, not_331_out, F1, not_332_out);
  and and_53 (and_53_out, not_333_out, not_334_out, not_335_out, not_336_out, not_337_out, not_338_out, F5, not_339_out, F3, not_340_out, F1, F0);
  and and_54 (and_54_out, not_341_out, not_342_out, not_343_out, not_344_out, not_345_out, not_346_out, F5, not_347_out, not_348_out, not_349_out, F1, F0);
  and and_55 (BEQ, not_350_out, not_351_out, not_352_out, OP2, not_353_out, not_354_out);
  and and_56 (BNE, not_355_out, not_356_out, not_357_out, OP2, not_358_out, OP0);
  and and_57 (JR, not_359_out, not_360_out, not_361_out, not_362_out, not_363_out, not_364_out, not_365_out, not_366_out, F3, not_367_out, not_368_out, not_369_out);
  and and_58 (and_58_out, not_370_out, not_371_out, not_372_out, not_373_out, not_374_out, not_375_out, not_376_out, not_377_out, F3, not_378_out, not_379_out, not_380_out);
  and and_59 (and_59_out, not_381_out, not_382_out, not_383_out, not_384_out, OP1, not_385_out);
  and and_60 (and_60_out, not_386_out, not_387_out, not_388_out, not_389_out, OP1, OP0);
  and and_61 (JAL, not_390_out, not_391_out, not_392_out, not_393_out, OP1, OP0);
  and and_62 (BLTZ, not_394_out, not_395_out, not_396_out, not_397_out, not_398_out, OP0);
  and and_63 (SB, OP5, not_399_out, OP3, not_400_out, not_401_out, not_402_out);
  and and_64 (LUI, not_403_out, not_404_out, OP3, OP2, OP1, OP0);
  and and_65 (ERET, not_405_out, OP4, not_406_out, not_407_out, not_408_out, not_409_out, not_410_out, F4, F3, not_411_out, not_412_out, not_413_out);
  or or_1 (MemWrite, and_2_out, and_3_out);
  or or_2 (ALU_SRC, and_4_out, and_5_out, and_6_out, and_7_out, and_8_out, and_9_out, and_10_out, and_11_out, and_12_out);
  or or_3 (SignedExt, and_34_out, and_35_out, and_36_out, and_37_out, and_38_out, and_39_out, and_40_out, and_41_out, and_42_out);
  or or_4 (JUMP, and_58_out, and_59_out, and_60_out);
  or or_5 (RegWrite, and_13_out, and_14_out, and_15_out, and_16_out, and_17_out, and_18_out, and_19_out, and_20_out, and_21_out, and_22_out, and_23_out, and_24_out, and_25_out, and_26_out, and_27_out, and_28_out, and_29_out, and_30_out, and_31_out, and_32_out);
  or or_6 (RegDst, and_43_out, and_44_out, and_45_out, and_46_out, and_47_out, and_48_out, and_49_out, and_50_out, and_51_out, and_52_out, and_53_out, and_54_out);
endmodule

// ALU
module MIPS_ALU (
  input  [4:0] shamt,
  input  [31:0] X,
  input  [31:0] Y,
  input  [3:0] AluOP,
  output Equal,
  output [31:0] Result,
  output [31:0] Result_2
);

  wire [0:0] comparator_1_lt, comparator_2_lt;
  wire [31:0] adder_1_out, AND_out, divider_1_out, divider_1_rem, multiplier_1_cout, multiplier_1_out,
       NOR_out, OR_out, shifter_1_out, shifter_2_out, shifter_3_out, subtractor_1_out, XOR_out;

  assign AND_out = X & Y;  // AND_Gate AND, 32 bits wide
  assign OR_out = X | Y;  // OR_Gate OR, 32 bits wide
  Shifter #(.width(32), .shift("ll")) shifter_1 (.in(Y), .\dist (shamt), .out(shifter_1_out));
  Shifter #(.width(32), .shift("ar")) shifter_2 (.in(Y), .\dist (shamt), .out(shifter_2_out));
  Shifter #(.width(32), .shift("lr")) shifter_3 (.in(Y), .\dist (shamt), .out(shifter_3_out));
  Multiplier #(.width(32)) multiplier_1 (.a(X), .b(Y), .out(multiplier_1_out), .cout(multiplier_1_cout));  // open: cin
  Divider #(.width(32)) divider_1 (.a(X), .b(Y), .out(divider_1_out), .rem(divider_1_rem));  // open: upper
  Adder #(.width(32)) adder_1 (.a(X), .b(Y), .out(adder_1_out));  // open: cin, cout
  Subtractor #(.width(32)) subtractor_1 (.a(X), .b(Y), .out(subtractor_1_out));  // open: bin, bout
  assign XOR_out = X ^ Y;  // XOR_Gate XOR, 32 bits wide
  assign NOR_out = ~(X | Y);  // NOR_Gate NOR, 32 bits wide
  Comparator #(.width(32), .mode("twosComplement")) comparator_1 (
    .a(X), .b(Y), .eq(Equal), .lt(comparator_1_lt[0]));  // open: gt
  Comparator #(.width(32), .mode("unsigned")) comparator_2 (.a(X), .b(Y), .lt(comparator_2_lt[0]));  // open: gt, eq
  Multiplexer #(.select(4), .width(32), .disabled("Z"), .enable("false")) multiplexer_1 (
    .in0(shifter_1_out), .in1(shifter_2_out), .in2(shifter_3_out), .in3(multiplier_1_out),
    .in4(divider_1_out), .in5(adder_1_out), .in6(subtractor_1_out), .in7(AND_out), .in8(OR_out),
    .in9(XOR_out), .in10(NOR_out), .in11({{31{1'b0}}, comparator_1_lt[0]}),
    .in12({{31{1'b0}}, comparator_2_lt[0]}), .in13({32{1'b0}}), .in14({32{1'b0}}), .in15({32{1'b0}}),
    .out(Result), .sel(AluOP));
  Multiplexer #(.select(4), .width(32), .disabled("Z"), .enable("false")) multiplexer_2 (
    .in0({32{1'b0}}), .in1({32{1'b0}}), .in2({32{1'b0}}), .in3(multiplier_1_cout), .in4(divider_1_rem),
    .in5({32{1'b0}}), .in6({32{1'b0}}), .in7({32{1'b0}}), .in8({32{1'b0}}), .in9({32{1'b0}}),
    .in10({32{1'b0}}), .in11({32{1'b0}}), .in12({32{1'b0}}), .in13({32{1'b0}}), .in14({32{1'b0}}),
    .in15({32{1'b0}}), .out(Result_2), .sel(AluOP));

  // Other names for the same wires on the sheet: Result2[31:0] = Result_2; S[3:0] = AluOP

  // Notes on the sheet:
  //   不要改变此引脚区域内容，也不要改变ALU封装形式
  //   输入引脚
  //   输出引脚
endmodule

module MIPS_Regifile (
  input  [31:0] Din,
  input  Clk,
  input  WE,
  input  [4:0] R1_num,
  input  [4:0] W_num,
  input  [4:0] R2_num,
  output [31:0] R1,
  output [31:0] R2
);

  // RegisterFile registerfile_1: pin names not known; wires that end beside it: Din, Clk, WE, W_num, R1_num, R2_num, R1, R2
endmodule

module \理想流水线  (
  output RegWrite,
  output MemWrite,
  output [31:0] IF_PC,
  output [31:0] ID_PC,
  output [31:0] EX_PC,
  output [31:0] M_PC,
  output [31:0] WB_PC,
  output [31:0] RDin,
  output [31:0] MDin,
  output [31:0] LedData
);

  wire and_1_out, and_2_out, CLK, clock_1_out, clock_2_out, comparator_1_eq, comparator_1_lt,
       comparator_2_eq, d_ff_1_q, ex_mem_1_equal_out, ex_mem_1_jal_out, ex_mem_1_memtoreg_out,
       ex_mem_1_regdst_out, ex_mem_1_regwrite_out, ex_mem_1_syscall_out, Go, Halt, id_ex_1_alu_src_out,
       id_ex_1_beq_out, id_ex_1_bne_out, id_ex_1_jal_out, id_ex_1_memtoreg_out, id_ex_1_memwrite_out,
       id_ex_1_regdst_in, id_ex_1_regwrite_out, id_ex_1_syscall_out, IR1, IR2, IR3, J2, JMP, JR, Ledout,
       mem_wb_1_jal_out, mem_wb_1_memtoreg_out, mem_wb_1_regdst_out, mem_wb_1_syscall_out, mips_alu_1_equal,
       nand_1_out, not_1_out, or_1_out, RST, SignedExt, W1, W2, W3, Write, \单周期硬布线控制器_1_alu_src ,
       \单周期硬布线控制器_1_beq , \单周期硬布线控制器_1_bne , \单周期硬布线控制器_1_jal , \单周期硬布线控制器_1_jmp , \单周期硬布线控制器_1_jr ,
       \单周期硬布线控制器_1_memtoreg , \单周期硬布线控制器_1_memwrite , \单周期硬布线控制器_1_regdst , \单周期硬布线控制器_1_regwrite ,
       \单周期硬布线控制器_1_syscall ;
  wire [3:0] id_ex_1_aluop_out, \单周期硬布线控制器_1_alu_op ;
  wire [4:0] multiplexer_2_out, multiplexer_3_out, multiplexer_8_out, W_num;
  wire [12:0] CNT_num;
  wire [15:0] \LoadUse次数 , \总周期数 , \插入气泡数 , \无条件分支数 , \条件分支成功数 ;
  wire [25:0] addr;
  wire [31:0] adder_3_out, bit_extender_1_out, bit_extender_2_out, ex_mem_1_aluresult_out, id_ex_1_imm_out,
       ID_IR, IF_IR, MEM_IR, mem_wb_1_aluresult_out, mem_wb_1_rd_out, mips_alu_1_result, mips_regifile_1_r2,
       multiplexer_1_out, multiplexer_4_out, multiplexer_5_out, multiplexer_6_out, multiplexer_7_out, PC4,
       PC_JR, PCimm, R1, R2, ram_1_data, register_1_q, register_2_q, shifter_1_out, WB_IR;
  wire [31:26] EX_IR;

  Button \u_总复位  (.out(RST));
  Button _1 (.out(IR1));
  Button _2 (.out(IR2));
  Button _3 (.out(IR3));
  // Probe on \总周期数 
  // Probe on \总周期数 
  Button \u_继续运行  (.out(Go));
  LED #(.active("true")) led_1 (.in(W1));
  LED #(.active("true")) led_2 (.in(W2));
  LED #(.active("true")) led_3 (.in(W3));
  Hex_Digit_Display hex_digit_display_1 (.value(LedData[31:28]));  // open: dp
  // Probe on IF_PC[19:0]
  // Mips_Probe mips_probe_1: pin names not known; wires that end beside it: IF_IR
  Hex_Digit_Display hex_digit_display_2 (.value(LedData[23:20]));  // open: dp
  Hex_Digit_Display hex_digit_display_3 (.value(LedData[27:24]));  // open: dp
  // Probe on ID_PC[19:0]
  // Mips_Probe mips_probe_2: pin names not known; wires that end beside it: ID_IR
  Hex_Digit_Display hex_digit_display_4 (.value(LedData[19:16]));  // open: dp
  Hex_Digit_Display hex_digit_display_5 (.value(LedData[15:12]));  // open: dp
  Hex_Digit_Display hex_digit_display_6 (.value(LedData[11:8]));  // open: dp
  Hex_Digit_Display hex_digit_display_7 (.value(LedData[7:4]));  // open: dp
  Clock #(.highDuration(1), .lowDuration(1)) clock_1 (.out(clock_1_out));
  // Probe on EX_PC[19:0]
  // Mips_Probe mips_probe_3: pin names not known; wires that end beside it: clock_1_out, {EX_IR, addr}, CLK
  Multiplexer #(.select(3), .width(32), .disabled("Z"), .enable("false")) multiplexer_1 (
    .in0(PC4), .in1(PCimm), .in2({PC4[31:28], addr, 2'b00}), .in6(PC_JR), .out(multiplexer_1_out),
    .sel({JR, JMP, J2}));  // open: in3, in4, in5, in7
  Hex_Digit_Display hex_digit_display_8 (.value(LedData[3:0]));  // open: dp
  or or_1 (or_1_out, ~Halt, Go);  // OR_Gate
  // Probe on \总周期数 
  // Probe on M_PC[19:0]
  // Mips_Probe mips_probe_4: pin names not known; wires that end beside it: MEM_IR
  Register #(.width(32), .trigger("rising"), .Select("low")) PC (
    .D(multiplexer_1_out), .en(or_1_out), .Q(IF_PC), .clk(CLK), .clr(RST));
  Counter #(.width(16), .max('hffff), .ongoal("wrap"), .trigger("rising"), .behavior("old")) counter_1 (
    .load(1'b0), .count(or_1_out), .Q(\总周期数 ), .clk(CLK), .clr(RST));  // open: D, carry, preset
  // Probe on \总周期数 
  // Probe on \无条件分支数 
  // Probe on \条件分支成功数 
  // Probe on \插入气泡数 
  // Probe on \LoadUse次数 
  // Probe on IF_PC[11:0]
  // Probe on WB_PC[19:0]
  // Mips_Probe mips_probe_5: pin names not known; wires that end beside it: WB_IR
  ROM #(.addrWidth(10), .dataWidth(32), .Select("high")) rom_1 (.addr(IF_PC[11:2]), .data(IF_IR));
  // Probe on EX_PC[11:0]
  // Probe on ID_PC[11:0]
  // Probe on M_PC[11:0]
  D_Flip_Flop #(.trigger("high"), .Pre_Clr_Positions("LEGACY"), .NegatePresetClear("false"), .enable("true"), .NewFFLayout("false")) d_ff_1 (.Q(d_ff_1_q));  // open: clk, D, Qn, preset, en, reset
  // Probe on 13'hc
  IF_ID if_id_1 (
    .IR_IN(IF_IR), .PC_IN(IF_PC), .IR(ID_IR), .PC(ID_PC), .reset(1'b0), .CLK(CLK), .CLEAR(RST), .ENABLE(Write));  // open: PJUMP_IN, PJUM_OUT
  Adder #(.width(32)) adder_1 (.a(IF_PC), .b(32'h4), .out(PC4));  // open: cin, cout
  // Probe on WB_PC[11:0]
  Comparator #(.width(13), .mode("twosComplement")) comparator_1 (
    .a(CNT_num), .b(13'hc), .eq(comparator_1_eq), .lt(comparator_1_lt));  // open: gt
  Clock #(.highDuration(1), .lowDuration(1)) clock_2 (.out(clock_2_out));
  // Mips_Probe mips_probe_6: pin names not known; wires that end beside it: IF_IR, ID_IR
  nand nand_1 (nand_1_out, d_ff_1_q, comparator_1_eq);
  Counter #(.width(13), .max('h1fff), .ongoal("stay"), .trigger("rising"), .behavior("old")) counter_2 (
    .count(comparator_1_lt), .Q(CNT_num), .clk(clock_2_out));  // open: load, D, carry, clr, preset
  assign CLK = nand_1_out ? clock_2_out : 1'bz;  // Controlled_Buffer controlled_buffer_1
  Pull_Resistor #(.pull(1)) pull_resistor_1 (.node(CLK));
  \单周期硬布线控制器  \u_单周期硬布线控制器_1  (
    .Func(ID_IR[5:0]), .OP(ID_IR[31:26]), .ALU_OP(\单周期硬布线控制器_1_alu_op ), .MemToReg(\单周期硬布线控制器_1_memtoreg ),
    .MemWrite(\单周期硬布线控制器_1_memwrite ), .ALU_SRC(\单周期硬布线控制器_1_alu_src ), .RegWrite(\单周期硬布线控制器_1_regwrite ),
    .SysCALL(\单周期硬布线控制器_1_syscall ), .SignedExt(SignedExt), .RegDst(\单周期硬布线控制器_1_regdst ),
    .JR(\单周期硬布线控制器_1_jr ), .JMP(\单周期硬布线控制器_1_jmp ), .Beq(\单周期硬布线控制器_1_beq ), .JAL(\单周期硬布线控制器_1_jal ),
    .Bne(\单周期硬布线控制器_1_bne ));  // open: ERET, BLTZ, LUI, SB
  Multiplexer #(.select(1), .width(5), .disabled("Z"), .enable("false")) multiplexer_2 (
    .in0(ID_IR[25:21]), .in1(5'b00010), .out(multiplexer_2_out), .sel(\单周期硬布线控制器_1_syscall ));
  Multiplexer #(.select(1), .width(5), .disabled("Z"), .enable("false")) multiplexer_3 (
    .in0(ID_IR[20:16]), .in1(5'b00100), .out(multiplexer_3_out), .sel(\单周期硬布线控制器_1_syscall ));
  assign bit_extender_1_out = {{16{1'b0}}, ID_IR[15:0]};  // Bit_Extender bit_extender_1
  assign bit_extender_2_out = {{16{ID_IR[15]}}, ID_IR[15:0]};  // Bit_Extender bit_extender_2
  Multiplexer #(.select(1), .width(32), .disabled("Z"), .enable("false")) multiplexer_4 (
    .in0(bit_extender_1_out), .in1(bit_extender_2_out), .out(multiplexer_4_out), .sel(SignedExt));
  MIPS_Regifile mips_regifile_1 (
    .Din(RDin), .Clk(CLK), .R1(PC_JR), .R2(mips_regifile_1_r2), .WE(RegWrite), .W_num(W_num),
    .R1_num(multiplexer_2_out), .R2_num(multiplexer_3_out));
  // Probe on mips_regifile_1_r2
  ID_EX id_ex_1 (
    .BEQ_IN(\单周期硬布线控制器_1_beq ), .BNE_IN(\单周期硬布线控制器_1_bne ), .MEMTOREG_IN(\单周期硬布线控制器_1_memtoreg ),
    .MEMWRITE_IN(\单周期硬布线控制器_1_memwrite ), .ALUOP_IN(\单周期硬布线控制器_1_alu_op ),
    .ALU_SRC_IN(\单周期硬布线控制器_1_alu_src ), .REGWRITE_IN(\单周期硬布线控制器_1_regwrite ), .JAL_IN(\单周期硬布线控制器_1_jal ),
    .REGDIST_IN(\单周期硬布线控制器_1_regdst ), .SYSCALL_IN(\单周期硬布线控制器_1_syscall ), .JMP_IN(\单周期硬布线控制器_1_jmp ),
    .JR_IN(\单周期硬布线控制器_1_jr ), .IR_IN(ID_IR), .PC_IN(ID_PC), .R2_IN(mips_regifile_1_r2), .R1_IN(PC_JR),
    .IMM_IN(multiplexer_4_out), .BEQ_OUT(id_ex_1_beq_out), .BNE_OUT(id_ex_1_bne_out),
    .MEMTOREG_OUT(id_ex_1_memtoreg_out), .MEMWRITE_OUT(id_ex_1_memwrite_out), .ALUOP_OUT(id_ex_1_aluop_out),
    .ALU_SRC_OUT(id_ex_1_alu_src_out), .REGWRITE_OUT(id_ex_1_regwrite_out), .JAL_OUT(id_ex_1_jal_out),
    .REGDST_IN(id_ex_1_regdst_in), .SYSCALL_OUT(id_ex_1_syscall_out), .JMP_OUT(JMP), .JR_OUT(JR),
    .IR_OUT({EX_IR, addr}), .PC_OUT(EX_PC), .R2_OUT(R2), .R1_OUT(R1), .IMM_OUT(id_ex_1_imm_out),
    .RESET(1'b0), .CLEAR(RST), .CLK(CLK), .ENABLE(Write));  // open: LUI_IN, LUI_OUT, SB_IN, SB_OUT, BLTZ_IN, BLTZ_OUT, RS_FORW_IN, RS_FORW_OUT, RT_FORW_IN, RT_FORW_OUT, ERET_IN, ERET_OUT, PJUMP_IN, PJUMP_OUT
  Multiplexer #(.select(1), .width(32), .disabled("Z"), .enable("false")) multiplexer_5 (
    .in0(R2), .in1(id_ex_1_imm_out), .out(multiplexer_5_out), .sel(id_ex_1_alu_src_out));
  Shifter #(.width(32), .shift("ll")) shifter_1 (.in(id_ex_1_imm_out), .\dist (5'b00010), .out(shifter_1_out));
  Multiplexer #(.select(1), .width(32), .disabled("Z"), .enable("false")) multiplexer_6 (
    .in0(multiplexer_5_out), .in1(32'h22), .out(multiplexer_6_out), .sel(id_ex_1_syscall_out));
  Adder #(.width(32)) adder_2 (.a(shifter_1_out), .b(PC4), .out(PCimm));  // open: cin, cout
  and and_1 (and_1_out, id_ex_1_beq_out, mips_alu_1_equal);
  and and_2 (and_2_out, id_ex_1_bne_out, ~mips_alu_1_equal);  // AND_Gate
  MIPS_ALU mips_alu_1 (
    .X(R1), .Y(multiplexer_6_out), .AluOP(id_ex_1_aluop_out), .Equal(mips_alu_1_equal),
    .Result(mips_alu_1_result), .shamt(addr[10:6]));  // open: Result_2
  or or_2 (J2, and_1_out, and_2_out);
  EX_MEM ex_mem_1 (
    .MemToReg_in(id_ex_1_memtoreg_out), .MemWrite_in(id_ex_1_memwrite_out),
    .RegWrite_in(id_ex_1_regwrite_out), .JAL_in(id_ex_1_jal_out), .RegDst_in(id_ex_1_regdst_in),
    .Syscall_in(id_ex_1_syscall_out), .equal_in(mips_alu_1_equal), .IR_in({EX_IR, addr}), .PC_in(EX_PC),
    .ALUResult_in(mips_alu_1_result), .R2_in(R2), .MemToReg_out(ex_mem_1_memtoreg_out),
    .MemWrite_out(MemWrite), .RegWrite_out(ex_mem_1_regwrite_out), .JAL_out(ex_mem_1_jal_out),
    .RegDst_out(ex_mem_1_regdst_out), .Syscall_out(ex_mem_1_syscall_out), .equal_out(ex_mem_1_equal_out),
    .IR_out(MEM_IR), .PC_out(M_PC), .ALUResult_out(ex_mem_1_aluresult_out), .R2_out(MDin), .RESET(1'b0),
    .CLK(CLK), .CLEAR(RST), .ENABLE(Write));  // open: R1_in, Imm_in, R1_out, Imm_out, SB_in, SB_out
  RAM #(.addrWidth(10), .dataWidth(32), .bus("separate"), .Select("high")) ram_1 (
    .addr(ex_mem_1_aluresult_out[11:2]), .din(MDin), .data(ram_1_data), .str(MemWrite), .clk(CLK), .clr(RST));  // open: sel, ld
  MEM_WB mem_wb_1 (
    .MemToReg_in(ex_mem_1_memtoreg_out), .MemWrite_in(MemWrite), .RegWrite_in(ex_mem_1_regwrite_out),
    .JAL_in(ex_mem_1_jal_out), .RegDst_in(ex_mem_1_regdst_out), .Syscall_in(ex_mem_1_syscall_out),
    .equal_in(ex_mem_1_equal_out), .IR_in(MEM_IR), .PC_in(M_PC), .ALUResult_in(ex_mem_1_aluresult_out),
    .RD_in(ram_1_data), .MemToReg_out(mem_wb_1_memtoreg_out), .RegWrite_out(RegWrite),
    .JAL_out(mem_wb_1_jal_out), .RegDst_out(mem_wb_1_regdst_out), .Syscall_out(mem_wb_1_syscall_out),
    .IR_out(WB_IR), .PC_out(WB_PC), .ALUResult_out(mem_wb_1_aluresult_out), .RD_out(mem_wb_1_rd_out),
    .\气泡_高电平时有效 (1'b0), .clk(CLK), .clear(RST), .enable(Write));  // open: R1_in, MemWrite_out, equal_out, R1_out, R2_in, R2_out
  Register #(.width(32), .trigger("rising"), .Select("low")) register_1 (
    .D(R1), .Q(register_1_q), .clk(CLK));  // open: en, clr
  Multiplexer #(.select(1), .width(32), .disabled("Z"), .enable("false")) multiplexer_7 (
    .in0(mem_wb_1_aluresult_out), .in1(mem_wb_1_rd_out), .out(multiplexer_7_out), .sel(mem_wb_1_memtoreg_out));
  not not_1 (not_1_out, Go);
  nand nand_2 (Write, not_1_out, Halt);
  Register #(.width(32), .trigger("rising"), .Select("low")) register_2 (
    .D(register_1_q), .Q(register_2_q), .clk(CLK));  // open: en, clr
  Multiplexer #(.select(1), .width(5), .disabled("Z"), .enable("false")) multiplexer_8 (
    .in0(WB_IR[20:16]), .in1(WB_IR[15:11]), .out(multiplexer_8_out), .sel(mem_wb_1_regdst_out));
  Adder #(.width(32)) adder_3 (.a(WB_PC), .b(32'h4), .out(adder_3_out));  // open: cin, cout
  Comparator #(.width(32), .mode("twosComplement")) comparator_2 (
    .a(register_2_q), .b(32'h32), .eq(comparator_2_eq));  // open: gt, lt
  Multiplexer #(.select(1), .width(32), .disabled("Z"), .enable("false")) multiplexer_9 (
    .in0(multiplexer_7_out), .in1(adder_3_out), .out(RDin), .sel(mem_wb_1_jal_out));
  Multiplexer #(.select(1), .width(5), .disabled("Z"), .enable("false")) multiplexer_10 (
    .in0(multiplexer_8_out), .in1({5{1'b1}}), .out(W_num), .sel(mem_wb_1_jal_out));
  and and_3 (Halt, comparator_2_eq, mem_wb_1_syscall_out);
  and and_4 (Ledout, ~comparator_2_eq, mem_wb_1_syscall_out);  // AND_Gate
  Register #(.width(32), .trigger("rising"), .Select("low")) register_3 (
    .D(R2), .en(Ledout), .Q(LedData), .clk(CLK), .clr(RST));

  // Other names for the same wires on the sheet: RD[4:0] = ID_IR[15:11]; MEM_PC[31:0] = M_PC; EX_IR[25:0] = addr;
  //   PC_JAL[31:2] = {PC4[31:28], addr}; shamt[4:0] = addr[10:6]

  // Notes on the sheet:
  //   中断源
  //   时空图监测，可删除
  //   中断等待指示
  //   数码管输出
  //   指令存储器
  //   contents of rom_1 (hex, n*v repeats v):
  //   20100000 20110000 20120000 20130000 36100000 36310001 36520002 36730003 ae100000 ae110004 ae120008
  //   ae13000c 2002000a 20110000 20120000 20130000 c
  //   控制位
  //   流水调试日志用
  //   暂停节拍，不能为0
  //   指令字
  //   戳工具置1进入计数暂停模式，ctrl+k时钟自动运行到对应节拍暂停
  //   ctrl+k关闭时钟连续运行，将控制位置零，进入单步调试模式调试
  //   用这个时钟源需要去掉电路中的其他时钟源
  //   OP
  //   Func
  //   rs
  //   rt
  //   rd
  //   可计数暂停的时钟源
  //   JMP
  //   JR
  //   OP
  //   Func
  //   Beq
  //   Bne
  //   MemToReg
  //   MemWrite
  //   AluOP
  //   AluSrcB
  //   RegWrite
  //   JAL
  //   RegDst
  //   Syscall
  //   为方便自动评测，需要输出流水线各段保存的PC值，注意是PC不是PC+4，另外ID段寄存器写入信息，Mem段内存写入信息也要输出
endmodule

module \气泡流水线  (
  output RegWrite,
  output MemWrite,
  output [31:0] IF_PC,
  output [31:0] ID_PC,
  output [31:0] EX_PC,
  output [31:0] M_PC,
  output [31:0] WB_PC,
  output [31:0] RDin,
  output [31:0] MDin,
  output [31:0] LedData
);

  wire and_1_out, and_2_out, and_3_out, and_4_out, and_5_out, and_6_out, and_7_out, and_8_out, and_9_out,
       and_10_out, and_11_out, and_12_out, BLTZ, CLK, clock_1_out, clock_2_out, comparator_1_eq,
       comparator_1_lt, comparator_2_gt, comparator_3_eq, d_ff_1_q, DataHazzard, EX_JAL, ex_mem_1_equal_out,
       ex_mem_1_memtoreg_out, ex_mem_1_syscall_out, EX_REGD, EX_REGWRITE, Go, Halt, id_ex_1_alu_src_out,
       id_ex_1_beq_out, id_ex_1_bne_out, id_ex_1_memtoreg_out, id_ex_1_memwrite_out, id_ex_1_sb_out,
       id_ex_1_syscall_out, IR1, IR2, IR3, J2, JMP, JR, Ledout, LUI, MEM_JAL, MEM_REGD, MEM_REGWRITE,
       mem_wb_1_jal_out, mem_wb_1_memtoreg_out, mem_wb_1_regdst_out, mem_wb_1_syscall_out, mips_alu_1_equal,
       nand_1_out, not_1_out, not_2_out, not_3_out, not_4_out, or_1_out, or_2_out, or_3_out, or_5_out, RST,
       SB_USE, SignedExt, stalls, W1, W2, W3, Write, \单周期硬布线控制器_1_alu_src , \单周期硬布线控制器_1_beq ,
       \单周期硬布线控制器_1_bltz , \单周期硬布线控制器_1_bne , \单周期硬布线控制器_1_jal , \单周期硬布线控制器_1_jmp , \单周期硬布线控制器_1_jr ,
       \单周期硬布线控制器_1_lui , \单周期硬布线控制器_1_memtoreg , \单周期硬布线控制器_1_memwrite , \单周期硬布线控制器_1_regdst ,
       \单周期硬布线控制器_1_regwrite , \单周期硬布线控制器_1_sb , \单周期硬布线控制器_1_syscall ;
  wire [1:0] sb_addr;
  wire [3:0] id_ex_1_aluop_out, \单周期硬布线控制器_1_alu_op ;
  wire [4:0] EX_REGTOWRITE, ID_R1_num, ID_R2_num, MEM_REGTOWRITE, multiplexer_5_out, multiplexer_10_out,
       multiplexer_18_out, shamt, W_num;
  wire [7:0] multiplexer_11_out, multiplexer_12_out, multiplexer_14_out, multiplexer_15_out;
  wire [12:0] CNT_num;
  wire [15:0] \LoadUse次数 , \总周期数 , \插入气泡数 , \无条件分支数 , \条件分支成功数 ;
  wire [25:0] addr;
  wire [27:0] adder_2_out;
  wire [31:0] adder_1_out, adder_4_out, bit_extender_1_out, bit_extender_2_out, DATA_CHA, ex_mem_1_r1_out,
       id_ex_1_imm_out, id_ex_1_r2_out, ID_IR, IF_IR, MEM_IR, mem_wb_1_aluresult_out, mem_wb_1_rd_out,
       mips_alu_1_result, mips_regifile_1_r1, mips_regifile_1_r2, multiplexer_1_out, multiplexer_4_out,
       multiplexer_6_out, multiplexer_8_out, multiplexer_17_out, PC_JR, PCimm, R1, R2, sb_r2, shifter_1_out,
       WB_IR;
  wire [31:2] ex_mem_1_aluresult_out;
  wire [31:26] EX_IR;
  wire [31:28] PC_JAL;

  Button \u_总复位  (.out(RST));
  Button _1 (.out(IR1));
  Button _2 (.out(IR2));
  Button _3 (.out(IR3));
  // Probe on \总周期数 
  // Probe on \总周期数 
  Button \u_继续运行  (.out(Go));
  LED #(.active("true")) led_1 (.in(W1));
  LED #(.active("true")) led_2 (.in(W2));
  LED #(.active("true")) led_3 (.in(W3));
  Hex_Digit_Display hex_digit_display_1 (.value(LedData[31:28]));  // open: dp
  // Probe on IF_PC[19:0]
  // Mips_Probe mips_probe_1: pin names not known; wires that end beside it: IF_IR
  Hex_Digit_Display hex_digit_display_2 (.value(LedData[27:24]));  // open: dp
  Hex_Digit_Display hex_digit_display_3 (.value(LedData[23:20]));  // open: dp
  // Probe on ID_PC[19:0]
  // Mips_Probe mips_probe_2: pin names not known; wires that end beside it: ID_IR
  or or_1 (or_1_out, JMP, JR);
  or or_2 (or_2_out, ~Halt, Go);  // OR_Gate
  Hex_Digit_Display hex_digit_display_4 (.value(LedData[15:12]));  // open: dp
  Hex_Digit_Display hex_digit_display_5 (.value(LedData[19:16]));  // open: dp
  and and_1 (and_1_out, Write, DataHazzard);
  and and_2 (and_2_out, or_1_out, or_2_out);
  and and_3 (and_3_out, J2, or_2_out);
  Hex_Digit_Display hex_digit_display_6 (.value(LedData[11:8]));  // open: dp
  Hex_Digit_Display hex_digit_display_7 (.value(LedData[7:4]));  // open: dp
  Clock #(.highDuration(1), .lowDuration(1)) clock_1 (.out(clock_1_out));
  // Probe on EX_PC[19:0]
  // Mips_Probe mips_probe_3: pin names not known; wires that end beside it: clock_1_out, {EX_IR, addr}, CLK
  Counter #(.width(16), .max('hffff), .ongoal("wrap"), .trigger("rising"), .behavior("old")) counter_1 (
    .D({16{1'b0}}), .count(and_1_out), .Q(\插入气泡数 ), .clk(CLK), .clr(RST));  // open: load, carry, preset
  Counter #(.width(16), .max('hffff), .ongoal("wrap"), .trigger("rising"), .behavior("old")) counter_2 (
    .count(and_2_out), .Q(\无条件分支数 ), .clk(CLK), .clr(RST));  // open: load, D, carry, preset
  Counter #(.width(16), .max('hffff), .ongoal("wrap"), .trigger("rising"), .behavior("old")) counter_3 (
    .count(and_3_out), .Q(\条件分支成功数 ), .clk(CLK), .clr(RST));  // open: load, D, carry, preset
  Multiplexer #(.select(3), .width(32), .disabled("Z"), .enable("false")) multiplexer_1 (
    .in0(adder_1_out), .in1(PCimm), .in2({PC_JAL, addr, 2'b00}), .in6(PC_JR), .out(multiplexer_1_out),
    .sel({JR, JMP, J2}));  // open: in3, in4, in5, in7
  and and_4 (and_4_out, not_1_out, or_3_out);
  not not_1 (not_1_out, DataHazzard);
  or or_3 (or_3_out, ~Halt, Go);  // OR_Gate
  Hex_Digit_Display hex_digit_display_8 (.value(LedData[3:0]));  // open: dp
  or or_4 (stalls, J2, JMP, JR);
  Register #(.width(32), .trigger("rising"), .Select("low")) PC (
    .D(multiplexer_1_out), .en(and_4_out), .Q(IF_PC), .clk(CLK), .clr(RST));
  Counter #(.width(16), .max('hffff), .ongoal("wrap"), .trigger("rising"), .behavior("old")) counter_4 (
    .load(1'b0), .count(or_3_out), .Q(\总周期数 ), .clk(CLK), .clr(RST));  // open: D, carry, preset
  // Probe on \总周期数 
  // Probe on M_PC[19:0]
  // Mips_Probe mips_probe_4: pin names not known; wires that end beside it: MEM_IR
  // Probe on \总周期数 
  // Probe on \无条件分支数 
  // Probe on \条件分支成功数 
  // Probe on \插入气泡数 
  // Probe on \LoadUse次数 
  ROM #(.addrWidth(10), .dataWidth(32), .Select("high")) rom_1 (.addr(IF_PC[11:2]), .data(IF_IR));
  // Probe on IF_PC[11:0]
  // Probe on WB_PC[19:0]
  // Mips_Probe mips_probe_5: pin names not known; wires that end beside it: WB_IR
  not not_2 (not_2_out, DataHazzard);
  and and_5 (and_5_out, not_2_out, Write);
  // Probe on EX_PC[11:0]
  // Probe on ID_PC[11:0]
  IF_ID if_id_1 (
    .IR_IN(IF_IR), .PC_IN(IF_PC), .IR(ID_IR), .PC(ID_PC), .reset(stalls), .CLK(CLK), .CLEAR(RST),
    .ENABLE(and_5_out));  // open: PJUMP_IN, PJUM_OUT
  Adder #(.width(32)) adder_1 (.a(IF_PC), .b(32'h4), .out(adder_1_out));  // open: cin, cout
  // Probe on M_PC[11:0]
  D_Flip_Flop #(.trigger("high"), .Pre_Clr_Positions("LEGACY"), .NegatePresetClear("false"), .enable("true"), .NewFFLayout("false")) d_ff_1 (.Q(d_ff_1_q));  // open: clk, D, Qn, preset, en, reset
  // Probe on 13'hc
  // Mips_Probe mips_probe_6: pin names not known; wires that end beside it: IF_IR, ID_IR
  // Probe on WB_PC[11:0]
  Comparator #(.width(13), .mode("twosComplement")) comparator_1 (
    .a(CNT_num), .b(13'hc), .eq(comparator_1_eq), .lt(comparator_1_lt));  // open: gt
  Clock #(.highDuration(1), .lowDuration(1)) clock_2 (.out(clock_2_out));
  nand nand_1 (nand_1_out, d_ff_1_q, comparator_1_eq);
  Counter #(.width(13), .max('h1fff), .ongoal("stay"), .trigger("rising"), .behavior("old")) counter_5 (
    .count(comparator_1_lt), .Q(CNT_num), .clk(clock_2_out));  // open: load, D, carry, clr, preset
  \数据相关检测  \u_数据相关检测_1  (
    .OP(ID_IR[31:26]), .FUNC(ID_IR[5:0]), .rs(ID_R1_num), .EX_RegWrite(EX_REGWRITE),
    .EX_writeToReg(EX_REGTOWRITE), .MEM_RegWrite(MEM_REGWRITE), .MEM_writeToReg(MEM_REGTOWRITE),
    .rt(ID_R2_num), .DataHazzard(DataHazzard));
  assign CLK = nand_1_out ? clock_2_out : 1'bz;  // Controlled_Buffer controlled_buffer_1
  Pull_Resistor #(.pull(1)) pull_resistor_1 (.node(CLK));
  \单周期硬布线控制器  \u_单周期硬布线控制器_1  (
    .Func(ID_IR[5:0]), .OP(ID_IR[31:26]), .ALU_OP(\单周期硬布线控制器_1_alu_op ), .MemToReg(\单周期硬布线控制器_1_memtoreg ),
    .MemWrite(\单周期硬布线控制器_1_memwrite ), .ALU_SRC(\单周期硬布线控制器_1_alu_src ), .RegWrite(\单周期硬布线控制器_1_regwrite ),
    .SysCALL(\单周期硬布线控制器_1_syscall ), .SignedExt(SignedExt), .RegDst(\单周期硬布线控制器_1_regdst ),
    .JR(\单周期硬布线控制器_1_jr ), .JMP(\单周期硬布线控制器_1_jmp ), .Beq(\单周期硬布线控制器_1_beq ), .JAL(\单周期硬布线控制器_1_jal ),
    .Bne(\单周期硬布线控制器_1_bne ), .BLTZ(\单周期硬布线控制器_1_bltz ), .LUI(\单周期硬布线控制器_1_lui ), .SB(\单周期硬布线控制器_1_sb ));  // open: ERET
  Multiplexer #(.select(1), .width(5), .disabled("Z"), .enable("false")) multiplexer_2 (
    .in0(ID_IR[25:21]), .in1(5'b00010), .out(ID_R1_num), .sel(\单周期硬布线控制器_1_syscall ));
  Multiplexer #(.select(1), .width(5), .disabled("Z"), .enable("false")) multiplexer_3 (
    .in0(ID_IR[20:16]), .in1(5'b00100), .out(ID_R2_num), .sel(\单周期硬布线控制器_1_syscall ));
  assign bit_extender_1_out = {{16{1'b0}}, ID_IR[15:0]};  // Bit_Extender bit_extender_1
  assign bit_extender_2_out = {{16{ID_IR[15]}}, ID_IR[15:0]};  // Bit_Extender bit_extender_2
  Multiplexer #(.select(1), .width(32), .disabled("Z"), .enable("false")) multiplexer_4 (
    .in0(bit_extender_1_out), .in1(bit_extender_2_out), .out(multiplexer_4_out), .sel(SignedExt));
  MIPS_Regifile mips_regifile_1 (
    .Din(RDin), .Clk(CLK), .R1(mips_regifile_1_r1), .R2(mips_regifile_1_r2), .WE(RegWrite), .W_num(W_num),
    .R1_num(ID_R1_num), .R2_num(ID_R2_num));
  or or_5 (or_5_out, DataHazzard, stalls);
  ID_EX id_ex_1 (
    .BEQ_IN(\单周期硬布线控制器_1_beq ), .BNE_IN(\单周期硬布线控制器_1_bne ), .MEMTOREG_IN(\单周期硬布线控制器_1_memtoreg ),
    .MEMWRITE_IN(\单周期硬布线控制器_1_memwrite ), .ALUOP_IN(\单周期硬布线控制器_1_alu_op ),
    .ALU_SRC_IN(\单周期硬布线控制器_1_alu_src ), .REGWRITE_IN(\单周期硬布线控制器_1_regwrite ), .JAL_IN(\单周期硬布线控制器_1_jal ),
    .REGDIST_IN(\单周期硬布线控制器_1_regdst ), .SYSCALL_IN(\单周期硬布线控制器_1_syscall ), .JMP_IN(\单周期硬布线控制器_1_jmp ),
    .JR_IN(\单周期硬布线控制器_1_jr ), .IR_IN(ID_IR), .PC_IN(ID_PC), .R2_IN(mips_regifile_1_r2),
    .R1_IN(mips_regifile_1_r1), .IMM_IN(multiplexer_4_out), .BEQ_OUT(id_ex_1_beq_out),
    .BNE_OUT(id_ex_1_bne_out), .MEMTOREG_OUT(id_ex_1_memtoreg_out), .MEMWRITE_OUT(id_ex_1_memwrite_out),
    .ALUOP_OUT(id_ex_1_aluop_out), .ALU_SRC_OUT(id_ex_1_alu_src_out), .REGWRITE_OUT(EX_REGWRITE),
    .JAL_OUT(EX_JAL), .REGDST_IN(EX_REGD), .SYSCALL_OUT(id_ex_1_syscall_out), .JMP_OUT(JMP), .JR_OUT(JR),
    .IR_OUT({EX_IR, addr}), .PC_OUT(EX_PC), .R2_OUT(id_ex_1_r2_out), .R1_OUT(PC_JR),
    .IMM_OUT(id_ex_1_imm_out), .RESET(or_5_out), .CLEAR(RST), .CLK(CLK), .ENABLE(Write),
    .LUI_IN(\单周期硬布线控制器_1_lui ), .LUI_OUT(LUI), .SB_IN(\单周期硬布线控制器_1_sb ), .SB_OUT(id_ex_1_sb_out),
    .BLTZ_IN(\单周期硬布线控制器_1_bltz ), .BLTZ_OUT(BLTZ));  // open: RS_FORW_IN, RS_FORW_OUT, RT_FORW_IN, RT_FORW_OUT, ERET_IN, ERET_OUT, PJUMP_IN, PJUMP_OUT
  Multiplexer #(.select(1), .width(5), .disabled("Z"), .enable("false")) multiplexer_5 (
    .in0(addr[20:16]), .in1(addr[15:11]), .out(multiplexer_5_out), .sel(EX_REGD));
  Multiplexer #(.select(1), .width(32), .disabled("Z"), .enable("false")) multiplexer_6 (
    .in0(id_ex_1_r2_out), .in1(id_ex_1_imm_out), .out(multiplexer_6_out), .sel(id_ex_1_alu_src_out));
  Adder #(.width(32)) adder_2 (.a(EX_PC), .b(32'h4), .out({PC_JAL, adder_2_out}));  // open: cin, cout
  Shifter #(.width(32), .shift("ll")) shifter_1 (.in(id_ex_1_imm_out), .\dist (5'b00010), .out(shifter_1_out));
  Multiplexer #(.select(1), .width(5), .disabled("Z"), .enable("false")) multiplexer_7 (
    .in0(multiplexer_5_out), .in1({5{1'b1}}), .out(EX_REGTOWRITE), .sel(EX_JAL));
  Comparator #(.width(32), .mode("twosComplement")) comparator_2 (
    .a({32{1'b0}}), .b(PC_JR), .gt(comparator_2_gt));  // open: eq, lt
  Multiplexer #(.select(1), .width(32), .disabled("Z"), .enable("false")) multiplexer_8 (
    .in0(multiplexer_6_out), .in1(32'h22), .out(multiplexer_8_out), .sel(id_ex_1_syscall_out));
  Adder #(.width(32)) adder_3 (.a({PC_JAL, adder_2_out}), .b(shifter_1_out), .out(PCimm));  // open: cin, cout
  and and_6 (and_6_out, comparator_2_gt, BLTZ);
  MIPS_ALU mips_alu_1 (
    .X(PC_JR), .Y(multiplexer_8_out), .AluOP(id_ex_1_aluop_out), .Equal(mips_alu_1_equal),
    .Result(mips_alu_1_result), .shamt(shamt));  // open: Result_2
  Multiplexer #(.select(1), .width(5), .disabled("Z"), .enable("false")) multiplexer_9 (
    .in0(addr[10:6]), .in1(5'b10000), .out(shamt), .sel(LUI));
  and and_7 (and_7_out, id_ex_1_beq_out, mips_alu_1_equal);
  or or_6 (J2, and_6_out, and_7_out, and_8_out);
  and and_8 (and_8_out, id_ex_1_bne_out, ~mips_alu_1_equal);  // AND_Gate
  EX_MEM ex_mem_1 (
    .MemToReg_in(id_ex_1_memtoreg_out), .MemWrite_in(id_ex_1_memwrite_out), .RegWrite_in(EX_REGWRITE),
    .JAL_in(EX_JAL), .RegDst_in(EX_REGD), .Syscall_in(id_ex_1_syscall_out), .equal_in(mips_alu_1_equal),
    .IR_in({EX_IR, addr}), .PC_in(EX_PC), .ALUResult_in(mips_alu_1_result), .R2_in(id_ex_1_r2_out),
    .R1_in(PC_JR), .MemToReg_out(ex_mem_1_memtoreg_out), .MemWrite_out(MemWrite),
    .RegWrite_out(MEM_REGWRITE), .JAL_out(MEM_JAL), .RegDst_out(MEM_REGD),
    .Syscall_out(ex_mem_1_syscall_out), .equal_out(ex_mem_1_equal_out), .IR_out(MEM_IR), .PC_out(M_PC),
    .ALUResult_out({ex_mem_1_aluresult_out, sb_addr}), .R2_out(sb_r2), .R1_out(ex_mem_1_r1_out),
    .RESET(1'b0), .CLK(CLK), .CLEAR(RST), .ENABLE(Write), .SB_in(id_ex_1_sb_out), .SB_out(SB_USE));  // open: Imm_in, Imm_out
  not not_3 (not_3_out, CLK);
  Multiplexer #(.select(1), .width(5), .disabled("Z"), .enable("false")) multiplexer_10 (
    .in0(MEM_IR[20:16]), .in1(MEM_IR[15:11]), .out(multiplexer_10_out), .sel(MEM_REGD));
  and and_9 (and_9_out, ~sb_addr[0], ~sb_addr[1]);  // AND_Gate
  and and_10 (and_10_out, sb_addr[0], ~sb_addr[1]);  // AND_Gate
  and and_11 (and_11_out, ~sb_addr[0], sb_addr[1]);  // AND_Gate
  and and_12 (and_12_out, sb_addr[0], sb_addr[1]);
  Multiplexer #(.select(1), .width(8), .disabled("Z"), .enable("false")) multiplexer_11 (
    .in0(DATA_CHA[7:0]), .in1(sb_r2[7:0]), .out(multiplexer_11_out), .sel(and_9_out));
  Multiplexer #(.select(1), .width(8), .disabled("Z"), .enable("false")) multiplexer_12 (
    .in0(DATA_CHA[15:8]), .in1(sb_r2[7:0]), .out(multiplexer_12_out), .sel(and_10_out));
  RAM #(.addrWidth(10), .dataWidth(32), .bus("separate"), .Select("high")) ram_1 (
    .addr(ex_mem_1_aluresult_out[11:2]), .din(MDin), .data(DATA_CHA), .str(MemWrite), .clk(not_3_out),
    .clr(RST));  // open: sel, ld
  Multiplexer #(.select(1), .width(5), .disabled("Z"), .enable("false")) multiplexer_13 (
    .in0(multiplexer_10_out), .in1({5{1'b1}}), .out(MEM_REGTOWRITE), .sel(MEM_JAL));
  Multiplexer #(.select(1), .width(8), .disabled("Z"), .enable("false")) multiplexer_14 (
    .in0(DATA_CHA[23:16]), .in1(sb_r2[7:0]), .out(multiplexer_14_out), .sel(and_11_out));
  Multiplexer #(.select(1), .width(8), .disabled("Z"), .enable("false")) multiplexer_15 (
    .in0(DATA_CHA[31:24]), .in1(sb_r2[7:0]), .out(multiplexer_15_out), .sel(and_12_out));
  MEM_WB mem_wb_1 (
    .MemToReg_in(ex_mem_1_memtoreg_out), .MemWrite_in(MemWrite), .RegWrite_in(MEM_REGWRITE),
    .JAL_in(MEM_JAL), .RegDst_in(MEM_REGD), .Syscall_in(ex_mem_1_syscall_out), .equal_in(ex_mem_1_equal_out),
    .IR_in(MEM_IR), .PC_in(M_PC), .ALUResult_in({ex_mem_1_aluresult_out, sb_addr}), .RD_in(DATA_CHA),
    .R1_in(ex_mem_1_r1_out), .MemToReg_out(mem_wb_1_memtoreg_out), .RegWrite_out(RegWrite),
    .JAL_out(mem_wb_1_jal_out), .RegDst_out(mem_wb_1_regdst_out), .Syscall_out(mem_wb_1_syscall_out),
    .IR_out(WB_IR), .PC_out(WB_PC), .ALUResult_out(mem_wb_1_aluresult_out), .RD_out(mem_wb_1_rd_out),
    .\气泡_高电平时有效 (1'b0), .clk(CLK), .clear(RST), .enable(Write), .R1_out(R1), .R2_in(sb_r2), .R2_out(R2));  // open: MemWrite_out, equal_out
  Multiplexer #(.select(1), .width(32), .disabled("Z"), .enable("false")) multiplexer_16 (
    .in0(sb_r2), .in1({multiplexer_15_out, multiplexer_14_out, multiplexer_12_out, multiplexer_11_out}),
    .out(MDin), .sel(SB_USE));
  Multiplexer #(.select(1), .width(32), .disabled("Z"), .enable("false")) multiplexer_17 (
    .in0(mem_wb_1_aluresult_out), .in1(mem_wb_1_rd_out), .out(multiplexer_17_out), .sel(mem_wb_1_memtoreg_out));
  not not_4 (not_4_out, Go);
  nand nand_2 (Write, not_4_out, Halt);
  Multiplexer #(.select(1), .width(5), .disabled("Z"), .enable("false")) multiplexer_18 (
    .in0(WB_IR[20:16]), .in1(WB_IR[15:11]), .out(multiplexer_18_out), .sel(mem_wb_1_regdst_out));
  Adder #(.width(32)) adder_4 (.a(WB_PC), .b(32'h4), .out(adder_4_out));  // open: cin, cout
  Multiplexer #(.select(1), .width(32), .disabled("Z"), .enable("false")) multiplexer_19 (
    .in0(multiplexer_17_out), .in1(adder_4_out), .out(RDin), .sel(mem_wb_1_jal_out));
  Multiplexer #(.select(1), .width(5), .disabled("Z"), .enable("false")) multiplexer_20 (
    .in0(multiplexer_18_out), .in1({5{1'b1}}), .out(W_num), .sel(mem_wb_1_jal_out));
  Comparator #(.width(32), .mode("twosComplement")) comparator_3 (
    .a(R1), .b(32'h22), .eq(comparator_3_eq));  // open: gt, lt
  and and_13 (Ledout, comparator_3_eq, mem_wb_1_syscall_out);
  and and_14 (Halt, ~comparator_3_eq, mem_wb_1_syscall_out);  // AND_Gate
  Register #(.width(32), .trigger("rising"), .Select("low")) register_1 (
    .D(R2), .en(Ledout), .Q(LedData), .clk(CLK), .clr(RST));

  // Other names for the same wires on the sheet: RD[4:0] = ID_IR[15:11]; MEM_PC[31:0] = M_PC; EX_IR[25:0] = addr;
  //   PC_JAL[27:2] = addr

  // Notes on the sheet:
  //   中断源
  //   时空图监测，可删除
  //   中断等待指示
  //   数码管输出
  //   指令存储器
  //   contents of rom_1 (hex, n*v repeats v):
  //   20110001 8000c05 20110001 20120002 20130003 8000c09 20110001 20120002 20130003 8000c0d 20110001
  //   20120002 20130003 8000c11 20110001 20120002 20130003 c000c14 2002000a c 20100000 22100001 102020
  //   20020022 c 22100002 102020 20020022 c 22100003 102020 20020022 c 22100004 102020 20020022 c 22100005
  //   102020 20020022 c 22100006 102020 20020022 c 22100007 102020 20020022 c 22100008 102020 20020022
  //   20020022 c 3e00008
  //   控制位
  //   流水调试日志用
  //   暂停节拍，不能为0
  //   OP
  //   Func
  //   rs
  //   rt
  //   rd
  //   指令字
  //   戳工具置1进入计数暂停模式，ctrl+k时钟自动运行到对应节拍暂停
  //   ctrl+k关闭时钟连续运行，将控制位置零，进入单步调试模式调试
  //   可计数暂停的时钟源
  //   JMP
  //   JR
  //   OP
  //   Func
  //   Beq
  //   Bne
  //   AluOP
  //   AluSrcB
  //   RegWrite
  //   JAL
  //   RegDst
  //   Syscall
  //   MemToReg
  //   MemWrite
  //   为方便自动评测，需要输出流水线各段保存的PC值，注意是PC不是PC+4，另外ID段寄存器写入信息，Mem段内存写入信息也要输出
endmodule
module \重定向流水线  (
  output RegWrite,
  output MemWrite,
  output [31:0] IF_PC,
  output [31:0] ID_PC,
  output [31:0] EX_PC,
  output [31:0] M_PC,
  output [31:0] WB_PC,
  output [31:0] RDin,
  output [31:0] MDin,
  output [31:0] LedData
);

  wire and_1_out, and_2_out, and_3_out, and_4_out, and_5_out, and_6_out, and_7_out, and_8_out, and_9_out,
       and_10_out, BLTZ, CLK, clock_1_out, clock_2_out, comparator_1_eq, comparator_1_lt, comparator_2_gt,
       comparator_3_eq, d_ff_1_q, EX_JAL, ex_mem_1_equal_out, ex_mem_1_memtoreg_out, ex_mem_1_regwrite_out,
       ex_mem_1_syscall_out, EX_REGD, Go, Halt, id_ex_1_alu_src_out, id_ex_1_beq_out, id_ex_1_bne_out,
       id_ex_1_memtoreg_out, id_ex_1_memwrite_out, id_ex_1_regwrite_out, id_ex_1_sb_out, id_ex_1_syscall_out,
       IR1, IR2, IR3, J2, JMP, JR, Ledout, LUI, MEM_JAL, MEM_REGD, mem_wb_1_jal_out, mem_wb_1_memtoreg_out,
       mem_wb_1_regdst_out, mem_wb_1_syscall_out, mips_alu_1_equal, nand_1_out, not_1_out, not_2_out,
       or_1_out, or_2_out, or_4_out, or_5_out, \PC_EN调试 , RST, SB_USE, SignedExt, W1, W2, W3, Write,
       \单周期硬布线控制器_1_alu_src , \单周期硬布线控制器_1_beq , \单周期硬布线控制器_1_bltz , \单周期硬布线控制器_1_bne , \单周期硬布线控制器_1_jal ,
       \单周期硬布线控制器_1_jmp , \单周期硬布线控制器_1_jr , \单周期硬布线控制器_1_lui , \单周期硬布线控制器_1_memtoreg ,
       \单周期硬布线控制器_1_memwrite , \单周期硬布线控制器_1_regdst , \单周期硬布线控制器_1_regwrite , \单周期硬布线控制器_1_sb ,
       \单周期硬布线控制器_1_syscall , \数据相关 , \数据相关检测_重定向_1_id_ex_stall , \数据相关检测_重定向_1_if_id_en ,
       \数据相关检测_重定向_1_if_id_stall ;
  wire [1:0] id_ex_1_rs_forw_out, id_ex_1_rt_forw_out, sb_addr, \数据相关检测_重定向_1_rsforward ,
       \数据相关检测_重定向_1_rtforward ;
  wire [3:0] id_ex_1_aluop_out, \单周期硬布线控制器_1_alu_op ;
  wire [4:0] EX_REGTOWRITE, ID_R1_num, ID_R2_num, MEM_REGTOWRITE, multiplexer_7_out, multiplexer_12_out,
       multiplexer_20_out, shamt, W_num;
  wire [7:0] multiplexer_13_out, multiplexer_14_out, multiplexer_15_out, multiplexer_17_out;
  wire [12:0] CNT_num;
  wire [15:0] \LoadUse次数 , \总周期数 , \插入气泡数 , \无条件分支数 , \条件分支成功数 ;
  wire [25:0] addr;
  wire [27:0] adder_2_out;
  wire [31:0] adder_1_out, adder_4_out, bit_extender_1_out, bit_extender_2_out, DATA_CHA, ex_mem_1_r1_out,
       id_ex_1_imm_out, id_ex_1_r1_out, id_ex_1_r2_out, ID_IR, IF_IR, MEM_IR, mem_wb_1_aluresult_out,
       mem_wb_1_rd_out, mips_alu_1_result, mips_regifile_1_r1, mips_regifile_1_r2, multiplexer_1_out,
       multiplexer_4_out, multiplexer_6_out, multiplexer_8_out, multiplexer_10_out, multiplexer_19_out,
       PC_JR, PCimm, R1, R2, sb_r2, shifter_1_out, WB_IR;
  wire [31:2] ex_mem_1_aluresult_out;
  wire [31:26] EX_IR;
  wire [31:28] PC_JAL;

  Button \u_总复位  (.out(RST));
  Button _1 (.out(IR1));
  Button _2 (.out(IR2));
  Button _3 (.out(IR3));
  // Probe on \总周期数 
  // Probe on \总周期数 
  Button \u_继续运行  (.out(Go));
  LED #(.active("true")) led_1 (.in(W1));
  LED #(.active("true")) led_2 (.in(W2));
  LED #(.active("true")) led_3 (.in(W3));
  Hex_Digit_Display hex_digit_display_1 (.value(LedData[31:28]));  // open: dp
  // Probe on IF_PC[19:0]
  // Mips_Probe mips_probe_1: pin names not known; wires that end beside it: IF_IR
  Hex_Digit_Display hex_digit_display_2 (.value(LedData[27:24]));  // open: dp
  Hex_Digit_Display hex_digit_display_3 (.value(LedData[23:20]));  // open: dp
  // Probe on ID_PC[19:0]
  // Mips_Probe mips_probe_2: pin names not known; wires that end beside it: ID_IR
  Hex_Digit_Display hex_digit_display_4 (.value(LedData[15:12]));  // open: dp
  Hex_Digit_Display hex_digit_display_5 (.value(LedData[19:16]));  // open: dp
  Hex_Digit_Display hex_digit_display_6 (.value(LedData[11:8]));  // open: dp
  Hex_Digit_Display hex_digit_display_7 (.value(LedData[7:4]));  // open: dp
  Clock #(.highDuration(1), .lowDuration(1)) clock_1 (.out(clock_1_out));
  // Probe on EX_PC[19:0]
  // Mips_Probe mips_probe_3: pin names not known; wires that end beside it: clock_1_out, {EX_IR, addr}, CLK
  Multiplexer #(.select(3), .width(32), .disabled("Z"), .enable("false")) multiplexer_1 (
    .in0(adder_1_out), .in1(PCimm), .in2({PC_JAL, addr, 2'b00}), .in6(PC_JR), .out(multiplexer_1_out),
    .sel({JR, JMP, J2}));  // open: in3, in4, in5, in7
  Hex_Digit_Display hex_digit_display_8 (.value(LedData[3:0]));  // open: dp
  Register #(.width(32), .trigger("rising"), .Select("low")) PC (
    .D(multiplexer_1_out), .en(\PC_EN调试 ), .Q(IF_PC), .clk(CLK), .clr(RST));
  // Probe on \总周期数 
  // Probe on M_PC[19:0]
  // Mips_Probe mips_probe_4: pin names not known; wires that end beside it: MEM_IR
  // Probe on \总周期数 
  // Probe on \无条件分支数 
  // Probe on \条件分支成功数 
  // Probe on \插入气泡数 
  // Probe on \LoadUse次数 
  ROM #(.addrWidth(10), .dataWidth(32), .Select("high")) rom_1 (.addr(IF_PC[11:2]), .data(IF_IR));
  // Probe on IF_PC[11:0]
  // Probe on WB_PC[19:0]
  // Mips_Probe mips_probe_5: pin names not known; wires that end beside it: WB_IR
  or or_1 (or_1_out, JMP, JR);
  or or_2 (or_2_out, ~Halt, Go);  // OR_Gate
  // Probe on ID_PC[11:0]
  // Probe on EX_PC[11:0]
  IF_ID if_id_1 (
    .IR_IN(IF_IR), .PC_IN(IF_PC), .IR(ID_IR), .PC(ID_PC), .reset(\数据相关检测_重定向_1_if_id_stall ), .CLK(CLK),
    .CLEAR(RST), .ENABLE(\数据相关检测_重定向_1_if_id_en ));  // open: PJUMP_IN, PJUM_OUT
  Adder #(.width(32)) adder_1 (.a(IF_PC), .b(32'h4), .out(adder_1_out));  // open: cin, cout
  Counter #(.width(16), .max('hffff), .ongoal("wrap"), .trigger("rising"), .behavior("old")) counter_1 (
    .count(and_1_out), .Q(\无条件分支数 ), .clk(CLK), .clr(RST));  // open: load, D, carry, preset
  and and_1 (and_1_out, or_1_out, or_2_out);
  and and_2 (and_2_out, J2, or_2_out);
  // Probe on M_PC[11:0]
  D_Flip_Flop #(.trigger("high"), .Pre_Clr_Positions("LEGACY"), .NegatePresetClear("false"), .enable("true"), .NewFFLayout("false")) d_ff_1 (.Q(d_ff_1_q));  // open: clk, D, Qn, preset, en, reset
  // Probe on 13'hc
  // Mips_Probe mips_probe_6: pin names not known; wires that end beside it: IF_IR, ID_IR
  Counter #(.width(16), .max('hffff), .ongoal("wrap"), .trigger("rising"), .behavior("old")) counter_2 (
    .count(and_2_out), .Q(\条件分支成功数 ), .clk(CLK), .clr(RST));  // open: load, D, carry, preset
  // Probe on WB_PC[11:0]
  Comparator #(.width(13), .mode("twosComplement")) comparator_1 (
    .a(CNT_num), .b(13'hc), .eq(comparator_1_eq), .lt(comparator_1_lt));  // open: gt
  Clock #(.highDuration(1), .lowDuration(1)) clock_2 (.out(clock_2_out));
  nand nand_1 (nand_1_out, d_ff_1_q, comparator_1_eq);
  Counter #(.width(13), .max('h1fff), .ongoal("stay"), .trigger("rising"), .behavior("old")) counter_3 (
    .count(comparator_1_lt), .Q(CNT_num), .clk(clock_2_out));  // open: load, D, carry, clr, preset
  assign CLK = nand_1_out ? clock_2_out : 1'bz;  // Controlled_Buffer controlled_buffer_1
  and and_3 (and_3_out, Write, \数据相关 );
  Pull_Resistor #(.pull(1)) pull_resistor_1 (.node(CLK));
  \单周期硬布线控制器  \u_单周期硬布线控制器_1  (
    .Func(ID_IR[5:0]), .OP(ID_IR[31:26]), .ALU_OP(\单周期硬布线控制器_1_alu_op ), .MemToReg(\单周期硬布线控制器_1_memtoreg ),
    .MemWrite(\单周期硬布线控制器_1_memwrite ), .ALU_SRC(\单周期硬布线控制器_1_alu_src ), .RegWrite(\单周期硬布线控制器_1_regwrite ),
    .SysCALL(\单周期硬布线控制器_1_syscall ), .SignedExt(SignedExt), .RegDst(\单周期硬布线控制器_1_regdst ),
    .JR(\单周期硬布线控制器_1_jr ), .JMP(\单周期硬布线控制器_1_jmp ), .Beq(\单周期硬布线控制器_1_beq ), .JAL(\单周期硬布线控制器_1_jal ),
    .Bne(\单周期硬布线控制器_1_bne ), .BLTZ(\单周期硬布线控制器_1_bltz ), .LUI(\单周期硬布线控制器_1_lui ), .SB(\单周期硬布线控制器_1_sb ));  // open: ERET
  Multiplexer #(.select(1), .width(5), .disabled("Z"), .enable("false")) multiplexer_2 (
    .in0(ID_IR[25:21]), .in1(5'b00010), .out(ID_R1_num), .sel(\单周期硬布线控制器_1_syscall ));
  Multiplexer #(.select(1), .width(5), .disabled("Z"), .enable("false")) multiplexer_3 (
    .in0(ID_IR[20:16]), .in1(5'b00100), .out(ID_R2_num), .sel(\单周期硬布线控制器_1_syscall ));
  assign bit_extender_1_out = {{16{1'b0}}, ID_IR[15:0]};  // Bit_Extender bit_extender_1
  assign bit_extender_2_out = {{16{ID_IR[15]}}, ID_IR[15:0]};  // Bit_Extender bit_extender_2
  Counter #(.width(16), .max('hffff), .ongoal("wrap"), .trigger("rising"), .behavior("old")) counter_4 (
    .count(and_3_out), .Q(\插入气泡数 ), .clk(CLK), .clr(RST));  // open: load, D, carry, preset
  Counter #(.width(16), .max('hffff), .ongoal("wrap"), .trigger("rising"), .behavior("old")) counter_5 (
    .load(1'b0), .count(\PC_EN调试 ), .Q(\总周期数 ), .clk(CLK), .clr(RST));  // open: D, carry, preset
  Multiplexer #(.select(1), .width(32), .disabled("Z"), .enable("false")) multiplexer_4 (
    .in0(bit_extender_1_out), .in1(bit_extender_2_out), .out(multiplexer_4_out), .sel(SignedExt));
  MIPS_Regifile mips_regifile_1 (
    .Din(RDin), .Clk(CLK), .R1(mips_regifile_1_r1), .R2(mips_regifile_1_r2), .WE(RegWrite), .W_num(W_num),
    .R1_num(ID_R1_num), .R2_num(ID_R2_num));
  ID_EX id_ex_1 (
    .BEQ_IN(\单周期硬布线控制器_1_beq ), .BNE_IN(\单周期硬布线控制器_1_bne ), .MEMTOREG_IN(\单周期硬布线控制器_1_memtoreg ),
    .MEMWRITE_IN(\单周期硬布线控制器_1_memwrite ), .ALUOP_IN(\单周期硬布线控制器_1_alu_op ),
    .ALU_SRC_IN(\单周期硬布线控制器_1_alu_src ), .REGWRITE_IN(\单周期硬布线控制器_1_regwrite ), .JAL_IN(\单周期硬布线控制器_1_jal ),
    .REGDIST_IN(\单周期硬布线控制器_1_regdst ), .SYSCALL_IN(\单周期硬布线控制器_1_syscall ), .JMP_IN(\单周期硬布线控制器_1_jmp ),
    .JR_IN(\单周期硬布线控制器_1_jr ), .IR_IN(ID_IR), .PC_IN(ID_PC), .R2_IN(mips_regifile_1_r2),
    .R1_IN(mips_regifile_1_r1), .IMM_IN(multiplexer_4_out), .BEQ_OUT(id_ex_1_beq_out),
    .BNE_OUT(id_ex_1_bne_out), .MEMTOREG_OUT(id_ex_1_memtoreg_out), .MEMWRITE_OUT(id_ex_1_memwrite_out),
    .ALUOP_OUT(id_ex_1_aluop_out), .ALU_SRC_OUT(id_ex_1_alu_src_out), .REGWRITE_OUT(id_ex_1_regwrite_out),
    .JAL_OUT(EX_JAL), .REGDST_IN(EX_REGD), .SYSCALL_OUT(id_ex_1_syscall_out), .JMP_OUT(JMP), .JR_OUT(JR),
    .IR_OUT({EX_IR, addr}), .PC_OUT(EX_PC), .R2_OUT(id_ex_1_r2_out), .R1_OUT(id_ex_1_r1_out),
    .IMM_OUT(id_ex_1_imm_out), .RESET(\数据相关检测_重定向_1_id_ex_stall ), .CLEAR(RST), .CLK(CLK), .ENABLE(Write),
    .LUI_IN(\单周期硬布线控制器_1_lui ), .LUI_OUT(LUI), .SB_IN(\单周期硬布线控制器_1_sb ), .SB_OUT(id_ex_1_sb_out),
    .BLTZ_IN(\单周期硬布线控制器_1_bltz ), .BLTZ_OUT(BLTZ), .RS_FORW_IN(\数据相关检测_重定向_1_rsforward ),
    .RS_FORW_OUT(id_ex_1_rs_forw_out), .RT_FORW_IN(\数据相关检测_重定向_1_rtforward ),
    .RT_FORW_OUT(id_ex_1_rt_forw_out));  // open: ERET_IN, ERET_OUT, PJUMP_IN, PJUMP_OUT
  Multiplexer #(.select(2), .width(32), .disabled("Z"), .enable("false")) multiplexer_5 (
    .in0(id_ex_1_r1_out), .in1(RDin), .in2({ex_mem_1_aluresult_out, sb_addr}),
    .in3({ex_mem_1_aluresult_out, sb_addr}), .out(PC_JR), .sel(id_ex_1_rs_forw_out));
  Multiplexer #(.select(2), .width(32), .disabled("Z"), .enable("false")) multiplexer_6 (
    .in0(id_ex_1_r2_out), .in1(RDin), .in2({ex_mem_1_aluresult_out, sb_addr}),
    .in3({ex_mem_1_aluresult_out, sb_addr}), .out(multiplexer_6_out), .sel(id_ex_1_rt_forw_out));
  Multiplexer #(.select(1), .width(5), .disabled("Z"), .enable("false")) multiplexer_7 (
    .in0(addr[20:16]), .in1(addr[15:11]), .out(multiplexer_7_out), .sel(EX_REGD));
  Multiplexer #(.select(1), .width(32), .disabled("Z"), .enable("false")) multiplexer_8 (
    .in0(multiplexer_6_out), .in1(id_ex_1_imm_out), .out(multiplexer_8_out), .sel(id_ex_1_alu_src_out));
  Adder #(.width(32)) adder_2 (.a(EX_PC), .b(32'h4), .out({PC_JAL, adder_2_out}));  // open: cin, cout
  Shifter #(.width(32), .shift("ll")) shifter_1 (.in(id_ex_1_imm_out), .\dist (5'b00010), .out(shifter_1_out));
  Multiplexer #(.select(1), .width(5), .disabled("Z"), .enable("false")) multiplexer_9 (
    .in0(multiplexer_7_out), .in1({5{1'b1}}), .out(EX_REGTOWRITE), .sel(EX_JAL));
  Comparator #(.width(32), .mode("twosComplement")) comparator_2 (
    .a({32{1'b0}}), .b(PC_JR), .gt(comparator_2_gt));  // open: eq, lt
  Multiplexer #(.select(1), .width(32), .disabled("Z"), .enable("false")) multiplexer_10 (
    .in0(multiplexer_8_out), .in1(32'h22), .out(multiplexer_10_out), .sel(id_ex_1_syscall_out));
  Adder #(.width(32)) adder_3 (.a({PC_JAL, adder_2_out}), .b(shifter_1_out), .out(PCimm));  // open: cin, cout
  MIPS_ALU mips_alu_1 (
    .X(PC_JR), .Y(multiplexer_10_out), .AluOP(id_ex_1_aluop_out), .Equal(mips_alu_1_equal),
    .Result(mips_alu_1_result), .shamt(shamt));  // open: Result_2
  Multiplexer #(.select(1), .width(5), .disabled("Z"), .enable("false")) multiplexer_11 (
    .in0(addr[10:6]), .in1(5'b10000), .out(shamt), .sel(LUI));
  and and_4 (and_4_out, comparator_2_gt, BLTZ);
  and and_5 (and_5_out, id_ex_1_beq_out, mips_alu_1_equal);
  or or_3 (J2, and_4_out, and_5_out, and_6_out);
  and and_6 (and_6_out, id_ex_1_bne_out, ~mips_alu_1_equal);  // AND_Gate
  or or_4 (or_4_out, J2, JR, JMP);
  EX_MEM ex_mem_1 (
    .MemToReg_in(id_ex_1_memtoreg_out), .MemWrite_in(id_ex_1_memwrite_out),
    .RegWrite_in(id_ex_1_regwrite_out), .JAL_in(EX_JAL), .RegDst_in(EX_REGD),
    .Syscall_in(id_ex_1_syscall_out), .equal_in(mips_alu_1_equal), .IR_in({EX_IR, addr}), .PC_in(EX_PC),
    .ALUResult_in(mips_alu_1_result), .R2_in(multiplexer_6_out), .R1_in(PC_JR),
    .MemToReg_out(ex_mem_1_memtoreg_out), .MemWrite_out(MemWrite), .RegWrite_out(ex_mem_1_regwrite_out),
    .JAL_out(MEM_JAL), .RegDst_out(MEM_REGD), .Syscall_out(ex_mem_1_syscall_out),
    .equal_out(ex_mem_1_equal_out), .IR_out(MEM_IR), .PC_out(M_PC),
    .ALUResult_out({ex_mem_1_aluresult_out, sb_addr}), .R2_out(sb_r2), .R1_out(ex_mem_1_r1_out),
    .RESET(1'b0), .CLK(CLK), .CLEAR(RST), .ENABLE(Write), .SB_in(id_ex_1_sb_out), .SB_out(SB_USE));  // open: Imm_in, Imm_out
  and and_7 (and_7_out, ~sb_addr[0], ~sb_addr[1]);  // AND_Gate
  and and_8 (and_8_out, sb_addr[0], ~sb_addr[1]);  // AND_Gate
  and and_9 (and_9_out, ~sb_addr[0], sb_addr[1]);  // AND_Gate
  and and_10 (and_10_out, sb_addr[0], sb_addr[1]);
  not not_1 (not_1_out, CLK);
  Multiplexer #(.select(1), .width(5), .disabled("Z"), .enable("false")) multiplexer_12 (
    .in0(MEM_IR[20:16]), .in1(MEM_IR[15:11]), .out(multiplexer_12_out), .sel(MEM_REGD));
  Multiplexer #(.select(1), .width(8), .disabled("Z"), .enable("false")) multiplexer_13 (
    .in0(DATA_CHA[7:0]), .in1(sb_r2[7:0]), .out(multiplexer_13_out), .sel(and_7_out));
  Multiplexer #(.select(1), .width(8), .disabled("Z"), .enable("false")) multiplexer_14 (
    .in0(DATA_CHA[15:8]), .in1(sb_r2[7:0]), .out(multiplexer_14_out), .sel(and_8_out));
  Multiplexer #(.select(1), .width(8), .disabled("Z"), .enable("false")) multiplexer_15 (
    .in0(DATA_CHA[23:16]), .in1(sb_r2[7:0]), .out(multiplexer_15_out), .sel(and_9_out));
  RAM #(.addrWidth(10), .dataWidth(32), .bus("separate"), .Select("high")) ram_1 (
    .addr(ex_mem_1_aluresult_out[11:2]), .din(MDin), .data(DATA_CHA), .str(MemWrite), .clk(not_1_out),
    .clr(RST));  // open: sel, ld
  Multiplexer #(.select(1), .width(5), .disabled("Z"), .enable("false")) multiplexer_16 (
    .in0(multiplexer_12_out), .in1({5{1'b1}}), .out(MEM_REGTOWRITE), .sel(MEM_JAL));
  Multiplexer #(.select(1), .width(8), .disabled("Z"), .enable("false")) multiplexer_17 (
    .in0(DATA_CHA[31:24]), .in1(sb_r2[7:0]), .out(multiplexer_17_out), .sel(and_10_out));
  MEM_WB mem_wb_1 (
    .MemToReg_in(ex_mem_1_memtoreg_out), .MemWrite_in(MemWrite), .RegWrite_in(ex_mem_1_regwrite_out),
    .JAL_in(MEM_JAL), .RegDst_in(MEM_REGD), .Syscall_in(ex_mem_1_syscall_out), .equal_in(ex_mem_1_equal_out),
    .IR_in(MEM_IR), .PC_in(M_PC), .ALUResult_in({ex_mem_1_aluresult_out, sb_addr}), .RD_in(DATA_CHA),
    .R1_in(ex_mem_1_r1_out), .MemToReg_out(mem_wb_1_memtoreg_out), .RegWrite_out(RegWrite),
    .JAL_out(mem_wb_1_jal_out), .RegDst_out(mem_wb_1_regdst_out), .Syscall_out(mem_wb_1_syscall_out),
    .IR_out(WB_IR), .PC_out(WB_PC), .ALUResult_out(mem_wb_1_aluresult_out), .RD_out(mem_wb_1_rd_out),
    .\气泡_高电平时有效 (1'b0), .clk(CLK), .clear(RST), .enable(Write), .R1_out(R1), .R2_in(sb_r2), .R2_out(R2));  // open: MemWrite_out, equal_out
  Multiplexer #(.select(1), .width(32), .disabled("Z"), .enable("false")) multiplexer_18 (
    .in0(sb_r2), .in1({multiplexer_17_out, multiplexer_15_out, multiplexer_14_out, multiplexer_13_out}),
    .out(MDin), .sel(SB_USE));
  Multiplexer #(.select(1), .width(32), .disabled("Z"), .enable("false")) multiplexer_19 (
    .in0(mem_wb_1_aluresult_out), .in1(mem_wb_1_rd_out), .out(multiplexer_19_out), .sel(mem_wb_1_memtoreg_out));
  or or_5 (or_5_out, ~Halt, Go);  // OR_Gate
  \数据相关检测_重定向  \u_数据相关检测_重定向_1  (
    .OP(ID_IR[31:26]), .FUNC(ID_IR[5:0]), .RS(ID_R1_num), .Halt_or_Go(or_5_out),
    .EX_MEMTOREG(id_ex_1_memtoreg_out), .EX_WRITEREG(EX_REGTOWRITE), .RT(ID_R2_num), .\J标记 (or_4_out),
    .MEM_REGW(ex_mem_1_regwrite_out), .MEM_WRITEREG(MEM_REGTOWRITE), .EX_REGW(id_ex_1_regwrite_out),
    .PC_EN(\PC_EN调试 ), .LOAD_USED(\数据相关 ), .IF_ID_EN(\数据相关检测_重定向_1_if_id_en ),
    .IF_ID_STALL(\数据相关检测_重定向_1_if_id_stall ), .ID_EX_STALL(\数据相关检测_重定向_1_id_ex_stall ),
    .RSFORWARD(\数据相关检测_重定向_1_rsforward ), .RTFORWARD(\数据相关检测_重定向_1_rtforward ));
  nand nand_2 (Write, not_2_out, Halt);
  Multiplexer #(.select(1), .width(5), .disabled("Z"), .enable("false")) multiplexer_20 (
    .in0(WB_IR[20:16]), .in1(WB_IR[15:11]), .out(multiplexer_20_out), .sel(mem_wb_1_regdst_out));
  Adder #(.width(32)) adder_4 (.a(WB_PC), .b(32'h4), .out(adder_4_out));  // open: cin, cout
  not not_2 (not_2_out, Go);
  Multiplexer #(.select(1), .width(32), .disabled("Z"), .enable("false")) multiplexer_21 (
    .in0(multiplexer_19_out), .in1(adder_4_out), .out(RDin), .sel(mem_wb_1_jal_out));
  Multiplexer #(.select(1), .width(5), .disabled("Z"), .enable("false")) multiplexer_22 (
    .in0(multiplexer_20_out), .in1({5{1'b1}}), .out(W_num), .sel(mem_wb_1_jal_out));
  Comparator #(.width(32), .mode("twosComplement")) comparator_3 (
    .a(R1), .b(32'h22), .eq(comparator_3_eq));  // open: gt, lt
  and and_11 (Ledout, comparator_3_eq, mem_wb_1_syscall_out);
  and and_12 (Halt, ~comparator_3_eq, mem_wb_1_syscall_out);  // AND_Gate
  Register #(.width(32), .trigger("rising"), .Select("low")) register_1 (
    .D(R2), .en(Ledout), .Q(LedData), .clk(CLK), .clr(RST));

  // Other names for the same wires on the sheet: RD[4:0] = ID_IR[15:11]; MEM_PC[31:0] = M_PC; EX_IR[25:0] = addr;
  //   PC_JAL[27:2] = addr

  // Notes on the sheet:
  //   中断源
  //   时空图监测，可删除
  //   中断等待指示
  //   数码管输出
  //   指令存储器
  //   contents of rom_1 (hex, n*v repeats v):
  //   20110001 8100005 20110001 20120002 20130003 8100009 20110001 20120002 20130003 810000d 20110001
  //   20120002 20130003 8100011 20110001 20120002 20130003 c1000fa 20100001 20110001 118fc0 112020
  //   20020022 c 118882 12200001 8100015 112020 20020022 c 20110001 118880 112020 20020022 c 12200001
  //   810001f 20110001 118fc0 112020 20020022 c 1188c3 112020 20020022 c 118903 112020 20020022 c 118903
  //   112020 20020022 c 118903 112020 20020022 c 118903 112020 20020022 c 118903 112020 20020022 c 118903
  //   112020 20020022 c 118903 112020 20020022 c 20100001 109fc0 139fc3 8021 2012000c 24160003 26100001
  //   3210000f 20080008 20090001 139900 2709825 132020 20020022 c 1094022 1500fff9 22100001 2018000f
  //   2188024 108700 20080008 20090001 139902 2709825 132021 20020022 c 1094022 1500fff9 108702 2c9b022
  //   12c00001 8100050 4020 1084027 84400 3508ffff 82021 20020022 c 2010ffff 20110000 ae300000 22100001
  //   22310004 ae300000 22100001 22310004 ae300000 22100001 22310004 ae300000 22100001 22310004 ae300000
  //   22100001 22310004 ae300000 22100001 22310004 ae300000 22100001 22310004 ae300000 22100001 22310004
  //   ae300000 22100001 22310004 ae300000 22100001 22310004 ae300000 22100001 22310004 ae300000 22100001
  //   22310004 ae300000 22100001 22310004 ae300000 22100001 22310004 ae300000 22100001 22310004 ae300000
  //   22100001 22310004 22100001 8020 2011003c 8e130000 8e340000 274402a 11000002 ae330000 ae140000
  //   2231fffc 1611fff8 102020 20020022 c 22100004 2011003c 1611fff2 20020032 c 20080001 20110010 112020
  //   20020022 c 200b0020 2288823 112020 20020022 c 216bffff 1560fffa 2002000a c 200b0008 3c11fedc
  //   3631ffff 112020 20020022 c 3c11ba98 112020 c 3c117654 112020 c 3c113210 112020 c 216bffff 1560fff0
  //   2002000a c 20090000 200b0020 20110000 20120001 a1310000 112020 20020022 c 2328820 21290001 216bffff
  //   1560fff8 200b0008 20090000 8d310000 112020 20020022 c 21290004 216bffff 1560fff9 2002000a c 2011fff1
  //   112020 20020022 c 22310001 620fffb 2002000a c 2002000a c 20100000 22100001 102020 20020022 c
  //   22100002 102020 20020022 c 22100003 102020 20020022 c 22100004 102020 20020022 c 22100005 102020
  //   20020022 c 22100006 102020 20020022 c 22100007 102020 20020022 c 22100008 102020 20020022 20020022 c
  //   3e00008
  //   控制位
  //   流水调试日志用
  //   暂停节拍，不能为0
  //   OP
  //   Func
  //   rs
  //   rt
  //   rd
  //   指令字
  //   戳工具置1进入计数暂停模式，ctrl+k时钟自动运行到对应节拍暂停
  //   ctrl+k关闭时钟连续运行，将控制位置零，进入单步调试模式调试
  //   指令调试器件
  //   可计数暂停的时钟源
  //   JMP
  //   JR
  //   OP
  //   Func
  //   Beq
  //   Bne
  //   AluOP
  //   AluSrcB
  //   RegWrite
  //   JAL
  //   RegDst
  //   Syscall
  //   MemToReg
  //   MemWrite
  //   为方便自动评测，需要输出流水线各段保存的PC值，注意是PC不是PC+4，另外ID段寄存器写入信息，Mem段内存写入信息也要输出
  //   SB指令电路
endmodule

module \动态分支预测  (
  output RegWrite,
  output MemWrite,
  output [31:0] IF_PC,
  output [31:0] ID_PC,
  output [31:0] EX_PC,
  output [31:0] M_PC,
  output [31:0] WB_PC,
  output [31:0] RDin,
  output [31:0] MDin,
  output [31:0] LedData
);

  wire and_1_out, and_2_out, and_3_out, and_4_out, and_5_out, and_6_out, and_7_out, and_8_out, and_9_out,
       and_10_out, BEQ, BLTZ, BNE, cache_1_pjump, CLK, clock_1_out, clock_2_out, comparator_1_eq,
       comparator_1_lt, comparator_2_gt, comparator_3_eq, d_ff_1_q, EX_BRANCHTAKEN, EX_JAL,
       ex_mem_1_equal_out, ex_mem_1_memtoreg_out, ex_mem_1_regwrite_out, ex_mem_1_syscall_out, EX_REGD, FAIL,
       Go, Halt, id_ex_1_alu_src_out, id_ex_1_memtoreg_out, id_ex_1_memwrite_out, id_ex_1_regwrite_out,
       id_ex_1_sb_out, id_ex_1_syscall_out, if_id_1_pjum_out, IR1, IR2, IR3, J2, JMP, JR, Ledout, LUI,
       MEM_JAL, MEM_REGD, mem_wb_1_jal_out, mem_wb_1_memtoreg_out, mem_wb_1_regdst_out, mem_wb_1_syscall_out,
       mips_alu_1_equal, nand_1_out, not_1_out, not_2_out, not_3_out, or_2_out, or_3_out, or_5_out,
       \PC_EN调试 , pjump, RST, SB_USE, SignedExt, W1, W2, W3, Write, \单周期硬布线控制器_1_alu_src , \单周期硬布线控制器_1_beq ,
       \单周期硬布线控制器_1_bltz , \单周期硬布线控制器_1_bne , \单周期硬布线控制器_1_jal , \单周期硬布线控制器_1_jmp , \单周期硬布线控制器_1_jr ,
       \单周期硬布线控制器_1_lui , \单周期硬布线控制器_1_memtoreg , \单周期硬布线控制器_1_memwrite , \单周期硬布线控制器_1_regdst ,
       \单周期硬布线控制器_1_regwrite , \单周期硬布线控制器_1_sb , \单周期硬布线控制器_1_syscall , \数据相关 , \数据相关检测_重定向_1_id_ex_stall ,
       \数据相关检测_重定向_1_if_id_en , \数据相关检测_重定向_1_if_id_stall ;
  wire [1:0] id_ex_1_rs_forw_out, id_ex_1_rt_forw_out, sb_addr, \数据相关检测_重定向_1_rsforward ,
       \数据相关检测_重定向_1_rtforward ;
  wire [3:0] id_ex_1_aluop_out, \单周期硬布线控制器_1_alu_op ;
  wire [4:0] EX_REGTOWRITE, ID_R1_num, ID_R2_num, MEM_REGTOWRITE, multiplexer_9_out, multiplexer_14_out,
       multiplexer_22_out, shamt, W_num;
  wire [7:0] multiplexer_15_out, multiplexer_16_out, multiplexer_17_out, multiplexer_19_out;
  wire [12:0] CNT_num;
  wire [15:0] \LoadUse次数 , \总周期数 , \插入气泡数 , \无条件分支数 , \条件分支成功数 ;
  wire [25:0] addr;
  wire [27:0] adder_2_out;
  wire [31:0] adder_1_out, adder_4_out, bit_extender_1_out, bit_extender_2_out, cache_1_branchaddr_out,
       controlled_buffer_1_out, DATA_CHA, ex_mem_1_r1_out, id_ex_1_imm_out, id_ex_1_r1_out, id_ex_1_r2_out,
       ID_IR, IF_IR, MEM_IR, mem_wb_1_aluresult_out, mem_wb_1_rd_out, mips_alu_1_result, mips_regifile_1_r1,
       mips_regifile_1_r2, multiplexer_1_out, multiplexer_2_out, multiplexer_3_out, multiplexer_6_out,
       multiplexer_8_out, multiplexer_10_out, multiplexer_12_out, multiplexer_21_out, PC_JR, PCimm, R1, R2,
       sb_r2, shifter_1_out, WB_IR;
  wire [31:2] ex_mem_1_aluresult_out;
  wire [31:26] EX_IR;
  wire [31:28] PC_JAL;

  Button \u_总复位  (.out(RST));
  Button _1 (.out(IR1));
  Button _2 (.out(IR2));
  Button _3 (.out(IR3));
  // Probe on \总周期数 
  // Probe on \总周期数 
  Button \u_继续运行  (.out(Go));
  LED #(.active("true")) led_1 (.in(W1));
  LED #(.active("true")) led_2 (.in(W2));
  LED #(.active("true")) led_3 (.in(W3));
  Hex_Digit_Display hex_digit_display_1 (.value(LedData[31:28]));  // open: dp
  // Probe on IF_PC[19:0]
  // Mips_Probe mips_probe_1: pin names not known; wires that end beside it: IF_IR
  Hex_Digit_Display hex_digit_display_2 (.value(LedData[23:20]));  // open: dp
  Hex_Digit_Display hex_digit_display_3 (.value(LedData[27:24]));  // open: dp
  // Probe on ID_PC[19:0]
  // Mips_Probe mips_probe_2: pin names not known; wires that end beside it: ID_IR
  assign controlled_buffer_1_out = J2 ? PCimm : 32'bz;  // Controlled_Buffer controlled_buffer_1
  assign controlled_buffer_1_out = JMP ? {PC_JAL, addr, 2'b00} : 32'bz;  // Controlled_Buffer controlled_buffer_2
  assign controlled_buffer_1_out = JR ? PC_JR : 32'bz;  // Controlled_Buffer controlled_buffer_3
  Hex_Digit_Display hex_digit_display_4 (.value(LedData[15:12]));  // open: dp
  Hex_Digit_Display hex_digit_display_5 (.value(LedData[19:16]));  // open: dp
  Multiplexer #(.select(3), .width(32), .disabled("Z"), .enable("false")) multiplexer_1 (
    .in0({PC_JAL, adder_2_out}), .in1(PCimm), .in2({PC_JAL, addr, 2'b00}), .in6(PC_JR),
    .out(multiplexer_1_out), .sel({JR, JMP, J2}));  // open: in3, in4, in5, in7
  Hex_Digit_Display hex_digit_display_6 (.value(LedData[7:4]));  // open: dp
  Hex_Digit_Display hex_digit_display_7 (.value(LedData[11:8]));  // open: dp
  Clock #(.highDuration(1), .lowDuration(1)) clock_1 (.out(clock_1_out));
  // Probe on EX_PC[19:0]
  // Mips_Probe mips_probe_3: pin names not known; wires that end beside it: clock_1_out, {EX_IR, addr}, CLK
  Multiplexer #(.select(1), .width(32), .disabled("Z"), .enable("false")) multiplexer_2 (
    .in0(multiplexer_3_out), .in1(multiplexer_1_out), .out(multiplexer_2_out), .sel(FAIL));
  Hex_Digit_Display hex_digit_display_8 (.value(LedData[3:0]));  // open: dp
  Register #(.width(32), .trigger("rising"), .Select("low")) PC (
    .D(multiplexer_2_out), .en(\PC_EN调试 ), .Q(IF_PC), .clk(CLK), .clr(RST));
  // Probe on \总周期数 
  // Probe on M_PC[19:0]
  // Mips_Probe mips_probe_4: pin names not known; wires that end beside it: MEM_IR
  cache cache_1 (
    .BranchAddr_out(cache_1_branchaddr_out), .BRANCH_TAKEN(EX_BRANCHTAKEN), .CLK(CLK),
    .BRANCK_ADDR(controlled_buffer_1_out), .PC(IF_PC), .EX_PC(EX_PC), .PJUMP(cache_1_pjump));  // open: MISS
  // Probe on \总周期数 
  // Probe on \无条件分支数 
  // Probe on \条件分支成功数 
  // Probe on \插入气泡数 
  // Probe on \LoadUse次数 
  ROM #(.addrWidth(10), .dataWidth(32), .Select("high")) rom_1 (.addr(IF_PC[11:2]), .data(IF_IR));
  // Probe on IF_PC[11:0]
  // Probe on WB_PC[19:0]
  // Mips_Probe mips_probe_5: pin names not known; wires that end beside it: WB_IR
  // Probe on ID_PC[11:0]
  // Probe on EX_PC[11:0]
  IF_ID if_id_1 (
    .IR_IN(IF_IR), .PC_IN(IF_PC), .IR(ID_IR), .PC(ID_PC), .reset(\数据相关检测_重定向_1_if_id_stall ), .CLK(CLK),
    .CLEAR(RST), .ENABLE(\数据相关检测_重定向_1_if_id_en ), .PJUMP_IN(cache_1_pjump), .PJUM_OUT(if_id_1_pjum_out));
  Adder #(.width(32)) adder_1 (.a(IF_PC), .b(32'h4), .out(adder_1_out));  // open: cin, cout
  // Probe on M_PC[11:0]
  D_Flip_Flop #(.trigger("high"), .Pre_Clr_Positions("LEGACY"), .NegatePresetClear("false"), .enable("true"), .NewFFLayout("false")) d_ff_1 (.Q(d_ff_1_q));  // open: clk, D, Qn, preset, en, reset
  // Probe on 13'h300
  Multiplexer #(.select(1), .width(32), .disabled("Z"), .enable("false")) multiplexer_3 (
    .in0(adder_1_out), .in1(cache_1_branchaddr_out), .out(multiplexer_3_out), .sel(cache_1_pjump));
  // Probe on WB_PC[11:0]
  Comparator #(.width(13), .mode("twosComplement")) comparator_1 (
    .a(CNT_num), .b(13'h300), .eq(comparator_1_eq), .lt(comparator_1_lt));  // open: gt
  Clock #(.highDuration(1), .lowDuration(1)) clock_2 (.out(clock_2_out));
  nand nand_1 (nand_1_out, d_ff_1_q, comparator_1_eq);
  Counter #(.width(13), .max('h1fff), .ongoal("stay"), .trigger("rising"), .behavior("old")) counter_1 (
    .count(comparator_1_lt), .Q(CNT_num), .clk(clock_2_out));  // open: load, D, carry, clr, preset
  assign CLK = nand_1_out ? clock_2_out : 1'bz;  // Controlled_Buffer controlled_buffer_4
  Pull_Resistor #(.pull(1)) pull_resistor_1 (.node(CLK));
  \单周期硬布线控制器  \u_单周期硬布线控制器_1  (
    .Func(ID_IR[5:0]), .OP(ID_IR[31:26]), .ALU_OP(\单周期硬布线控制器_1_alu_op ), .MemToReg(\单周期硬布线控制器_1_memtoreg ),
    .MemWrite(\单周期硬布线控制器_1_memwrite ), .ALU_SRC(\单周期硬布线控制器_1_alu_src ), .RegWrite(\单周期硬布线控制器_1_regwrite ),
    .SysCALL(\单周期硬布线控制器_1_syscall ), .SignedExt(SignedExt), .RegDst(\单周期硬布线控制器_1_regdst ),
    .JR(\单周期硬布线控制器_1_jr ), .JMP(\单周期硬布线控制器_1_jmp ), .Beq(\单周期硬布线控制器_1_beq ), .JAL(\单周期硬布线控制器_1_jal ),
    .Bne(\单周期硬布线控制器_1_bne ), .BLTZ(\单周期硬布线控制器_1_bltz ), .LUI(\单周期硬布线控制器_1_lui ), .SB(\单周期硬布线控制器_1_sb ));  // open: ERET
  Multiplexer #(.select(1), .width(5), .disabled("Z"), .enable("false")) multiplexer_4 (
    .in0(ID_IR[25:21]), .in1(5'b00010), .out(ID_R1_num), .sel(\单周期硬布线控制器_1_syscall ));
  Multiplexer #(.select(1), .width(5), .disabled("Z"), .enable("false")) multiplexer_5 (
    .in0(ID_IR[20:16]), .in1(5'b00100), .out(ID_R2_num), .sel(\单周期硬布线控制器_1_syscall ));
  assign bit_extender_1_out = {{16{1'b0}}, ID_IR[15:0]};  // Bit_Extender bit_extender_1
  assign bit_extender_2_out = {{16{ID_IR[15]}}, ID_IR[15:0]};  // Bit_Extender bit_extender_2
  Multiplexer #(.select(1), .width(32), .disabled("Z"), .enable("false")) multiplexer_6 (
    .in0(bit_extender_1_out), .in1(bit_extender_2_out), .out(multiplexer_6_out), .sel(SignedExt));
  MIPS_Regifile mips_regifile_1 (
    .Din(RDin), .Clk(CLK), .R1(mips_regifile_1_r1), .R2(mips_regifile_1_r2), .WE(RegWrite), .W_num(W_num),
    .R1_num(ID_R1_num), .R2_num(ID_R2_num));
  ID_EX id_ex_1 (
    .BEQ_IN(\单周期硬布线控制器_1_beq ), .BNE_IN(\单周期硬布线控制器_1_bne ), .MEMTOREG_IN(\单周期硬布线控制器_1_memtoreg ),
    .MEMWRITE_IN(\单周期硬布线控制器_1_memwrite ), .ALUOP_IN(\单周期硬布线控制器_1_alu_op ),
    .ALU_SRC_IN(\单周期硬布线控制器_1_alu_src ), .REGWRITE_IN(\单周期硬布线控制器_1_regwrite ), .JAL_IN(\单周期硬布线控制器_1_jal ),
    .REGDIST_IN(\单周期硬布线控制器_1_regdst ), .SYSCALL_IN(\单周期硬布线控制器_1_syscall ), .JMP_IN(\单周期硬布线控制器_1_jmp ),
    .JR_IN(\单周期硬布线控制器_1_jr ), .IR_IN(ID_IR), .PC_IN(ID_PC), .R2_IN(mips_regifile_1_r2),
    .R1_IN(mips_regifile_1_r1), .IMM_IN(multiplexer_6_out), .BEQ_OUT(BEQ), .BNE_OUT(BNE),
    .MEMTOREG_OUT(id_ex_1_memtoreg_out), .MEMWRITE_OUT(id_ex_1_memwrite_out), .ALUOP_OUT(id_ex_1_aluop_out),
    .ALU_SRC_OUT(id_ex_1_alu_src_out), .REGWRITE_OUT(id_ex_1_regwrite_out), .JAL_OUT(EX_JAL),
    .REGDST_IN(EX_REGD), .SYSCALL_OUT(id_ex_1_syscall_out), .JMP_OUT(JMP), .JR_OUT(JR),
    .IR_OUT({EX_IR, addr}), .PC_OUT(EX_PC), .R2_OUT(id_ex_1_r2_out), .R1_OUT(id_ex_1_r1_out),
    .IMM_OUT(id_ex_1_imm_out), .RESET(\数据相关检测_重定向_1_id_ex_stall ), .CLEAR(RST), .CLK(CLK), .ENABLE(Write),
    .LUI_IN(\单周期硬布线控制器_1_lui ), .LUI_OUT(LUI), .SB_IN(\单周期硬布线控制器_1_sb ), .SB_OUT(id_ex_1_sb_out),
    .BLTZ_IN(\单周期硬布线控制器_1_bltz ), .BLTZ_OUT(BLTZ), .RS_FORW_IN(\数据相关检测_重定向_1_rsforward ),
    .RS_FORW_OUT(id_ex_1_rs_forw_out), .RT_FORW_IN(\数据相关检测_重定向_1_rtforward ),
    .RT_FORW_OUT(id_ex_1_rt_forw_out), .PJUMP_IN(if_id_1_pjum_out), .PJUMP_OUT(pjump));  // open: ERET_IN, ERET_OUT
  Multiplexer #(.select(2), .width(32), .disabled("Z"), .enable("false")) multiplexer_7 (
    .in0(id_ex_1_r1_out), .in1(RDin), .in2({ex_mem_1_aluresult_out, sb_addr}),
    .in3({ex_mem_1_aluresult_out, sb_addr}), .out(PC_JR), .sel(id_ex_1_rs_forw_out));
  Multiplexer #(.select(2), .width(32), .disabled("Z"), .enable("false")) multiplexer_8 (
    .in0(id_ex_1_r2_out), .in1(RDin), .in2({ex_mem_1_aluresult_out, sb_addr}),
    .in3({ex_mem_1_aluresult_out, sb_addr}), .out(multiplexer_8_out), .sel(id_ex_1_rt_forw_out));
  Multiplexer #(.select(1), .width(5), .disabled("Z"), .enable("false")) multiplexer_9 (
    .in0(addr[20:16]), .in1(addr[15:11]), .out(multiplexer_9_out), .sel(EX_REGD));
  Multiplexer #(.select(1), .width(32), .disabled("Z"), .enable("false")) multiplexer_10 (
    .in0(multiplexer_8_out), .in1(id_ex_1_imm_out), .out(multiplexer_10_out), .sel(id_ex_1_alu_src_out));
  Adder #(.width(32)) adder_2 (.a(EX_PC), .b(32'h4), .out({PC_JAL, adder_2_out}));  // open: cin, cout
  Shifter #(.width(32), .shift("ll")) shifter_1 (.in(id_ex_1_imm_out), .\dist (5'b00010), .out(shifter_1_out));
  Multiplexer #(.select(1), .width(5), .disabled("Z"), .enable("false")) multiplexer_11 (
    .in0(multiplexer_9_out), .in1({5{1'b1}}), .out(EX_REGTOWRITE), .sel(EX_JAL));
  Comparator #(.width(32), .mode("twosComplement")) comparator_2 (
    .a({32{1'b0}}), .b(PC_JR), .gt(comparator_2_gt));  // open: eq, lt
  Multiplexer #(.select(1), .width(32), .disabled("Z"), .enable("false")) multiplexer_12 (
    .in0(multiplexer_10_out), .in1(32'h22), .out(multiplexer_12_out), .sel(id_ex_1_syscall_out));
  Adder #(.width(32)) adder_3 (.a({PC_JAL, adder_2_out}), .b(shifter_1_out), .out(PCimm));  // open: cin, cout
  MIPS_ALU mips_alu_1 (
    .X(PC_JR), .Y(multiplexer_12_out), .AluOP(id_ex_1_aluop_out), .Equal(mips_alu_1_equal),
    .Result(mips_alu_1_result), .shamt(shamt));  // open: Result_2
  Multiplexer #(.select(1), .width(5), .disabled("Z"), .enable("false")) multiplexer_13 (
    .in0(addr[10:6]), .in1(5'b10000), .out(shamt), .sel(LUI));
  and and_1 (and_1_out, comparator_2_gt, BLTZ);
  or or_1 (J2, and_1_out, and_2_out, and_3_out);
  and and_2 (and_2_out, BEQ, mips_alu_1_equal);
  and and_3 (and_3_out, BNE, ~mips_alu_1_equal);  // AND_Gate
  or or_2 (or_2_out, JMP, JR);
  or or_3 (or_3_out, ~Halt, Go);  // OR_Gate
  or or_4 (EX_BRANCHTAKEN, J2, JR, JMP);
  EX_MEM ex_mem_1 (
    .MemToReg_in(id_ex_1_memtoreg_out), .MemWrite_in(id_ex_1_memwrite_out),
    .RegWrite_in(id_ex_1_regwrite_out), .JAL_in(EX_JAL), .RegDst_in(EX_REGD),
    .Syscall_in(id_ex_1_syscall_out), .equal_in(mips_alu_1_equal), .IR_in({EX_IR, addr}), .PC_in(EX_PC),
    .ALUResult_in(mips_alu_1_result), .R2_in(multiplexer_8_out), .R1_in(PC_JR),
    .MemToReg_out(ex_mem_1_memtoreg_out), .MemWrite_out(MemWrite), .RegWrite_out(ex_mem_1_regwrite_out),
    .JAL_out(MEM_JAL), .RegDst_out(MEM_REGD), .Syscall_out(ex_mem_1_syscall_out),
    .equal_out(ex_mem_1_equal_out), .IR_out(MEM_IR), .PC_out(M_PC),
    .ALUResult_out({ex_mem_1_aluresult_out, sb_addr}), .R2_out(sb_r2), .R1_out(ex_mem_1_r1_out),
    .RESET(1'b0), .CLK(CLK), .CLEAR(RST), .ENABLE(Write), .SB_in(id_ex_1_sb_out), .SB_out(SB_USE));  // open: Imm_in, Imm_out
  and and_4 (and_4_out, or_2_out, or_3_out);
  and and_5 (and_5_out, J2, or_3_out);
  xor xor_1 (FAIL, EX_BRANCHTAKEN, pjump);
  and and_6 (and_6_out, ~sb_addr[0], ~sb_addr[1]);  // AND_Gate
  and and_7 (and_7_out, sb_addr[0], ~sb_addr[1]);  // AND_Gate
  and and_8 (and_8_out, ~sb_addr[0], sb_addr[1]);  // AND_Gate
  and and_9 (and_9_out, sb_addr[0], sb_addr[1]);
  Counter #(.width(16), .max('hffff), .ongoal("wrap"), .trigger("rising"), .behavior("old")) counter_2 (
    .count(and_4_out), .Q(\无条件分支数 ), .clk(CLK), .clr(RST));  // open: load, D, carry, preset
  Counter #(.width(16), .max('hffff), .ongoal("wrap"), .trigger("rising"), .behavior("old")) counter_3 (
    .count(and_5_out), .Q(\条件分支成功数 ), .clk(CLK), .clr(RST));  // open: load, D, carry, preset
  not not_1 (not_1_out, CLK);
  Multiplexer #(.select(1), .width(5), .disabled("Z"), .enable("false")) multiplexer_14 (
    .in0(MEM_IR[20:16]), .in1(MEM_IR[15:11]), .out(multiplexer_14_out), .sel(MEM_REGD));
  Multiplexer #(.select(1), .width(8), .disabled("Z"), .enable("false")) multiplexer_15 (
    .in0(DATA_CHA[7:0]), .in1(sb_r2[7:0]), .out(multiplexer_15_out), .sel(and_6_out));
  Multiplexer #(.select(1), .width(8), .disabled("Z"), .enable("false")) multiplexer_16 (
    .in0(DATA_CHA[15:8]), .in1(sb_r2[7:0]), .out(multiplexer_16_out), .sel(and_7_out));
  Multiplexer #(.select(1), .width(8), .disabled("Z"), .enable("false")) multiplexer_17 (
    .in0(DATA_CHA[23:16]), .in1(sb_r2[7:0]), .out(multiplexer_17_out), .sel(and_8_out));
  RAM #(.addrWidth(10), .dataWidth(32), .bus("separate"), .Select("high")) ram_1 (
    .addr(ex_mem_1_aluresult_out[11:2]), .din(MDin), .data(DATA_CHA), .str(MemWrite), .clk(not_1_out),
    .clr(RST));  // open: sel, ld
  Multiplexer #(.select(1), .width(5), .disabled("Z"), .enable("false")) multiplexer_18 (
    .in0(multiplexer_14_out), .in1({5{1'b1}}), .out(MEM_REGTOWRITE), .sel(MEM_JAL));
  Multiplexer #(.select(1), .width(8), .disabled("Z"), .enable("false")) multiplexer_19 (
    .in0(DATA_CHA[31:24]), .in1(sb_r2[7:0]), .out(multiplexer_19_out), .sel(and_9_out));
  and and_10 (and_10_out, Write, \数据相关 );
  MEM_WB mem_wb_1 (
    .MemToReg_in(ex_mem_1_memtoreg_out), .MemWrite_in(MemWrite), .RegWrite_in(ex_mem_1_regwrite_out),
    .JAL_in(MEM_JAL), .RegDst_in(MEM_REGD), .Syscall_in(ex_mem_1_syscall_out), .equal_in(ex_mem_1_equal_out),
    .IR_in(MEM_IR), .PC_in(M_PC), .ALUResult_in({ex_mem_1_aluresult_out, sb_addr}), .RD_in(DATA_CHA),
    .R1_in(ex_mem_1_r1_out), .MemToReg_out(mem_wb_1_memtoreg_out), .RegWrite_out(RegWrite),
    .JAL_out(mem_wb_1_jal_out), .RegDst_out(mem_wb_1_regdst_out), .Syscall_out(mem_wb_1_syscall_out),
    .IR_out(WB_IR), .PC_out(WB_PC), .ALUResult_out(mem_wb_1_aluresult_out), .RD_out(mem_wb_1_rd_out),
    .\气泡_高电平时有效 (1'b0), .clk(CLK), .clear(RST), .enable(Write), .R1_out(R1), .R2_in(sb_r2), .R2_out(R2));  // open: MemWrite_out, equal_out
  Multiplexer #(.select(1), .width(32), .disabled("Z"), .enable("false")) multiplexer_20 (
    .in0(sb_r2), .in1({multiplexer_19_out, multiplexer_17_out, multiplexer_16_out, multiplexer_15_out}),
    .out(MDin), .sel(SB_USE));
  Counter #(.width(16), .max('hffff), .ongoal("wrap"), .trigger("rising"), .behavior("old")) counter_4 (
    .count(and_10_out), .Q(\插入气泡数 ), .clk(CLK), .clr(RST));  // open: load, D, carry, preset
  Counter #(.width(16), .max('hffff), .ongoal("wrap"), .trigger("rising"), .behavior("old")) counter_5 (
    .load(1'b0), .count(not_2_out), .Q(\总周期数 ), .clk(CLK), .clr(RST));  // open: D, carry, preset
  not not_2 (not_2_out, Halt);
  Multiplexer #(.select(1), .width(32), .disabled("Z"), .enable("false")) multiplexer_21 (
    .in0(mem_wb_1_aluresult_out), .in1(mem_wb_1_rd_out), .out(multiplexer_21_out), .sel(mem_wb_1_memtoreg_out));
  or or_5 (or_5_out, ~Halt, Go);  // OR_Gate
  \数据相关检测_重定向  \u_数据相关检测_重定向_1  (
    .OP(ID_IR[31:26]), .FUNC(ID_IR[5:0]), .RS(ID_R1_num), .Halt_or_Go(or_5_out),
    .EX_MEMTOREG(id_ex_1_memtoreg_out), .EX_WRITEREG(EX_REGTOWRITE), .RT(ID_R2_num), .\J标记 (FAIL),
    .MEM_REGW(ex_mem_1_regwrite_out), .MEM_WRITEREG(MEM_REGTOWRITE), .EX_REGW(id_ex_1_regwrite_out),
    .PC_EN(\PC_EN调试 ), .LOAD_USED(\数据相关 ), .IF_ID_EN(\数据相关检测_重定向_1_if_id_en ),
    .IF_ID_STALL(\数据相关检测_重定向_1_if_id_stall ), .ID_EX_STALL(\数据相关检测_重定向_1_id_ex_stall ),
    .RSFORWARD(\数据相关检测_重定向_1_rsforward ), .RTFORWARD(\数据相关检测_重定向_1_rtforward ));
  nand nand_2 (Write, not_3_out, Halt);
  Multiplexer #(.select(1), .width(5), .disabled("Z"), .enable("false")) multiplexer_22 (
    .in0(WB_IR[20:16]), .in1(WB_IR[15:11]), .out(multiplexer_22_out), .sel(mem_wb_1_regdst_out));
  Adder #(.width(32)) adder_4 (.a(WB_PC), .b(32'h4), .out(adder_4_out));  // open: cin, cout
  not not_3 (not_3_out, Go);
  Multiplexer #(.select(1), .width(32), .disabled("Z"), .enable("false")) multiplexer_23 (
    .in0(multiplexer_21_out), .in1(adder_4_out), .out(RDin), .sel(mem_wb_1_jal_out));
  Multiplexer #(.select(1), .width(5), .disabled("Z"), .enable("false")) multiplexer_24 (
    .in0(multiplexer_22_out), .in1({5{1'b1}}), .out(W_num), .sel(mem_wb_1_jal_out));
  Comparator #(.width(32), .mode("twosComplement")) comparator_3 (
    .a(R1), .b(32'h22), .eq(comparator_3_eq));  // open: gt, lt
  and and_11 (Ledout, comparator_3_eq, mem_wb_1_syscall_out);
  and and_12 (Halt, ~comparator_3_eq, mem_wb_1_syscall_out);  // AND_Gate
  Register #(.width(32), .trigger("rising"), .Select("low")) register_1 (
    .D(R2), .en(Ledout), .Q(LedData), .clk(CLK), .clr(RST));

  // Other names for the same wires on the sheet: RD[4:0] = ID_IR[15:11]; MEM_PC[31:0] = M_PC; EX_IR[25:0] = addr;
  //   PC_JAL[27:2] = addr

  // Notes on the sheet:
  //   中断源
  //   时空图监测，可删除
  //   中断等待指示
  //   数码管输出
  //   指令存储器
  //   contents of rom_1 (hex, n*v repeats v):
  //   20110001 8100005 20110001 20120002 20130003 8100009 20110001 20120002 20130003 810000d 20110001
  //   20120002 20130003 8100011 20110001 20120002 20130003 c1000fa 20100001 20110001 118fc0 112020
  //   20020022 c 118882 12200001 8100015 112020 20020022 c 20110001 118880 112020 20020022 c 12200001
  //   810001f 20110001 118fc0 112020 20020022 c 1188c3 112020 20020022 c 118903 112020 20020022 c 118903
  //   112020 20020022 c 118903 112020 20020022 c 118903 112020 20020022 c 118903 112020 20020022 c 118903
  //   112020 20020022 c 118903 112020 20020022 c 20100001 109fc0 139fc3 8021 2012000c 24160003 26100001
  //   3210000f 20080008 20090001 139900 2709825 132020 20020022 c 1094022 1500fff9 22100001 2018000f
  //   2188024 108700 20080008 20090001 139902 2709825 132021 20020022 c 1094022 1500fff9 108702 2c9b022
  //   12c00001 8100050 4020 1084027 84400 3508ffff 82021 20020022 c 2010ffff 20110000 ae300000 22100001
  //   22310004 ae300000 22100001 22310004 ae300000 22100001 22310004 ae300000 22100001 22310004 ae300000
  //   22100001 22310004 ae300000 22100001 22310004 ae300000 22100001 22310004 ae300000 22100001 22310004
  //   ae300000 22100001 22310004 ae300000 22100001 22310004 ae300000 22100001 22310004 ae300000 22100001
  //   22310004 ae300000 22100001 22310004 ae300000 22100001 22310004 ae300000 22100001 22310004 ae300000
  //   22100001 22310004 22100001 8020 2011003c 8e130000 8e340000 274402a 11000002 ae330000 ae140000
  //   2231fffc 1611fff8 102020 20020022 c 22100004 2011003c 1611fff2 20020032 c 20080001 20110010 112020
  //   20020022 c 200b0020 2288823 112020 20020022 c 216bffff 1560fffa 2002000a c 200b0008 3c11fedc
  //   3631ffff 112020 20020022 c 3c11ba98 112020 c 3c117654 112020 c 3c113210 112020 c 216bffff 1560fff0
  //   2002000a c 20090000 200b0020 20110000 20120001 a1310000 112020 20020022 c 2328820 21290001 216bffff
  //   1560fff8 200b0008 20090000 8d310000 112020 20020022 c 21290004 216bffff 1560fff9 2002000a c 2011fff1
  //   112020 20020022 c 22310001 620fffb 2002000a c 2002000a c 20100000 22100001 102020 20020022 c
  //   22100002 102020 20020022 c 22100003 102020 20020022 c 22100004 102020 20020022 c 22100005 102020
  //   20020022 c 22100006 102020 20020022 c 22100007 102020 20020022 c 22100008 102020 20020022 20020022 c
  //   3e00008
  //   控制位
  //   流水调试日志用
  //   暂停节拍，不能为0
  //   OP
  //   Func
  //   rs
  //   rt
  //   rd
  //   指令字
  //   戳工具置1进入计数暂停模式，ctrl+k时钟自动运行到对应节拍暂停
  //   ctrl+k关闭时钟连续运行，将控制位置零，进入单步调试模式调试
  //   可计数暂停的时钟源
  //   JMP
  //   JR
  //   OP
  //   Func
  //   Beq
  //   Bne
  //   AluOP
  //   AluSrcB
  //   RegWrite
  //   JAL
  //   RegDst
  //   Syscall
  //   MemToReg
  //   MemWrite
  //   为方便自动评测，需要输出流水线各段保存的PC值，注意是PC不是PC+4，另外ID段寄存器写入信息，Mem段内存写入信息也要输出
  //   指令调试器件
  //   SB指令电路
endmodule

module \数据相关检测_重定向  (
  input  [5:0] OP,
  input  [5:0] FUNC,
  input  [4:0] RS,
  input  Halt_or_Go,
  input  EX_MEMTOREG,
  input  [4:0] EX_WRITEREG,
  input  [4:0] RT,
  input  \J标记 ,
  input  MEM_REGW,
  input  [4:0] MEM_WRITEREG,
  input  EX_REGW,
  output PC_EN,
  output LOAD_USED,
  output IF_ID_EN,
  output IF_ID_STALL,
  output ID_EX_STALL,
  output [1:0] RSFORWARD,
  output [1:0] RTFORWARD
);

  wire and_1_out, and_2_out, comparator_1_eq, comparator_2_eq, comparator_3_eq, comparator_4_eq,
       comparator_5_eq, comparator_6_eq, not_1_out, not_2_out, \源寄存器使用情况_1_r1_used , \源寄存器使用情况_1_r2_used ;
  wire [1:0] and_3_out, and_5_out;

  \源寄存器使用情况  \u_源寄存器使用情况_1  (.R1_Used(\源寄存器使用情况_1_r1_used ), .R2_Used(\源寄存器使用情况_1_r2_used ), .OP(OP), .FUNC(FUNC));
  Comparator #(.width(5), .mode("twosComplement")) comparator_1 (
    .a(RS), .b({5{1'b0}}), .eq(comparator_1_eq));  // open: gt, lt
  Comparator #(.width(5), .mode("twosComplement")) comparator_2 (
    .a(RS), .b(EX_WRITEREG), .eq(comparator_2_eq));  // open: gt, lt
  Comparator #(.width(5), .mode("twosComplement")) comparator_3 (
    .a(RT), .b({5{1'b0}}), .eq(comparator_3_eq));  // open: gt, lt
  Comparator #(.width(5), .mode("twosComplement")) comparator_4 (
    .a(RT), .b(EX_WRITEREG), .eq(comparator_4_eq));  // open: gt, lt
  Comparator #(.width(5), .mode("twosComplement")) comparator_5 (
    .a(RS), .b(MEM_WRITEREG), .eq(comparator_5_eq));  // open: gt, lt
  Comparator #(.width(5), .mode("twosComplement")) comparator_6 (
    .a(RT), .b(MEM_WRITEREG), .eq(comparator_6_eq));  // open: gt, lt
  not not_1 (not_1_out, comparator_1_eq);
  not not_2 (not_2_out, comparator_3_eq);
  and and_1 (and_1_out, \源寄存器使用情况_1_r1_used , not_1_out, EX_MEMTOREG, comparator_2_eq);
  and and_2 (and_2_out, \源寄存器使用情况_1_r2_used , not_2_out, EX_MEMTOREG, comparator_4_eq);
  and and_3 (and_3_out[0], \源寄存器使用情况_1_r1_used , not_1_out, MEM_REGW, comparator_5_eq);
  and and_4 (and_3_out[1], \源寄存器使用情况_1_r1_used , not_1_out, EX_REGW, comparator_2_eq);
  and and_5 (and_5_out[0], \源寄存器使用情况_1_r2_used , not_2_out, MEM_REGW, comparator_6_eq);
  and and_6 (and_5_out[1], \源寄存器使用情况_1_r2_used , not_2_out, EX_REGW, comparator_4_eq);
  or or_1 (LOAD_USED, and_1_out, and_2_out);
  Multiplexer #(.select(2), .width(2), .disabled("Z"), .enable("false")) multiplexer_1 (
    .in0(2'b00), .in1(2'b01), .in2(2'b10), .in3(2'b10), .out(RSFORWARD), .sel(and_3_out));
  Multiplexer #(.select(2), .width(2), .disabled("Z"), .enable("false")) multiplexer_2 (
    .in0(2'b00), .in1(2'b01), .in2(2'b10), .in3(2'b10), .out(RTFORWARD), .sel(and_5_out));
  and and_7 (PC_EN, Halt_or_Go, ~LOAD_USED);  // AND_Gate
  and and_8 (IF_ID_EN, Halt_or_Go, ~LOAD_USED);  // AND_Gate
  or or_2 (ID_EX_STALL, LOAD_USED, \J标记 );

  assign IF_ID_STALL = \J标记 ;
endmodule

module \中断按键参考电路  (
  input  \同步清零信号 ,
  output \与中断屏蔽位与 
);

  wire \_1号中断_out , and_1_out, clock_1_out, d_ff_1_q, or_1_out, or_2_out;

  Clock #(.highDuration(1), .lowDuration(1)) clock_1 (.out(clock_1_out));
  Button \_1号中断  (.out(\_1号中断_out ));
  or or_1 (or_1_out, \与中断屏蔽位与 , d_ff_1_q);
  LED #(.active("true")) \_1号中断等待指示灯  (.in(or_1_out));
  D_Flip_Flop #(.trigger("rising"), .Pre_Clr_Positions("LEGACY"), .NegatePresetClear("false"), .enable("true"), .NewFFLayout("false")) d_ff_1 (
    .clk(\_1号中断_out ), .D(1'b1), .Q(d_ff_1_q), .reset(\与中断屏蔽位与 ));  // open: Qn, preset, en
  or or_2 (or_2_out, d_ff_1_q, \与中断屏蔽位与 );
  and and_1 (and_1_out, or_2_out, ~\同步清零信号 );  // AND_Gate
  D_Flip_Flop #(.trigger("rising"), .Pre_Clr_Positions("LEGACY"), .NegatePresetClear("false"), .enable("true"), .NewFFLayout("false")) IR1 (
    .clk(clock_1_out), .D(and_1_out), .Q(\与中断屏蔽位与 ));  // open: Qn, preset, en, reset
  \单周期硬布线控制器  \u_单周期硬布线控制器_1  ();  // open: Func, OP, ALU_OP, MemToReg, MemWrite, ALU_SRC, RegWrite, SysCALL, SignedExt, RegDst, JR, JMP, Beq, JAL, Bne, ERET, BLTZ, LUI, SB

  // Notes on the sheet:
  //   中断信号采样参考电路
  //   Reset 
endmodule

module \单周期MIPS_单级中断  (
  input  IR1,
  input  IR2,
  input  IR3,
  output RegWrite,
  output MemWrite,
  output [31:0] PC,
  output [31:0] IR,
  output [31:0] RDin,
  output [31:0] MDin,
  output [31:0] LedData
);

  wire AluSrcB, and_1_out, and_2_out, and_3_out, and_4_out, and_5_out, and_8_out, Beq, Bne, CLK, CLR1, CLR2,
       CLR3, comparator_1_eq, comparator_2_eq, comparator_3_eq, comparator_4_eq, comparator_5_eq, d_ff_1_q,
       d_ff_2_q, d_ff_3_q, Equal, ERET, Go, Halt, IE, INT, INT0, INT1, INT2, INT3, IR1_t, IR2_t, IR3_t, IRA,
       IRB, IRC, J2, JAL, JMP, JR, LED, MemToReg, not_1_out, not_2_out, not_3_out, or_1_out, or_3_out,
       or_10_out, or_11_out, or_12_out, RegDst, SignedExt, Syscall, W1, W2, W3;
  wire [1:0] priority_encoder_1_out, register_2_q;
  wire [3:0] AluOP;
  wire [4:0] multiplexer_4_out, multiplexer_5_out, multiplexer_6_out, multiplexer_7_out;
  wire [15:0] \总周期数 ;
  wire [31:0] bit_extender_1_out, bit_extender_2_out, EPC_ADDR, INT_ADDR, mips_alu_1_result,
       multiplexer_2_out, multiplexer_3_out, multiplexer_8_out, multiplexer_11_out, PC4, PC_JR, PCimm,
       ram_1_data, RET_ADDR, shifter_1_out;

  Clock #(.highDuration(1), .lowDuration(1)) clock_1 (.out(CLK));
  Button _1 ();  // open: out
  Button _2 ();  // open: out
  Button _3 ();  // open: out
  Button \u_继续运行  (.out(Go));
  LED #(.active("true")) led_1 (.in(W1));
  LED #(.active("true")) led_2 (.in(W2));
  LED #(.active("true")) led_3 (.in(W3));
  not not_1 (not_1_out, Equal);
  Hex_Digit_Display hex_digit_display_1 (.value(LedData[31:28]));  // open: dp
  Comparator #(.width(16), .mode("twosComplement")) comparator_1 (
    .a(16'h23b), .b(\总周期数 ), .eq(comparator_1_eq));  // open: gt, lt
  Comparator #(.width(16), .mode("twosComplement")) comparator_2 (
    .a(\总周期数 ), .b(16'h1), .eq(comparator_2_eq));  // open: gt, lt
  Comparator #(.width(16), .mode("twosComplement")) comparator_3 (
    .a(\总周期数 ), .b(16'h4), .eq(comparator_3_eq));  // open: gt, lt
  Comparator #(.width(16), .mode("twosComplement")) comparator_4 (
    .a(\总周期数 ), .b(16'h7), .eq(comparator_4_eq));  // open: gt, lt
  Multiplexer #(.select(3), .width(32), .disabled("Z"), .enable("false")) multiplexer_1 (
    .in0(PC4), .in1(PCimm), .in2({PC4[31:28], IR[25:0], 2'b00}), .in6(PC_JR), .out(RET_ADDR),
    .sel({JR, JMP, J2}));  // open: in3, in4, in5, in7
  and and_1 (and_1_out, Beq, Equal);
  and and_2 (and_2_out, Bne, not_1_out);
  Adder #(.width(32)) adder_1 (.a(PC), .b(32'h4), .out(PC4));  // open: cin, cout
  Hex_Digit_Display hex_digit_display_2 (.value(LedData[27:24]));  // open: dp
  Hex_Digit_Display hex_digit_display_3 (.value(LedData[23:20]));  // open: dp
  or or_1 (or_1_out, comparator_1_eq, comparator_2_eq);
  assign IRA = or_1_out ? ~CLK : 1'bz;  // Controlled_Inverter controlled_inverter_1
  assign IRB = comparator_3_eq ? ~CLK : 1'bz;  // Controlled_Inverter controlled_inverter_2
  assign IRC = comparator_4_eq ? ~CLK : 1'bz;  // Controlled_Inverter controlled_inverter_3
  Multiplexer #(.select(1), .width(32), .disabled("Z"), .enable("false")) multiplexer_2 (
    .in0(RET_ADDR), .in1(INT_ADDR), .out(multiplexer_2_out), .sel(INT));
  Multiplexer #(.select(1), .width(32), .disabled("Z"), .enable("false")) multiplexer_3 (
    .in0(multiplexer_2_out), .in1(EPC_ADDR), .out(multiplexer_3_out), .sel(ERET));
  or or_2 (J2, and_1_out, and_2_out);
  Hex_Digit_Display hex_digit_display_4 (.value(LedData[15:12]));  // open: dp
  Hex_Digit_Display hex_digit_display_5 (.value(LedData[19:16]));  // open: dp
  Pull_Resistor #(.pull(0)) pull_resistor_1 (.node(IRA));
  Pull_Resistor #(.pull(0)) pull_resistor_2 (.node(IRB));
  Pull_Resistor #(.pull(0)) pull_resistor_3 (.node(IRC));
  or or_3 (or_3_out, not_2_out, Go);
  not not_2 (not_2_out, Halt);
  Hex_Digit_Display hex_digit_display_6 (.value(LedData[11:8]));  // open: dp
  Hex_Digit_Display hex_digit_display_7 (.value(LedData[7:4]));  // open: dp
  // Probe on \总周期数 
  Counter #(.width(16), .max('hffff), .ongoal("wrap"), .trigger("rising"), .behavior("old")) counter_1 (
    .load(1'b0), .count(or_3_out), .Q(\总周期数 ), .clk(CLK), .clr(1'b0));  // open: D, carry, preset
  Register #(.width(32), .trigger("rising"), .Select("low")) u_PC (
    .D(multiplexer_3_out), .en(or_3_out), .Q(PC), .clk(CLK), .clr(1'b0));
  Hex_Digit_Display hex_digit_display_8 (.value(LedData[3:0]));  // open: dp
  Register #(.width(32), .trigger("rising"), .Select("low")) register_1 (
    .D(MDin), .en(LED), .Q(LedData), .clk(CLK), .clr(1'b0));
  or or_4 (IR1_t, IR1, IRA);
  ROM #(.addrWidth(10), .dataWidth(32), .Select("high")) rom_1 (.addr(PC[11:2]), .data(IR));
  or or_5 (IR2_t, IR2, IRB);
  // Mips_Probe mips_probe_1: pin names not known; wires that end beside it: IR
  or or_6 (IR3_t, IR3, IRC);
  Multiplexer #(.select(1), .width(5), .disabled("Z"), .enable("false")) multiplexer_4 (
    .in0(IR[20:16]), .in1(IR[15:11]), .out(multiplexer_4_out), .sel(RegDst));
  Multiplexer #(.select(1), .width(5), .disabled("Z"), .enable("false")) multiplexer_5 (
    .in0(IR[25:21]), .in1(5'b00010), .out(multiplexer_5_out), .sel(Syscall));
  Multiplexer #(.select(1), .width(5), .disabled("Z"), .enable("false")) multiplexer_6 (
    .in0(IR[20:16]), .in1(5'b00100), .out(multiplexer_6_out), .sel(Syscall));
  Multiplexer #(.select(1), .width(5), .disabled("Z"), .enable("false")) multiplexer_7 (
    .in0(multiplexer_4_out), .in1({5{1'b1}}), .out(multiplexer_7_out), .sel(JAL));
  assign bit_extender_1_out = {{16{1'b0}}, IR[15:0]};  // Bit_Extender bit_extender_1
  assign bit_extender_2_out = {{16{IR[15]}}, IR[15:0]};  // Bit_Extender bit_extender_2
  Shifter #(.width(32), .shift("ll")) shifter_1 (.in(bit_extender_2_out), .\dist (5'b00010), .out(shifter_1_out));
  D_Flip_Flop #(.trigger("rising"), .Pre_Clr_Positions("LEGACY"), .NegatePresetClear("false"), .enable("true"), .NewFFLayout("false")) d_ff_1 (
    .clk(IR1_t), .D(1'b1), .Q(d_ff_1_q), .reset(INT1));  // open: Qn, preset, en
  or or_7 (W1, INT1, d_ff_1_q);
  D_Flip_Flop #(.trigger("rising"), .Pre_Clr_Positions("LEGACY"), .NegatePresetClear("false"), .enable("true"), .NewFFLayout("false")) d_ff_2 (
    .clk(IR2_t), .D(1'b1), .Q(d_ff_2_q), .reset(INT2));  // open: Qn, preset, en
  or or_8 (W2, INT2, d_ff_2_q);
  D_Flip_Flop #(.trigger("rising"), .Pre_Clr_Positions("LEGACY"), .NegatePresetClear("false"), .enable("true"), .NewFFLayout("false")) d_ff_3 (
    .clk(IR3_t), .D(1'b1), .Q(d_ff_3_q), .reset(INT3));  // open: Qn, preset, en
  or or_9 (W3, INT3, d_ff_3_q);
  MIPS_Regifile mips_regifile_1 (
    .Din(RDin), .Clk(CLK), .R1(PC_JR), .R2(MDin), .WE(RegWrite), .W_num(multiplexer_7_out),
    .R1_num(multiplexer_5_out), .R2_num(multiplexer_6_out));
  Comparator #(.width(32), .mode("twosComplement")) comparator_5 (
    .a(32'h22), .b(PC_JR), .eq(comparator_5_eq));  // open: gt, lt
  Adder #(.width(32)) adder_2 (.a(shifter_1_out), .b(PC4), .out(PCimm));  // open: cin, cout
  or or_10 (or_10_out, d_ff_1_q, INT1);
  and and_3 (and_3_out, or_10_out, ~CLR1);  // AND_Gate
  or or_11 (or_11_out, d_ff_2_q, INT2);
  and and_4 (and_4_out, or_11_out, ~CLR2);  // AND_Gate
  or or_12 (or_12_out, d_ff_3_q, INT3);
  and and_5 (and_5_out, or_12_out, ~CLR3);  // AND_Gate
  and and_6 (LED, Syscall, comparator_5_eq);
  not not_3 (not_3_out, comparator_5_eq);
  and and_7 (Halt, not_3_out, Syscall);
  Multiplexer #(.select(2), .width(32), .disabled("Z"), .enable("false")) multiplexer_8 (
    .in0(MDin), .in1(MDin), .in2(bit_extender_1_out), .in3(bit_extender_2_out), .out(multiplexer_8_out),
    .sel({AluSrcB, SignedExt}));
  D_Flip_Flop #(.trigger("rising"), .Pre_Clr_Positions("LEGACY"), .NegatePresetClear("false"), .enable("true"), .NewFFLayout("false")) u_IR1 (
    .clk(CLK), .D(and_3_out), .Q(INT1));  // open: Qn, preset, en, reset
  D_Flip_Flop #(.trigger("rising"), .Pre_Clr_Positions("LEGACY"), .NegatePresetClear("false"), .enable("true"), .NewFFLayout("false")) u_IR2 (
    .clk(CLK), .D(and_4_out), .Q(INT2));  // open: Qn, preset, en, reset
  D_Flip_Flop #(.trigger("rising"), .Pre_Clr_Positions("LEGACY"), .NegatePresetClear("false"), .enable("true"), .NewFFLayout("false")) u_IR3 (
    .clk(CLK), .D(and_5_out), .Q(INT3));  // open: Qn, preset, en, reset
  Multiplexer #(.select(1), .width(32), .disabled("Z"), .enable("false")) multiplexer_9 (
    .in0(multiplexer_11_out), .in1(PC4), .out(RDin), .sel(JAL));
  \单周期硬布线控制器  \u_单周期硬布线控制器_1  (
    .Func(IR[5:0]), .OP(IR[31:26]), .ALU_OP(AluOP), .MemToReg(MemToReg), .MemWrite(MemWrite),
    .ALU_SRC(AluSrcB), .RegWrite(RegWrite), .SysCALL(Syscall), .SignedExt(SignedExt), .RegDst(RegDst),
    .JR(JR), .JMP(JMP), .Beq(Beq), .JAL(JAL), .Bne(Bne), .ERET(ERET));  // open: BLTZ, LUI, SB
  MIPS_ALU mips_alu_1 (
    .X(PC_JR), .Y(multiplexer_8_out), .AluOP(AluOP), .Equal(Equal), .Result(mips_alu_1_result),
    .shamt(IR[10:6]));  // open: Result_2
  and and_8 (and_8_out, INT0, ~ERET);  // AND_Gate
  or or_13 (INT0, INT3, INT2, INT1);
  D_Flip_Flop #(.trigger("rising"), .Pre_Clr_Positions("ABOVE_BELOW"), .NegatePresetClear("false"), .enable("false"), .NewFFLayout("true")) d_ff_4 (
    .clk(CLK), .D(and_8_out), .Q(IE));  // open: Qn, preset, reset
  Priority_Encoder #(.select(2), .disabled("Z")) priority_encoder_1 (
    .in0(INT1), .in1(INT2), .in2(INT3), .out(priority_encoder_1_out));  // open: in3, gs, en_out, en_in
  Register #(.width(32), .trigger("rising"), .Select("low")) \EPC寄存器  (
    .D(RET_ADDR), .en(INT), .Q(EPC_ADDR), .clk(CLK));  // open: clr
  Multiplexer #(.select(2), .width(32), .disabled("Z"), .enable("false")) multiplexer_10 (
    .in0(32'h30ac), .in1(32'h3150), .in2(32'h31f4), .out(INT_ADDR), .sel(priority_encoder_1_out));  // open: in3
  Register #(.width(2), .trigger("rising"), .Select("low")) register_2 (
    .D(priority_encoder_1_out), .en(INT), .Q(register_2_q), .clk(CLK));  // open: clr
  Demultiplexer #(.select(2), .width(1), .tristate("false"), .disabled("Z"), .enable("false")) demultiplexer_1 (
    .out0(CLR1), .out1(CLR2), .out2(CLR3), .in(ERET), .sel(register_2_q));  // open: out3
  RAM #(.addrWidth(10), .dataWidth(32), .bus("separate"), .Select("high")) ram_1 (
    .addr(mips_alu_1_result[11:2]), .din(MDin), .data(ram_1_data), .str(MemWrite), .clk(CLK), .clr(1'b0));  // open: sel, ld
  and and_9 (INT, INT0, ~IE);  // AND_Gate
  Multiplexer #(.select(1), .width(32), .disabled("Z"), .enable("false")) multiplexer_11 (
    .in0(mips_alu_1_result), .in1(ram_1_data), .out(multiplexer_11_out), .sel(MemToReg));

  // Other names for the same wires on the sheet: addr[25:0] = IR[25:0]; Func[5:0] = IR[5:0]; imm[15:0] = IR[15:0];
  //   PC_JAL[31:2] = {PC4[31:28], IR[25:0]}; shamt[4:0] = IR[10:6]; rd[4:0] = IR[15:11]; rt[4:0] = IR[20:16];
  //   rs[4:0] = IR[25:21]; OP[5:0] = IR[31:26]; LEDD[31:0] = MDin

  // Notes on the sheet:
  //   中断源
  //   中断等待指示
  //   总复位信号应将除ROM以外所有存储组件全部清零
  //   单级中断测试信号模拟器
  //   数码管输出
  //   数码管输出应该用寄存器锁存，否则显示数据只能一闪而过
  //   指令存储器
  //   contents of rom_1 (hex, n*v repeats v):
  //   201d07d0 20100001 109fc0 139fc3 8021 2012000c 24160008 26100001 3210000f 20080008 20090001 139900
  //   2709825 132020 20020022 c 1094022 1500fff9 22100001 2018000f 2188024 108700 20080008 20090001 139902
  //   2709825 132021 20020022 c 1094022 1500fff9 108702 2c9b022 12c00001 8000c07 4020 1084027 84400
  //   3508ffff 82021 20020022 c 8000c01 afa20000 23bd0004 afa40000 23bd0004 afb00000 23bd0004 afb30000
  //   23bd0004 afb40000 23bd0004 afb50000 23bd0004 afb60000 23bd0004 20160001 20140003 20150001 168020
  //   108100 2149825 132020 20020022 c 1600fffa 295a022 1680fff7 23bdfffc 8fb60000 23bdfffc 8fb50000
  //   23bdfffc 8fb40000 23bdfffc 8fb30000 23bdfffc 8fb00000 23bdfffc 8fa40000 23bdfffc 8fa20000 42000018
  //   afa20000 23bd0004 afa40000 23bd0004 afb00000 23bd0004 afb30000 23bd0004 afb40000 23bd0004 afb50000
  //   23bd0004 afb60000 23bd0004 20160002 20140003 20150001 168020 108100 2149825 132020 20020022 c
  //   1600fffa 295a022 1680fff7 23bdfffc 8fb60000 23bdfffc 8fb50000 23bdfffc 8fb40000 23bdfffc 8fb30000
  //   23bdfffc 8fb00000 23bdfffc 8fa40000 23bdfffc 8fa20000 42000018 afa20000 23bd0004 afa40000 23bd0004
  //   afb00000 23bd0004 afb30000 23bd0004 afb40000 23bd0004 afb50000 23bd0004 afb60000 23bd0004 20160003
  //   20140003 20150001 168020 108100 2149825 132020 20020022 c 1600fffa 295a022 1680fff7 23bdfffc
  //   8fb60000 23bdfffc 8fb50000 23bdfffc 8fb40000 23bdfffc 8fb30000 23bdfffc 8fb00000 23bdfffc 8fa40000
  //   23bdfffc 8fa20000 42000018
  //   OP
  //   Func
  //   rs
  //   指令字
  //   rt
  //   rd
  //   为方便自动评测，需要输出PC，IR，寄存器堆写如数据RDin
  //   RAM写使能MemWrite、RAM写入数据MDin等信号
  //   Reset 
  //   Reset 
  //   Reset 
  //   Beq
  //   JMP
  //   JR
  //   Bne
  //   OP
  //   JAL
  //   Func
  //   Syscall
  //   MemToReg
  //   MemWrite
  //   AluOP
  //   AluSrcB
  //   RegWrite
  //   RegDst
endmodule

module \单周期MIPS_多级中断  (
  input  IR1,
  input  IR2,
  input  IR3,
  output RegWrite,
  output MemWrite,
  output [31:0] PC,
  output [31:0] IR,
  output [31:0] RDin,
  output [31:0] MDin,
  output [31:0] LedData
);

  wire AluSrcB, and_1_out, and_2_out, and_3_out, and_4_out, and_5_out, and_10_out, Beq, Bne, CLK, CLR1, CLR2,
       CLR3, comparator_1_eq, comparator_2_eq, comparator_3_eq, comparator_4_eq, comparator_5_eq,
       comparator_6_eq, comparator_7_gt, d_ff_1_q, d_ff_2_q, d_ff_3_q, d_ff_4_qn, Equal, ERET, Go, Halt, INT,
       INT0, INT1, INT2, INT3, IR1_t, IR2_t, IR3_t, IRA, IRB, IRC, J2, JAL, JMP, JR, LED, MemToReg, MFC0,
       MTC0, nor_1_out, not_1_out, not_2_out, not_3_out, or_1_out, or_2_out, or_4_out, or_11_out, or_12_out,
       or_13_out, or_14_out, or_16_out, or_17_out, RegDst, SignedExt, Syscall, W1, W2, W3;
  wire [1:0] IR_N, IR_Q;
  wire [3:0] AluOP;
  wire [4:0] multiplexer_4_out, multiplexer_5_out, multiplexer_6_out, multiplexer_7_out;
  wire [15:0] \总周期数 ;
  wire [31:0] bit_extender_1_out, bit_extender_2_out, bit_extender_3_out, EPC_ADDR, INT_ADDR,
       mips_alu_1_result, multiplexer_2_out, multiplexer_3_out, multiplexer_8_out, multiplexer_11_out, PC4,
       PC_JR, PCimm, ram_1_data, RET_ADDR, shifter_1_out, \硬件堆栈_pop ;

  Clock #(.highDuration(1), .lowDuration(1)) clock_1 (.out(CLK));
  Button _1 ();  // open: out
  Button _2 ();  // open: out
  Button _3 ();  // open: out
  Button \u_继续运行  (.out(Go));
  LED #(.active("true")) led_1 (.in(W1));
  LED #(.active("true")) led_2 (.in(W2));
  LED #(.active("true")) led_3 (.in(W3));
  not not_1 (not_1_out, Equal);
  Hex_Digit_Display hex_digit_display_1 (.value(LedData[31:28]));  // open: dp
  Comparator #(.width(16), .mode("twosComplement")) comparator_1 (
    .a(\总周期数 ), .b(16'h7), .eq(comparator_1_eq));  // open: gt, lt
  Comparator #(.width(16), .mode("twosComplement")) comparator_2 (
    .a(\总周期数 ), .b(16'h241), .eq(comparator_2_eq));  // open: gt, lt
  Multiplexer #(.select(3), .width(32), .disabled("Z"), .enable("false")) multiplexer_1 (
    .in0(PC4), .in1(PCimm), .in2({PC4[31:28], IR[25:0], 2'b00}), .in6(PC_JR), .out(RET_ADDR),
    .sel({JR, JMP, J2}));  // open: in3, in4, in5, in7
  and and_1 (and_1_out, Beq, Equal);
  and and_2 (and_2_out, Bne, not_1_out);
  Adder #(.width(32)) adder_1 (.a(PC), .b(32'h4), .out(PC4));  // open: cin, cout
  Hex_Digit_Display hex_digit_display_2 (.value(LedData[27:24]));  // open: dp
  Hex_Digit_Display hex_digit_display_3 (.value(LedData[23:20]));  // open: dp
  Comparator #(.width(16), .mode("twosComplement")) comparator_3 (
    .a(16'h258), .b(\总周期数 ), .eq(comparator_3_eq));  // open: gt, lt
  or or_1 (or_1_out, comparator_3_eq, comparator_4_eq);
  Comparator #(.width(16), .mode("twosComplement")) comparator_4 (
    .a(\总周期数 ), .b(16'h1), .eq(comparator_4_eq));  // open: gt, lt
  Comparator #(.width(16), .mode("twosComplement")) comparator_5 (
    .a(\总周期数 ), .b(16'h4), .eq(comparator_5_eq));  // open: gt, lt
  or or_2 (or_2_out, comparator_1_eq, comparator_2_eq);
  Multiplexer #(.select(1), .width(32), .disabled("Z"), .enable("false")) multiplexer_2 (
    .in0(RET_ADDR), .in1(INT_ADDR), .out(multiplexer_2_out), .sel(INT));
  or or_3 (J2, and_1_out, and_2_out);
  Hex_Digit_Display hex_digit_display_4 (.value(LedData[15:12]));  // open: dp
  Hex_Digit_Display hex_digit_display_5 (.value(LedData[19:16]));  // open: dp
  Pull_Resistor #(.pull(0)) pull_resistor_1 (.node(IRA));
  assign IRA = or_1_out ? ~CLK : 1'bz;  // Controlled_Inverter controlled_inverter_1
  Pull_Resistor #(.pull(0)) pull_resistor_2 (.node(IRB));
  assign IRB = comparator_5_eq ? ~CLK : 1'bz;  // Controlled_Inverter controlled_inverter_2
  Pull_Resistor #(.pull(0)) pull_resistor_3 (.node(IRC));
  assign IRC = or_2_out ? ~CLK : 1'bz;  // Controlled_Inverter controlled_inverter_3
  Multiplexer #(.select(1), .width(32), .disabled("Z"), .enable("false")) multiplexer_3 (
    .in0(multiplexer_2_out), .in1(EPC_ADDR), .out(multiplexer_3_out), .sel(ERET));
  or or_4 (or_4_out, not_2_out, Go);
  not not_2 (not_2_out, Halt);
  Hex_Digit_Display hex_digit_display_6 (.value(LedData[7:4]));  // open: dp
  Hex_Digit_Display hex_digit_display_7 (.value(LedData[11:8]));  // open: dp
  // Probe on \总周期数 
  Counter #(.width(16), .max('hffff), .ongoal("wrap"), .trigger("rising"), .behavior("old")) counter_1 (
    .load(1'b0), .count(or_4_out), .Q(\总周期数 ), .clk(CLK), .clr(1'b0));  // open: D, carry, preset
  Register #(.width(32), .trigger("rising"), .Select("low")) u_PC (
    .D(multiplexer_3_out), .en(or_4_out), .Q(PC), .clk(CLK), .clr(1'b0));
  Hex_Digit_Display hex_digit_display_8 (.value(LedData[3:0]));  // open: dp
  or or_5 (IR1_t, IR1, IRA);
  or or_6 (IR2_t, IR2, IRB);
  // Mips_Probe mips_probe_1: pin names not known; wires that end beside it: IR
  ROM #(.addrWidth(10), .dataWidth(32), .Select("high")) rom_1 (.addr(PC[11:2]), .data(IR));
  or or_7 (IR3_t, IR3, IRC);
  Multiplexer #(.select(1), .width(5), .disabled("Z"), .enable("false")) multiplexer_4 (
    .in0(IR[20:16]), .in1(IR[15:11]), .out(multiplexer_4_out), .sel(RegDst));
  Register #(.width(32), .trigger("rising"), .Select("low")) register_1 (
    .D(MDin), .en(LED), .Q(LedData), .clk(CLK), .clr(1'b0));
  Multiplexer #(.select(1), .width(5), .disabled("Z"), .enable("false")) multiplexer_5 (
    .in0(IR[25:21]), .in1(5'b00010), .out(multiplexer_5_out), .sel(Syscall));
  Multiplexer #(.select(1), .width(5), .disabled("Z"), .enable("false")) multiplexer_6 (
    .in0(IR[20:16]), .in1(5'b00100), .out(multiplexer_6_out), .sel(Syscall));
  Multiplexer #(.select(1), .width(5), .disabled("Z"), .enable("false")) multiplexer_7 (
    .in0(multiplexer_4_out), .in1({5{1'b1}}), .out(multiplexer_7_out), .sel(JAL));
  assign bit_extender_1_out = {{16{1'b0}}, IR[15:0]};  // Bit_Extender bit_extender_1
  assign bit_extender_2_out = {{16{IR[15]}}, IR[15:0]};  // Bit_Extender bit_extender_2
  Shifter #(.width(32), .shift("ll")) shifter_1 (.in(bit_extender_2_out), .\dist (5'b00010), .out(shifter_1_out));
  D_Flip_Flop #(.trigger("rising"), .Pre_Clr_Positions("LEGACY"), .NegatePresetClear("false"), .enable("true"), .NewFFLayout("false")) d_ff_1 (
    .clk(IR1_t), .D(1'b1), .Q(d_ff_1_q), .reset(INT1));  // open: Qn, preset, en
  or or_8 (W1, INT1, d_ff_1_q);
  D_Flip_Flop #(.trigger("rising"), .Pre_Clr_Positions("LEGACY"), .NegatePresetClear("false"), .enable("true"), .NewFFLayout("false")) d_ff_2 (
    .clk(IR2_t), .D(1'b1), .Q(d_ff_2_q), .reset(INT2));  // open: Qn, preset, en
  or or_9 (W2, INT2, d_ff_2_q);
  D_Flip_Flop #(.trigger("rising"), .Pre_Clr_Positions("LEGACY"), .NegatePresetClear("false"), .enable("true"), .NewFFLayout("false")) d_ff_3 (
    .clk(IR3_t), .D(1'b1), .Q(d_ff_3_q), .reset(INT3));  // open: Qn, preset, en
  or or_10 (W3, INT3, d_ff_3_q);
  MIPS_Regifile mips_regifile_1 (
    .Din(RDin), .Clk(CLK), .R1(PC_JR), .R2(MDin), .WE(RegWrite), .W_num(multiplexer_7_out),
    .R1_num(multiplexer_5_out), .R2_num(multiplexer_6_out));
  Comparator #(.width(32), .mode("twosComplement")) comparator_6 (
    .a(32'h22), .b(PC_JR), .eq(comparator_6_eq));  // open: gt, lt
  Adder #(.width(32)) adder_2 (.a(shifter_1_out), .b(PC4), .out(PCimm));  // open: cin, cout
  or or_11 (or_11_out, d_ff_1_q, INT1);
  and and_3 (and_3_out, or_11_out, ~CLR1);  // AND_Gate
  or or_12 (or_12_out, d_ff_2_q, INT2);
  and and_4 (and_4_out, or_12_out, ~CLR2);  // AND_Gate
  or or_13 (or_13_out, d_ff_3_q, INT3);
  and and_5 (and_5_out, or_13_out, ~CLR3);  // AND_Gate
  and and_6 (MTC0, ~IR[26], ~IR[27], ~IR[28], ~IR[29], IR[30], ~IR[31], ~IR[21], ~IR[22], IR[23], ~IR[24], ~IR[25]);  // AND_Gate
  and and_7 (MFC0, ~IR[26], ~IR[27], ~IR[28], ~IR[29], IR[30], ~IR[31], ~IR[21], ~IR[22], ~IR[23], ~IR[24], ~IR[25]);  // AND_Gate
  and and_8 (LED, Syscall, comparator_6_eq);
  not not_3 (not_3_out, comparator_6_eq);
  and and_9 (Halt, not_3_out, Syscall);
  Multiplexer #(.select(2), .width(32), .disabled("Z"), .enable("false")) multiplexer_8 (
    .in0(MDin), .in1(MDin), .in2(bit_extender_1_out), .in3(bit_extender_2_out), .out(multiplexer_8_out),
    .sel({AluSrcB, SignedExt}));
  D_Flip_Flop #(.trigger("rising"), .Pre_Clr_Positions("LEGACY"), .NegatePresetClear("false"), .enable("true"), .NewFFLayout("false")) u_IR1 (
    .clk(CLK), .D(and_3_out), .Q(INT1));  // open: Qn, preset, en, reset
  D_Flip_Flop #(.trigger("rising"), .Pre_Clr_Positions("LEGACY"), .NegatePresetClear("false"), .enable("true"), .NewFFLayout("false")) u_IR2 (
    .clk(CLK), .D(and_4_out), .Q(INT2));  // open: Qn, preset, en, reset
  D_Flip_Flop #(.trigger("rising"), .Pre_Clr_Positions("LEGACY"), .NegatePresetClear("false"), .enable("true"), .NewFFLayout("false")) u_IR3 (
    .clk(CLK), .D(and_5_out), .Q(INT3));  // open: Qn, preset, en, reset
  Multiplexer #(.select(1), .width(32), .disabled("Z"), .enable("false")) multiplexer_9 (
    .in0(multiplexer_11_out), .in1(PC4), .out(RDin), .sel(JAL));
  \单周期硬布线控制器  \u_单周期硬布线控制器_1  (
    .Func(IR[5:0]), .OP(IR[31:26]), .ALU_OP(AluOP), .MemToReg(MemToReg), .MemWrite(MemWrite),
    .ALU_SRC(AluSrcB), .RegWrite(RegWrite), .SysCALL(Syscall), .SignedExt(SignedExt), .RegDst(RegDst),
    .JR(JR), .JMP(JMP), .Beq(Beq), .JAL(JAL), .Bne(Bne), .ERET(ERET));  // open: BLTZ, LUI, SB
  MIPS_ALU mips_alu_1 (
    .X(PC_JR), .Y(multiplexer_8_out), .AluOP(AluOP), .Equal(Equal), .Result(mips_alu_1_result),
    .shamt(IR[10:6]));  // open: Result_2
  or or_14 (or_14_out, INT0, MTC0);
  nor nor_1 (nor_1_out, MFC0, ERET);
  or or_15 (INT0, INT3, INT2, INT1);
  and and_10 (and_10_out, or_14_out, nor_1_out);
  Priority_Encoder #(.select(2), .disabled("Z")) priority_encoder_1 (
    .in0(1'b1), .in1(INT1), .in2(INT2), .in3(INT3), .out(IR_N));  // open: gs, en_out, en_in
  D_Flip_Flop #(.trigger("rising"), .Pre_Clr_Positions("ABOVE_BELOW"), .NegatePresetClear("false"), .enable("false"), .NewFFLayout("true")) d_ff_4 (
    .clk(CLK), .D(and_10_out), .Qn(d_ff_4_qn));  // open: Q, preset, reset
  Multiplexer #(.select(2), .width(32), .disabled("Z"), .enable("false")) multiplexer_10 (
    .in1(32'h30ac), .in2(32'h3158), .in3(32'h3204), .out(INT_ADDR), .sel(IR_N));  // open: in0
  \硬件堆栈  \u_硬件堆栈  (
    .push_pop(ERET), .CLK(CLK), .ENABLE(or_17_out), .RESTART(1'b0), .PUSH(bit_extender_3_out),
    .POP(\硬件堆栈_pop ));
  assign bit_extender_3_out = {{30{1'b0}}, IR_N};  // Bit_Extender bit_extender_3
  \硬件堆栈  \u_硬件堆栈_2  (.push_pop(ERET), .CLK(CLK), .ENABLE(or_16_out), .RESTART(1'b0), .PUSH(RET_ADDR), .POP(EPC_ADDR));
  or or_16 (or_16_out, INT, ERET);
  RAM #(.addrWidth(10), .dataWidth(32), .bus("separate"), .Select("high")) ram_1 (
    .addr(mips_alu_1_result[11:2]), .din(MDin), .data(ram_1_data), .str(MemWrite), .clk(CLK), .clr(1'b0));  // open: sel, ld
  Comparator #(.width(2), .mode("unsigned")) comparator_7 (.a(IR_N), .b(IR_Q), .gt(comparator_7_gt));  // open: eq, lt
  or or_17 (or_17_out, INT, ERET);
  Multiplexer #(.select(1), .width(32), .disabled("Z"), .enable("false")) multiplexer_11 (
    .in0(mips_alu_1_result), .in1(ram_1_data), .out(multiplexer_11_out), .sel(MemToReg));
  and and_11 (INT, INT0, d_ff_4_qn, comparator_7_gt);
  Bit_Extender #(.in_width(32), .out_width(2), .\type ("zero")) bit_extender_4 (.in(\硬件堆栈_pop ), .out(IR_Q));
  Demultiplexer #(.select(2), .width(1), .tristate("false"), .disabled("Z"), .enable("false")) demultiplexer_1 (
    .out1(CLR1), .out2(CLR2), .out3(CLR3), .in(ERET), .sel(IR_Q));  // open: out0

  // Other names for the same wires on the sheet: addr[25:0] = IR[25:0]; Func[5:0] = IR[5:0]; imm[15:0] = IR[15:0];
  //   PC_JAL[31:2] = {PC4[31:28], IR[25:0]}; shamt[4:0] = IR[10:6]; Rs[4:0] = IR[25:21]; OP[5:0] = IR[31:26];
  //   LEDD[31:0] = MDin

  // Notes on the sheet:
  //   中断源
  //   中断等待指示
  //   总复位信号应将除ROM以外所有存储组件全部清零
  //   多级中断测试信号模拟器
  //   数码管输出
  //   数码管输出应该用寄存器锁存，否则显示数据只能一闪而过
  //   指令存储器
  //   OP
  //   rs
  //   指令字
  //   contents of rom_1 (hex, n*v repeats v):
  //   201d07d0 20100001 109fc0 139fc3 8021 2012000c 24160008 26100001 3210000f 20080008 20090001 139900
  //   2709825 132020 20020022 c 1094022 1500fff9 22100001 2018000f 2188024 108700 20080008 20090001 139902
  //   2709825 132021 20020022 c 1094022 1500fff9 108702 2c9b022 12c00001 8000c07 4020 1084027 84400
  //   3508ffff 82021 20020022 c 8000c01 afa20000 23bd0004 afa40000 23bd0004 afb00000 23bd0004 afb30000
  //   23bd0004 afb40000 23bd0004 afb50000 23bd0004 afb60000 23bd0004 40000000 20160001 20140003 20150001
  //   168020 108100 2149825 132020 20020022 c 1600fffa 295a022 1680fff7 40800000 23bdfffc 8fb60000
  //   23bdfffc 8fb50000 23bdfffc 8fb40000 23bdfffc 8fb30000 23bdfffc 8fb00000 23bdfffc 8fa40000 23bdfffc
  //   8fa20000 42000018 afa20000 23bd0004 afa40000 23bd0004 afb00000 23bd0004 afb30000 23bd0004 afb40000
  //   23bd0004 afb50000 23bd0004 afb60000 23bd0004 40000000 20160002 20140003 20150001 168020 108100
  //   2149825 132020 20020022 c 1600fffa 295a022 1680fff7 40800000 23bdfffc 8fb60000 23bdfffc 8fb50000
  //   23bdfffc 8fb40000 23bdfffc 8fb30000 23bdfffc 8fb00000 23bdfffc 8fa40000 23bdfffc 8fa20000 42000018
  //   afa20000 23bd0004 afa40000 23bd0004 afb00000 23bd0004 afb30000 23bd0004 afb40000 23bd0004 afb50000
  //   23bd0004 afb60000 23bd0004 40000000 20160003 20140003 20150001 168020 108100 2149825 132020 20020022
  //   c 1600fffa 295a022 1680fff7 40800000 23bdfffc 8fb60000 23bdfffc 8fb50000 23bdfffc 8fb40000 23bdfffc
  //   8fb30000 23bdfffc 8fb00000 23bdfffc 8fa40000 23bdfffc 8fa20000 42000018
  //   rt
  //   rd
  //   Func
  //   为方便自动评测，需要输出PC，IR，寄存器堆写如数据RDin
  //   RAM写使能MemWrite、RAM写入数据MDin等信号
  //   Reset 
  //   Reset 
  //   Reset 
  //   Beq
  //   JMP
  //   JR
  //   Bne
  //   OP
  //   JAL
  //   Func
  //   Syscall
  //   MemToReg
  //   MemWrite
  //   AluOP
  //   AluSrcB
  //   RegWrite
  //   RegDst
endmodule

module \流水线中断  (
  output RegWrite,
  output MemWrite,
  output [31:0] IF_PC,
  output [31:0] ID_PC,
  output [31:0] EX_PC,
  output [31:0] M_PC,
  output [31:0] WB_PC,
  output [31:0] RDin,
  output [31:0] MDin,
  output [31:0] LedData
);

  wire and_1_out, and_2_out, and_3_out, and_4_out, and_5_out, and_6_out, and_7_out, and_9_out, and_10_out,
       and_11_out, and_12_out, and_13_out, and_14_out, and_15_out, BLTZ, CLK, CLR1, CLR2, CLR3,
       comparator_1_gt, comparator_2_eq, d_ff_1_q, d_ff_2_q, d_ff_3_q, ERET, EX_JAL, ex_mem_1_equal_out,
       ex_mem_1_memtoreg_out, ex_mem_1_regwrite_out, ex_mem_1_syscall_out, EX_REGD, Go, Halt,
       id_ex_1_alu_src_out, id_ex_1_beq_out, id_ex_1_bne_out, id_ex_1_memtoreg_out, id_ex_1_memwrite_out,
       id_ex_1_regwrite_out, id_ex_1_sb_out, id_ex_1_syscall_out, IE, INT, INT0, INT1, INT2, INT3, IR1, IR2,
       IR3, J2, JMP, JR, Ledout, LUI, MEM_JAL, MEM_REGD, mem_wb_1_jal_out, mem_wb_1_memtoreg_out,
       mem_wb_1_regdst_out, mem_wb_1_syscall_out, mips_alu_1_equal, not_1_out, not_2_out, or_1_out, or_2_out,
       or_6_out, or_7_out, or_8_out, or_11_out, or_12_out, \PC_EN调试 , RST, SB_USE, SignedExt, W1, W2, W3,
       Write, \单周期硬布线控制器_1_alu_src , \单周期硬布线控制器_1_beq , \单周期硬布线控制器_1_bltz , \单周期硬布线控制器_1_bne ,
       \单周期硬布线控制器_1_eret , \单周期硬布线控制器_1_jal , \单周期硬布线控制器_1_jmp , \单周期硬布线控制器_1_jr , \单周期硬布线控制器_1_lui ,
       \单周期硬布线控制器_1_memtoreg , \单周期硬布线控制器_1_memwrite , \单周期硬布线控制器_1_regdst , \单周期硬布线控制器_1_regwrite ,
       \单周期硬布线控制器_1_sb , \单周期硬布线控制器_1_syscall , \数据相关 , \数据相关检测_重定向_1_id_ex_stall , \数据相关检测_重定向_1_if_id_en ,
       \数据相关检测_重定向_1_if_id_stall ;
  wire [1:0] id_ex_1_rs_forw_out, id_ex_1_rt_forw_out, priority_encoder_1_out, register_1_q, sb_addr,
       \数据相关检测_重定向_1_rsforward , \数据相关检测_重定向_1_rtforward ;
  wire [3:0] id_ex_1_aluop_out, \单周期硬布线控制器_1_alu_op ;
  wire [4:0] EX_REGTOWRITE, ID_R1_num, ID_R2_num, MEM_REGTOWRITE, multiplexer_10_out, multiplexer_16_out,
       multiplexer_24_out, shamt, W_num;
  wire [7:0] multiplexer_17_out, multiplexer_18_out, multiplexer_19_out, multiplexer_21_out;
  wire [15:0] \LoadUse次数 , \总周期数 , \插入气泡数 , \无条件分支数 , \条件分支成功数 ;
  wire [25:0] addr;
  wire [27:0] adder_2_out;
  wire [31:0] adder_1_out, adder_4_out, bit_extender_1_out, bit_extender_2_out, DATA_CHA, EPC_ADDR,
       ex_mem_1_r1_out, id_ex_1_imm_out, id_ex_1_r1_out, id_ex_1_r2_out, ID_IR, IF_IR, INT_ADDR, MEM_IR,
       mem_wb_1_aluresult_out, mem_wb_1_rd_out, mips_alu_1_result, mips_regifile_1_r1, mips_regifile_1_r2,
       multiplexer_1_out, multiplexer_2_out, multiplexer_3_out, multiplexer_6_out, multiplexer_9_out,
       multiplexer_11_out, multiplexer_13_out, multiplexer_23_out, PC_JR, PCimm, R1, R2, RET_ADDR, sb_r2,
       shifter_1_out, WB_IR;
  wire [31:2] ex_mem_1_aluresult_out;
  wire [31:26] EX_IR;
  wire [31:28] PC_JAL;

  Button \u_总复位  (.out(RST));
  Button _1 (.out(IR1));
  Button _2 (.out(IR2));
  Button _3 (.out(IR3));
  // Probe on \总周期数 
  // Probe on \总周期数 
  Button \u_继续运行  (.out(Go));
  LED #(.active("true")) led_1 (.in(W1));
  LED #(.active("true")) led_2 (.in(W2));
  LED #(.active("true")) led_3 (.in(W3));
  Hex_Digit_Display hex_digit_display_1 (.value(LedData[31:28]));  // open: dp
  // Probe on IF_PC[19:0]
  // Mips_Probe mips_probe_1: pin names not known; wires that end beside it: IF_IR
  Hex_Digit_Display hex_digit_display_2 (.value(LedData[27:24]));  // open: dp
  Hex_Digit_Display hex_digit_display_3 (.value(LedData[23:20]));  // open: dp
  // Probe on ID_PC[19:0]
  // Mips_Probe mips_probe_2: pin names not known; wires that end beside it: ID_IR
  Multiplexer #(.select(3), .width(32), .disabled("Z"), .enable("false")) multiplexer_1 (
    .in0(adder_1_out), .in1(PCimm), .in2({PC_JAL, addr, 2'b00}), .in6(PC_JR), .out(multiplexer_1_out),
    .sel({JR, JMP, J2}));  // open: in3, in4, in5, in7
  Hex_Digit_Display hex_digit_display_4 (.value(LedData[19:16]));  // open: dp
  Hex_Digit_Display hex_digit_display_5 (.value(LedData[15:12]));  // open: dp
  Multiplexer #(.select(1), .width(32), .disabled("Z"), .enable("false")) multiplexer_2 (
    .in0(multiplexer_1_out), .in1(INT_ADDR), .out(multiplexer_2_out), .sel(INT));
  Multiplexer #(.select(1), .width(32), .disabled("Z"), .enable("false")) multiplexer_3 (
    .in0(multiplexer_2_out), .in1(EPC_ADDR), .out(multiplexer_3_out), .sel(ERET));
  Hex_Digit_Display hex_digit_display_6 (.value(LedData[7:4]));  // open: dp
  Hex_Digit_Display hex_digit_display_7 (.value(LedData[11:8]));  // open: dp
  Clock #(.highDuration(1), .lowDuration(1)) clock_1 (.out(CLK));
  // Probe on EX_PC[19:0]
  // Mips_Probe mips_probe_3: pin names not known; wires that end beside it: {EX_IR, addr}
  Hex_Digit_Display hex_digit_display_8 (.value(LedData[3:0]));  // open: dp
  Register #(.width(32), .trigger("rising"), .Select("low")) PC (
    .D(multiplexer_3_out), .en(\PC_EN调试 ), .Q(IF_PC), .clk(CLK), .clr(RST));
  // Probe on \总周期数 
  // Probe on M_PC[19:0]
  // Mips_Probe mips_probe_4: pin names not known; wires that end beside it: MEM_IR
  // Probe on \总周期数 
  // Probe on \无条件分支数 
  // Probe on \条件分支成功数 
  // Probe on \插入气泡数 
  // Probe on \LoadUse次数 
  ROM #(.addrWidth(10), .dataWidth(32), .Select("high")) rom_1 (.addr(IF_PC[11:2]), .data(IF_IR));
  // Probe on IF_PC[11:0]
  // Probe on WB_PC[19:0]
  // Mips_Probe mips_probe_5: pin names not known; wires that end beside it: WB_IR
  or or_1 (or_1_out, JMP, JR);
  or or_2 (or_2_out, ~Halt, Go);  // OR_Gate
  or or_3 (W1, INT1, d_ff_1_q);
  or or_4 (W2, INT2, d_ff_2_q);
  or or_5 (W3, INT3, d_ff_3_q);
  // Probe on EX_PC[11:0]
  // Probe on ID_PC[11:0]
  IF_ID if_id_1 (
    .IR_IN(IF_IR), .PC_IN(IF_PC), .IR(ID_IR), .PC(ID_PC), .reset(\数据相关检测_重定向_1_if_id_stall ), .CLK(CLK),
    .CLEAR(RST), .ENABLE(\数据相关检测_重定向_1_if_id_en ));  // open: PJUMP_IN, PJUM_OUT
  Adder #(.width(32)) adder_1 (.a(IF_PC), .b(32'h4), .out(adder_1_out));  // open: cin, cout
  Counter #(.width(16), .max('hffff), .ongoal("wrap"), .trigger("rising"), .behavior("old")) counter_1 (
    .count(and_1_out), .Q(\无条件分支数 ), .clk(CLK), .clr(RST));  // open: load, D, carry, preset
  and and_1 (and_1_out, or_1_out, or_2_out);
  and and_2 (and_2_out, J2, or_2_out);
  D_Flip_Flop #(.trigger("rising"), .Pre_Clr_Positions("LEGACY"), .NegatePresetClear("false"), .enable("true"), .NewFFLayout("false")) d_ff_1 (
    .clk(IR1), .D(1'b1), .Q(d_ff_1_q), .reset(INT1));  // open: Qn, preset, en
  D_Flip_Flop #(.trigger("rising"), .Pre_Clr_Positions("LEGACY"), .NegatePresetClear("false"), .enable("true"), .NewFFLayout("false")) d_ff_2 (
    .clk(IR2), .D(1'b1), .Q(d_ff_2_q), .reset(INT2));  // open: Qn, preset, en
  D_Flip_Flop #(.trigger("rising"), .Pre_Clr_Positions("LEGACY"), .NegatePresetClear("false"), .enable("true"), .NewFFLayout("false")) d_ff_3 (
    .clk(IR3), .D(1'b1), .Q(d_ff_3_q), .reset(INT3));  // open: Qn, preset, en
  // Probe on M_PC[11:0]
  // Mips_Probe mips_probe_6: pin names not known; wires that end beside it: IF_IR, ID_IR
  Counter #(.width(16), .max('hffff), .ongoal("wrap"), .trigger("rising"), .behavior("old")) counter_2 (
    .count(and_2_out), .Q(\条件分支成功数 ), .clk(CLK), .clr(RST));  // open: load, D, carry, preset
  or or_6 (or_6_out, d_ff_1_q, INT1);
  and and_3 (and_3_out, or_6_out, ~CLR1);  // AND_Gate
  or or_7 (or_7_out, d_ff_2_q, INT2);
  and and_4 (and_4_out, or_7_out, ~CLR2);  // AND_Gate
  or or_8 (or_8_out, d_ff_3_q, INT3);
  and and_5 (and_5_out, or_8_out, ~CLR3);  // AND_Gate
  // Probe on WB_PC[11:0]
  D_Flip_Flop #(.trigger("rising"), .Pre_Clr_Positions("LEGACY"), .NegatePresetClear("false"), .enable("true"), .NewFFLayout("false")) u_IR1 (
    .clk(CLK), .D(and_3_out), .Q(INT1));  // open: Qn, preset, en, reset
  D_Flip_Flop #(.trigger("rising"), .Pre_Clr_Positions("LEGACY"), .NegatePresetClear("false"), .enable("true"), .NewFFLayout("false")) u_IR2 (
    .clk(CLK), .D(and_4_out), .Q(INT2));  // open: Qn, preset, en, reset
  D_Flip_Flop #(.trigger("rising"), .Pre_Clr_Positions("LEGACY"), .NegatePresetClear("false"), .enable("true"), .NewFFLayout("false")) u_IR3 (
    .clk(CLK), .D(and_5_out), .Q(INT3));  // open: Qn, preset, en, reset
  and and_6 (and_6_out, Write, \数据相关 );
  \单周期硬布线控制器  \u_单周期硬布线控制器_1  (
    .Func(ID_IR[5:0]), .OP(ID_IR[31:26]), .ALU_OP(\单周期硬布线控制器_1_alu_op ), .MemToReg(\单周期硬布线控制器_1_memtoreg ),
    .MemWrite(\单周期硬布线控制器_1_memwrite ), .ALU_SRC(\单周期硬布线控制器_1_alu_src ), .RegWrite(\单周期硬布线控制器_1_regwrite ),
    .SysCALL(\单周期硬布线控制器_1_syscall ), .SignedExt(SignedExt), .RegDst(\单周期硬布线控制器_1_regdst ),
    .JR(\单周期硬布线控制器_1_jr ), .JMP(\单周期硬布线控制器_1_jmp ), .Beq(\单周期硬布线控制器_1_beq ), .JAL(\单周期硬布线控制器_1_jal ),
    .Bne(\单周期硬布线控制器_1_bne ), .ERET(\单周期硬布线控制器_1_eret ), .BLTZ(\单周期硬布线控制器_1_bltz ), .LUI(\单周期硬布线控制器_1_lui ),
    .SB(\单周期硬布线控制器_1_sb ));
  Multiplexer #(.select(1), .width(5), .disabled("Z"), .enable("false")) multiplexer_4 (
    .in0(ID_IR[25:21]), .in1(5'b00010), .out(ID_R1_num), .sel(\单周期硬布线控制器_1_syscall ));
  Multiplexer #(.select(1), .width(5), .disabled("Z"), .enable("false")) multiplexer_5 (
    .in0(ID_IR[20:16]), .in1(5'b00100), .out(ID_R2_num), .sel(\单周期硬布线控制器_1_syscall ));
  assign bit_extender_1_out = {{16{1'b0}}, ID_IR[15:0]};  // Bit_Extender bit_extender_1
  assign bit_extender_2_out = {{16{ID_IR[15]}}, ID_IR[15:0]};  // Bit_Extender bit_extender_2
  Counter #(.width(16), .max('hffff), .ongoal("wrap"), .trigger("rising"), .behavior("old")) counter_3 (
    .count(and_6_out), .Q(\插入气泡数 ), .clk(CLK), .clr(RST));  // open: load, D, carry, preset
  Counter #(.width(16), .max('hffff), .ongoal("wrap"), .trigger("rising"), .behavior("old")) counter_4 (
    .load(1'b0), .count(\PC_EN调试 ), .Q(\总周期数 ), .clk(CLK), .clr(RST));  // open: D, carry, preset
  and and_7 (and_7_out, INT0, ~ERET);  // AND_Gate
  or or_9 (INT0, INT3, INT2, INT1);
  Multiplexer #(.select(1), .width(32), .disabled("Z"), .enable("false")) multiplexer_6 (
    .in0(bit_extender_1_out), .in1(bit_extender_2_out), .out(multiplexer_6_out), .sel(SignedExt));
  D_Flip_Flop #(.trigger("rising"), .Pre_Clr_Positions("ABOVE_BELOW"), .NegatePresetClear("false"), .enable("false"), .NewFFLayout("true")) d_ff_4 (
    .clk(CLK), .D(and_7_out), .Qn(IE));  // open: Q, preset, reset
  Priority_Encoder #(.select(2), .disabled("Z")) priority_encoder_1 (
    .in0(INT1), .in1(INT2), .in2(INT3), .out(priority_encoder_1_out));  // open: in3, gs, en_out, en_in
  Register #(.width(32), .trigger("rising"), .Select("low")) \EPC寄存器  (
    .D(RET_ADDR), .en(INT), .Q(EPC_ADDR), .clk(CLK), .clr(RST));
  MIPS_Regifile mips_regifile_1 (
    .Din(RDin), .Clk(CLK), .R1(mips_regifile_1_r1), .R2(mips_regifile_1_r2), .WE(RegWrite), .W_num(W_num),
    .R1_num(ID_R1_num), .R2_num(ID_R2_num));
  Multiplexer #(.select(2), .width(32), .disabled("Z"), .enable("false")) multiplexer_7 (
    .in0(32'h30ac), .in1(32'h3150), .in2(32'h31f4), .out(INT_ADDR), .sel(priority_encoder_1_out));  // open: in3
  Register #(.width(2), .trigger("rising"), .Select("low")) register_1 (
    .D(priority_encoder_1_out), .en(INT), .Q(register_1_q), .clk(CLK));  // open: clr
  and and_8 (INT, INT0, IE);
  Demultiplexer #(.select(2), .width(1), .tristate("false"), .disabled("Z"), .enable("false")) demultiplexer_1 (
    .out0(CLR1), .out1(CLR2), .out2(CLR3), .in(ERET), .sel(register_1_q));  // open: out3
  ID_EX id_ex_1 (
    .BEQ_IN(\单周期硬布线控制器_1_beq ), .BNE_IN(\单周期硬布线控制器_1_bne ), .MEMTOREG_IN(\单周期硬布线控制器_1_memtoreg ),
    .MEMWRITE_IN(\单周期硬布线控制器_1_memwrite ), .ALUOP_IN(\单周期硬布线控制器_1_alu_op ),
    .ALU_SRC_IN(\单周期硬布线控制器_1_alu_src ), .REGWRITE_IN(\单周期硬布线控制器_1_regwrite ), .JAL_IN(\单周期硬布线控制器_1_jal ),
    .REGDIST_IN(\单周期硬布线控制器_1_regdst ), .SYSCALL_IN(\单周期硬布线控制器_1_syscall ), .JMP_IN(\单周期硬布线控制器_1_jmp ),
    .JR_IN(\单周期硬布线控制器_1_jr ), .IR_IN(ID_IR), .PC_IN(ID_PC), .R2_IN(mips_regifile_1_r2),
    .R1_IN(mips_regifile_1_r1), .IMM_IN(multiplexer_6_out), .BEQ_OUT(id_ex_1_beq_out),
    .BNE_OUT(id_ex_1_bne_out), .MEMTOREG_OUT(id_ex_1_memtoreg_out), .MEMWRITE_OUT(id_ex_1_memwrite_out),
    .ALUOP_OUT(id_ex_1_aluop_out), .ALU_SRC_OUT(id_ex_1_alu_src_out), .REGWRITE_OUT(id_ex_1_regwrite_out),
    .JAL_OUT(EX_JAL), .REGDST_IN(EX_REGD), .SYSCALL_OUT(id_ex_1_syscall_out), .JMP_OUT(JMP), .JR_OUT(JR),
    .IR_OUT({EX_IR, addr}), .PC_OUT(EX_PC), .R2_OUT(id_ex_1_r2_out), .R1_OUT(id_ex_1_r1_out),
    .IMM_OUT(id_ex_1_imm_out), .RESET(\数据相关检测_重定向_1_id_ex_stall ), .CLEAR(RST), .CLK(CLK), .ENABLE(Write),
    .LUI_IN(\单周期硬布线控制器_1_lui ), .LUI_OUT(LUI), .SB_IN(\单周期硬布线控制器_1_sb ), .SB_OUT(id_ex_1_sb_out),
    .BLTZ_IN(\单周期硬布线控制器_1_bltz ), .BLTZ_OUT(BLTZ), .RS_FORW_IN(\数据相关检测_重定向_1_rsforward ),
    .RS_FORW_OUT(id_ex_1_rs_forw_out), .RT_FORW_IN(\数据相关检测_重定向_1_rtforward ),
    .RT_FORW_OUT(id_ex_1_rt_forw_out), .ERET_IN(\单周期硬布线控制器_1_eret ), .ERET_OUT(ERET));  // open: PJUMP_IN, PJUMP_OUT
  Multiplexer #(.select(2), .width(32), .disabled("Z"), .enable("false")) multiplexer_8 (
    .in0(id_ex_1_r1_out), .in1(RDin), .in2({ex_mem_1_aluresult_out, sb_addr}),
    .in3({ex_mem_1_aluresult_out, sb_addr}), .out(PC_JR), .sel(id_ex_1_rs_forw_out));
  Multiplexer #(.select(2), .width(32), .disabled("Z"), .enable("false")) multiplexer_9 (
    .in0(id_ex_1_r2_out), .in1(RDin), .in2({ex_mem_1_aluresult_out, sb_addr}),
    .in3({ex_mem_1_aluresult_out, sb_addr}), .out(multiplexer_9_out), .sel(id_ex_1_rt_forw_out));
  Multiplexer #(.select(1), .width(5), .disabled("Z"), .enable("false")) multiplexer_10 (
    .in0(addr[20:16]), .in1(addr[15:11]), .out(multiplexer_10_out), .sel(EX_REGD));
  Multiplexer #(.select(1), .width(32), .disabled("Z"), .enable("false")) multiplexer_11 (
    .in0(multiplexer_9_out), .in1(id_ex_1_imm_out), .out(multiplexer_11_out), .sel(id_ex_1_alu_src_out));
  Adder #(.width(32)) adder_2 (.a(EX_PC), .b(32'h4), .out({PC_JAL, adder_2_out}));  // open: cin, cout
  Shifter #(.width(32), .shift("ll")) shifter_1 (.in(id_ex_1_imm_out), .\dist (5'b00010), .out(shifter_1_out));
  Multiplexer #(.select(1), .width(5), .disabled("Z"), .enable("false")) multiplexer_12 (
    .in0(multiplexer_10_out), .in1({5{1'b1}}), .out(EX_REGTOWRITE), .sel(EX_JAL));
  Comparator #(.width(32), .mode("twosComplement")) comparator_1 (
    .a({32{1'b0}}), .b(PC_JR), .gt(comparator_1_gt));  // open: eq, lt
  Multiplexer #(.select(1), .width(32), .disabled("Z"), .enable("false")) multiplexer_13 (
    .in0(multiplexer_11_out), .in1(32'h22), .out(multiplexer_13_out), .sel(id_ex_1_syscall_out));
  Adder #(.width(32)) adder_3 (.a({PC_JAL, adder_2_out}), .b(shifter_1_out), .out(PCimm));  // open: cin, cout
  MIPS_ALU mips_alu_1 (
    .X(PC_JR), .Y(multiplexer_13_out), .AluOP(id_ex_1_aluop_out), .Equal(mips_alu_1_equal),
    .Result(mips_alu_1_result), .shamt(shamt));  // open: Result_2
  Multiplexer #(.select(1), .width(5), .disabled("Z"), .enable("false")) multiplexer_14 (
    .in0(addr[10:6]), .in1(5'b10000), .out(shamt), .sel(LUI));
  and and_9 (and_9_out, comparator_1_gt, BLTZ);
  and and_10 (and_10_out, id_ex_1_beq_out, mips_alu_1_equal);
  or or_10 (J2, and_9_out, and_10_out, and_11_out);
  and and_11 (and_11_out, id_ex_1_bne_out, ~mips_alu_1_equal);  // AND_Gate
  or or_11 (or_11_out, J2, JR, INT, ERET, JMP);
  EX_MEM ex_mem_1 (
    .MemToReg_in(id_ex_1_memtoreg_out), .MemWrite_in(id_ex_1_memwrite_out),
    .RegWrite_in(id_ex_1_regwrite_out), .JAL_in(EX_JAL), .RegDst_in(EX_REGD),
    .Syscall_in(id_ex_1_syscall_out), .equal_in(mips_alu_1_equal), .IR_in({EX_IR, addr}), .PC_in(EX_PC),
    .ALUResult_in(mips_alu_1_result), .R2_in(multiplexer_9_out), .R1_in(PC_JR),
    .MemToReg_out(ex_mem_1_memtoreg_out), .MemWrite_out(MemWrite), .RegWrite_out(ex_mem_1_regwrite_out),
    .JAL_out(MEM_JAL), .RegDst_out(MEM_REGD), .Syscall_out(ex_mem_1_syscall_out),
    .equal_out(ex_mem_1_equal_out), .IR_out(MEM_IR), .PC_out(M_PC),
    .ALUResult_out({ex_mem_1_aluresult_out, sb_addr}), .R2_out(sb_r2), .R1_out(ex_mem_1_r1_out),
    .RESET(1'b0), .CLK(CLK), .CLEAR(RST), .ENABLE(Write), .SB_in(id_ex_1_sb_out), .SB_out(SB_USE));  // open: Imm_in, Imm_out
  Multiplexer #(.select(3), .width(32), .disabled("Z"), .enable("false")) multiplexer_15 (
    .in0({PC_JAL, adder_2_out}), .in1(PCimm), .in2({PC_JAL, addr, 2'b00}), .in6(PC_JR), .out(RET_ADDR),
    .sel({JR, JMP, J2}));  // open: in3, in4, in5, in7
  and and_12 (and_12_out, ~sb_addr[0], ~sb_addr[1]);  // AND_Gate
  and and_13 (and_13_out, sb_addr[0], ~sb_addr[1]);  // AND_Gate
  and and_14 (and_14_out, ~sb_addr[0], sb_addr[1]);  // AND_Gate
  and and_15 (and_15_out, sb_addr[0], sb_addr[1]);
  not not_1 (not_1_out, CLK);
  Multiplexer #(.select(1), .width(5), .disabled("Z"), .enable("false")) multiplexer_16 (
    .in0(MEM_IR[20:16]), .in1(MEM_IR[15:11]), .out(multiplexer_16_out), .sel(MEM_REGD));
  Multiplexer #(.select(1), .width(8), .disabled("Z"), .enable("false")) multiplexer_17 (
    .in0(DATA_CHA[7:0]), .in1(sb_r2[7:0]), .out(multiplexer_17_out), .sel(and_12_out));
  Multiplexer #(.select(1), .width(8), .disabled("Z"), .enable("false")) multiplexer_18 (
    .in0(DATA_CHA[15:8]), .in1(sb_r2[7:0]), .out(multiplexer_18_out), .sel(and_13_out));
  Multiplexer #(.select(1), .width(8), .disabled("Z"), .enable("false")) multiplexer_19 (
    .in0(DATA_CHA[23:16]), .in1(sb_r2[7:0]), .out(multiplexer_19_out), .sel(and_14_out));
  RAM #(.addrWidth(10), .dataWidth(32), .bus("separate"), .Select("high")) ram_1 (
    .addr(ex_mem_1_aluresult_out[11:2]), .din(MDin), .data(DATA_CHA), .str(MemWrite), .clk(not_1_out),
    .clr(RST));  // open: sel, ld
  Multiplexer #(.select(1), .width(5), .disabled("Z"), .enable("false")) multiplexer_20 (
    .in0(multiplexer_16_out), .in1({5{1'b1}}), .out(MEM_REGTOWRITE), .sel(MEM_JAL));
  Multiplexer #(.select(1), .width(8), .disabled("Z"), .enable("false")) multiplexer_21 (
    .in0(DATA_CHA[31:24]), .in1(sb_r2[7:0]), .out(multiplexer_21_out), .sel(and_15_out));
  MEM_WB mem_wb_1 (
    .MemToReg_in(ex_mem_1_memtoreg_out), .MemWrite_in(MemWrite), .RegWrite_in(ex_mem_1_regwrite_out),
    .JAL_in(MEM_JAL), .RegDst_in(MEM_REGD), .Syscall_in(ex_mem_1_syscall_out), .equal_in(ex_mem_1_equal_out),
    .IR_in(MEM_IR), .PC_in(M_PC), .ALUResult_in({ex_mem_1_aluresult_out, sb_addr}), .RD_in(DATA_CHA),
    .R1_in(ex_mem_1_r1_out), .MemToReg_out(mem_wb_1_memtoreg_out), .RegWrite_out(RegWrite),
    .JAL_out(mem_wb_1_jal_out), .RegDst_out(mem_wb_1_regdst_out), .Syscall_out(mem_wb_1_syscall_out),
    .IR_out(WB_IR), .PC_out(WB_PC), .ALUResult_out(mem_wb_1_aluresult_out), .RD_out(mem_wb_1_rd_out),
    .\气泡_高电平时有效 (1'b0), .clk(CLK), .clear(RST), .enable(Write), .R1_out(R1), .R2_in(sb_r2), .R2_out(R2));  // open: MemWrite_out, equal_out
  Multiplexer #(.select(1), .width(32), .disabled("Z"), .enable("false")) multiplexer_22 (
    .in0(sb_r2), .in1({multiplexer_21_out, multiplexer_19_out, multiplexer_18_out, multiplexer_17_out}),
    .out(MDin), .sel(SB_USE));
  Multiplexer #(.select(1), .width(32), .disabled("Z"), .enable("false")) multiplexer_23 (
    .in0(mem_wb_1_aluresult_out), .in1(mem_wb_1_rd_out), .out(multiplexer_23_out), .sel(mem_wb_1_memtoreg_out));
  or or_12 (or_12_out, ~Halt, Go);  // OR_Gate
  \数据相关检测_重定向  \u_数据相关检测_重定向_1  (
    .OP(ID_IR[31:26]), .FUNC(ID_IR[5:0]), .RS(ID_R1_num), .Halt_or_Go(or_12_out),
    .EX_MEMTOREG(id_ex_1_memtoreg_out), .EX_WRITEREG(EX_REGTOWRITE), .RT(ID_R2_num), .\J标记 (or_11_out),
    .MEM_REGW(ex_mem_1_regwrite_out), .MEM_WRITEREG(MEM_REGTOWRITE), .EX_REGW(id_ex_1_regwrite_out),
    .PC_EN(\PC_EN调试 ), .LOAD_USED(\数据相关 ), .IF_ID_EN(\数据相关检测_重定向_1_if_id_en ),
    .IF_ID_STALL(\数据相关检测_重定向_1_if_id_stall ), .ID_EX_STALL(\数据相关检测_重定向_1_id_ex_stall ),
    .RSFORWARD(\数据相关检测_重定向_1_rsforward ), .RTFORWARD(\数据相关检测_重定向_1_rtforward ));
  nand nand_1 (Write, not_2_out, Halt);
  Multiplexer #(.select(1), .width(5), .disabled("Z"), .enable("false")) multiplexer_24 (
    .in0(WB_IR[20:16]), .in1(WB_IR[15:11]), .out(multiplexer_24_out), .sel(mem_wb_1_regdst_out));
  Adder #(.width(32)) adder_4 (.a(WB_PC), .b(32'h4), .out(adder_4_out));  // open: cin, cout
  not not_2 (not_2_out, Go);
  Multiplexer #(.select(1), .width(32), .disabled("Z"), .enable("false")) multiplexer_25 (
    .in0(multiplexer_23_out), .in1(adder_4_out), .out(RDin), .sel(mem_wb_1_jal_out));
  Multiplexer #(.select(1), .width(5), .disabled("Z"), .enable("false")) multiplexer_26 (
    .in0(multiplexer_24_out), .in1({5{1'b1}}), .out(W_num), .sel(mem_wb_1_jal_out));
  Comparator #(.width(32), .mode("twosComplement")) comparator_2 (
    .a(R1), .b(32'h22), .eq(comparator_2_eq));  // open: gt, lt
  and and_16 (Ledout, comparator_2_eq, mem_wb_1_syscall_out);
  and and_17 (Halt, ~comparator_2_eq, mem_wb_1_syscall_out);  // AND_Gate
  Register #(.width(32), .trigger("rising"), .Select("low")) register_2 (
    .D(R2), .en(Ledout), .Q(LedData), .clk(CLK), .clr(RST));

  // Other names for the same wires on the sheet: RD[4:0] = ID_IR[15:11]; MEM_PC[31:0] = M_PC; EX_IR[25:0] = addr;
  //   PC_JAL[27:2] = addr

  // Notes on the sheet:
  //   中断源
  //   时空图监测，可删除
  //   中断等待指示
  //   数码管输出
  //   指令存储器
  //   contents of rom_1 (hex, n*v repeats v):
  //   201d07d0 20100001 109fc0 139fc3 8021 2012000c 24160008 26100001 3210000f 20080008 20090001 139900
  //   2709825 132020 20020022 c 1094022 1500fff9 22100001 2018000f 2188024 108700 20080008 20090001 139902
  //   2709825 132021 20020022 c 1094022 1500fff9 108702 2c9b022 12c00001 8000c07 4020 1084027 84400
  //   3508ffff 82021 20020022 c 8000c01 afa20000 23bd0004 afa40000 23bd0004 afb00000 23bd0004 afb30000
  //   23bd0004 afb40000 23bd0004 afb50000 23bd0004 afb60000 23bd0004 20160001 20140003 20150001 168020
  //   108100 2149825 132020 20020022 c 1600fffa 295a022 1680fff7 23bdfffc 8fb60000 23bdfffc 8fb50000
  //   23bdfffc 8fb40000 23bdfffc 8fb30000 23bdfffc 8fb00000 23bdfffc 8fa40000 23bdfffc 8fa20000 42000018
  //   afa20000 23bd0004 afa40000 23bd0004 afb00000 23bd0004 afb30000 23bd0004 afb40000 23bd0004 afb50000
  //   23bd0004 afb60000 23bd0004 20160002 20140003 20150001 168020 108100 2149825 132020 20020022 c
  //   1600fffa 295a022 1680fff7 23bdfffc 8fb60000 23bdfffc 8fb50000 23bdfffc 8fb40000 23bdfffc 8fb30000
  //   23bdfffc 8fb00000 23bdfffc 8fa40000 23bdfffc 8fa20000 42000018 afa20000 23bd0004 afa40000 23bd0004
  //   afb00000 23bd0004 afb30000 23bd0004 afb40000 23bd0004 afb50000 23bd0004 afb60000 23bd0004 20160003
  //   20140003 20150001 168020 108100 2149825 132020 20020022 c 1600fffa 295a022 1680fff7 23bdfffc
  //   8fb60000 23bdfffc 8fb50000 23bdfffc 8fb40000 23bdfffc 8fb30000 23bdfffc 8fb00000 23bdfffc 8fa40000
  //   23bdfffc 8fa20000 42000018
  //   流水调试日志用
  //   OP
  //   Func
  //   rs
  //   rt
  //   rd
  //   指令字
  //   指令调试器件
  //   Reset 
  //   Reset 
  //   Reset 
  //   JMP
  //   JR
  //   OP
  //   Func
  //   Beq
  //   Bne
  //   AluOP
  //   AluSrcB
  //   RegWrite
  //   JAL
  //   RegDst
  //   Syscall
  //   MemToReg
  //   MemWrite
  //   为方便自动评测，需要输出流水线各段保存的PC值，注意是PC不是PC+4，另外ID段寄存器写入信息，Mem段内存写入信息也要输出
  //   SB指令电路
endmodule

module \封装正确性测试  (
);

  wire IR1, IR2, IR3, MemW, RegW;
  wire [31:0] EX_PC, ID_PC, IF_PC, IR, LED, MDin, MDinr, MEM_PC, PC, RDin, RDinr, WB_PC;

  \单周期MIPS  \u_单周期mips_1  (
    .RegWrite(RegW), .MemWrite(MemW), .PC(PC), .IR(IR), .RDin(RDin), .MDin(MDin), .LedData(LED));  // open: IR1, IR2, IR3
  \气泡流水线  \u_气泡流水线_1  (
    .RegWrite(RegW), .MemWrite(MemW), .IF_PC(IF_PC), .ID_PC(ID_PC), .EX_PC(EX_PC), .M_PC(MEM_PC),
    .WB_PC(WB_PC), .RDin(RDinr), .MDin(MDinr), .LedData(LED));
  \单周期MIPS_单级中断  \u_单周期mips_单级中断_1  (
    .IR1(IR1), .IR2(IR2), .IR3(IR3), .RegWrite(RegW), .MemWrite(MemW), .PC(PC), .IR(IR), .RDin(RDin),
    .MDin(MDin), .LedData(LED));
  \理想流水线  \u_理想流水线_1  (
    .RegWrite(RegW), .MemWrite(MemW), .IF_PC(IF_PC), .ID_PC(ID_PC), .EX_PC(EX_PC), .M_PC(MEM_PC),
    .WB_PC(WB_PC), .RDin(RDinr), .MDin(MDinr), .LedData(LED));
  \重定向流水线  \u_重定向流水线_1  (
    .RegWrite(RegW), .MemWrite(MemW), .IF_PC(IF_PC), .ID_PC(ID_PC), .EX_PC(EX_PC), .M_PC(MEM_PC),
    .WB_PC(WB_PC), .RDin(RDinr), .MDin(MDinr), .LedData(LED));
  \单周期MIPS_多级中断  \u_单周期mips_多级中断_1  (
    .IR1(IR1), .IR2(IR2), .IR3(IR3), .RegWrite(RegW), .MemWrite(MemW), .PC(PC), .IR(IR), .RDin(RDin),
    .MDin(MDin), .LedData(LED));

  // Notes on the sheet:
  //   单周期封装测试
  //   气泡流水封装测试
  //   单周期+单级中断封装测试
  //   请检查上面封装有无位宽不匹配，引脚标签是否和连接的标签相对应，否则无法在educoder平台上正确测试
  //   理想流水封装测试
  //   重定向流水封装测试
  //   单周期+多级中断封装测试
endmodule

module IF_ID (
  input  reset,
  input  CLK,
  input  CLEAR,
  input  ENABLE,
  input  PJUMP_IN,
  input  [31:0] IR_IN,
  input  [31:0] PC_IN,
  output PJUM_OUT,
  output [31:0] IR,
  output [31:0] PC
);

  wire multiplexer_1_out;
  wire [31:0] multiplexer_2_out, multiplexer_3_out;

  Multiplexer #(.select(1), .width(1), .disabled("Z"), .enable("false")) multiplexer_1 (
    .in0(PJUMP_IN), .in1(1'b0), .out(multiplexer_1_out), .sel(reset));
  Multiplexer #(.select(1), .width(32), .disabled("Z"), .enable("false")) multiplexer_2 (
    .in0(IR_IN), .in1({32{1'b0}}), .out(multiplexer_2_out), .sel(reset));
  Multiplexer #(.select(1), .width(32), .disabled("Z"), .enable("false")) multiplexer_3 (
    .in0(PC_IN), .in1({32{1'b0}}), .out(multiplexer_3_out), .sel(reset));
  Register #(.width(1), .trigger("rising"), .Select("low")) u_PC (
    .D(multiplexer_1_out), .en(ENABLE), .Q(PJUM_OUT), .clk(CLK), .clr(CLEAR));
  Register #(.width(32), .trigger("rising"), .Select("low")) u_IR (
    .D(multiplexer_2_out), .en(ENABLE), .Q(IR), .clk(CLK), .clr(CLEAR));
  Register #(.width(32), .trigger("rising"), .Select("low")) PC_2 (
    .D(multiplexer_3_out), .en(ENABLE), .Q(PC), .clk(CLK), .clr(CLEAR));
endmodule
module ID_EX (
  input  RESET,
  input  CLEAR,
  input  CLK,
  input  ENABLE,
  input  PJUMP_IN,
  input  ERET_IN,
  input  BEQ_IN,
  input  BNE_IN,
  input  MEMTOREG_IN,
  input  MEMWRITE_IN,
  input  [3:0] ALUOP_IN,
  input  ALU_SRC_IN,
  input  REGWRITE_IN,
  input  JAL_IN,
  input  REGDIST_IN,
  input  SYSCALL_IN,
  input  JMP_IN,
  input  JR_IN,
  input  LUI_IN,
  input  SB_IN,
  input  BLTZ_IN,
  input  [1:0] RS_FORW_IN,
  input  [1:0] RT_FORW_IN,
  input  [31:0] IR_IN,
  input  [31:0] PC_IN,
  input  [31:0] R2_IN,
  input  [31:0] R1_IN,
  input  [31:0] IMM_IN,
  output PJUMP_OUT,
  output ERET_OUT,
  output BEQ_OUT,
  output BNE_OUT,
  output MEMTOREG_OUT,
  output MEMWRITE_OUT,
  output [3:0] ALUOP_OUT,
  output ALU_SRC_OUT,
  output REGWRITE_OUT,
  output JAL_OUT,
  output REGDST_IN,
  output SYSCALL_OUT,
  output JMP_OUT,
  output JR_OUT,
  output LUI_OUT,
  output SB_OUT,
  output BLTZ_OUT,
  output [1:0] RS_FORW_OUT,
  output [1:0] RT_FORW_OUT,
  output [31:0] IR_OUT,
  output [31:0] PC_OUT,
  output [31:0] R2_OUT,
  output [31:0] R1_OUT,
  output [31:0] IMM_OUT
);

  wire multiplexer_1_out, multiplexer_2_out, multiplexer_3_out, multiplexer_4_out, multiplexer_5_out,
       multiplexer_6_out, multiplexer_8_out, multiplexer_9_out, multiplexer_10_out, multiplexer_11_out,
       multiplexer_12_out, multiplexer_13_out, multiplexer_14_out, multiplexer_15_out, multiplexer_16_out,
       multiplexer_17_out;
  wire [1:0] multiplexer_18_out, multiplexer_19_out;
  wire [3:0] multiplexer_7_out;
  wire [31:0] multiplexer_20_out, multiplexer_21_out, multiplexer_22_out, multiplexer_23_out,
       multiplexer_24_out;

  Multiplexer #(.select(1), .width(1), .disabled("Z"), .enable("false")) multiplexer_1 (
    .in0(PJUMP_IN), .in1(1'b0), .out(multiplexer_1_out), .sel(RESET));
  Multiplexer #(.select(1), .width(1), .disabled("Z"), .enable("false")) multiplexer_2 (
    .in0(ERET_IN), .in1(1'b0), .out(multiplexer_2_out), .sel(RESET));
  Multiplexer #(.select(1), .width(1), .disabled("Z"), .enable("false")) multiplexer_3 (
    .in0(BEQ_IN), .in1(1'b0), .out(multiplexer_3_out), .sel(RESET));
  Multiplexer #(.select(1), .width(1), .disabled("Z"), .enable("false")) multiplexer_4 (
    .in0(BNE_IN), .in1(1'b0), .out(multiplexer_4_out), .sel(RESET));
  Multiplexer #(.select(1), .width(1), .disabled("Z"), .enable("false")) multiplexer_5 (
    .in0(MEMTOREG_IN), .in1(1'b0), .out(multiplexer_5_out), .sel(RESET));
  Multiplexer #(.select(1), .width(1), .disabled("Z"), .enable("false")) multiplexer_6 (
    .in0(MEMWRITE_IN), .in1(1'b0), .out(multiplexer_6_out), .sel(RESET));
  Multiplexer #(.select(1), .width(4), .disabled("Z"), .enable("false")) multiplexer_7 (
    .in0(ALUOP_IN), .in1(4'b0000), .out(multiplexer_7_out), .sel(RESET));
  Multiplexer #(.select(1), .width(1), .disabled("Z"), .enable("false")) multiplexer_8 (
    .in0(ALU_SRC_IN), .in1(1'b0), .out(multiplexer_8_out), .sel(RESET));
  Multiplexer #(.select(1), .width(1), .disabled("Z"), .enable("false")) multiplexer_9 (
    .in0(REGWRITE_IN), .in1(1'b0), .out(multiplexer_9_out), .sel(RESET));
  Multiplexer #(.select(1), .width(1), .disabled("Z"), .enable("false")) multiplexer_10 (
    .in0(JAL_IN), .in1(1'b0), .out(multiplexer_10_out), .sel(RESET));
  Multiplexer #(.select(1), .width(1), .disabled("Z"), .enable("false")) multiplexer_11 (
    .in0(REGDIST_IN), .in1(1'b0), .out(multiplexer_11_out), .sel(RESET));
  Multiplexer #(.select(1), .width(1), .disabled("Z"), .enable("false")) multiplexer_12 (
    .in0(SYSCALL_IN), .in1(1'b0), .out(multiplexer_12_out), .sel(RESET));
  Multiplexer #(.select(1), .width(1), .disabled("Z"), .enable("false")) multiplexer_13 (
    .in0(JMP_IN), .in1(1'b0), .out(multiplexer_13_out), .sel(RESET));
  Multiplexer #(.select(1), .width(1), .disabled("Z"), .enable("false")) multiplexer_14 (
    .in0(JR_IN), .in1(1'b0), .out(multiplexer_14_out), .sel(RESET));
  Multiplexer #(.select(1), .width(1), .disabled("Z"), .enable("false")) multiplexer_15 (
    .in0(LUI_IN), .in1(1'b0), .out(multiplexer_15_out), .sel(RESET));
  Multiplexer #(.select(1), .width(1), .disabled("Z"), .enable("false")) multiplexer_16 (
    .in0(SB_IN), .in1(1'b0), .out(multiplexer_16_out), .sel(RESET));
  Multiplexer #(.select(1), .width(1), .disabled("Z"), .enable("false")) multiplexer_17 (
    .in0(BLTZ_IN), .in1(1'b0), .out(multiplexer_17_out), .sel(RESET));
  Multiplexer #(.select(1), .width(2), .disabled("Z"), .enable("false")) multiplexer_18 (
    .in0(RS_FORW_IN), .in1(2'b00), .out(multiplexer_18_out), .sel(RESET));
  Multiplexer #(.select(1), .width(2), .disabled("Z"), .enable("false")) multiplexer_19 (
    .in0(RT_FORW_IN), .in1(2'b00), .out(multiplexer_19_out), .sel(RESET));
  Multiplexer #(.select(1), .width(32), .disabled("Z"), .enable("false")) multiplexer_20 (
    .in0(IR_IN), .in1({32{1'b0}}), .out(multiplexer_20_out), .sel(RESET));
  Multiplexer #(.select(1), .width(32), .disabled("Z"), .enable("false")) multiplexer_21 (
    .in0(PC_IN), .in1({32{1'b0}}), .out(multiplexer_21_out), .sel(RESET));
  Multiplexer #(.select(1), .width(32), .disabled("Z"), .enable("false")) multiplexer_22 (
    .in0(R2_IN), .in1({32{1'b0}}), .out(multiplexer_22_out), .sel(RESET));
  Multiplexer #(.select(1), .width(32), .disabled("Z"), .enable("false")) multiplexer_23 (
    .in0(R1_IN), .in1({32{1'b0}}), .out(multiplexer_23_out), .sel(RESET));
  Multiplexer #(.select(1), .width(32), .disabled("Z"), .enable("false")) multiplexer_24 (
    .in0(IMM_IN), .in1({32{1'b0}}), .out(multiplexer_24_out), .sel(RESET));
  Register #(.width(1), .trigger("rising"), .Select("low")) register_1 (
    .D(multiplexer_1_out), .en(ENABLE), .Q(PJUMP_OUT), .clk(CLK), .clr(CLEAR));
  Register #(.width(1), .trigger("rising"), .Select("low")) register_2 (
    .D(multiplexer_2_out), .en(ENABLE), .Q(ERET_OUT), .clk(CLK), .clr(CLEAR));
  Register #(.width(1), .trigger("rising"), .Select("low")) register_3 (
    .D(multiplexer_3_out), .en(ENABLE), .Q(BEQ_OUT), .clk(CLK), .clr(CLEAR));
  Register #(.width(1), .trigger("rising"), .Select("low")) register_4 (
    .D(multiplexer_4_out), .en(ENABLE), .Q(BNE_OUT), .clk(CLK), .clr(CLEAR));
  Register #(.width(1), .trigger("rising"), .Select("low")) register_5 (
    .D(multiplexer_5_out), .en(ENABLE), .Q(MEMTOREG_OUT), .clk(CLK), .clr(CLEAR));
  Register #(.width(1), .trigger("rising"), .Select("low")) register_6 (
    .D(multiplexer_6_out), .en(ENABLE), .Q(MEMWRITE_OUT), .clk(CLK), .clr(CLEAR));
  Register #(.width(4), .trigger("rising"), .Select("low")) register_7 (
    .D(multiplexer_7_out), .en(ENABLE), .Q(ALUOP_OUT), .clk(CLK), .clr(CLEAR));
  Register #(.width(1), .trigger("rising"), .Select("low")) register_8 (
    .D(multiplexer_8_out), .en(ENABLE), .Q(ALU_SRC_OUT), .clk(CLK), .clr(CLEAR));
  Register #(.width(1), .trigger("rising"), .Select("low")) register_9 (
    .D(multiplexer_9_out), .en(ENABLE), .Q(REGWRITE_OUT), .clk(CLK), .clr(CLEAR));
  Register #(.width(1), .trigger("rising"), .Select("low")) register_10 (
    .D(multiplexer_10_out), .en(ENABLE), .Q(JAL_OUT), .clk(CLK), .clr(CLEAR));
  Register #(.width(1), .trigger("rising"), .Select("low")) register_11 (
    .D(multiplexer_11_out), .en(ENABLE), .Q(REGDST_IN), .clk(CLK), .clr(CLEAR));
  Register #(.width(1), .trigger("rising"), .Select("low")) register_12 (
    .D(multiplexer_12_out), .en(ENABLE), .Q(SYSCALL_OUT), .clk(CLK), .clr(CLEAR));
  Register #(.width(1), .trigger("rising"), .Select("low")) register_13 (
    .D(multiplexer_13_out), .en(ENABLE), .Q(JMP_OUT), .clk(CLK), .clr(CLEAR));
  Register #(.width(1), .trigger("rising"), .Select("low")) register_14 (
    .D(multiplexer_14_out), .en(ENABLE), .Q(JR_OUT), .clk(CLK), .clr(CLEAR));
  Register #(.width(1), .trigger("rising"), .Select("low")) register_15 (
    .D(multiplexer_15_out), .en(ENABLE), .Q(LUI_OUT), .clk(CLK), .clr(CLEAR));
  Register #(.width(1), .trigger("rising"), .Select("low")) register_16 (
    .D(multiplexer_16_out), .en(ENABLE), .Q(SB_OUT), .clk(CLK), .clr(CLEAR));
  Register #(.width(1), .trigger("rising"), .Select("low")) register_17 (
    .D(multiplexer_17_out), .en(ENABLE), .Q(BLTZ_OUT), .clk(CLK), .clr(CLEAR));
  Register #(.width(2), .trigger("rising"), .Select("low")) register_18 (
    .D(multiplexer_18_out), .en(ENABLE), .Q(RS_FORW_OUT), .clk(CLK), .clr(CLEAR));
  Register #(.width(2), .trigger("rising"), .Select("low")) register_19 (
    .D(multiplexer_19_out), .en(ENABLE), .Q(RT_FORW_OUT), .clk(CLK), .clr(CLEAR));
  Register #(.width(32), .trigger("rising"), .Select("low")) register_20 (
    .D(multiplexer_20_out), .en(ENABLE), .Q(IR_OUT), .clk(CLK), .clr(CLEAR));
  Register #(.width(32), .trigger("rising"), .Select("low")) register_21 (
    .D(multiplexer_21_out), .en(ENABLE), .Q(PC_OUT), .clk(CLK), .clr(CLEAR));
  Register #(.width(32), .trigger("rising"), .Select("low")) register_22 (
    .D(multiplexer_22_out), .en(ENABLE), .Q(R2_OUT), .clk(CLK), .clr(CLEAR));
  Register #(.width(32), .trigger("rising"), .Select("low")) register_23 (
    .D(multiplexer_23_out), .en(ENABLE), .Q(R1_OUT), .clk(CLK), .clr(CLEAR));
  Register #(.width(32), .trigger("rising"), .Select("low")) register_24 (
    .D(multiplexer_24_out), .en(ENABLE), .Q(IMM_OUT), .clk(CLK), .clr(CLEAR));
endmodule

module EX_MEM (
  input  RESET,
  input  CLK,
  input  CLEAR,
  input  ENABLE,
  input  MemToReg_in,
  input  MemWrite_in,
  input  RegWrite_in,
  input  JAL_in,
  input  RegDst_in,
  input  Syscall_in,
  input  equal_in,
  input  SB_in,
  input  [31:0] IR_in,
  input  [31:0] PC_in,
  input  [31:0] ALUResult_in,
  input  [31:0] R2_in,
  input  [31:0] R1_in,
  input  [31:0] Imm_in,
  output MemToReg_out,
  output MemWrite_out,
  output RegWrite_out,
  output JAL_out,
  output RegDst_out,
  output Syscall_out,
  output equal_out,
  output SB_out,
  output [31:0] IR_out,
  output [31:0] PC_out,
  output [31:0] ALUResult_out,
  output [31:0] R2_out,
  output [31:0] R1_out,
  output [31:0] Imm_out
);

  wire multiplexer_1_out, multiplexer_2_out, multiplexer_3_out, multiplexer_4_out, multiplexer_5_out,
       multiplexer_6_out, multiplexer_7_out, multiplexer_8_out;
  wire [31:0] multiplexer_9_out, multiplexer_10_out, multiplexer_11_out, multiplexer_12_out,
       multiplexer_13_out, multiplexer_14_out;

  Multiplexer #(.select(1), .width(1), .disabled("Z"), .enable("false")) multiplexer_1 (
    .in0(MemToReg_in), .in1(1'b0), .out(multiplexer_1_out), .sel(RESET));
  Multiplexer #(.select(1), .width(1), .disabled("Z"), .enable("false")) multiplexer_2 (
    .in0(MemWrite_in), .in1(1'b0), .out(multiplexer_2_out), .sel(RESET));
  Multiplexer #(.select(1), .width(1), .disabled("Z"), .enable("false")) multiplexer_3 (
    .in0(RegWrite_in), .in1(1'b0), .out(multiplexer_3_out), .sel(RESET));
  Multiplexer #(.select(1), .width(1), .disabled("Z"), .enable("false")) multiplexer_4 (
    .in0(JAL_in), .in1(1'b0), .out(multiplexer_4_out), .sel(RESET));
  Multiplexer #(.select(1), .width(1), .disabled("Z"), .enable("false")) multiplexer_5 (
    .in0(RegDst_in), .in1(1'b0), .out(multiplexer_5_out), .sel(RESET));
  Multiplexer #(.select(1), .width(1), .disabled("Z"), .enable("false")) multiplexer_6 (
    .in0(Syscall_in), .in1(1'b0), .out(multiplexer_6_out), .sel(RESET));
  Multiplexer #(.select(1), .width(1), .disabled("Z"), .enable("false")) multiplexer_7 (
    .in0(equal_in), .in1(1'b0), .out(multiplexer_7_out), .sel(RESET));
  Multiplexer #(.select(1), .width(1), .disabled("Z"), .enable("false")) multiplexer_8 (
    .in0(SB_in), .in1(1'b0), .out(multiplexer_8_out), .sel(RESET));
  Multiplexer #(.select(1), .width(32), .disabled("Z"), .enable("false")) multiplexer_9 (
    .in0(IR_in), .in1({32{1'b0}}), .out(multiplexer_9_out), .sel(RESET));
  Multiplexer #(.select(1), .width(32), .disabled("Z"), .enable("false")) multiplexer_10 (
    .in0(PC_in), .in1({32{1'b0}}), .out(multiplexer_10_out), .sel(RESET));
  Multiplexer #(.select(1), .width(32), .disabled("Z"), .enable("false")) multiplexer_11 (
    .in0(ALUResult_in), .in1({32{1'b0}}), .out(multiplexer_11_out), .sel(RESET));
  Multiplexer #(.select(1), .width(32), .disabled("Z"), .enable("false")) multiplexer_12 (
    .in0(R2_in), .in1({32{1'b0}}), .out(multiplexer_12_out), .sel(RESET));
  Multiplexer #(.select(1), .width(32), .disabled("Z"), .enable("false")) multiplexer_13 (
    .in0(R1_in), .in1({32{1'b0}}), .out(multiplexer_13_out), .sel(RESET));
  Multiplexer #(.select(1), .width(32), .disabled("Z"), .enable("false")) multiplexer_14 (
    .in0(Imm_in), .in1({32{1'b0}}), .out(multiplexer_14_out), .sel(RESET));
  Register #(.width(1), .trigger("rising"), .Select("low")) MemToReg (
    .D(multiplexer_1_out), .en(ENABLE), .Q(MemToReg_out), .clk(CLK), .clr(CLEAR));
  Register #(.width(1), .trigger("rising"), .Select("low")) MemWrite (
    .D(multiplexer_2_out), .en(ENABLE), .Q(MemWrite_out), .clk(CLK), .clr(CLEAR));
  Register #(.width(1), .trigger("rising"), .Select("low")) RegWrite (
    .D(multiplexer_3_out), .en(ENABLE), .Q(RegWrite_out), .clk(CLK), .clr(CLEAR));
  Register #(.width(1), .trigger("rising"), .Select("low")) JAL (
    .D(multiplexer_4_out), .en(ENABLE), .Q(JAL_out), .clk(CLK), .clr(CLEAR));
  Register #(.width(1), .trigger("rising"), .Select("low")) RegDst (
    .D(multiplexer_5_out), .en(ENABLE), .Q(RegDst_out), .clk(CLK), .clr(CLEAR));
  Register #(.width(1), .trigger("rising"), .Select("low")) Syscall (
    .D(multiplexer_6_out), .en(ENABLE), .Q(Syscall_out), .clk(CLK), .clr(CLEAR));
  Register #(.width(1), .trigger("rising"), .Select("low")) equal (
    .D(multiplexer_7_out), .en(ENABLE), .Q(equal_out), .clk(CLK), .clr(CLEAR));
  Register #(.width(1), .trigger("rising"), .Select("low")) SB (
    .D(multiplexer_8_out), .en(ENABLE), .Q(SB_out), .clk(CLK), .clr(CLEAR));
  Register #(.width(32), .trigger("rising"), .Select("low")) IR (
    .D(multiplexer_9_out), .en(ENABLE), .Q(IR_out), .clk(CLK), .clr(CLEAR));
  Register #(.width(32), .trigger("rising"), .Select("low")) PC (
    .D(multiplexer_10_out), .en(ENABLE), .Q(PC_out), .clk(CLK), .clr(CLEAR));
  Register #(.width(32), .trigger("rising"), .Select("low")) ALUResult (
    .D(multiplexer_11_out), .en(ENABLE), .Q(ALUResult_out), .clk(CLK), .clr(CLEAR));
  Register #(.width(32), .trigger("rising"), .Select("low")) R2 (
    .D(multiplexer_12_out), .en(ENABLE), .Q(R2_out), .clk(CLK), .clr(CLEAR));
  Register #(.width(32), .trigger("rising"), .Select("low")) R2_2 (
    .D(multiplexer_13_out), .en(ENABLE), .Q(R1_out), .clk(CLK), .clr(CLEAR));
  Register #(.width(32), .trigger("rising"), .Select("low")) R2_3 (
    .D(multiplexer_14_out), .en(ENABLE), .Q(Imm_out), .clk(CLK), .clr(CLEAR));
endmodule

module MEM_WB (
  input  \气泡_高电平时有效 ,
  input  clk,
  input  clear,
  input  enable,
  input  MemToReg_in,
  input  MemWrite_in,
  input  RegWrite_in,
  input  JAL_in,
  input  RegDst_in,
  input  Syscall_in,
  input  equal_in,
  input  [31:0] IR_in,
  input  [31:0] PC_in,
  input  [31:0] ALUResult_in,
  input  [31:0] RD_in,
  input  [31:0] R1_in,
  input  [31:0] R2_in,
  output MemToReg_out,
  output MemWrite_out,
  output RegWrite_out,
  output JAL_out,
  output RegDst_out,
  output Syscall_out,
  output equal_out,
  output [31:0] IR_out,
  output [31:0] PC_out,
  output [31:0] ALUResult_out,
  output [31:0] RD_out,
  output [31:0] R1_out,
  output [31:0] R2_out
);

  wire multiplexer_1_out, multiplexer_2_out, multiplexer_3_out, multiplexer_4_out, multiplexer_5_out,
       multiplexer_6_out, multiplexer_7_out;
  wire [31:0] multiplexer_8_out, multiplexer_9_out, multiplexer_10_out, multiplexer_11_out,
       multiplexer_12_out, multiplexer_13_out;

  Multiplexer #(.select(1), .width(1), .disabled("Z"), .enable("false")) multiplexer_1 (
    .in0(MemToReg_in), .in1(1'b0), .out(multiplexer_1_out), .sel(\气泡_高电平时有效 ));
  Multiplexer #(.select(1), .width(1), .disabled("Z"), .enable("false")) multiplexer_2 (
    .in0(MemWrite_in), .in1(1'b0), .out(multiplexer_2_out), .sel(\气泡_高电平时有效 ));
  Multiplexer #(.select(1), .width(1), .disabled("Z"), .enable("false")) multiplexer_3 (
    .in0(RegWrite_in), .in1(1'b0), .out(multiplexer_3_out), .sel(\气泡_高电平时有效 ));
  Multiplexer #(.select(1), .width(1), .disabled("Z"), .enable("false")) multiplexer_4 (
    .in0(JAL_in), .in1(1'b0), .out(multiplexer_4_out), .sel(\气泡_高电平时有效 ));
  Multiplexer #(.select(1), .width(1), .disabled("Z"), .enable("false")) multiplexer_5 (
    .in0(RegDst_in), .in1(1'b0), .out(multiplexer_5_out), .sel(\气泡_高电平时有效 ));
  Multiplexer #(.select(1), .width(1), .disabled("Z"), .enable("false")) multiplexer_6 (
    .in0(Syscall_in), .in1(1'b0), .out(multiplexer_6_out), .sel(\气泡_高电平时有效 ));
  Multiplexer #(.select(1), .width(1), .disabled("Z"), .enable("false")) multiplexer_7 (
    .in0(equal_in), .in1(1'b0), .out(multiplexer_7_out), .sel(\气泡_高电平时有效 ));
  Multiplexer #(.select(1), .width(32), .disabled("Z"), .enable("false")) multiplexer_8 (
    .in0(IR_in), .in1({32{1'b0}}), .out(multiplexer_8_out), .sel(\气泡_高电平时有效 ));
  Multiplexer #(.select(1), .width(32), .disabled("Z"), .enable("false")) multiplexer_9 (
    .in0(PC_in), .in1({32{1'b0}}), .out(multiplexer_9_out), .sel(\气泡_高电平时有效 ));
  Multiplexer #(.select(1), .width(32), .disabled("Z"), .enable("false")) multiplexer_10 (
    .in0(ALUResult_in), .in1({32{1'b0}}), .out(multiplexer_10_out), .sel(\气泡_高电平时有效 ));
  Multiplexer #(.select(1), .width(32), .disabled("Z"), .enable("false")) multiplexer_11 (
    .in0(RD_in), .in1({32{1'b0}}), .out(multiplexer_11_out), .sel(\气泡_高电平时有效 ));
  Multiplexer #(.select(1), .width(32), .disabled("Z"), .enable("false")) multiplexer_12 (
    .in0(R1_in), .in1({32{1'b0}}), .out(multiplexer_12_out), .sel(\气泡_高电平时有效 ));
  Multiplexer #(.select(1), .width(32), .disabled("Z"), .enable("false")) multiplexer_13 (
    .in0(R2_in), .in1({32{1'b0}}), .out(multiplexer_13_out), .sel(\气泡_高电平时有效 ));
  Register #(.width(1), .trigger("rising"), .Select("low")) MemToReg (
    .D(multiplexer_1_out), .en(enable), .Q(MemToReg_out), .clk(clk), .clr(clear));
  Register #(.width(1), .trigger("rising"), .Select("low")) MemWrite (
    .D(multiplexer_2_out), .en(enable), .Q(MemWrite_out), .clk(clk), .clr(clear));
  Register #(.width(1), .trigger("rising"), .Select("low")) RegWrite (
    .D(multiplexer_3_out), .en(enable), .Q(RegWrite_out), .clk(clk), .clr(clear));
  Register #(.width(1), .trigger("rising"), .Select("low")) JAL (
    .D(multiplexer_4_out), .en(enable), .Q(JAL_out), .clk(clk), .clr(clear));
  Register #(.width(1), .trigger("rising"), .Select("low")) RegDst (
    .D(multiplexer_5_out), .en(enable), .Q(RegDst_out), .clk(clk), .clr(clear));
  Register #(.width(1), .trigger("rising"), .Select("low")) Syscall (
    .D(multiplexer_6_out), .en(enable), .Q(Syscall_out), .clk(clk), .clr(clear));
  Register #(.width(1), .trigger("rising"), .Select("low")) equal (
    .D(multiplexer_7_out), .en(enable), .Q(equal_out), .clk(clk), .clr(clear));
  Register #(.width(32), .trigger("rising"), .Select("low")) IR (
    .D(multiplexer_8_out), .en(enable), .Q(IR_out), .clk(clk), .clr(clear));
  Register #(.width(32), .trigger("rising"), .Select("low")) PC (
    .D(multiplexer_9_out), .en(enable), .Q(PC_out), .clk(clk), .clr(clear));
  Register #(.width(32), .trigger("rising"), .Select("low")) ALUResult (
    .D(multiplexer_10_out), .en(enable), .Q(ALUResult_out), .clk(clk), .clr(clear));
  Register #(.width(32), .trigger("rising"), .Select("low")) RD (
    .D(multiplexer_11_out), .en(enable), .Q(RD_out), .clk(clk), .clr(clear));
  Register #(.width(32), .trigger("rising"), .Select("low")) R1 (
    .D(multiplexer_12_out), .en(enable), .Q(R1_out), .clk(clk), .clr(clear));
  Register #(.width(32), .trigger("rising"), .Select("low")) R2 (
    .D(multiplexer_13_out), .en(enable), .Q(R2_out), .clk(clk), .clr(clear));
endmodule

module \中断ERET  (
  input  OP0,
  input  OP1,
  input  OP2,
  input  OP3,
  input  OP4,
  input  OP5,
  input  F0,
  input  F1,
  input  F2,
  input  F3,
  input  F4,
  input  F5,
  output ERET
);

  wire not_1_out, not_2_out, not_3_out, not_4_out, not_5_out, not_6_out, not_7_out, not_8_out, not_9_out;

  not not_1 (not_1_out, OP5);
  not not_2 (not_2_out, OP3);
  not not_3 (not_3_out, OP2);
  not not_4 (not_4_out, OP1);
  not not_5 (not_5_out, OP0);
  not not_6 (not_6_out, F5);
  not not_7 (not_7_out, F2);
  not not_8 (not_8_out, F1);
  not not_9 (not_9_out, F0);
  and and_1 (ERET, not_1_out, OP4, not_2_out, not_3_out, not_4_out, not_5_out, not_6_out, F4, F3, not_7_out, not_8_out, not_9_out);
endmodule

module \硬件堆栈  (
  input  [31:0] PUSH,
  input  push_pop,
  input  CLK,
  input  ENABLE,
  input  RESTART,
  output [31:0] POP
);

  wire [31:0] multiplexer_1_out, multiplexer_2_out, multiplexer_3_out, multiplexer_4_out, multiplexer_5_out,
       multiplexer_6_out, multiplexer_7_out, multiplexer_8_out, register_2_q, register_3_q, register_4_q,
       register_5_q, register_6_q, register_7_q, register_8_q;

  Multiplexer #(.select(1), .width(32), .disabled("Z"), .enable("false")) multiplexer_1 (
    .in0(PUSH), .in1(register_2_q), .out(multiplexer_1_out), .sel(push_pop));
  Register #(.width(32), .trigger("rising"), .Select("low")) register_1 (
    .D(multiplexer_1_out), .en(ENABLE), .Q(POP), .clk(CLK), .clr(RESTART));
  Multiplexer #(.select(1), .width(32), .disabled("Z"), .enable("false")) multiplexer_2 (
    .in0(POP), .in1(register_3_q), .out(multiplexer_2_out), .sel(push_pop));
  Register #(.width(32), .trigger("rising"), .Select("low")) register_2 (
    .D(multiplexer_2_out), .en(ENABLE), .Q(register_2_q), .clk(CLK), .clr(RESTART));
  Multiplexer #(.select(1), .width(32), .disabled("Z"), .enable("false")) multiplexer_3 (
    .in0(register_2_q), .in1(register_4_q), .out(multiplexer_3_out), .sel(push_pop));
  Register #(.width(32), .trigger("rising"), .Select("low")) register_3 (
    .D(multiplexer_3_out), .en(ENABLE), .Q(register_3_q), .clk(CLK), .clr(RESTART));
  Multiplexer #(.select(1), .width(32), .disabled("Z"), .enable("false")) multiplexer_4 (
    .in0(register_3_q), .in1(register_5_q), .out(multiplexer_4_out), .sel(push_pop));
  Register #(.width(32), .trigger("rising"), .Select("low")) register_4 (
    .D(multiplexer_4_out), .en(ENABLE), .Q(register_4_q), .clk(CLK), .clr(RESTART));
  Multiplexer #(.select(1), .width(32), .disabled("Z"), .enable("false")) multiplexer_5 (
    .in0(register_4_q), .in1(register_6_q), .out(multiplexer_5_out), .sel(push_pop));
  Multiplexer #(.select(1), .width(32), .disabled("Z"), .enable("false")) multiplexer_6 (
    .in0(register_5_q), .in1(register_7_q), .out(multiplexer_6_out), .sel(push_pop));
  Register #(.width(32), .trigger("rising"), .Select("low")) register_5 (
    .D(multiplexer_5_out), .en(ENABLE), .Q(register_5_q), .clk(CLK), .clr(RESTART));
  Register #(.width(32), .trigger("rising"), .Select("low")) register_6 (
    .D(multiplexer_6_out), .en(ENABLE), .Q(register_6_q), .clk(CLK), .clr(RESTART));
  Multiplexer #(.select(1), .width(32), .disabled("Z"), .enable("false")) multiplexer_7 (
    .in0(register_6_q), .in1(register_8_q), .out(multiplexer_7_out), .sel(push_pop));
  Multiplexer #(.select(1), .width(32), .disabled("Z"), .enable("false")) multiplexer_8 (
    .in0(register_7_q), .in1({32{1'b0}}), .out(multiplexer_8_out), .sel(push_pop));
  Register #(.width(32), .trigger("rising"), .Select("low")) register_7 (
    .D(multiplexer_7_out), .en(ENABLE), .Q(register_7_q), .clk(CLK), .clr(RESTART));
  Register #(.width(32), .trigger("rising"), .Select("low")) register_8 (
    .D(multiplexer_8_out), .en(ENABLE), .Q(register_8_q), .clk(CLK), .clr(RESTART));
endmodule

module TTT (
);

  IF_ID if_id_1 ();  // open: IR_IN, PC_IN, IR, PC, reset, CLK, CLEAR, ENABLE, PJUMP_IN, PJUM_OUT
  ID_EX id_ex_1 ();  // open: BEQ_IN, BNE_IN, MEMTOREG_IN, MEMWRITE_IN, ALUOP_IN, ALU_SRC_IN, REGWRITE_IN, JAL_IN, REGDIST_IN, SYSCALL_IN, JMP_IN, JR_IN, IR_IN, PC_IN, R2_IN, R1_IN, IMM_IN, BEQ_OUT, BNE_OUT, MEMTOREG_OUT, MEMWRITE_OUT, ALUOP_OUT, ALU_SRC_OUT, REGWRITE_OUT, JAL_OUT, REGDST_IN, SYSCALL_OUT, JMP_OUT, JR_OUT, IR_OUT, PC_OUT, R2_OUT, R1_OUT, IMM_OUT, RESET, CLEAR, CLK, ENABLE, LUI_IN, LUI_OUT, SB_IN, SB_OUT, BLTZ_IN, BLTZ_OUT, RS_FORW_IN, RS_FORW_OUT, RT_FORW_IN, RT_FORW_OUT, ERET_IN, ERET_OUT, PJUMP_IN, PJUMP_OUT
  EX_MEM ex_mem_1 ();  // open: MemToReg_in, MemWrite_in, RegWrite_in, JAL_in, RegDst_in, Syscall_in, equal_in, IR_in, PC_in, ALUResult_in, R2_in, R1_in, Imm_in, MemToReg_out, MemWrite_out, RegWrite_out, JAL_out, RegDst_out, Syscall_out, equal_out, IR_out, PC_out, ALUResult_out, R2_out, R1_out, Imm_out, RESET, CLK, CLEAR, ENABLE, SB_in, SB_out
  MEM_WB mem_wb_1 ();  // open: MemToReg_in, MemWrite_in, RegWrite_in, JAL_in, RegDst_in, Syscall_in, equal_in, IR_in, PC_in, ALUResult_in, RD_in, R1_in, MemToReg_out, MemWrite_out, RegWrite_out, JAL_out, RegDst_out, Syscall_out, equal_out, IR_out, PC_out, ALUResult_out, RD_out, 气泡_高电平时有效, clk, clear, enable, R1_out, R2_in, R2_out
endmodule

module \源寄存器使用情况  (
  input  [5:0] OP,
  input  [5:0] FUNC,
  output R1_Used,
  output R2_Used
);

  wire and_1_out, and_2_out, and_3_out, and_4_out, and_5_out, and_6_out, and_7_out, and_8_out, and_9_out,
       and_10_out, and_11_out, and_12_out, and_13_out, and_14_out, and_15_out, and_16_out, and_17_out,
       and_18_out, and_19_out, and_20_out, and_21_out, and_22_out, and_23_out, and_24_out, and_25_out,
       and_26_out, and_27_out, and_28_out, and_29_out, and_30_out, and_31_out, and_32_out, and_33_out,
       and_34_out, and_35_out, and_36_out, and_37_out, and_38_out, and_39_out, and_40_out, and_41_out,
       not_1_out, not_2_out, not_3_out, not_4_out, not_5_out, not_6_out, not_7_out, not_8_out, not_9_out,
       not_10_out, not_11_out, not_12_out, not_13_out, not_14_out, not_15_out, not_16_out, not_17_out,
       not_18_out, not_19_out, not_20_out, not_21_out, not_22_out, not_23_out, not_24_out, not_25_out,
       not_26_out, not_27_out, not_28_out, not_29_out, not_30_out, not_31_out, not_32_out, not_33_out,
       not_34_out, not_35_out, not_36_out, not_37_out, not_38_out, not_39_out, not_40_out, not_41_out,
       not_42_out, not_43_out, not_44_out, not_45_out, not_46_out, not_47_out, not_48_out, not_49_out,
       not_50_out, not_51_out, not_52_out, not_53_out, not_54_out, not_55_out, not_56_out, not_57_out,
       not_58_out, not_59_out, not_60_out, not_61_out, not_62_out, not_63_out, not_64_out, not_65_out,
       not_66_out, not_67_out, not_68_out, not_69_out, not_70_out, not_71_out, not_72_out, not_73_out,
       not_74_out, not_75_out, not_76_out, not_77_out, not_78_out, not_79_out, not_80_out, not_81_out,
       not_82_out, not_83_out, not_84_out, not_85_out, not_86_out, not_87_out, not_88_out, not_89_out,
       not_90_out, not_91_out, not_92_out, not_93_out, not_94_out, not_95_out, not_96_out, not_97_out,
       not_98_out, not_99_out, not_100_out, not_101_out, not_102_out, not_103_out, not_104_out, not_105_out,
       not_106_out, not_107_out, not_108_out, not_109_out, not_110_out, not_111_out, not_112_out,
       not_113_out, not_114_out, not_115_out, not_116_out, not_117_out, not_118_out, not_119_out,
       not_120_out, not_121_out, not_122_out, not_123_out, not_124_out, not_125_out, not_126_out,
       not_127_out, not_128_out, not_129_out, not_130_out, not_131_out, not_132_out, not_133_out,
       not_134_out, not_135_out, not_136_out, not_137_out, not_138_out, not_139_out, not_140_out,
       not_141_out, not_142_out, not_143_out, not_144_out, not_145_out, not_146_out, not_147_out,
       not_148_out, not_149_out, not_150_out, not_151_out, not_152_out, not_153_out, not_154_out,
       not_155_out, not_156_out, not_157_out, not_158_out, not_159_out, not_160_out, not_161_out,
       not_162_out, not_163_out, not_164_out, not_165_out, not_166_out, not_167_out, not_168_out,
       not_169_out, not_170_out, not_171_out, not_172_out, not_173_out, not_174_out, not_175_out,
       not_176_out, not_177_out, not_178_out, not_179_out, not_180_out, not_181_out, not_182_out,
       not_183_out, not_184_out, not_185_out, not_186_out, not_187_out, not_188_out, not_189_out,
       not_190_out, not_191_out, not_192_out, not_193_out, not_194_out, not_195_out, not_196_out,
       not_197_out, not_198_out, not_199_out, not_200_out, not_201_out, not_202_out, not_203_out,
       not_204_out, not_205_out, not_206_out, not_207_out, not_208_out, not_209_out, not_210_out,
       not_211_out, not_212_out, not_213_out, not_214_out, not_215_out, not_216_out, not_217_out,
       not_218_out, not_219_out, not_220_out, not_221_out, not_222_out, not_223_out, not_224_out,
       not_225_out, not_226_out, not_227_out, not_228_out, not_229_out, not_230_out, not_231_out,
       not_232_out, not_233_out, not_234_out, not_235_out, not_236_out, not_237_out, not_238_out,
       not_239_out, not_240_out, not_241_out, not_242_out, not_243_out, not_244_out, not_245_out,
       not_246_out, not_247_out, not_248_out, not_249_out, not_250_out, not_251_out, not_252_out,
       not_253_out, not_254_out, not_255_out, not_256_out, not_257_out, not_258_out, not_259_out,
       not_260_out, not_261_out, not_262_out, not_263_out, not_264_out, not_265_out, not_266_out,
       not_267_out, not_268_out, not_269_out, not_270_out, not_271_out, not_272_out, not_273_out,
       not_274_out, not_275_out, not_276_out, not_277_out, not_278_out, not_279_out, not_280_out,
       not_281_out, not_282_out, not_283_out, not_284_out, not_285_out, not_286_out, not_287_out,
       not_288_out, not_289_out, not_290_out, not_291_out, not_292_out, not_293_out, not_294_out;

  not not_1 (not_1_out, OP[5]);
  not not_2 (not_2_out, OP[4]);
  not not_3 (not_3_out, OP[3]);
  not not_4 (not_4_out, OP[2]);
  not not_5 (not_5_out, OP[1]);
  not not_6 (not_6_out, OP[0]);
  not not_7 (not_7_out, FUNC[4]);
  not not_8 (not_8_out, FUNC[3]);
  not not_9 (not_9_out, FUNC[2]);
  not not_10 (not_10_out, FUNC[1]);
  not not_11 (not_11_out, FUNC[0]);
  not not_12 (not_12_out, OP[5]);
  not not_13 (not_13_out, OP[4]);
  not not_14 (not_14_out, OP[3]);
  not not_15 (not_15_out, OP[2]);
  not not_16 (not_16_out, OP[1]);
  not not_17 (not_17_out, OP[0]);
  not not_18 (not_18_out, FUNC[4]);
  not not_19 (not_19_out, FUNC[3]);
  not not_20 (not_20_out, FUNC[2]);
  not not_21 (not_21_out, FUNC[1]);
  not not_22 (not_22_out, OP[5]);
  not not_23 (not_23_out, OP[4]);
  not not_24 (not_24_out, OP[3]);
  not not_25 (not_25_out, OP[2]);
  not not_26 (not_26_out, OP[1]);
  not not_27 (not_27_out, OP[0]);
  not not_28 (not_28_out, FUNC[4]);
  not not_29 (not_29_out, FUNC[3]);
  not not_30 (not_30_out, FUNC[2]);
  not not_31 (not_31_out, FUNC[0]);
  not not_32 (not_32_out, OP[5]);
  not not_33 (not_33_out, OP[4]);
  not not_34 (not_34_out, OP[3]);
  not not_35 (not_35_out, OP[2]);
  not not_36 (not_36_out, OP[1]);
  not not_37 (not_37_out, OP[0]);
  not not_38 (not_38_out, FUNC[4]);
  not not_39 (not_39_out, FUNC[3]);
  not not_40 (not_40_out, FUNC[1]);
  not not_41 (not_41_out, FUNC[0]);
  not not_42 (not_42_out, OP[5]);
  not not_43 (not_43_out, OP[4]);
  not not_44 (not_44_out, OP[3]);
  not not_45 (not_45_out, OP[2]);
  not not_46 (not_46_out, OP[1]);
  not not_47 (not_47_out, OP[0]);
  not not_48 (not_48_out, FUNC[4]);
  not not_49 (not_49_out, FUNC[3]);
  not not_50 (not_50_out, FUNC[1]);
  not not_51 (not_51_out, OP[5]);
  not not_52 (not_52_out, OP[4]);
  not not_53 (not_53_out, OP[3]);
  not not_54 (not_54_out, OP[2]);
  not not_55 (not_55_out, OP[1]);
  not not_56 (not_56_out, OP[0]);
  not not_57 (not_57_out, FUNC[4]);
  not not_58 (not_58_out, FUNC[3]);
  not not_59 (not_59_out, OP[5]);
  not not_60 (not_60_out, OP[4]);
  not not_61 (not_61_out, OP[3]);
  not not_62 (not_62_out, OP[2]);
  not not_63 (not_63_out, OP[1]);
  not not_64 (not_64_out, OP[0]);
  not not_65 (not_65_out, FUNC[4]);
  not not_66 (not_66_out, FUNC[2]);
  not not_67 (not_67_out, FUNC[0]);
  not not_68 (not_68_out, OP[5]);
  not not_69 (not_69_out, OP[4]);
  not not_70 (not_70_out, OP[3]);
  not not_71 (not_71_out, OP[2]);
  not not_72 (not_72_out, OP[1]);
  not not_73 (not_73_out, OP[0]);
  not not_74 (not_74_out, FUNC[4]);
  not not_75 (not_75_out, FUNC[2]);
  not not_76 (not_76_out, OP[5]);
  not not_77 (not_77_out, OP[4]);
  not not_78 (not_78_out, OP[3]);
  not not_79 (not_79_out, OP[2]);
  not not_80 (not_80_out, OP[1]);
  not not_81 (not_81_out, OP[0]);
  not not_82 (not_82_out, FUNC[5]);
  not not_83 (not_83_out, FUNC[4]);
  not not_84 (not_84_out, FUNC[2]);
  not not_85 (not_85_out, FUNC[1]);
  not not_86 (not_86_out, FUNC[0]);
  not not_87 (not_87_out, OP[5]);
  not not_88 (not_88_out, OP[4]);
  not not_89 (not_89_out, OP[3]);
  not not_90 (not_90_out, OP[2]);
  not not_91 (not_91_out, OP[1]);
  not not_92 (not_92_out, OP[0]);
  not not_93 (not_93_out, FUNC[5]);
  not not_94 (not_94_out, FUNC[4]);
  not not_95 (not_95_out, FUNC[1]);
  not not_96 (not_96_out, FUNC[0]);
  not not_97 (not_97_out, OP[5]);
  not not_98 (not_98_out, OP[4]);
  not not_99 (not_99_out, OP[3]);
  not not_100 (not_100_out, OP[1]);
  not not_101 (not_101_out, OP[0]);
  not not_102 (not_102_out, OP[5]);
  not not_103 (not_103_out, OP[4]);
  not not_104 (not_104_out, OP[3]);
  not not_105 (not_105_out, OP[1]);
  not not_106 (not_106_out, OP[5]);
  not not_107 (not_107_out, OP[4]);
  not not_108 (not_108_out, OP[2]);
  not not_109 (not_109_out, OP[1]);
  not not_110 (not_110_out, OP[0]);
  not not_111 (not_111_out, OP[5]);
  not not_112 (not_112_out, OP[4]);
  not not_113 (not_113_out, OP[1]);
  not not_114 (not_114_out, OP[0]);
  not not_115 (not_115_out, OP[5]);
  not not_116 (not_116_out, OP[4]);
  not not_117 (not_117_out, OP[2]);
  not not_118 (not_118_out, OP[1]);
  not not_119 (not_119_out, OP[5]);
  not not_120 (not_120_out, OP[4]);
  not not_121 (not_121_out, OP[2]);
  not not_122 (not_122_out, OP[0]);
  not not_123 (not_123_out, OP[5]);
  not not_124 (not_124_out, OP[4]);
  not not_125 (not_125_out, OP[1]);
  not not_126 (not_126_out, OP[4]);
  not not_127 (not_127_out, OP[3]);
  not not_128 (not_128_out, OP[2]);
  not not_129 (not_129_out, OP[4]);
  not not_130 (not_130_out, OP[2]);
  not not_131 (not_131_out, OP[5]);
  not not_132 (not_132_out, OP[4]);
  not not_133 (not_133_out, OP[3]);
  not not_134 (not_134_out, OP[2]);
  not not_135 (not_135_out, OP[1]);
  not not_136 (not_136_out, OP[0]);
  not not_137 (not_137_out, FUNC[4]);
  not not_138 (not_138_out, FUNC[3]);
  not not_139 (not_139_out, FUNC[2]);
  not not_140 (not_140_out, OP[5]);
  not not_141 (not_141_out, OP[4]);
  not not_142 (not_142_out, OP[4]);
  not not_143 (not_143_out, OP[2]);
  not not_144 (not_144_out, OP[1]);
  not not_145 (not_145_out, OP[0]);
  not not_146 (not_146_out, OP[5]);
  not not_147 (not_147_out, OP[4]);
  not not_148 (not_148_out, OP[3]);
  not not_149 (not_149_out, OP[2]);
  not not_150 (not_150_out, OP[1]);
  not not_151 (not_151_out, OP[5]);
  not not_152 (not_152_out, OP[4]);
  not not_153 (not_153_out, OP[3]);
  not not_154 (not_154_out, OP[2]);
  not not_155 (not_155_out, OP[1]);
  not not_156 (not_156_out, OP[0]);
  not not_157 (not_157_out, FUNC[5]);
  not not_158 (not_158_out, FUNC[4]);
  not not_159 (not_159_out, FUNC[3]);
  not not_160 (not_160_out, FUNC[2]);
  not not_161 (not_161_out, FUNC[1]);
  not not_162 (not_162_out, FUNC[0]);
  not not_163 (not_163_out, OP[5]);
  not not_164 (not_164_out, OP[4]);
  not not_165 (not_165_out, OP[3]);
  not not_166 (not_166_out, OP[2]);
  not not_167 (not_167_out, OP[1]);
  not not_168 (not_168_out, OP[0]);
  not not_169 (not_169_out, FUNC[5]);
  not not_170 (not_170_out, FUNC[4]);
  not not_171 (not_171_out, FUNC[3]);
  not not_172 (not_172_out, FUNC[2]);
  not not_173 (not_173_out, OP[5]);
  not not_174 (not_174_out, OP[4]);
  not not_175 (not_175_out, OP[3]);
  not not_176 (not_176_out, OP[2]);
  not not_177 (not_177_out, OP[1]);
  not not_178 (not_178_out, OP[0]);
  not not_179 (not_179_out, FUNC[5]);
  not not_180 (not_180_out, FUNC[4]);
  not not_181 (not_181_out, FUNC[3]);
  not not_182 (not_182_out, FUNC[2]);
  not not_183 (not_183_out, FUNC[0]);
  not not_184 (not_184_out, OP[5]);
  not not_185 (not_185_out, OP[4]);
  not not_186 (not_186_out, OP[3]);
  not not_187 (not_187_out, OP[2]);
  not not_188 (not_188_out, OP[1]);
  not not_189 (not_189_out, OP[0]);
  not not_190 (not_190_out, FUNC[4]);
  not not_191 (not_191_out, FUNC[3]);
  not not_192 (not_192_out, FUNC[2]);
  not not_193 (not_193_out, FUNC[1]);
  not not_194 (not_194_out, FUNC[0]);
  not not_195 (not_195_out, OP[5]);
  not not_196 (not_196_out, OP[4]);
  not not_197 (not_197_out, OP[3]);
  not not_198 (not_198_out, OP[2]);
  not not_199 (not_199_out, OP[1]);
  not not_200 (not_200_out, OP[0]);
  not not_201 (not_201_out, FUNC[4]);
  not not_202 (not_202_out, FUNC[3]);
  not not_203 (not_203_out, FUNC[2]);
  not not_204 (not_204_out, FUNC[1]);
  not not_205 (not_205_out, OP[5]);
  not not_206 (not_206_out, OP[4]);
  not not_207 (not_207_out, OP[3]);
  not not_208 (not_208_out, OP[2]);
  not not_209 (not_209_out, OP[1]);
  not not_210 (not_210_out, OP[0]);
  not not_211 (not_211_out, FUNC[4]);
  not not_212 (not_212_out, FUNC[3]);
  not not_213 (not_213_out, FUNC[2]);
  not not_214 (not_214_out, FUNC[0]);
  not not_215 (not_215_out, OP[5]);
  not not_216 (not_216_out, OP[4]);
  not not_217 (not_217_out, OP[3]);
  not not_218 (not_218_out, OP[2]);
  not not_219 (not_219_out, OP[1]);
  not not_220 (not_220_out, OP[0]);
  not not_221 (not_221_out, FUNC[4]);
  not not_222 (not_222_out, FUNC[3]);
  not not_223 (not_223_out, FUNC[1]);
  not not_224 (not_224_out, FUNC[0]);
  not not_225 (not_225_out, OP[5]);
  not not_226 (not_226_out, OP[4]);
  not not_227 (not_227_out, OP[3]);
  not not_228 (not_228_out, OP[2]);
  not not_229 (not_229_out, OP[1]);
  not not_230 (not_230_out, OP[0]);
  not not_231 (not_231_out, FUNC[4]);
  not not_232 (not_232_out, FUNC[3]);
  not not_233 (not_233_out, FUNC[1]);
  not not_234 (not_234_out, OP[5]);
  not not_235 (not_235_out, OP[4]);
  not not_236 (not_236_out, OP[3]);
  not not_237 (not_237_out, OP[2]);
  not not_238 (not_238_out, OP[1]);
  not not_239 (not_239_out, OP[0]);
  not not_240 (not_240_out, FUNC[4]);
  not not_241 (not_241_out, FUNC[3]);
  not not_242 (not_242_out, OP[5]);
  not not_243 (not_243_out, OP[4]);
  not not_244 (not_244_out, OP[3]);
  not not_245 (not_245_out, OP[2]);
  not not_246 (not_246_out, OP[1]);
  not not_247 (not_247_out, OP[0]);
  not not_248 (not_248_out, FUNC[4]);
  not not_249 (not_249_out, FUNC[2]);
  not not_250 (not_250_out, FUNC[0]);
  not not_251 (not_251_out, OP[5]);
  not not_252 (not_252_out, OP[4]);
  not not_253 (not_253_out, OP[3]);
  not not_254 (not_254_out, OP[2]);
  not not_255 (not_255_out, OP[1]);
  not not_256 (not_256_out, OP[0]);
  not not_257 (not_257_out, FUNC[4]);
  not not_258 (not_258_out, FUNC[2]);
  not not_259 (not_259_out, OP[5]);
  not not_260 (not_260_out, OP[4]);
  not not_261 (not_261_out, OP[3]);
  not not_262 (not_262_out, OP[2]);
  not not_263 (not_263_out, OP[1]);
  not not_264 (not_264_out, OP[0]);
  not not_265 (not_265_out, FUNC[5]);
  not not_266 (not_266_out, FUNC[4]);
  not not_267 (not_267_out, FUNC[1]);
  not not_268 (not_268_out, FUNC[0]);
  not not_269 (not_269_out, OP[5]);
  not not_270 (not_270_out, OP[4]);
  not not_271 (not_271_out, OP[3]);
  not not_272 (not_272_out, OP[1]);
  not not_273 (not_273_out, OP[0]);
  not not_274 (not_274_out, OP[5]);
  not not_275 (not_275_out, OP[4]);
  not not_276 (not_276_out, OP[3]);
  not not_277 (not_277_out, OP[1]);
  not not_278 (not_278_out, OP[4]);
  not not_279 (not_279_out, OP[2]);
  not not_280 (not_280_out, OP[5]);
  not not_281 (not_281_out, OP[4]);
  not not_282 (not_282_out, OP[3]);
  not not_283 (not_283_out, OP[2]);
  not not_284 (not_284_out, OP[1]);
  not not_285 (not_285_out, OP[0]);
  not not_286 (not_286_out, FUNC[4]);
  not not_287 (not_287_out, FUNC[3]);
  not not_288 (not_288_out, FUNC[2]);
  not not_289 (not_289_out, OP[5]);
  not not_290 (not_290_out, OP[4]);
  not not_291 (not_291_out, OP[4]);
  not not_292 (not_292_out, OP[2]);
  not not_293 (not_293_out, OP[1]);
  not not_294 (not_294_out, OP[0]);
  and and_1 (and_1_out, not_1_out, not_2_out, not_3_out, not_4_out, not_5_out, not_6_out, FUNC[5], not_7_out, not_8_out, not_9_out, not_10_out, not_11_out);
  and and_2 (and_2_out, not_12_out, not_13_out, not_14_out, not_15_out, not_16_out, not_17_out, FUNC[5], not_18_out, not_19_out, not_20_out, not_21_out, FUNC[0]);
  and and_3 (and_3_out, not_22_out, not_23_out, not_24_out, not_25_out, not_26_out, not_27_out, FUNC[5], not_28_out, not_29_out, not_30_out, FUNC[1], not_31_out);
  and and_4 (and_4_out, not_32_out, not_33_out, not_34_out, not_35_out, not_36_out, not_37_out, FUNC[5], not_38_out, not_39_out, FUNC[2], not_40_out, not_41_out);
  and and_5 (and_5_out, not_42_out, not_43_out, not_44_out, not_45_out, not_46_out, not_47_out, FUNC[5], not_48_out, not_49_out, FUNC[2], not_50_out, FUNC[0]);
  and and_6 (and_6_out, not_51_out, not_52_out, not_53_out, not_54_out, not_55_out, not_56_out, FUNC[5], not_57_out, not_58_out, FUNC[2], FUNC[1], FUNC[0]);
  and and_7 (and_7_out, not_59_out, not_60_out, not_61_out, not_62_out, not_63_out, not_64_out, FUNC[5], not_65_out, FUNC[3], not_66_out, FUNC[1], not_67_out);
  and and_8 (and_8_out, not_68_out, not_69_out, not_70_out, not_71_out, not_72_out, not_73_out, FUNC[5], not_74_out, FUNC[3], not_75_out, FUNC[1], FUNC[0]);
  and and_9 (and_9_out, not_76_out, not_77_out, not_78_out, not_79_out, not_80_out, not_81_out, not_82_out, not_83_out, FUNC[3], not_84_out, not_85_out, not_86_out);
  and and_10 (and_10_out, not_87_out, not_88_out, not_89_out, not_90_out, not_91_out, not_92_out, not_93_out, not_94_out, FUNC[3], FUNC[2], not_95_out, not_96_out);
  and and_11 (and_11_out, not_97_out, not_98_out, not_99_out, OP[2], not_100_out, not_101_out);
  and and_12 (and_12_out, not_102_out, not_103_out, not_104_out, OP[2], not_105_out, OP[0]);
  and and_13 (and_13_out, not_106_out, not_107_out, OP[3], not_108_out, not_109_out, not_110_out);
  and and_14 (and_14_out, not_111_out, not_112_out, OP[3], OP[2], not_113_out, not_114_out);
  and and_15 (and_15_out, not_115_out, not_116_out, OP[3], not_117_out, not_118_out, OP[0]);
  and and_16 (and_16_out, not_119_out, not_120_out, OP[3], not_121_out, OP[1], not_122_out);
  and and_17 (and_17_out, not_123_out, not_124_out, OP[3], OP[2], not_125_out, OP[0]);
  and and_18 (and_18_out, OP[5], not_126_out, not_127_out, not_128_out, OP[1], OP[0]);
  and and_19 (and_19_out, OP[5], not_129_out, OP[3], not_130_out, OP[1], OP[0]);
  and and_20 (and_20_out, not_131_out, not_132_out, not_133_out, not_134_out, not_135_out, not_136_out, FUNC[5], not_137_out, not_138_out, not_139_out, FUNC[1], FUNC[0]);
  and and_21 (and_21_out, not_140_out, not_141_out, OP[3], OP[2], OP[1], OP[0]);
  and and_22 (and_22_out, OP[5], not_142_out, OP[3], not_143_out, not_144_out, not_145_out);
  and and_23 (and_23_out, not_146_out, not_147_out, not_148_out, not_149_out, not_150_out, OP[0]);
  and and_24 (and_24_out, not_151_out, not_152_out, not_153_out, not_154_out, not_155_out, not_156_out, not_157_out, not_158_out, not_159_out, not_160_out, not_161_out, not_162_out);
  and and_25 (and_25_out, not_163_out, not_164_out, not_165_out, not_166_out, not_167_out, not_168_out, not_169_out, not_170_out, not_171_out, not_172_out, FUNC[1], FUNC[0]);
  and and_26 (and_26_out, not_173_out, not_174_out, not_175_out, not_176_out, not_177_out, not_178_out, not_179_out, not_180_out, not_181_out, not_182_out, FUNC[1], not_183_out);
  and and_27 (and_27_out, not_184_out, not_185_out, not_186_out, not_187_out, not_188_out, not_189_out, FUNC[5], not_190_out, not_191_out, not_192_out, not_193_out, not_194_out);
  and and_28 (and_28_out, not_195_out, not_196_out, not_197_out, not_198_out, not_199_out, not_200_out, FUNC[5], not_201_out, not_202_out, not_203_out, not_204_out, FUNC[0]);
  and and_29 (and_29_out, not_205_out, not_206_out, not_207_out, not_208_out, not_209_out, not_210_out, FUNC[5], not_211_out, not_212_out, not_213_out, FUNC[1], not_214_out);
  and and_30 (and_30_out, not_215_out, not_216_out, not_217_out, not_218_out, not_219_out, not_220_out, FUNC[5], not_221_out, not_222_out, FUNC[2], not_223_out, not_224_out);
  and and_31 (and_31_out, not_225_out, not_226_out, not_227_out, not_228_out, not_229_out, not_230_out, FUNC[5], not_231_out, not_232_out, FUNC[2], not_233_out, FUNC[0]);
  and and_32 (and_32_out, not_234_out, not_235_out, not_236_out, not_237_out, not_238_out, not_239_out, FUNC[5], not_240_out, not_241_out, FUNC[2], FUNC[1], FUNC[0]);
  and and_33 (and_33_out, not_242_out, not_243_out, not_244_out, not_245_out, not_246_out, not_247_out, FUNC[5], not_248_out, FUNC[3], not_249_out, FUNC[1], not_250_out);
  and and_34 (and_34_out, not_251_out, not_252_out, not_253_out, not_254_out, not_255_out, not_256_out, FUNC[5], not_257_out, FUNC[3], not_258_out, FUNC[1], FUNC[0]);
  and and_35 (and_35_out, not_259_out, not_260_out, not_261_out, not_262_out, not_263_out, not_264_out, not_265_out, not_266_out, FUNC[3], FUNC[2], not_267_out, not_268_out);
  and and_36 (and_36_out, not_269_out, not_270_out, not_271_out, OP[2], not_272_out, not_273_out);
  and and_37 (and_37_out, not_274_out, not_275_out, not_276_out, OP[2], not_277_out, OP[0]);
  and and_38 (and_38_out, OP[5], not_278_out, OP[3], not_279_out, OP[1], OP[0]);
  and and_39 (and_39_out, not_280_out, not_281_out, not_282_out, not_283_out, not_284_out, not_285_out, FUNC[5], not_286_out, not_287_out, not_288_out, FUNC[1], FUNC[0]);
  and and_40 (and_40_out, not_289_out, not_290_out, OP[3], OP[2], OP[1], OP[0]);
  and and_41 (and_41_out, OP[5], not_291_out, OP[3], not_292_out, not_293_out, not_294_out);
  or or_1 (R2_Used, and_24_out, and_25_out, and_26_out, and_27_out, and_28_out, and_29_out, and_30_out, and_31_out, and_32_out, and_33_out, and_34_out, and_35_out, and_36_out, and_37_out, and_38_out, and_39_out, and_40_out, and_41_out);
  or or_2 (R1_Used, and_1_out, and_2_out, and_3_out, and_4_out, and_5_out, and_6_out, and_7_out, and_8_out, and_9_out, and_10_out, and_11_out, and_12_out, and_13_out, and_14_out, and_15_out, and_16_out, and_17_out, and_18_out, and_19_out, and_20_out, and_21_out, and_22_out, and_23_out);
endmodule

module \数据相关检测  (
  input  [5:0] OP,
  input  [5:0] FUNC,
  input  [4:0] rs,
  input  EX_RegWrite,
  input  [4:0] EX_writeToReg,
  input  MEM_RegWrite,
  input  [4:0] MEM_writeToReg,
  input  [4:0] rt,
  output DataHazzard
);

  wire and_1_out, and_2_out, and_3_out, and_4_out, comparator_1_eq, comparator_2_eq, comparator_3_eq,
       comparator_4_eq, comparator_5_eq, comparator_6_eq, not_1_out, not_2_out, \源寄存器使用情况_1_r1_used ,
       \源寄存器使用情况_1_r2_used ;

  \源寄存器使用情况  \u_源寄存器使用情况_1  (.R1_Used(\源寄存器使用情况_1_r1_used ), .R2_Used(\源寄存器使用情况_1_r2_used ), .OP(OP), .FUNC(FUNC));
  Comparator #(.width(5), .mode("twosComplement")) comparator_1 (
    .a(rs), .b({5{1'b0}}), .eq(comparator_1_eq));  // open: gt, lt
  not not_1 (not_1_out, comparator_1_eq);
  Comparator #(.width(5), .mode("twosComplement")) comparator_2 (
    .a(rs), .b(EX_writeToReg), .eq(comparator_2_eq));  // open: gt, lt
  Comparator #(.width(5), .mode("twosComplement")) comparator_3 (
    .a(rs), .b(MEM_writeToReg), .eq(comparator_3_eq));  // open: gt, lt
  not not_2 (not_2_out, comparator_4_eq);
  Comparator #(.width(5), .mode("twosComplement")) comparator_4 (
    .a(rt), .b({5{1'b0}}), .eq(comparator_4_eq));  // open: gt, lt
  Comparator #(.width(5), .mode("twosComplement")) comparator_5 (
    .a(EX_writeToReg), .b(rt), .eq(comparator_5_eq));  // open: gt, lt
  Comparator #(.width(5), .mode("twosComplement")) comparator_6 (
    .a(MEM_writeToReg), .b(rt), .eq(comparator_6_eq));  // open: gt, lt
  and and_1 (and_1_out, \源寄存器使用情况_1_r1_used , not_1_out, comparator_2_eq, EX_RegWrite);
  and and_2 (and_2_out, \源寄存器使用情况_1_r1_used , not_1_out, MEM_RegWrite, comparator_3_eq);
  and and_3 (and_3_out, \源寄存器使用情况_1_r2_used , not_2_out, EX_RegWrite, comparator_5_eq);
  and and_4 (and_4_out, \源寄存器使用情况_1_r2_used , not_2_out, MEM_RegWrite, comparator_6_eq);
  or or_1 (DataHazzard, and_1_out, and_2_out, and_3_out, and_4_out);
endmodule

module FSM (
  input  HIT,
  input  RST,
  input  CLK,
  input  EN,
  output Z
);

  wire and_1_out, and_2_out, and_3_out, D1_q, D1_qn, or_1_out, xor_1_out;

  D_Flip_Flop #(.trigger("rising"), .Pre_Clr_Positions("ABOVE_BELOW"), .NegatePresetClear("false"), .enable("true"), .NewFFLayout("true")) D2 (
    .clk(CLK), .D(or_1_out), .Q(Z), .preset(RST), .en(EN));  // open: Qn, reset
  D_Flip_Flop #(.trigger("rising"), .Pre_Clr_Positions("ABOVE_BELOW"), .NegatePresetClear("false"), .enable("true"), .NewFFLayout("true")) D1 (
    .clk(CLK), .D(and_3_out), .Q(D1_q), .Qn(D1_qn), .preset(RST), .en(EN));  // open: reset
  and and_1 (and_1_out, Z, D1_qn);
  and and_2 (and_2_out, HIT, D1_q);
  xor xor_1 (xor_1_out, HIT, Z);
  or or_1 (or_1_out, and_1_out, and_2_out);
  and and_3 (and_3_out, xor_1_out, D1_qn);
endmodule

module MAX (
  input  [15:0] Y,
  input  [15:0] X,
  input  [2:0] NO_Y,
  input  [2:0] NO_X,
  output [15:0] MAX,
  output [2:0] NO_Max
);

  wire comparator_1_eq, comparator_1_gt, or_1_out;

  Multiplexer #(.select(1), .width(16), .disabled("Z"), .enable("false")) multiplexer_1 (
    .in0(Y), .in1(X), .out(MAX), .sel(or_1_out));
  or or_1 (or_1_out, comparator_1_gt, comparator_1_eq);
  Comparator #(.width(16), .mode("unsigned")) comparator_1 (
    .a(X), .b(Y), .gt(comparator_1_gt), .eq(comparator_1_eq));  // open: lt
  Multiplexer #(.select(1), .width(3), .disabled("Z"), .enable("false")) multiplexer_2 (
    .in0(NO_Y), .in1(NO_X), .out(NO_Max), .sel(or_1_out));
endmodule

module \CACHE槽  (
  input  CLK,
  input  [31:0] PC_IN,
  input  [31:0] BranchAddr_IN,
  input  BranchTaken,
  input  WRITE,
  input  Load,
  input  EN,
  output valid,
  output [31:0] PC_OUT,
  output [15:0] Count,
  output [31:0] BranchAddr_OUT,
  output Jump
);

  wire fsm_1_z, not_1_out, or_1_out;
  wire [31:0] DATA_q;

  not not_1 (not_1_out, or_1_out);
  or or_1 (or_1_out, WRITE, Load);
  Register #(.width(1), .trigger("rising"), .Select("low")) u_VALID (
    .D(1'b1), .en(WRITE), .Q(valid), .clk(CLK));  // open: clr
  Register #(.width(32), .trigger("rising"), .Select("low")) TAG (
    .D(PC_IN), .en(WRITE), .Q(PC_OUT), .clk(CLK));  // open: clr
  Counter #(.width(16), .max('hffff), .ongoal("wrap"), .trigger("rising"), .behavior("old")) counter_1 (
    .load(or_1_out), .D({16{1'b0}}), .count(not_1_out), .Q(Count), .clk(CLK));  // open: carry, clr, preset
  Register #(.width(32), .trigger("rising"), .Select("low")) DATA (
    .D(BranchAddr_IN), .en(WRITE), .Q(DATA_q), .clk(CLK));  // open: clr
  FSM fsm_1 (.RST(WRITE), .CLK(CLK), .EN(EN), .Z(fsm_1_z), .HIT(BranchTaken));
  assign BranchAddr_OUT = Load ? DATA_q : 32'bz;  // Controlled_Buffer controlled_buffer_1
  assign Jump = Load ? fsm_1_z : 1'bz;  // Controlled_Buffer controlled_buffer_2
endmodule

module cache (
  input  [31:0] BRANCK_ADDR,
  input  CLK,
  input  BRANCH_TAKEN,
  input  [31:0] PC,
  input  [31:0] EX_PC,
  output [31:0] BranchAddr_out,
  output PJUMP,
  output MISS
);

  wire and_1_out, and_2_out, and_3_out, and_4_out, and_5_out, and_6_out, and_7_out, and_8_out, and_9_out,
       comparator_1_eq, comparator_2_eq, comparator_3_eq, comparator_4_eq, comparator_5_eq, comparator_6_eq,
       comparator_7_eq, comparator_8_eq, comparator_9_eq, comparator_10_eq, comparator_11_eq,
       comparator_12_eq, comparator_13_eq, comparator_14_eq, comparator_15_eq, comparator_16_eq,
       decoder_1_out0, decoder_1_out1, decoder_1_out2, decoder_1_out3, decoder_1_out4, decoder_1_out5,
       decoder_1_out6, decoder_1_out7, EN0, EN1, EN2, EN3, EN4, EN5, EN6, EN7, EX_MISS, JUMP, LAOD0, LAOD1,
       LAOD2, LAOD3, LAOD4, LAOD5, LAOD6, LAOD7, VAL0, VAL1, VAL2, VAL3, VAL4, VAL5, VAL6, VAL7;
  wire [2:0] max_1_no_max, max_2_no_max, max_3_no_max, max_4_no_max, max_5_no_max, max_6_no_max, max_7_no_max;
  wire [15:0] COUNT0, COUNT1, COUNT2, COUNT3, COUNT4, COUNT5, COUNT6, COUNT7, max_1_max, max_2_max,
       max_3_max, max_4_max, max_5_max, max_6_max;
  wire [31:0] PC0, PC1, PC2, PC3, PC4, PC5, PC6, PC7;

  MAX max_1 (.Y(COUNT1), .X(COUNT0), .NO_Y(3'b001), .NO_X(3'b000), .MAX(max_1_max), .NO_Max(max_1_no_max));
  MAX max_2 (.Y(COUNT3), .X(COUNT2), .NO_Y(3'b011), .NO_X(3'b010), .MAX(max_2_max), .NO_Max(max_2_no_max));
  MAX max_3 (.Y(COUNT5), .X(COUNT4), .NO_Y(3'b101), .NO_X(3'b100), .MAX(max_3_max), .NO_Max(max_3_no_max));
  MAX max_4 (.Y(COUNT7), .X(COUNT6), .NO_Y(3'b111), .NO_X(3'b110), .MAX(max_4_max), .NO_Max(max_4_no_max));
  MAX max_5 (
    .Y(max_2_max), .X(max_1_max), .NO_Y(max_2_no_max), .NO_X(max_1_no_max), .MAX(max_5_max),
    .NO_Max(max_5_no_max));
  MAX max_6 (
    .Y(max_4_max), .X(max_3_max), .NO_Y(max_4_no_max), .NO_X(max_3_no_max), .MAX(max_6_max),
    .NO_Max(max_6_no_max));
  MAX max_7 (
    .Y(max_6_max), .X(max_5_max), .NO_Y(max_6_no_max), .NO_X(max_5_no_max), .NO_Max(max_7_no_max));  // open: MAX
  and and_1 (and_1_out, EX_MISS, BRANCH_TAKEN);
  Decoder #(.select(3), .tristate("false"), .disabled(0), .enable("true")) decoder_1 (
    .out0(decoder_1_out0), .out1(decoder_1_out1), .out2(decoder_1_out2), .out3(decoder_1_out3),
    .out4(decoder_1_out4), .out5(decoder_1_out5), .out6(decoder_1_out6), .out7(decoder_1_out7),
    .sel(max_7_no_max), .en(and_1_out));
  and and_2 (and_2_out, decoder_1_out0, and_1_out);
  and and_3 (and_3_out, decoder_1_out1, and_1_out);
  and and_4 (and_4_out, decoder_1_out2, and_1_out);
  and and_5 (and_5_out, decoder_1_out3, and_1_out);
  and and_6 (and_6_out, decoder_1_out4, and_1_out);
  and and_7 (and_7_out, decoder_1_out5, and_1_out);
  and and_8 (and_8_out, decoder_1_out6, and_1_out);
  and and_9 (and_9_out, decoder_1_out7, and_1_out);
  \CACHE槽  \cache槽_1  (
    .CLK(CLK), .PC_IN(EX_PC), .BranchAddr_IN(BRANCK_ADDR), .BranchTaken(BRANCH_TAKEN), .WRITE(and_2_out),
    .Load(LAOD0), .valid(VAL0), .PC_OUT(PC0), .Count(COUNT0), .BranchAddr_OUT(BranchAddr_out), .Jump(JUMP),
    .EN(EN0));
  \CACHE槽  \cache槽_2  (
    .CLK(CLK), .PC_IN(EX_PC), .BranchAddr_IN(BRANCK_ADDR), .BranchTaken(BRANCH_TAKEN), .WRITE(and_3_out),
    .Load(LAOD1), .valid(VAL1), .PC_OUT(PC1), .Count(COUNT1), .BranchAddr_OUT(BranchAddr_out), .Jump(JUMP),
    .EN(EN1));
  \CACHE槽  \cache槽_3  (
    .CLK(CLK), .PC_IN(EX_PC), .BranchAddr_IN(BRANCK_ADDR), .BranchTaken(BRANCH_TAKEN), .WRITE(and_4_out),
    .Load(LAOD2), .valid(VAL2), .PC_OUT(PC2), .Count(COUNT2), .BranchAddr_OUT(BranchAddr_out), .Jump(JUMP),
    .EN(EN2));
  \CACHE槽  \cache槽_4  (
    .CLK(CLK), .PC_IN(EX_PC), .BranchAddr_IN(BRANCK_ADDR), .BranchTaken(BRANCH_TAKEN), .WRITE(and_5_out),
    .Load(LAOD3), .valid(VAL3), .PC_OUT(PC3), .Count(COUNT3), .BranchAddr_OUT(BranchAddr_out), .Jump(JUMP),
    .EN(EN3));
  \CACHE槽  \cache槽_5  (
    .CLK(CLK), .PC_IN(EX_PC), .BranchAddr_IN(BRANCK_ADDR), .BranchTaken(BRANCH_TAKEN), .WRITE(and_6_out),
    .Load(LAOD4), .valid(VAL4), .PC_OUT(PC4), .Count(COUNT4), .BranchAddr_OUT(BranchAddr_out), .Jump(JUMP),
    .EN(EN4));
  \CACHE槽  \cache槽_6  (
    .CLK(CLK), .PC_IN(EX_PC), .BranchAddr_IN(BRANCK_ADDR), .BranchTaken(BRANCH_TAKEN), .WRITE(and_7_out),
    .Load(LAOD5), .valid(VAL5), .PC_OUT(PC5), .Count(COUNT5), .BranchAddr_OUT(BranchAddr_out), .Jump(JUMP),
    .EN(EN5));
  \CACHE槽  \cache槽_7  (
    .CLK(CLK), .PC_IN(EX_PC), .BranchAddr_IN(BRANCK_ADDR), .BranchTaken(BRANCH_TAKEN), .WRITE(and_8_out),
    .Load(LAOD6), .valid(VAL6), .PC_OUT(PC6), .Count(COUNT6), .BranchAddr_OUT(BranchAddr_out), .Jump(JUMP),
    .EN(EN6));
  \CACHE槽  \cache槽_8  (
    .CLK(CLK), .PC_IN(EX_PC), .BranchAddr_IN(BRANCK_ADDR), .BranchTaken(BRANCH_TAKEN), .WRITE(and_9_out),
    .Load(LAOD7), .valid(VAL7), .PC_OUT(PC7), .Count(COUNT7), .BranchAddr_OUT(BranchAddr_out), .Jump(JUMP),
    .EN(EN7));
  Comparator #(.width(32), .mode("twosComplement")) comparator_1 (
    .a(PC), .b(PC0), .eq(comparator_1_eq));  // open: gt, lt
  Comparator #(.width(32), .mode("twosComplement")) comparator_2 (
    .a(PC), .b(PC1), .eq(comparator_2_eq));  // open: gt, lt
  Comparator #(.width(32), .mode("twosComplement")) comparator_3 (
    .a(PC), .b(PC2), .eq(comparator_3_eq));  // open: gt, lt
  Comparator #(.width(32), .mode("twosComplement")) comparator_4 (
    .a(PC), .b(PC3), .eq(comparator_4_eq));  // open: gt, lt
  Comparator #(.width(32), .mode("twosComplement")) comparator_5 (
    .a(PC), .b(PC4), .eq(comparator_5_eq));  // open: gt, lt
  Comparator #(.width(32), .mode("twosComplement")) comparator_6 (
    .a(PC), .b(PC5), .eq(comparator_6_eq));  // open: gt, lt
  Comparator #(.width(32), .mode("twosComplement")) comparator_7 (
    .a(PC), .b(PC6), .eq(comparator_7_eq));  // open: gt, lt
  Comparator #(.width(32), .mode("twosComplement")) comparator_8 (
    .a(PC), .b(PC7), .eq(comparator_8_eq));  // open: gt, lt
  Comparator #(.width(32), .mode("twosComplement")) comparator_9 (
    .a(EX_PC), .b(PC0), .eq(comparator_9_eq));  // open: gt, lt
  Comparator #(.width(32), .mode("twosComplement")) comparator_10 (
    .a(EX_PC), .b(PC1), .eq(comparator_10_eq));  // open: gt, lt
  Comparator #(.width(32), .mode("twosComplement")) comparator_11 (
    .a(EX_PC), .b(PC2), .eq(comparator_11_eq));  // open: gt, lt
  Comparator #(.width(32), .mode("twosComplement")) comparator_12 (
    .a(EX_PC), .b(PC3), .eq(comparator_12_eq));  // open: gt, lt
  Comparator #(.width(32), .mode("twosComplement")) comparator_13 (
    .a(EX_PC), .b(PC4), .eq(comparator_13_eq));  // open: gt, lt
  Comparator #(.width(32), .mode("twosComplement")) comparator_14 (
    .a(EX_PC), .b(PC5), .eq(comparator_14_eq));  // open: gt, lt
  Comparator #(.width(32), .mode("twosComplement")) comparator_15 (
    .a(EX_PC), .b(PC6), .eq(comparator_15_eq));  // open: gt, lt
  Comparator #(.width(32), .mode("twosComplement")) comparator_16 (
    .a(EX_PC), .b(PC7), .eq(comparator_16_eq));  // open: gt, lt
  and and_10 (LAOD0, comparator_1_eq, VAL0);
  and and_11 (LAOD1, comparator_2_eq, VAL1);
  and and_12 (LAOD2, comparator_3_eq, VAL2);
  and and_13 (LAOD3, comparator_4_eq, VAL3);
  and and_14 (LAOD4, comparator_5_eq, VAL4);
  and and_15 (LAOD5, comparator_6_eq, VAL5);
  and and_16 (LAOD6, comparator_7_eq, VAL6);
  and and_17 (LAOD7, comparator_8_eq, VAL7);
  and and_18 (EN0, comparator_9_eq, VAL0);
  and and_19 (EN1, comparator_10_eq, VAL1);
  and and_20 (EN2, comparator_11_eq, VAL2);
  and and_21 (EN3, comparator_12_eq, VAL3);
  and and_22 (EN4, comparator_13_eq, VAL4);
  and and_23 (EN5, comparator_14_eq, VAL5);
  and and_24 (EN6, comparator_15_eq, VAL6);
  and and_25 (EN7, comparator_16_eq, VAL7);
  nor nor_1 (MISS, LAOD0, LAOD1, LAOD2, LAOD3, LAOD4, LAOD5, LAOD6, LAOD7);
  nor nor_2 (EX_MISS, EN0, EN1, EN2, EN3, EN4, EN5, EN6, EN7);
  and and_26 (PJUMP, JUMP, ~MISS);  // AND_Gate
endmodule

module \数据相关检测_动态分支预测  (
  input  [5:0] OP,
  input  [5:0] FUNC,
  input  [4:0] RS,
  input  Halt_or_Go,
  input  EX_MEMTOREG,
  input  [4:0] EX_WRITEREG,
  input  [4:0] RT,
  input  \J标记 ,
  input  MEM_REGW,
  input  [4:0] MEM_WRITEREG,
  input  EX_REGW,
  output PC_EN,
  output LOAD_USED,
  output IF_ID_EN,
  output IF_ID_STALL,
  output ID_EX_STALL,
  output [1:0] RSFORWARD,
  output [1:0] RTFORWARD
);

  wire and_1_out, and_2_out, comparator_1_eq, comparator_2_eq, comparator_3_eq, comparator_4_eq,
       comparator_5_eq, comparator_6_eq, not_1_out, not_2_out, \源寄存器使用情况_1_r1_used , \源寄存器使用情况_1_r2_used ;
  wire [1:0] and_3_out, and_5_out;

  \源寄存器使用情况  \u_源寄存器使用情况_1  (.R1_Used(\源寄存器使用情况_1_r1_used ), .R2_Used(\源寄存器使用情况_1_r2_used ), .OP(OP), .FUNC(FUNC));
  Comparator #(.width(5), .mode("twosComplement")) comparator_1 (
    .a(RS), .b({5{1'b0}}), .eq(comparator_1_eq));  // open: gt, lt
  Comparator #(.width(5), .mode("twosComplement")) comparator_2 (
    .a(RS), .b(EX_WRITEREG), .eq(comparator_2_eq));  // open: gt, lt
  Comparator #(.width(5), .mode("twosComplement")) comparator_3 (
    .a(RT), .b({5{1'b0}}), .eq(comparator_3_eq));  // open: gt, lt
  Comparator #(.width(5), .mode("twosComplement")) comparator_4 (
    .a(RT), .b(EX_WRITEREG), .eq(comparator_4_eq));  // open: gt, lt
  Comparator #(.width(5), .mode("twosComplement")) comparator_5 (
    .a(RS), .b(MEM_WRITEREG), .eq(comparator_5_eq));  // open: gt, lt
  Comparator #(.width(5), .mode("twosComplement")) comparator_6 (
    .a(RT), .b(MEM_WRITEREG), .eq(comparator_6_eq));  // open: gt, lt
  not not_1 (not_1_out, comparator_1_eq);
  not not_2 (not_2_out, comparator_3_eq);
  and and_1 (and_1_out, \源寄存器使用情况_1_r1_used , not_1_out, EX_MEMTOREG, comparator_2_eq);
  and and_2 (and_2_out, \源寄存器使用情况_1_r2_used , not_2_out, EX_MEMTOREG, comparator_4_eq);
  and and_3 (and_3_out[0], \源寄存器使用情况_1_r1_used , not_1_out, MEM_REGW, comparator_5_eq);
  and and_4 (and_3_out[1], \源寄存器使用情况_1_r1_used , not_1_out, EX_REGW, comparator_2_eq);
  and and_5 (and_5_out[0], \源寄存器使用情况_1_r2_used , not_2_out, MEM_REGW, comparator_6_eq);
  and and_6 (and_5_out[1], \源寄存器使用情况_1_r2_used , not_2_out, EX_REGW, comparator_4_eq);
  or or_1 (LOAD_USED, and_1_out, and_2_out);
  Multiplexer #(.select(2), .width(2), .disabled("Z"), .enable("false")) multiplexer_1 (
    .in0(2'b00), .in1(2'b01), .in2(2'b10), .in3(2'b10), .out(RSFORWARD), .sel(and_3_out));
  Multiplexer #(.select(2), .width(2), .disabled("Z"), .enable("false")) multiplexer_2 (
    .in0(2'b00), .in1(2'b01), .in2(2'b10), .in3(2'b10), .out(RTFORWARD), .sel(and_5_out));
  and and_7 (PC_EN, Halt_or_Go, ~LOAD_USED);  // AND_Gate
  and and_8 (IF_ID_EN, Halt_or_Go, ~LOAD_USED);  // AND_Gate
  or or_2 (ID_EX_STALL, LOAD_USED, \J标记 );

  assign IF_ID_STALL = \J标记 ;
endmodule

module \团队CPU  (
  output [31:0] out_1
);

  wire and_1_out, and_2_out, and_3_out, and_4_out, and_5_out, and_6_out, and_7_out, and_9_out, and_10_out,
       and_11_out, and_12_out, and_13_out, and_14_out, and_15_out, BLTZ, CLK, CLR1, CLR2, CLR3,
       comparator_1_gt, comparator_2_eq, d_ff_1_q, d_ff_2_q, d_ff_3_q, ERET, EX_JAL, ex_mem_1_equal_out,
       ex_mem_1_memtoreg_out, ex_mem_1_regwrite_out, ex_mem_1_syscall_out, EX_REGD, Go, Halt,
       id_ex_1_alu_src_out, id_ex_1_beq_out, id_ex_1_bne_out, id_ex_1_memtoreg_out, id_ex_1_memwrite_out,
       id_ex_1_regwrite_out, id_ex_1_sb_out, id_ex_1_syscall_out, IE, INT, INT0, INT1, INT2, INT3, IR1, IR2,
       IR3, J2, JMP, JR, Ledout, LUI, MEM_JAL, MEM_REGD, mem_wb_1_jal_out, mem_wb_1_memtoreg_out,
       mem_wb_1_regdst_out, mem_wb_1_syscall_out, MemWrite, mips_alu_1_equal, not_1_out, not_2_out, or_1_out,
       or_2_out, or_6_out, or_7_out, or_8_out, or_11_out, or_12_out, \PC_EN调试 , RegWrite, RST, SB_USE,
       SignedExt, W1, W2, W3, Write, \单周期硬布线控制器_1_alu_src , \单周期硬布线控制器_1_beq , \单周期硬布线控制器_1_bltz ,
       \单周期硬布线控制器_1_bne , \单周期硬布线控制器_1_eret , \单周期硬布线控制器_1_jal , \单周期硬布线控制器_1_jmp , \单周期硬布线控制器_1_jr ,
       \单周期硬布线控制器_1_lui , \单周期硬布线控制器_1_memtoreg , \单周期硬布线控制器_1_memwrite , \单周期硬布线控制器_1_regdst ,
       \单周期硬布线控制器_1_regwrite , \单周期硬布线控制器_1_sb , \单周期硬布线控制器_1_syscall , \数据相关 , \数据相关检测_重定向_1_id_ex_stall ,
       \数据相关检测_重定向_1_if_id_en , \数据相关检测_重定向_1_if_id_stall ;
  wire [1:0] id_ex_1_rs_forw_out, id_ex_1_rt_forw_out, priority_encoder_1_out, register_1_q, sb_addr,
       \数据相关检测_重定向_1_rsforward , \数据相关检测_重定向_1_rtforward ;
  wire [3:0] id_ex_1_aluop_out, \单周期硬布线控制器_1_alu_op ;
  wire [4:0] EX_REGTOWRITE, ID_R1_num, ID_R2_num, MEM_REGTOWRITE, multiplexer_10_out, multiplexer_16_out,
       multiplexer_24_out, shamt, W_num;
  wire [7:0] multiplexer_17_out, multiplexer_18_out, multiplexer_19_out, multiplexer_21_out;
  wire [15:0] \LoadUse次数 , \总周期数 , \插入气泡数 , \无条件分支数 , \条件分支成功数 ;
  wire [25:0] addr;
  wire [27:0] adder_2_out;
  wire [31:0] adder_1_out, adder_4_out, bit_extender_1_out, bit_extender_2_out, DATA_CHA, EPC_ADDR,
       ex_mem_1_r1_out, EX_PC, id_ex_1_imm_out, id_ex_1_r1_out, id_ex_1_r2_out, ID_IR, ID_PC, IF_IR, IF_PC,
       INT_ADDR, MDin, MEM_IR, MEM_PC, mem_wb_1_aluresult_out, mem_wb_1_rd_out, mips_alu_1_result,
       mips_regifile_1_r1, mips_regifile_1_r2, multiplexer_1_out, multiplexer_2_out, multiplexer_3_out,
       multiplexer_6_out, multiplexer_9_out, multiplexer_11_out, multiplexer_13_out, multiplexer_23_out,
       PC_JR, PCimm, R1, R2, RDin, RET_ADDR, sb_r2, shifter_1_out, WB_IR, WB_PC;
  wire [31:2] ex_mem_1_aluresult_out;
  wire [31:26] EX_IR;
  wire [31:28] PC_JAL;

  Button \u_总复位  (.out(RST));
  Button _1 (.out(IR1));
  Button _2 (.out(IR2));
  Button _3 (.out(IR3));
  // Probe on \总周期数 
  // Probe on \总周期数 
  Button \u_继续运行  (.out(Go));
  LED #(.active("true")) led_1 (.in(W1));
  LED #(.active("true")) led_2 (.in(W2));
  LED #(.active("true")) led_3 (.in(W3));
  Hex_Digit_Display hex_digit_display_1 (.value(out_1[31:28]));  // open: dp
  // Probe on IF_PC[19:0]
  // Mips_Probe mips_probe_1: pin names not known; wires that end beside it: IF_IR
  Hex_Digit_Display hex_digit_display_2 (.value(out_1[23:20]));  // open: dp
  Hex_Digit_Display hex_digit_display_3 (.value(out_1[27:24]));  // open: dp
  // Probe on ID_PC[19:0]
  // Mips_Probe mips_probe_2: pin names not known; wires that end beside it: ID_IR
  Multiplexer #(.select(3), .width(32), .disabled("Z"), .enable("false")) multiplexer_1 (
    .in0(adder_1_out), .in1(PCimm), .in2({PC_JAL, addr, 2'b00}), .in6(PC_JR), .out(multiplexer_1_out),
    .sel({JR, JMP, J2}));  // open: in3, in4, in5, in7
  Hex_Digit_Display hex_digit_display_4 (.value(out_1[19:16]));  // open: dp
  Hex_Digit_Display hex_digit_display_5 (.value(out_1[15:12]));  // open: dp
  Multiplexer #(.select(1), .width(32), .disabled("Z"), .enable("false")) multiplexer_2 (
    .in0(multiplexer_1_out), .in1(INT_ADDR), .out(multiplexer_2_out), .sel(INT));
  Multiplexer #(.select(1), .width(32), .disabled("Z"), .enable("false")) multiplexer_3 (
    .in0(multiplexer_2_out), .in1(EPC_ADDR), .out(multiplexer_3_out), .sel(ERET));
  Hex_Digit_Display hex_digit_display_6 (.value(out_1[7:4]));  // open: dp
  Hex_Digit_Display hex_digit_display_7 (.value(out_1[11:8]));  // open: dp
  Clock #(.highDuration(1), .lowDuration(1)) clock_1 (.out(CLK));
  // Probe on EX_PC[19:0]
  // Mips_Probe mips_probe_3: pin names not known; wires that end beside it: {EX_IR, addr}
  Hex_Digit_Display hex_digit_display_8 (.value(out_1[3:0]));  // open: dp
  Register #(.width(32), .trigger("rising"), .Select("low")) PC (
    .D(multiplexer_3_out), .en(\PC_EN调试 ), .Q(IF_PC), .clk(CLK), .clr(RST));
  // Probe on \总周期数 
  // Probe on MEM_PC[19:0]
  // Mips_Probe mips_probe_4: pin names not known; wires that end beside it: MEM_IR
  // Probe on \总周期数 
  // Probe on \无条件分支数 
  // Probe on \条件分支成功数 
  // Probe on \插入气泡数 
  // Probe on \LoadUse次数 
  ROM #(.addrWidth(10), .dataWidth(32), .Select("high")) rom_1 (.addr(IF_PC[11:2]), .data(IF_IR));
  // Probe on IF_PC[11:0]
  // Probe on WB_PC[19:0]
  // Mips_Probe mips_probe_5: pin names not known; wires that end beside it: WB_IR
  or or_1 (or_1_out, JMP, JR);
  or or_2 (or_2_out, ~Halt, Go);  // OR_Gate
  or or_3 (W1, INT1, d_ff_1_q);
  or or_4 (W2, INT2, d_ff_2_q);
  or or_5 (W3, INT3, d_ff_3_q);
  // Probe on ID_PC[11:0]
  // Probe on EX_PC[11:0]
  IF_ID if_id_1 (
    .IR_IN(IF_IR), .PC_IN(IF_PC), .IR(ID_IR), .PC(ID_PC), .reset(\数据相关检测_重定向_1_if_id_stall ), .CLK(CLK),
    .CLEAR(RST), .ENABLE(\数据相关检测_重定向_1_if_id_en ));  // open: PJUMP_IN, PJUM_OUT
  Adder #(.width(32)) adder_1 (.a(IF_PC), .b(32'h4), .out(adder_1_out));  // open: cin, cout
  Counter #(.width(16), .max('hffff), .ongoal("wrap"), .trigger("rising"), .behavior("old")) counter_1 (
    .count(and_1_out), .Q(\无条件分支数 ), .clk(CLK), .clr(RST));  // open: load, D, carry, preset
  and and_1 (and_1_out, or_1_out, or_2_out);
  and and_2 (and_2_out, J2, or_2_out);
  D_Flip_Flop #(.trigger("rising"), .Pre_Clr_Positions("LEGACY"), .NegatePresetClear("false"), .enable("true"), .NewFFLayout("false")) d_ff_1 (
    .clk(IR1), .D(1'b1), .Q(d_ff_1_q), .reset(INT1));  // open: Qn, preset, en
  D_Flip_Flop #(.trigger("rising"), .Pre_Clr_Positions("LEGACY"), .NegatePresetClear("false"), .enable("true"), .NewFFLayout("false")) d_ff_2 (
    .clk(IR2), .D(1'b1), .Q(d_ff_2_q), .reset(INT2));  // open: Qn, preset, en
  D_Flip_Flop #(.trigger("rising"), .Pre_Clr_Positions("LEGACY"), .NegatePresetClear("false"), .enable("true"), .NewFFLayout("false")) d_ff_3 (
    .clk(IR3), .D(1'b1), .Q(d_ff_3_q), .reset(INT3));  // open: Qn, preset, en
  // Probe on MEM_PC[11:0]
  // Mips_Probe mips_probe_6: pin names not known; wires that end beside it: IF_IR, ID_IR
  Counter #(.width(16), .max('hffff), .ongoal("wrap"), .trigger("rising"), .behavior("old")) counter_2 (
    .count(and_2_out), .Q(\条件分支成功数 ), .clk(CLK), .clr(RST));  // open: load, D, carry, preset
  or or_6 (or_6_out, d_ff_1_q, INT1);
  and and_3 (and_3_out, or_6_out, ~CLR1);  // AND_Gate
  or or_7 (or_7_out, d_ff_2_q, INT2);
  and and_4 (and_4_out, or_7_out, ~CLR2);  // AND_Gate
  or or_8 (or_8_out, d_ff_3_q, INT3);
  and and_5 (and_5_out, or_8_out, ~CLR3);  // AND_Gate
  // Probe on WB_PC[11:0]
  D_Flip_Flop #(.trigger("rising"), .Pre_Clr_Positions("LEGACY"), .NegatePresetClear("false"), .enable("true"), .NewFFLayout("false")) u_IR1 (
    .clk(CLK), .D(and_3_out), .Q(INT1));  // open: Qn, preset, en, reset
  D_Flip_Flop #(.trigger("rising"), .Pre_Clr_Positions("LEGACY"), .NegatePresetClear("false"), .enable("true"), .NewFFLayout("false")) u_IR2 (
    .clk(CLK), .D(and_4_out), .Q(INT2));  // open: Qn, preset, en, reset
  D_Flip_Flop #(.trigger("rising"), .Pre_Clr_Positions("LEGACY"), .NegatePresetClear("false"), .enable("true"), .NewFFLayout("false")) u_IR3 (
    .clk(CLK), .D(and_5_out), .Q(INT3));  // open: Qn, preset, en, reset
  and and_6 (and_6_out, Write, \数据相关 );
  \单周期硬布线控制器  \u_单周期硬布线控制器_1  (
    .Func(ID_IR[5:0]), .OP(ID_IR[31:26]), .ALU_OP(\单周期硬布线控制器_1_alu_op ), .MemToReg(\单周期硬布线控制器_1_memtoreg ),
    .MemWrite(\单周期硬布线控制器_1_memwrite ), .ALU_SRC(\单周期硬布线控制器_1_alu_src ), .RegWrite(\单周期硬布线控制器_1_regwrite ),
    .SysCALL(\单周期硬布线控制器_1_syscall ), .SignedExt(SignedExt), .RegDst(\单周期硬布线控制器_1_regdst ),
    .JR(\单周期硬布线控制器_1_jr ), .JMP(\单周期硬布线控制器_1_jmp ), .Beq(\单周期硬布线控制器_1_beq ), .JAL(\单周期硬布线控制器_1_jal ),
    .Bne(\单周期硬布线控制器_1_bne ), .ERET(\单周期硬布线控制器_1_eret ), .BLTZ(\单周期硬布线控制器_1_bltz ), .LUI(\单周期硬布线控制器_1_lui ),
    .SB(\单周期硬布线控制器_1_sb ));
  Multiplexer #(.select(1), .width(5), .disabled("Z"), .enable("false")) multiplexer_4 (
    .in0(ID_IR[25:21]), .in1(5'b00010), .out(ID_R1_num), .sel(\单周期硬布线控制器_1_syscall ));
  Multiplexer #(.select(1), .width(5), .disabled("Z"), .enable("false")) multiplexer_5 (
    .in0(ID_IR[20:16]), .in1(5'b00100), .out(ID_R2_num), .sel(\单周期硬布线控制器_1_syscall ));
  assign bit_extender_1_out = {{16{1'b0}}, ID_IR[15:0]};  // Bit_Extender bit_extender_1
  assign bit_extender_2_out = {{16{ID_IR[15]}}, ID_IR[15:0]};  // Bit_Extender bit_extender_2
  Counter #(.width(16), .max('hffff), .ongoal("wrap"), .trigger("rising"), .behavior("old")) counter_3 (
    .count(and_6_out), .Q(\插入气泡数 ), .clk(CLK), .clr(RST));  // open: load, D, carry, preset
  Counter #(.width(16), .max('hffff), .ongoal("wrap"), .trigger("rising"), .behavior("old")) counter_4 (
    .load(1'b0), .count(\PC_EN调试 ), .Q(\总周期数 ), .clk(CLK), .clr(RST));  // open: D, carry, preset
  and and_7 (and_7_out, INT0, ~ERET);  // AND_Gate
  or or_9 (INT0, INT3, INT2, INT1);
  Multiplexer #(.select(1), .width(32), .disabled("Z"), .enable("false")) multiplexer_6 (
    .in0(bit_extender_1_out), .in1(bit_extender_2_out), .out(multiplexer_6_out), .sel(SignedExt));
  D_Flip_Flop #(.trigger("rising"), .Pre_Clr_Positions("ABOVE_BELOW"), .NegatePresetClear("false"), .enable("false"), .NewFFLayout("true")) d_ff_4 (
    .clk(CLK), .D(and_7_out), .Qn(IE));  // open: Q, preset, reset
  Priority_Encoder #(.select(2), .disabled("Z")) priority_encoder_1 (
    .in0(INT1), .in1(INT2), .in2(INT3), .out(priority_encoder_1_out));  // open: in3, gs, en_out, en_in
  Register #(.width(32), .trigger("rising"), .Select("low")) \EPC寄存器  (
    .D(RET_ADDR), .en(INT), .Q(EPC_ADDR), .clk(CLK), .clr(RST));
  MIPS_Regifile mips_regifile_1 (
    .Din(RDin), .Clk(CLK), .R1(mips_regifile_1_r1), .R2(mips_regifile_1_r2), .WE(RegWrite), .W_num(W_num),
    .R1_num(ID_R1_num), .R2_num(ID_R2_num));
  Multiplexer #(.select(2), .width(32), .disabled("Z"), .enable("false")) multiplexer_7 (
    .in0(32'h30ac), .in1(32'h3150), .in2(32'h31f4), .out(INT_ADDR), .sel(priority_encoder_1_out));  // open: in3
  Register #(.width(2), .trigger("rising"), .Select("low")) register_1 (
    .D(priority_encoder_1_out), .en(INT), .Q(register_1_q), .clk(CLK));  // open: clr
  and and_8 (INT, INT0, IE);
  Demultiplexer #(.select(2), .width(1), .tristate("false"), .disabled("Z"), .enable("false")) demultiplexer_1 (
    .out0(CLR1), .out1(CLR2), .out2(CLR3), .in(ERET), .sel(register_1_q));  // open: out3
  ID_EX id_ex_1 (
    .BEQ_IN(\单周期硬布线控制器_1_beq ), .BNE_IN(\单周期硬布线控制器_1_bne ), .MEMTOREG_IN(\单周期硬布线控制器_1_memtoreg ),
    .MEMWRITE_IN(\单周期硬布线控制器_1_memwrite ), .ALUOP_IN(\单周期硬布线控制器_1_alu_op ),
    .ALU_SRC_IN(\单周期硬布线控制器_1_alu_src ), .REGWRITE_IN(\单周期硬布线控制器_1_regwrite ), .JAL_IN(\单周期硬布线控制器_1_jal ),
    .REGDIST_IN(\单周期硬布线控制器_1_regdst ), .SYSCALL_IN(\单周期硬布线控制器_1_syscall ), .JMP_IN(\单周期硬布线控制器_1_jmp ),
    .JR_IN(\单周期硬布线控制器_1_jr ), .IR_IN(ID_IR), .PC_IN(ID_PC), .R2_IN(mips_regifile_1_r2),
    .R1_IN(mips_regifile_1_r1), .IMM_IN(multiplexer_6_out), .BEQ_OUT(id_ex_1_beq_out),
    .BNE_OUT(id_ex_1_bne_out), .MEMTOREG_OUT(id_ex_1_memtoreg_out), .MEMWRITE_OUT(id_ex_1_memwrite_out),
    .ALUOP_OUT(id_ex_1_aluop_out), .ALU_SRC_OUT(id_ex_1_alu_src_out), .REGWRITE_OUT(id_ex_1_regwrite_out),
    .JAL_OUT(EX_JAL), .REGDST_IN(EX_REGD), .SYSCALL_OUT(id_ex_1_syscall_out), .JMP_OUT(JMP), .JR_OUT(JR),
    .IR_OUT({EX_IR, addr}), .PC_OUT(EX_PC), .R2_OUT(id_ex_1_r2_out), .R1_OUT(id_ex_1_r1_out),
    .IMM_OUT(id_ex_1_imm_out), .RESET(\数据相关检测_重定向_1_id_ex_stall ), .CLEAR(RST), .CLK(CLK), .ENABLE(Write),
    .LUI_IN(\单周期硬布线控制器_1_lui ), .LUI_OUT(LUI), .SB_IN(\单周期硬布线控制器_1_sb ), .SB_OUT(id_ex_1_sb_out),
    .BLTZ_IN(\单周期硬布线控制器_1_bltz ), .BLTZ_OUT(BLTZ), .RS_FORW_IN(\数据相关检测_重定向_1_rsforward ),
    .RS_FORW_OUT(id_ex_1_rs_forw_out), .RT_FORW_IN(\数据相关检测_重定向_1_rtforward ),
    .RT_FORW_OUT(id_ex_1_rt_forw_out), .ERET_IN(\单周期硬布线控制器_1_eret ), .ERET_OUT(ERET));  // open: PJUMP_IN, PJUMP_OUT
  Multiplexer #(.select(2), .width(32), .disabled("Z"), .enable("false")) multiplexer_8 (
    .in0(id_ex_1_r1_out), .in1(RDin), .in2({ex_mem_1_aluresult_out, sb_addr}),
    .in3({ex_mem_1_aluresult_out, sb_addr}), .out(PC_JR), .sel(id_ex_1_rs_forw_out));
  Multiplexer #(.select(2), .width(32), .disabled("Z"), .enable("false")) multiplexer_9 (
    .in0(id_ex_1_r2_out), .in1(RDin), .in2({ex_mem_1_aluresult_out, sb_addr}),
    .in3({ex_mem_1_aluresult_out, sb_addr}), .out(multiplexer_9_out), .sel(id_ex_1_rt_forw_out));
  Multiplexer #(.select(1), .width(5), .disabled("Z"), .enable("false")) multiplexer_10 (
    .in0(addr[20:16]), .in1(addr[15:11]), .out(multiplexer_10_out), .sel(EX_REGD));
  Multiplexer #(.select(1), .width(32), .disabled("Z"), .enable("false")) multiplexer_11 (
    .in0(multiplexer_9_out), .in1(id_ex_1_imm_out), .out(multiplexer_11_out), .sel(id_ex_1_alu_src_out));
  Adder #(.width(32)) adder_2 (.a(EX_PC), .b(32'h4), .out({PC_JAL, adder_2_out}));  // open: cin, cout
  Shifter #(.width(32), .shift("ll")) shifter_1 (.in(id_ex_1_imm_out), .\dist (5'b00010), .out(shifter_1_out));
  Multiplexer #(.select(1), .width(5), .disabled("Z"), .enable("false")) multiplexer_12 (
    .in0(multiplexer_10_out), .in1({5{1'b1}}), .out(EX_REGTOWRITE), .sel(EX_JAL));
  Comparator #(.width(32), .mode("twosComplement")) comparator_1 (
    .a({32{1'b0}}), .b(PC_JR), .gt(comparator_1_gt));  // open: eq, lt
  Multiplexer #(.select(1), .width(32), .disabled("Z"), .enable("false")) multiplexer_13 (
    .in0(multiplexer_11_out), .in1(32'h22), .out(multiplexer_13_out), .sel(id_ex_1_syscall_out));
  Adder #(.width(32)) adder_3 (.a({PC_JAL, adder_2_out}), .b(shifter_1_out), .out(PCimm));  // open: cin, cout
  MIPS_ALU mips_alu_1 (
    .X(PC_JR), .Y(multiplexer_13_out), .AluOP(id_ex_1_aluop_out), .Equal(mips_alu_1_equal),
    .Result(mips_alu_1_result), .shamt(shamt));  // open: Result_2
  Multiplexer #(.select(1), .width(5), .disabled("Z"), .enable("false")) multiplexer_14 (
    .in0(addr[10:6]), .in1(5'b10000), .out(shamt), .sel(LUI));
  and and_9 (and_9_out, comparator_1_gt, BLTZ);
  or or_10 (J2, and_9_out, and_10_out, and_11_out);
  and and_10 (and_10_out, id_ex_1_beq_out, mips_alu_1_equal);
  and and_11 (and_11_out, id_ex_1_bne_out, ~mips_alu_1_equal);  // AND_Gate
  or or_11 (or_11_out, J2, JR, INT, ERET, JMP);
  EX_MEM ex_mem_1 (
    .MemToReg_in(id_ex_1_memtoreg_out), .MemWrite_in(id_ex_1_memwrite_out),
    .RegWrite_in(id_ex_1_regwrite_out), .JAL_in(EX_JAL), .RegDst_in(EX_REGD),
    .Syscall_in(id_ex_1_syscall_out), .equal_in(mips_alu_1_equal), .IR_in({EX_IR, addr}), .PC_in(EX_PC),
    .ALUResult_in(mips_alu_1_result), .R2_in(multiplexer_9_out), .R1_in(PC_JR),
    .MemToReg_out(ex_mem_1_memtoreg_out), .MemWrite_out(MemWrite), .RegWrite_out(ex_mem_1_regwrite_out),
    .JAL_out(MEM_JAL), .RegDst_out(MEM_REGD), .Syscall_out(ex_mem_1_syscall_out),
    .equal_out(ex_mem_1_equal_out), .IR_out(MEM_IR), .PC_out(MEM_PC),
    .ALUResult_out({ex_mem_1_aluresult_out, sb_addr}), .R2_out(sb_r2), .R1_out(ex_mem_1_r1_out),
    .RESET(1'b0), .CLK(CLK), .CLEAR(RST), .ENABLE(Write), .SB_in(id_ex_1_sb_out), .SB_out(SB_USE));  // open: Imm_in, Imm_out
  Multiplexer #(.select(3), .width(32), .disabled("Z"), .enable("false")) multiplexer_15 (
    .in0({PC_JAL, adder_2_out}), .in1(PCimm), .in2({PC_JAL, addr, 2'b00}), .in6(PC_JR), .out(RET_ADDR),
    .sel({JR, JMP, J2}));  // open: in3, in4, in5, in7
  and and_12 (and_12_out, ~sb_addr[0], ~sb_addr[1]);  // AND_Gate
  and and_13 (and_13_out, sb_addr[0], ~sb_addr[1]);  // AND_Gate
  and and_14 (and_14_out, ~sb_addr[0], sb_addr[1]);  // AND_Gate
  and and_15 (and_15_out, sb_addr[0], sb_addr[1]);
  not not_1 (not_1_out, CLK);
  Multiplexer #(.select(1), .width(5), .disabled("Z"), .enable("false")) multiplexer_16 (
    .in0(MEM_IR[20:16]), .in1(MEM_IR[15:11]), .out(multiplexer_16_out), .sel(MEM_REGD));
  Multiplexer #(.select(1), .width(8), .disabled("Z"), .enable("false")) multiplexer_17 (
    .in0(DATA_CHA[7:0]), .in1(sb_r2[7:0]), .out(multiplexer_17_out), .sel(and_12_out));
  Multiplexer #(.select(1), .width(8), .disabled("Z"), .enable("false")) multiplexer_18 (
    .in0(DATA_CHA[15:8]), .in1(sb_r2[7:0]), .out(multiplexer_18_out), .sel(and_13_out));
  Multiplexer #(.select(1), .width(8), .disabled("Z"), .enable("false")) multiplexer_19 (
    .in0(DATA_CHA[23:16]), .in1(sb_r2[7:0]), .out(multiplexer_19_out), .sel(and_14_out));
  RAM #(.addrWidth(10), .dataWidth(32), .bus("separate"), .Select("high")) ram_1 (
    .addr(ex_mem_1_aluresult_out[11:2]), .din(MDin), .data(DATA_CHA), .str(MemWrite), .clk(not_1_out),
    .clr(RST));  // open: sel, ld
  Multiplexer #(.select(1), .width(5), .disabled("Z"), .enable("false")) multiplexer_20 (
    .in0(multiplexer_16_out), .in1({5{1'b1}}), .out(MEM_REGTOWRITE), .sel(MEM_JAL));
  Multiplexer #(.select(1), .width(8), .disabled("Z"), .enable("false")) multiplexer_21 (
    .in0(DATA_CHA[31:24]), .in1(sb_r2[7:0]), .out(multiplexer_21_out), .sel(and_15_out));
  MEM_WB mem_wb_1 (
    .MemToReg_in(ex_mem_1_memtoreg_out), .MemWrite_in(MemWrite), .RegWrite_in(ex_mem_1_regwrite_out),
    .JAL_in(MEM_JAL), .RegDst_in(MEM_REGD), .Syscall_in(ex_mem_1_syscall_out), .equal_in(ex_mem_1_equal_out),
    .IR_in(MEM_IR), .PC_in(MEM_PC), .ALUResult_in({ex_mem_1_aluresult_out, sb_addr}), .RD_in(DATA_CHA),
    .R1_in(ex_mem_1_r1_out), .MemToReg_out(mem_wb_1_memtoreg_out), .RegWrite_out(RegWrite),
    .JAL_out(mem_wb_1_jal_out), .RegDst_out(mem_wb_1_regdst_out), .Syscall_out(mem_wb_1_syscall_out),
    .IR_out(WB_IR), .PC_out(WB_PC), .ALUResult_out(mem_wb_1_aluresult_out), .RD_out(mem_wb_1_rd_out),
    .\气泡_高电平时有效 (1'b0), .clk(CLK), .clear(RST), .enable(Write), .R1_out(R1), .R2_in(sb_r2), .R2_out(R2));  // open: MemWrite_out, equal_out
  Multiplexer #(.select(1), .width(32), .disabled("Z"), .enable("false")) multiplexer_22 (
    .in0(sb_r2), .in1({multiplexer_21_out, multiplexer_19_out, multiplexer_18_out, multiplexer_17_out}),
    .out(MDin), .sel(SB_USE));
  Multiplexer #(.select(1), .width(32), .disabled("Z"), .enable("false")) multiplexer_23 (
    .in0(mem_wb_1_aluresult_out), .in1(mem_wb_1_rd_out), .out(multiplexer_23_out), .sel(mem_wb_1_memtoreg_out));
  or or_12 (or_12_out, ~Halt, Go);  // OR_Gate
  \数据相关检测_重定向  \u_数据相关检测_重定向_1  (
    .OP(ID_IR[31:26]), .FUNC(ID_IR[5:0]), .RS(ID_R1_num), .Halt_or_Go(or_12_out),
    .EX_MEMTOREG(id_ex_1_memtoreg_out), .EX_WRITEREG(EX_REGTOWRITE), .RT(ID_R2_num), .\J标记 (or_11_out),
    .MEM_REGW(ex_mem_1_regwrite_out), .MEM_WRITEREG(MEM_REGTOWRITE), .EX_REGW(id_ex_1_regwrite_out),
    .PC_EN(\PC_EN调试 ), .LOAD_USED(\数据相关 ), .IF_ID_EN(\数据相关检测_重定向_1_if_id_en ),
    .IF_ID_STALL(\数据相关检测_重定向_1_if_id_stall ), .ID_EX_STALL(\数据相关检测_重定向_1_id_ex_stall ),
    .RSFORWARD(\数据相关检测_重定向_1_rsforward ), .RTFORWARD(\数据相关检测_重定向_1_rtforward ));
  nand nand_1 (Write, not_2_out, Halt);
  Multiplexer #(.select(1), .width(5), .disabled("Z"), .enable("false")) multiplexer_24 (
    .in0(WB_IR[20:16]), .in1(WB_IR[15:11]), .out(multiplexer_24_out), .sel(mem_wb_1_regdst_out));
  Adder #(.width(32)) adder_4 (.a(WB_PC), .b(32'h4), .out(adder_4_out));  // open: cin, cout
  not not_2 (not_2_out, Go);
  Multiplexer #(.select(1), .width(32), .disabled("Z"), .enable("false")) multiplexer_25 (
    .in0(multiplexer_23_out), .in1(adder_4_out), .out(RDin), .sel(mem_wb_1_jal_out));
  Multiplexer #(.select(1), .width(5), .disabled("Z"), .enable("false")) multiplexer_26 (
    .in0(multiplexer_24_out), .in1({5{1'b1}}), .out(W_num), .sel(mem_wb_1_jal_out));
  Comparator #(.width(32), .mode("twosComplement")) comparator_2 (
    .a(R1), .b(32'h22), .eq(comparator_2_eq));  // open: gt, lt
  and and_16 (Ledout, comparator_2_eq, mem_wb_1_syscall_out);
  and and_17 (Halt, ~comparator_2_eq, mem_wb_1_syscall_out);  // AND_Gate
  Register #(.width(32), .trigger("rising"), .Select("low")) register_2 (
    .D(R2), .en(Ledout), .Q(out_1), .clk(CLK), .clr(RST));

  // Other names for the same wires on the sheet: RD[4:0] = ID_IR[15:11]; LedData[31:0] = out_1; EX_IR[25:0] = addr;
  //   PC_JAL[27:2] = addr

  // Notes on the sheet:
  //   中断源
  //   时空图监测，可删除
  //   中断等待指示
  //   数码管输出
  //   指令存储器
  //   contents of rom_1 (hex, n*v repeats v):
  //   3c010100 34210000 12020 20020022 c 20020001 c 20012290 10360001 8100007 20020001 c
  //   流水调试日志用
  //   OP
  //   Func
  //   rs
  //   rt
  //   rd
  //   指令字
  //   指令调试器件
  //   Reset 
  //   Reset 
  //   Reset 
  //   JMP
  //   JR
  //   OP
  //   Func
  //   Beq
  //   Bne
  //   AluOP
  //   AluSrcB
  //   RegWrite
  //   JAL
  //   RegDst
  //   Syscall
  //   MemToReg
  //   MemWrite
  //   SB指令电路
endmodule

module \五子棋  (
);

  wire clock_1_out, lcd_video_1_p1;
  wire [2:0] mips_ram_1_p1_2;
  wire [6:0] lcd_video_1_p4, lcd_video_1_p5;
  wire [15:0] multiplexer_1_out;
  wire [23:0] lcd_video_1_p7;
  wire [31:7] mips_ram_1_p1;

  \团队CPU  \u_团队cpu_1  ();  // open: out_1
  Clock #(.highDuration(1), .lowDuration(1)) clock_1 (.out(clock_1_out));
  Multiplexer #(.select(3), .width(16), .disabled("Z"), .enable("false")) multiplexer_1 (
    .in0({16{1'b1}}), .in1(16'h3e0), .in2(16'h1f), .out(multiplexer_1_out), .sel(mips_ram_1_p1_2));  // open: in3, in4, in5, in6, in7
  // LCD_Video lcd_video_1: pin names not known; wires that end beside it: lcd_video_1_p1, clock_1_out, 1'b1, lcd_video_1_p4, lcd_video_1_p5, multiplexer_1_out, lcd_video_1_p7
  Button button_1 (.out(lcd_video_1_p1));
  Counter #(.width(24), .max('hffffff), .ongoal("wrap"), .trigger("rising"), .behavior("new")) counter_1 (
    .Q(lcd_video_1_p7), .clk(clock_1_out), .clr(lcd_video_1_p1));  // open: load, D, count, carry, preset, down
  // MIPS_RAM mips_ram_1: pin names not known; wires that end beside it: {mips_ram_1_p1[31:19], mips_ram_1_p1_2, mips_ram_1_p1[15], lcd_video_1_p5, mips_ram_1_p1[7], lcd_video_1_p4}
endmodule
